// Logisim project adventure_4.circ as structural Verilog: 8 circuits, main circuit main
// 1
module main (
);

  wire clock, clr, controlled_buffer_1_out, controlled_buffer_2_out, counter_1_carry, down, left, not_1_out,
       not_2_out, or_1_out, or_2_out, right, up;
  wire [4:0] counter_1_q, counter_2_q;
  wire [9:0] register_1_q;
  wire [20:0] pseudo_reg_1_out_24, pseudo_reg_1_out_25, pseudo_reg_1_out_26, pseudo_reg_1_out_27,
       pseudo_reg_1_out_28, pseudo_reg_1_out_29, pseudo_reg_1_out_30, pseudo_reg_1_out_31,
       pseudo_reg_1_out_32, pseudo_reg_1_out_33, pseudo_reg_1_out_34, pseudo_reg_1_out_35,
       pseudo_reg_1_out_36, pseudo_reg_1_out_37, pseudo_reg_1_out_38, pseudo_reg_1_out_39,
       pseudo_reg_1_out_40, pseudo_reg_1_out_41, pseudo_reg_1_out_42, pseudo_reg_1_out_43,
       pseudo_reg_1_out_44;

  Clock clock_1 (.out(clock));
  Button button_1 (.out(clr));
  Register #(.width(10)) register_1 (
    .D({counter_1_q, counter_2_q}), .Q(register_1_q), .clk(clock), .clr(clr));  // open: en
  Joystick joystick_1 ();  // open: x, y
  or or_1 (or_1_out, right, left);
  or or_2 (or_2_out, up, down);
  assign controlled_buffer_1_out = left ? not_1_out : 1'bz;  // Controlled_Buffer controlled_buffer_1
  not not_1 (not_1_out, right);
  assign controlled_buffer_2_out = down ? not_2_out : 1'bz;  // Controlled_Buffer controlled_buffer_2
  not not_2 (not_2_out, up);
  Counter #(.width(5), .max('h15)) counter_1 (
    .load(left), .count(controlled_buffer_1_out), .Q(counter_1_q), .carry(counter_1_carry), .clk(or_1_out),
    .clr(clr));  // open: D
  Counter #(.width(5), .max('h15)) counter_2 (
    .load(down), .count(controlled_buffer_2_out), .Q(counter_2_q), .clk(or_2_out), .clr(clr));  // open: D, carry
  Register #(.width(5)) register_2 (.D(register_1_q[9:5]), .clk(clock), .clr(clr));  // open: en, Q
  Register #(.width(5)) register_3 (.D(register_1_q[4:0]), .clk(clock), .clr(clr));  // open: en, Q
  Button button_2 (.out(up));
  Button button_3 (.out(left));
  Button button_4 (.out(right));
  Button button_5 (.out(down));
  pseudo_reg pseudo_reg_1 (
    .in_22(register_1_q[4:0]), .in_23(register_1_q[9:5]), .out_34(pseudo_reg_1_out_34),
    .out_24(pseudo_reg_1_out_24), .out_25(pseudo_reg_1_out_25), .out_35(pseudo_reg_1_out_35),
    .out_26(pseudo_reg_1_out_26), .out_36(pseudo_reg_1_out_36), .out_37(pseudo_reg_1_out_37),
    .out_27(pseudo_reg_1_out_27), .out_38(pseudo_reg_1_out_38), .out_28(pseudo_reg_1_out_28),
    .out_39(pseudo_reg_1_out_39), .out_29(pseudo_reg_1_out_29), .out_40(pseudo_reg_1_out_40),
    .out_30(pseudo_reg_1_out_30), .out_41(pseudo_reg_1_out_41), .out_31(pseudo_reg_1_out_31),
    .out_42(pseudo_reg_1_out_42), .out_32(pseudo_reg_1_out_32), .out_43(pseudo_reg_1_out_43),
    .out_33(pseudo_reg_1_out_33), .out_44(pseudo_reg_1_out_44), .in_11(21'h11e060), .in_1(21'h11e060),
    .in_2(21'h11e3f9), .in_3(21'h100381), .in_4(21'h1ff381), .in_5(21'h1), .in_6(21'h1), .in_7(21'h1ff381),
    .in_8(21'h100381), .in_12(21'h11e3ff), .in_13(21'h1003f9), .in_14(21'h1ff381), .in_15(21'h1ff381),
    .in_16(21'h1), .in_17(21'h1ff381), .in_18(21'h1ff381), .in_19(21'h1003f9), .in_20(21'h11e3ff),
    .in_21(21'h11e060), .in_9(21'h11e3f9), .in_10(21'h11e060));
  DotMatrix #(.matrixcols(21), .matrixrows(21)) dotmatrix_1 (
    .col0(pseudo_reg_1_out_34), .col1(pseudo_reg_1_out_24), .col2(pseudo_reg_1_out_35),
    .col3(pseudo_reg_1_out_25), .col4(pseudo_reg_1_out_36), .col5(pseudo_reg_1_out_26),
    .col6(pseudo_reg_1_out_37), .col7(pseudo_reg_1_out_27), .col8(pseudo_reg_1_out_38),
    .col9(pseudo_reg_1_out_28), .col10(pseudo_reg_1_out_39), .col11(pseudo_reg_1_out_29),
    .col12(pseudo_reg_1_out_40), .col13(pseudo_reg_1_out_30), .col14(pseudo_reg_1_out_41),
    .col15(pseudo_reg_1_out_31), .col16(pseudo_reg_1_out_42), .col17(pseudo_reg_1_out_32),
    .col18(pseudo_reg_1_out_43), .col19(pseudo_reg_1_out_33), .col20(pseudo_reg_1_out_44));
  ROM #(.addrWidth(7), .dataWidth(21)) rom_1 ();  // open: addr, data, sel

  // Notes on the sheet:
  //   coor X
  //   coor Y
endmodule

module _16_bit_AND (
  input  [20:0] \input ,
  input  switch,
  output [20:0] \output 
);

  assign \output  = \input  & {21{switch}};  // AND_Gate and_1, 21 bits wide
endmodule

module column_switch (
  input  [3:0] in_1,
  input  [3:0] in_2
);
endmodule

module inc_dec (
  input  [4:0] X,
  input  on_off,
  input  inc_dec,
  output [4:0] R,
  output OFL
);

  wire and_2_out, and_3_out;
  wire [4:0] and_1_out, xor_1_out, xor_2_out, xor_3_out;
  wire [4:4] decoder_1_out0, decoder_1_out1;

  Decoder #(.enable("false")) decoder_1 (.out0(decoder_1_out0[4]), .out1(decoder_1_out1[4]), .sel(inc_dec));
  assign xor_1_out = {5{decoder_1_out0[4]}} ^ X;  // XOR_Gate xor_1, 5 bits wide
  assign xor_2_out = {5{decoder_1_out1[4]}} ^ xor_3_out;  // XOR_Gate xor_2, 5 bits wide
  assign and_1_out = xor_1_out & xor_2_out;  // AND_Gate and_1, 5 bits wide
  and and_2 (and_2_out, and_1_out[4], inc_dec);
  and and_3 (and_3_out, and_1_out[4], ~inc_dec);  // AND_Gate
  assign xor_3_out = X ^ {and_1_out[3:0], 1'b1};  // XOR_Gate xor_3, 5 bits wide
  or or_1 (OFL, and_2_out, and_3_out);
  Multiplexer #(.width(5), .enable("false")) multiplexer_1 (.in0(X), .in1(xor_3_out), .out(R), .sel(on_off));
endmodule

module granca_detection (
  input  Up,
  input  Down,
  input  [7:0] in_3,
  input  Left,
  input  Right,
  output out_6
);

  wire and_1_out, and_2_out, nor_1_out, nor_2_out;

  Pull_Resistor pull_resistor_1 (.node(Up));
  Pull_Resistor pull_resistor_2 (.node(Down));
  Pull_Resistor pull_resistor_3 (.node(Left));
  Pull_Resistor pull_resistor_4 (.node(Right));
  and and_1 (and_1_out, Up, in_3[3], in_3[2], in_3[1], in_3[0]);
  and and_2 (and_2_out, in_3[7], in_3[6], in_3[5], in_3[4], Right);
  nor nor_1 (nor_1_out, ~Down, in_3[0], in_3[1], in_3[2], in_3[3]);  // NOR_Gate
  nor nor_2 (nor_2_out, in_3[4], in_3[5], in_3[6], in_3[7], ~Left);  // NOR_Gate
  or or_1 (out_6, and_1_out, nor_1_out, nor_2_out, and_2_out);
endmodule

module movement (
  input  Right,
  input  Down,
  input  Left,
  input  Up,
  input  Clock,
  input  Clear,
  output out_7,
  output out_8,
  output out_9,
  output out_10
);

  wire and_1_out, counter_1_carry, or_3_out, xnor_1_out, xor_1_out;
  wire [1:0] multiplexer_1_out, or_1_out, register_1_q, register_2_q;

  or or_1 (or_1_out[0], Down, Right);
  or or_2 (or_1_out[1], Right, Left);
  or or_3 (or_3_out, Right, Down, Left, Up);
  Register #(.width(2)) register_1 (.D(or_1_out), .Q(register_1_q), .clk(or_3_out), .clr(Clear));  // open: en
  Register #(.width(2)) register_2 (.D(multiplexer_1_out), .Q(register_2_q), .clk(or_3_out), .clr(Clear));  // open: en
  xnor xnor_1 (xnor_1_out, register_2_q[1], register_1_q[1]);
  and and_1 (and_1_out, xnor_1_out, xor_1_out);
  xor xor_1 (xor_1_out, register_2_q[0], register_1_q[0]);
  Multiplexer #(.width(2)) multiplexer_1 (
    .in0(register_1_q), .in1(register_2_q), .out(multiplexer_1_out), .sel(and_1_out));  // open: en
  Counter #(.width(3), .max('h5)) counter_1 (
    .carry(counter_1_carry), .clk(Clock), .clr(Clear));  // open: load, D, count, Q
  Demultiplexer #(.select(2)) demultiplexer_1 (
    .out0(out_7), .out1(out_8), .out2(out_9), .out3(out_10), .in(counter_1_carry), .sel(multiplexer_1_out));  // open: en

  // Other names for the same wires on the sheet: clr = Clear

  // Notes on the sheet:
  //   новое напр.
  //   текушее напр.
endmodule

module pseudo_reg (
  input  [20:0] in_1,
  input  [20:0] in_2,
  input  [20:0] in_3,
  input  [20:0] in_4,
  input  [20:0] in_5,
  input  [20:0] in_6,
  input  [20:0] in_7,
  input  [20:0] in_8,
  input  [20:0] in_9,
  input  [20:0] in_10,
  input  [20:0] in_11,
  input  [20:0] in_12,
  input  [20:0] in_13,
  input  [20:0] in_14,
  input  [20:0] in_15,
  input  [20:0] in_16,
  input  [20:0] in_17,
  input  [20:0] in_18,
  input  [20:0] in_19,
  input  [20:0] in_20,
  input  [20:0] in_21,
  input  [4:0] in_22,
  input  [4:0] in_23,
  output [20:0] out_24,
  output [20:0] out_25,
  output [20:0] out_26,
  output [20:0] out_27,
  output [20:0] out_28,
  output [20:0] out_29,
  output [20:0] out_30,
  output [20:0] out_31,
  output [20:0] out_32,
  output [20:0] out_33,
  output [20:0] out_34,
  output [20:0] out_35,
  output [20:0] out_36,
  output [20:0] out_37,
  output [20:0] out_38,
  output [20:0] out_39,
  output [20:0] out_40,
  output [20:0] out_41,
  output [20:0] out_42,
  output [20:0] out_43,
  output [20:0] out_44
);

  wire decoder_1_out21, decoder_2_out0, decoder_2_out1, decoder_2_out2, decoder_2_out3, decoder_2_out4,
       decoder_2_out5, decoder_2_out6, decoder_2_out7, decoder_2_out8, decoder_2_out9, decoder_2_out10,
       decoder_2_out11, decoder_2_out12, decoder_2_out13, decoder_2_out14, decoder_2_out15, decoder_2_out16,
       decoder_2_out17, decoder_2_out18, decoder_2_out19, decoder_2_out20, decoder_2_out21;
  wire [20:0] decoder_1_out0, n16_bit_and_1_output, n16_bit_and_2_output, n16_bit_and_3_output,
       n16_bit_and_4_output, n16_bit_and_5_output, n16_bit_and_6_output, n16_bit_and_7_output,
       n16_bit_and_8_output, n16_bit_and_9_output, n16_bit_and_10_output, n16_bit_and_11_output,
       n16_bit_and_12_output, n16_bit_and_13_output, n16_bit_and_14_output, n16_bit_and_15_output,
       n16_bit_and_16_output, n16_bit_and_17_output, n16_bit_and_18_output, n16_bit_and_19_output,
       n16_bit_and_20_output, n16_bit_and_21_output;

  Decoder #(.select(5), .disabled(0), .enable("false")) decoder_1 (
    .out0(decoder_1_out0[0]), .out1(decoder_1_out0[1]), .out2(decoder_1_out0[2]), .out3(decoder_1_out0[3]),
    .out4(decoder_1_out0[4]), .out5(decoder_1_out0[5]), .out6(decoder_1_out0[6]), .out7(decoder_1_out0[7]),
    .out8(decoder_1_out0[8]), .out9(decoder_1_out0[9]), .out10(decoder_1_out0[10]),
    .out11(decoder_1_out0[11]), .out12(decoder_1_out0[12]), .out13(decoder_1_out0[13]),
    .out14(decoder_1_out0[14]), .out15(decoder_1_out0[15]), .out16(decoder_1_out0[16]),
    .out17(decoder_1_out0[17]), .out18(decoder_1_out0[18]), .out19(decoder_1_out0[19]),
    .out20(decoder_1_out0[20]), .out21(decoder_1_out21), .out22(decoder_1_out21), .out23(decoder_1_out21),
    .out24(decoder_1_out21), .out25(decoder_1_out21), .out26(decoder_1_out21), .out27(decoder_1_out21),
    .out28(decoder_1_out21), .out29(decoder_1_out21), .out30(decoder_1_out21), .out31(decoder_1_out21),
    .sel(in_22));
  assign out_34 = in_11 | n16_bit_and_1_output;  // OR_Gate or_1, 21 bits wide
  _16_bit_AND u_16_bit_and_1 (.\input (decoder_1_out0), .switch(decoder_2_out0), .\output (n16_bit_and_1_output));
  assign out_24 = in_1 | n16_bit_and_3_output;  // OR_Gate or_2, 21 bits wide
  assign out_35 = in_12 | n16_bit_and_2_output;  // OR_Gate or_3, 21 bits wide
  _16_bit_AND u_16_bit_and_2 (.\input (decoder_1_out0), .switch(decoder_2_out2), .\output (n16_bit_and_2_output));
  _16_bit_AND u_16_bit_and_3 (.\input (decoder_1_out0), .switch(decoder_2_out1), .\output (n16_bit_and_3_output));
  assign out_25 = in_2 | n16_bit_and_4_output;  // OR_Gate or_4, 21 bits wide
  assign out_36 = in_13 | n16_bit_and_5_output;  // OR_Gate or_5, 21 bits wide
  _16_bit_AND u_16_bit_and_4 (.\input (decoder_1_out0), .switch(decoder_2_out3), .\output (n16_bit_and_4_output));
  _16_bit_AND u_16_bit_and_5 (.\input (decoder_1_out0), .switch(decoder_2_out4), .\output (n16_bit_and_5_output));
  Decoder #(.select(5), .disabled(0), .enable("false")) decoder_2 (
    .out0(decoder_2_out0), .out1(decoder_2_out1), .out2(decoder_2_out2), .out3(decoder_2_out3),
    .out4(decoder_2_out4), .out5(decoder_2_out5), .out6(decoder_2_out6), .out7(decoder_2_out7),
    .out8(decoder_2_out8), .out9(decoder_2_out9), .out10(decoder_2_out10), .out11(decoder_2_out11),
    .out12(decoder_2_out12), .out13(decoder_2_out13), .out14(decoder_2_out14), .out15(decoder_2_out15),
    .out16(decoder_2_out16), .out17(decoder_2_out17), .out18(decoder_2_out18), .out19(decoder_2_out19),
    .out20(decoder_2_out20), .out21(decoder_2_out21), .out22(decoder_2_out21), .out23(decoder_2_out21),
    .out24(decoder_2_out21), .out25(decoder_2_out21), .out26(decoder_2_out21), .out27(decoder_2_out21),
    .out28(decoder_2_out21), .out29(decoder_2_out21), .out30(decoder_2_out21), .out31(decoder_2_out21),
    .sel(in_23));
  assign out_26 = in_3 | n16_bit_and_7_output;  // OR_Gate or_6, 21 bits wide
  assign out_37 = in_14 | n16_bit_and_6_output;  // OR_Gate or_7, 21 bits wide
  _16_bit_AND u_16_bit_and_6 (.\input (decoder_1_out0), .switch(decoder_2_out6), .\output (n16_bit_and_6_output));
  _16_bit_AND u_16_bit_and_7 (.\input (decoder_1_out0), .switch(decoder_2_out5), .\output (n16_bit_and_7_output));
  assign out_27 = in_4 | n16_bit_and_9_output;  // OR_Gate or_8, 21 bits wide
  assign out_38 = in_15 | n16_bit_and_8_output;  // OR_Gate or_9, 21 bits wide
  _16_bit_AND u_16_bit_and_8 (.\input (decoder_1_out0), .switch(decoder_2_out8), .\output (n16_bit_and_8_output));
  _16_bit_AND u_16_bit_and_9 (.\input (decoder_1_out0), .switch(decoder_2_out7), .\output (n16_bit_and_9_output));
  assign out_28 = in_5 | n16_bit_and_10_output;  // OR_Gate or_10, 21 bits wide
  assign out_39 = in_16 | n16_bit_and_11_output;  // OR_Gate or_11, 21 bits wide
  _16_bit_AND u_16_bit_and_10 (.\input (decoder_1_out0), .switch(decoder_2_out9), .\output (n16_bit_and_10_output));
  _16_bit_AND u_16_bit_and_11 (.\input (decoder_1_out0), .switch(decoder_2_out10), .\output (n16_bit_and_11_output));
  assign out_29 = in_6 | n16_bit_and_13_output;  // OR_Gate or_12, 21 bits wide
  assign out_40 = in_17 | n16_bit_and_12_output;  // OR_Gate or_13, 21 bits wide
  _16_bit_AND u_16_bit_and_12 (.\input (decoder_1_out0), .switch(decoder_2_out12), .\output (n16_bit_and_12_output));
  _16_bit_AND u_16_bit_and_13 (.\input (decoder_1_out0), .switch(decoder_2_out11), .\output (n16_bit_and_13_output));
  assign out_30 = in_7 | n16_bit_and_15_output;  // OR_Gate or_14, 21 bits wide
  assign out_41 = in_18 | n16_bit_and_14_output;  // OR_Gate or_15, 21 bits wide
  _16_bit_AND u_16_bit_and_14 (.\input (decoder_1_out0), .switch(decoder_2_out14), .\output (n16_bit_and_14_output));
  _16_bit_AND u_16_bit_and_15 (.\input (decoder_1_out0), .switch(decoder_2_out13), .\output (n16_bit_and_15_output));
  assign out_31 = in_8 | n16_bit_and_16_output;  // OR_Gate or_16, 21 bits wide
  assign out_42 = in_19 | n16_bit_and_17_output;  // OR_Gate or_17, 21 bits wide
  _16_bit_AND u_16_bit_and_16 (.\input (decoder_1_out0), .switch(decoder_2_out15), .\output (n16_bit_and_16_output));
  _16_bit_AND u_16_bit_and_17 (.\input (decoder_1_out0), .switch(decoder_2_out16), .\output (n16_bit_and_17_output));
  assign out_32 = in_9 | n16_bit_and_19_output;  // OR_Gate or_18, 21 bits wide
  assign out_43 = in_20 | n16_bit_and_18_output;  // OR_Gate or_19, 21 bits wide
  _16_bit_AND u_16_bit_and_18 (.\input (decoder_1_out0), .switch(decoder_2_out18), .\output (n16_bit_and_18_output));
  _16_bit_AND u_16_bit_and_19 (.\input (decoder_1_out0), .switch(decoder_2_out17), .\output (n16_bit_and_19_output));
  assign out_33 = in_10 | n16_bit_and_20_output;  // OR_Gate or_20, 21 bits wide
  assign out_44 = in_21 | n16_bit_and_21_output;  // OR_Gate or_21, 21 bits wide
  _16_bit_AND u_16_bit_and_20 (.\input (decoder_1_out0), .switch(decoder_2_out19), .\output (n16_bit_and_20_output));
  _16_bit_AND u_16_bit_and_21 (.\input (decoder_1_out0), .switch(decoder_2_out20), .\output (n16_bit_and_21_output));
endmodule

module maps (
  input  [20:0] in_1,
  input  [20:0] in_2,
  input  [20:0] in_3,
  input  [20:0] in_4,
  input  [20:0] in_5,
  input  [20:0] in_6,
  input  [20:0] in_7,
  input  [20:0] in_8,
  input  [20:0] in_9,
  input  [20:0] in_10,
  input  [20:0] in_11
);

  DotMatrix #(.matrixcols(21), .matrixrows(21)) dotmatrix_1 (
    .col0(in_1), .col1(in_2), .col2(in_3), .col3(in_4), .col4(in_5), .col5(in_6), .col6(in_7), .col7(in_8),
    .col8(in_9), .col9(in_10), .col10(in_11), .col11(in_10), .col12(in_9), .col13(in_8), .col14(in_7),
    .col15(in_6), .col16(in_5), .col17(in_4), .col18(in_3), .col19(in_2), .col20(in_1));
  // Probe on in_1
  // Probe on in_2
  // Probe on in_3
  // Probe on in_4
  // Probe on in_5
  // Probe on in_6
  // Probe on in_7
  // Probe on in_8
  // Probe on in_9
  // Probe on in_10
  // Probe on in_11
  DotMatrix #(.matrixcols(21), .matrixrows(21)) dotmatrix_2 (
    .col0(21'h11e060), .col1(21'h11e060), .col2(21'h11e3ff), .col3(21'h11e3f9), .col4(21'h1003f9),
    .col5(21'h100381), .col6(21'h1ff381), .col7(21'h1ff381), .col8(21'h1ff381), .col9(21'h1), .col10(21'h1),
    .col11(21'h1), .col12(21'h1ff381), .col13(21'h1ff381), .col14(21'h1ff381), .col15(21'h100381),
    .col16(21'h1003f9), .col17(21'h11e3f9), .col18(21'h11e3ff), .col19(21'h11e060), .col20(21'h11e060));
endmodule
