// Logisim project MAIN_FILE_no_step_back.circ as structural Verilog: 4 circuits, main circuit main
module main (
);

  wire and_1_out, button_2_out, button_3_out, button_4_out, button_5_out, clock, clr, counter_1_carry,
       decoder_2_out0, decoder_2_out1, decoder_2_out2, decoder_2_out3, decoder_2_out4, decoder_2_out5,
       decoder_2_out6, decoder_2_out7, decoder_2_out8, decoder_2_out9, decoder_2_out10, decoder_2_out11,
       decoder_2_out12, decoder_2_out13, decoder_2_out14, decoder_2_out15, down, left, or_1_out, or_2_out,
       or_5_out, or_6_out, right, up, xnor_1_out, xor_1_out;
  wire [1:0] multiplexer_1_out, or_3_out, register_2_q, register_3_q;
  wire [3:0] inc_dec_1_r, inc_dec_2_r, register_1_q, register_1_q_2, undriven;
  wire [15:0] decoder_1_out0, n16_bit_and_1_output, n16_bit_and_2_output, n16_bit_and_3_output,
       n16_bit_and_4_output, n16_bit_and_5_output, n16_bit_and_6_output, n16_bit_and_7_output,
       n16_bit_and_8_output, n16_bit_and_9_output, n16_bit_and_10_output, n16_bit_and_11_output,
       n16_bit_and_12_output, n16_bit_and_13_output, n16_bit_and_14_output, n16_bit_and_15_output,
       n16_bit_and_16_output;

  Register register_1 (
    .D({inc_dec_1_r, inc_dec_2_r}), .Q({register_1_q_2, register_1_q}), .clk(clock), .clr(clr));  // open: en
  Clock clock_1 (.out(clock));
  Button button_1 (.out(clr));
  or or_1 (or_1_out, left, right);
  inc_dec inc_dec_1 (.X(register_1_q_2), .on_off(or_1_out), .inc_dec(right), .R(inc_dec_1_r));
  Button button_2 (.out(button_2_out));
  Button button_3 (.out(button_3_out));
  Button button_4 (.out(button_4_out));
  Button button_5 (.out(button_5_out));
  inc_dec inc_dec_2 (.X(register_1_q), .on_off(or_6_out), .inc_dec(up), .R(inc_dec_2_r));
  or or_2 (or_2_out, up, down);
  inc_dec inc_dec_3 (.X(undriven), .on_off(or_2_out), .inc_dec(up));  // open: R
  or or_3 (or_3_out[0], button_5_out, button_4_out);
  or or_4 (or_3_out[1], button_4_out, button_3_out);
  or or_5 (or_5_out, button_4_out, button_5_out, button_3_out, button_2_out);
  Decoder #(.select(4), .disabled(0), .enable("false")) decoder_1 (
    .out0(decoder_1_out0[0]), .out1(decoder_1_out0[1]), .out2(decoder_1_out0[2]), .out3(decoder_1_out0[3]),
    .out4(decoder_1_out0[4]), .out5(decoder_1_out0[5]), .out6(decoder_1_out0[6]), .out7(decoder_1_out0[7]),
    .out8(decoder_1_out0[8]), .out9(decoder_1_out0[9]), .out10(decoder_1_out0[10]),
    .out11(decoder_1_out0[11]), .out12(decoder_1_out0[12]), .out13(decoder_1_out0[13]),
    .out14(decoder_1_out0[14]), .out15(decoder_1_out0[15]), .sel(register_1_q));
  or or_6 (or_6_out, up, down);
  Register #(.width(2)) register_2 (.D(or_3_out), .Q(register_2_q), .clk(or_5_out), .clr(clr));  // open: en
  Register #(.width(2)) register_3 (.D(multiplexer_1_out), .Q(register_3_q), .clk(or_5_out), .clr(clr));  // open: en
  DotMatrix #(.matrixcols(16), .matrixrows(16)) dotmatrix_1 (
    .col0(n16_bit_and_2_output), .col1(n16_bit_and_1_output), .col2(n16_bit_and_4_output),
    .col3(n16_bit_and_3_output), .col4(n16_bit_and_6_output), .col5(n16_bit_and_5_output),
    .col6(n16_bit_and_7_output), .col7(n16_bit_and_8_output), .col8(n16_bit_and_10_output),
    .col9(n16_bit_and_9_output), .col10(n16_bit_and_12_output), .col11(n16_bit_and_11_output),
    .col12(n16_bit_and_14_output), .col13(n16_bit_and_13_output), .col14(n16_bit_and_16_output),
    .col15(n16_bit_and_15_output));
  _16_bit_AND u_16_bit_and_1 (.\input (decoder_1_out0), .switch(decoder_2_out1), .\output (n16_bit_and_1_output));
  _16_bit_AND u_16_bit_and_2 (.\input (decoder_1_out0), .switch(decoder_2_out0), .\output (n16_bit_and_2_output));
  xnor xnor_1 (xnor_1_out, register_3_q[1], register_2_q[1]);
  xor xor_1 (xor_1_out, register_3_q[0], register_2_q[0]);
  _16_bit_AND u_16_bit_and_3 (.\input (decoder_1_out0), .switch(decoder_2_out3), .\output (n16_bit_and_3_output));
  _16_bit_AND u_16_bit_and_4 (.\input (decoder_1_out0), .switch(decoder_2_out2), .\output (n16_bit_and_4_output));
  Decoder #(.select(4), .disabled(0), .enable("false")) decoder_2 (
    .out0(decoder_2_out0), .out1(decoder_2_out1), .out2(decoder_2_out2), .out3(decoder_2_out3),
    .out4(decoder_2_out4), .out5(decoder_2_out5), .out6(decoder_2_out6), .out7(decoder_2_out7),
    .out8(decoder_2_out8), .out9(decoder_2_out9), .out10(decoder_2_out10), .out11(decoder_2_out11),
    .out12(decoder_2_out12), .out13(decoder_2_out13), .out14(decoder_2_out14), .out15(decoder_2_out15),
    .sel(register_1_q_2));
  Multiplexer #(.width(2)) multiplexer_1 (
    .in0(register_2_q), .in1(register_3_q), .out(multiplexer_1_out), .sel(and_1_out));  // open: en
  and and_1 (and_1_out, xnor_1_out, xor_1_out);
  _16_bit_AND u_16_bit_and_5 (.\input (decoder_1_out0), .switch(decoder_2_out5), .\output (n16_bit_and_5_output));
  _16_bit_AND u_16_bit_and_6 (.\input (decoder_1_out0), .switch(decoder_2_out4), .\output (n16_bit_and_6_output));
  _16_bit_AND u_16_bit_and_7 (.\input (decoder_1_out0), .switch(decoder_2_out6), .\output (n16_bit_and_7_output));
  _16_bit_AND u_16_bit_and_8 (.\input (decoder_1_out0), .switch(decoder_2_out7), .\output (n16_bit_and_8_output));
  Counter #(.width(3), .max('h5)) counter_1 (
    .carry(counter_1_carry), .clk(clock), .clr(clr));  // open: load, D, count, Q
  Demultiplexer #(.select(2)) demultiplexer_1 (
    .out0(up), .out1(down), .out2(left), .out3(right), .in(counter_1_carry), .sel(multiplexer_1_out));  // open: en
  _16_bit_AND u_16_bit_and_9 (.\input (decoder_1_out0), .switch(decoder_2_out9), .\output (n16_bit_and_9_output));
  _16_bit_AND u_16_bit_and_10 (.\input (decoder_1_out0), .switch(decoder_2_out8), .\output (n16_bit_and_10_output));
  _16_bit_AND u_16_bit_and_11 (.\input (decoder_1_out0), .switch(decoder_2_out11), .\output (n16_bit_and_11_output));
  _16_bit_AND u_16_bit_and_12 (.\input (decoder_1_out0), .switch(decoder_2_out10), .\output (n16_bit_and_12_output));
  _16_bit_AND u_16_bit_and_13 (.\input (decoder_1_out0), .switch(decoder_2_out13), .\output (n16_bit_and_13_output));
  _16_bit_AND u_16_bit_and_14 (.\input (decoder_1_out0), .switch(decoder_2_out12), .\output (n16_bit_and_14_output));
  Button button_6 ();  // open: out
  _16_bit_AND u_16_bit_and_15 (.\input (decoder_1_out0), .switch(decoder_2_out15), .\output (n16_bit_and_15_output));
  _16_bit_AND u_16_bit_and_16 (.\input (decoder_1_out0), .switch(decoder_2_out14), .\output (n16_bit_and_16_output));

  // Notes on the sheet:
  //   новое напр.
  //   текушее напр.
endmodule

module _16_bit_AND (
  input  [15:0] \input ,
  input  switch,
  output [15:0] \output 
);

  assign \output  = \input  & {16{switch}};  // AND_Gate and_1, 16 bits wide
endmodule

module column_switch (
  input  [3:0] in_1,
  input  [3:0] in_2
);
endmodule

module inc_dec (
  input  [3:0] X,
  input  on_off,
  input  inc_dec,
  output [3:0] R
);

  wire [3:0] and_1_out, xor_1_out, xor_2_out, xor_3_out;
  wire [3:3] decoder_1_out0, decoder_1_out1;

  Decoder #(.enable("false")) decoder_1 (.out0(decoder_1_out0[3]), .out1(decoder_1_out1[3]), .sel(inc_dec));
  assign xor_1_out = {4{decoder_1_out0[3]}} ^ X;  // XOR_Gate xor_1, 4 bits wide
  assign xor_2_out = {4{decoder_1_out1[3]}} ^ xor_3_out;  // XOR_Gate xor_2, 4 bits wide
  assign and_1_out = xor_1_out & xor_2_out;  // AND_Gate and_1, 4 bits wide
  assign xor_3_out = X ^ {and_1_out[2:0], 1'b1};  // XOR_Gate xor_3, 4 bits wide
  Multiplexer #(.width(4), .enable("false")) multiplexer_1 (.in0(X), .in1(xor_3_out), .out(R), .sel(on_off));
endmodule
