// Logisim project adventure_2 (2).circ as structural Verilog: 8 circuits, main circuit main
// 1
module main (
  input  Right,
  input  Down,
  input  Left,
  input  Up
);

  wire and_1_out, click, clock, clr, down_t, left_t, or_1_out, or_2_out, or_5_out, right_t, up_t;
  wire [1:0] or_3_out, register_4_q;
  wire [4:0] inc_dec_1_r, inc_dec_2_r;
  wire [9:0] register_1_q;
  wire [20:0] pseudo_reg_1_out_3, pseudo_reg_1_out_4, pseudo_reg_1_out_5, pseudo_reg_1_out_6,
       pseudo_reg_1_out_7, pseudo_reg_1_out_8, pseudo_reg_1_out_9, pseudo_reg_1_out_10, pseudo_reg_1_out_11,
       pseudo_reg_1_out_12, pseudo_reg_1_out_13, pseudo_reg_1_out_14, pseudo_reg_1_out_15,
       pseudo_reg_1_out_16, pseudo_reg_1_out_17, pseudo_reg_1_out_18, pseudo_reg_1_out_19,
       pseudo_reg_1_out_20, pseudo_reg_1_out_21, pseudo_reg_1_out_22, pseudo_reg_1_out_23;

  Clock clock_1 (.out(clock));
  Button button_1 (.out(clr));
  Register #(.width(10)) register_1 (
    .D({inc_dec_2_r, inc_dec_1_r}), .Q(register_1_q), .clk(and_1_out));  // open: en, clr
  and and_1 (and_1_out, clock, click);
  Button button_2 (.out(up_t));
  Button button_3 (.out(left_t));
  Button button_4 (.out(right_t));
  Button button_5 (.out(down_t));
  or or_1 (or_1_out, left_t, right_t);
  inc_dec inc_dec_1 (.X(register_1_q[4:0]), .on_off(or_2_out), .inc_dec(up_t), .R(inc_dec_1_r));  // open: OFL
  inc_dec inc_dec_2 (.X(register_1_q[9:5]), .on_off(or_1_out), .inc_dec(right_t), .R(inc_dec_2_r));  // open: OFL
  Register #(.width(5)) register_2 (.D(register_1_q[9:5]), .clk(clock), .clr(clr));  // open: en, Q
  or or_2 (or_2_out, up_t, down_t);
  Register #(.width(5)) register_3 (.D(register_1_q[4:0]), .clk(clock), .clr(clr));  // open: en, Q
  pseudo_reg pseudo_reg_1 (
    .in_1(register_1_q[4:0]), .in_2(register_1_q[9:5]), .out_13(pseudo_reg_1_out_13),
    .out_3(pseudo_reg_1_out_3), .out_4(pseudo_reg_1_out_4), .out_14(pseudo_reg_1_out_14),
    .out_5(pseudo_reg_1_out_5), .out_15(pseudo_reg_1_out_15), .out_16(pseudo_reg_1_out_16),
    .out_6(pseudo_reg_1_out_6), .out_17(pseudo_reg_1_out_17), .out_7(pseudo_reg_1_out_7),
    .out_18(pseudo_reg_1_out_18), .out_8(pseudo_reg_1_out_8), .out_19(pseudo_reg_1_out_19),
    .out_9(pseudo_reg_1_out_9), .out_20(pseudo_reg_1_out_20), .out_10(pseudo_reg_1_out_10),
    .out_21(pseudo_reg_1_out_21), .out_11(pseudo_reg_1_out_11), .out_22(pseudo_reg_1_out_22),
    .out_12(pseudo_reg_1_out_12), .out_23(pseudo_reg_1_out_23));
  DotMatrix #(.matrixcols(21), .matrixrows(21)) dotmatrix_1 (
    .col0(pseudo_reg_1_out_13), .col1(pseudo_reg_1_out_3), .col2(pseudo_reg_1_out_4),
    .col3(pseudo_reg_1_out_14), .col4(pseudo_reg_1_out_5), .col5(pseudo_reg_1_out_15),
    .col6(pseudo_reg_1_out_16), .col7(pseudo_reg_1_out_6), .col8(pseudo_reg_1_out_17),
    .col9(pseudo_reg_1_out_7), .col10(pseudo_reg_1_out_18), .col11(pseudo_reg_1_out_8),
    .col12(pseudo_reg_1_out_19), .col13(pseudo_reg_1_out_9), .col14(pseudo_reg_1_out_20),
    .col15(pseudo_reg_1_out_10), .col16(pseudo_reg_1_out_21), .col17(pseudo_reg_1_out_11),
    .col18(pseudo_reg_1_out_22), .col19(pseudo_reg_1_out_12), .col20(pseudo_reg_1_out_23));
  or or_3 (or_3_out[0], Down, Right);
  or or_4 (or_3_out[1], Right, Left);
  or or_5 (or_5_out, Right, Down, Left, Up);
  Register #(.width(2)) register_4 (.D(or_3_out), .Q(register_4_q), .clk(or_5_out));  // open: en, clr
  or or_6 (click, right_t, down_t, left_t, up_t);

  // Notes on the sheet:
  //   coor X
  //   coor Y
endmodule

module _16_bit_AND (
  input  [20:0] \input ,
  input  switch,
  output [20:0] \output 
);

  assign \output  = \input  & {21{switch}};  // AND_Gate and_1, 21 bits wide
endmodule

module column_switch (
  input  [3:0] in_1,
  input  [3:0] in_2
);
endmodule

module inc_dec (
  input  [4:0] X,
  input  on_off,
  input  inc_dec,
  output [4:0] R,
  output OFL
);

  wire and_2_out, and_3_out;
  wire [4:0] and_1_out, xor_1_out, xor_2_out, xor_3_out;
  wire [4:4] decoder_1_out0, decoder_1_out1;

  Decoder #(.enable("false")) decoder_1 (.out0(decoder_1_out0[4]), .out1(decoder_1_out1[4]), .sel(inc_dec));
  assign xor_1_out = {5{decoder_1_out0[4]}} ^ X;  // XOR_Gate xor_1, 5 bits wide
  assign xor_2_out = {5{decoder_1_out1[4]}} ^ xor_3_out;  // XOR_Gate xor_2, 5 bits wide
  assign and_1_out = xor_1_out & xor_2_out;  // AND_Gate and_1, 5 bits wide
  and and_2 (and_2_out, and_1_out[4], inc_dec);
  and and_3 (and_3_out, and_1_out[4], ~inc_dec);  // AND_Gate
  assign xor_3_out = X ^ {and_1_out[3:0], 1'b1};  // XOR_Gate xor_3, 5 bits wide
  or or_1 (OFL, and_2_out, and_3_out);
  Multiplexer #(.width(5), .enable("false")) multiplexer_1 (.in0(X), .in1(xor_3_out), .out(R), .sel(on_off));
endmodule

module granca_detection (
  input  Up,
  input  Down,
  input  [7:0] in_3,
  input  Left,
  input  Right,
  output out_6
);

  wire and_1_out, and_2_out, nor_1_out, nor_2_out;

  Pull_Resistor pull_resistor_1 (.node(Up));
  Pull_Resistor pull_resistor_2 (.node(Down));
  Pull_Resistor pull_resistor_3 (.node(Left));
  Pull_Resistor pull_resistor_4 (.node(Right));
  and and_1 (and_1_out, Up, in_3[3], in_3[2], in_3[1], in_3[0]);
  and and_2 (and_2_out, in_3[7], in_3[6], in_3[5], in_3[4], Right);
  nor nor_1 (nor_1_out, ~Down, in_3[0], in_3[1], in_3[2], in_3[3]);  // NOR_Gate
  nor nor_2 (nor_2_out, in_3[4], in_3[5], in_3[6], in_3[7], ~Left);  // NOR_Gate
  or or_1 (out_6, and_1_out, nor_1_out, nor_2_out, and_2_out);
endmodule

module movement (
  input  Right,
  input  Down,
  input  Left,
  input  Up,
  input  Clock,
  input  Clear,
  output out_7,
  output out_8,
  output out_9,
  output out_10
);

  wire and_1_out, counter_1_carry, or_3_out, xnor_1_out, xor_1_out;
  wire [1:0] multiplexer_1_out, or_1_out, register_1_q, register_2_q;

  or or_1 (or_1_out[0], Down, Right);
  or or_2 (or_1_out[1], Right, Left);
  or or_3 (or_3_out, Right, Down, Left, Up);
  Register #(.width(2)) register_1 (.D(or_1_out), .Q(register_1_q), .clk(or_3_out), .clr(Clear));  // open: en
  Register #(.width(2)) register_2 (.D(multiplexer_1_out), .Q(register_2_q), .clk(or_3_out), .clr(Clear));  // open: en
  xnor xnor_1 (xnor_1_out, register_2_q[1], register_1_q[1]);
  and and_1 (and_1_out, xnor_1_out, xor_1_out);
  xor xor_1 (xor_1_out, register_2_q[0], register_1_q[0]);
  Multiplexer #(.width(2)) multiplexer_1 (
    .in0(register_1_q), .in1(register_2_q), .out(multiplexer_1_out), .sel(and_1_out));  // open: en
  Counter #(.width(3), .max('h5)) counter_1 (
    .carry(counter_1_carry), .clk(Clock), .clr(Clear));  // open: load, D, count, Q
  Demultiplexer #(.select(2)) demultiplexer_1 (
    .out0(out_7), .out1(out_8), .out2(out_9), .out3(out_10), .in(counter_1_carry), .sel(multiplexer_1_out));  // open: en

  // Other names for the same wires on the sheet: clr = Clear

  // Notes on the sheet:
  //   новое напр.
  //   текушее напр.
endmodule

module pseudo_reg (
  input  [4:0] in_1,
  input  [4:0] in_2,
  output [20:0] out_3,
  output [20:0] out_4,
  output [20:0] out_5,
  output [20:0] out_6,
  output [20:0] out_7,
  output [20:0] out_8,
  output [20:0] out_9,
  output [20:0] out_10,
  output [20:0] out_11,
  output [20:0] out_12,
  output [20:0] out_13,
  output [20:0] out_14,
  output [20:0] out_15,
  output [20:0] out_16,
  output [20:0] out_17,
  output [20:0] out_18,
  output [20:0] out_19,
  output [20:0] out_20,
  output [20:0] out_21,
  output [20:0] out_22,
  output [20:0] out_23
);

  wire decoder_1_out21, decoder_2_out0, decoder_2_out1, decoder_2_out2, decoder_2_out3, decoder_2_out4,
       decoder_2_out5, decoder_2_out6, decoder_2_out7, decoder_2_out8, decoder_2_out9, decoder_2_out10,
       decoder_2_out11, decoder_2_out12, decoder_2_out13, decoder_2_out14, decoder_2_out15, decoder_2_out16,
       decoder_2_out17, decoder_2_out18, decoder_2_out19, decoder_2_out20, decoder_2_out21;
  wire [20:0] decoder_1_out0;

  Decoder #(.select(5), .disabled(0), .enable("false")) decoder_1 (
    .out0(decoder_1_out0[0]), .out1(decoder_1_out0[1]), .out2(decoder_1_out0[2]), .out3(decoder_1_out0[3]),
    .out4(decoder_1_out0[4]), .out5(decoder_1_out0[5]), .out6(decoder_1_out0[6]), .out7(decoder_1_out0[7]),
    .out8(decoder_1_out0[8]), .out9(decoder_1_out0[9]), .out10(decoder_1_out0[10]),
    .out11(decoder_1_out0[11]), .out12(decoder_1_out0[12]), .out13(decoder_1_out0[13]),
    .out14(decoder_1_out0[14]), .out15(decoder_1_out0[15]), .out16(decoder_1_out0[16]),
    .out17(decoder_1_out0[17]), .out18(decoder_1_out0[18]), .out19(decoder_1_out0[19]),
    .out20(decoder_1_out0[20]), .out21(decoder_1_out21), .out22(decoder_1_out21), .out23(decoder_1_out21),
    .out24(decoder_1_out21), .out25(decoder_1_out21), .out26(decoder_1_out21), .out27(decoder_1_out21),
    .out28(decoder_1_out21), .out29(decoder_1_out21), .out30(decoder_1_out21), .out31(decoder_1_out21),
    .sel(in_1));
  _16_bit_AND u_16_bit_and_1 (.\input (decoder_1_out0), .switch(decoder_2_out0), .\output (out_13));
  _16_bit_AND u_16_bit_and_2 (.\input (decoder_1_out0), .switch(decoder_2_out1), .\output (out_3));
  _16_bit_AND u_16_bit_and_3 (.\input (decoder_1_out0), .switch(decoder_2_out3), .\output (out_4));
  _16_bit_AND u_16_bit_and_4 (.\input (decoder_1_out0), .switch(decoder_2_out2), .\output (out_14));
  Decoder #(.select(5), .disabled(0), .enable("false")) decoder_2 (
    .out0(decoder_2_out0), .out1(decoder_2_out1), .out2(decoder_2_out2), .out3(decoder_2_out3),
    .out4(decoder_2_out4), .out5(decoder_2_out5), .out6(decoder_2_out6), .out7(decoder_2_out7),
    .out8(decoder_2_out8), .out9(decoder_2_out9), .out10(decoder_2_out10), .out11(decoder_2_out11),
    .out12(decoder_2_out12), .out13(decoder_2_out13), .out14(decoder_2_out14), .out15(decoder_2_out15),
    .out16(decoder_2_out16), .out17(decoder_2_out17), .out18(decoder_2_out18), .out19(decoder_2_out19),
    .out20(decoder_2_out20), .out21(decoder_2_out21), .out22(decoder_2_out21), .out23(decoder_2_out21),
    .out24(decoder_2_out21), .out25(decoder_2_out21), .out26(decoder_2_out21), .out27(decoder_2_out21),
    .out28(decoder_2_out21), .out29(decoder_2_out21), .out30(decoder_2_out21), .out31(decoder_2_out21),
    .sel(in_2));
  _16_bit_AND u_16_bit_and_5 (.\input (decoder_1_out0), .switch(decoder_2_out5), .\output (out_5));
  _16_bit_AND u_16_bit_and_6 (.\input (decoder_1_out0), .switch(decoder_2_out4), .\output (out_15));
  _16_bit_AND u_16_bit_and_7 (.\input (decoder_1_out0), .switch(decoder_2_out7), .\output (out_6));
  _16_bit_AND u_16_bit_and_8 (.\input (decoder_1_out0), .switch(decoder_2_out6), .\output (out_16));
  _16_bit_AND u_16_bit_and_9 (.\input (decoder_1_out0), .switch(decoder_2_out8), .\output (out_17));
  _16_bit_AND u_16_bit_and_10 (.\input (decoder_1_out0), .switch(decoder_2_out9), .\output (out_7));
  _16_bit_AND u_16_bit_and_11 (.\input (decoder_1_out0), .switch(decoder_2_out11), .\output (out_8));
  _16_bit_AND u_16_bit_and_12 (.\input (decoder_1_out0), .switch(decoder_2_out10), .\output (out_18));
  _16_bit_AND u_16_bit_and_13 (.\input (decoder_1_out0), .switch(decoder_2_out13), .\output (out_9));
  _16_bit_AND u_16_bit_and_14 (.\input (decoder_1_out0), .switch(decoder_2_out12), .\output (out_19));
  _16_bit_AND u_16_bit_and_15 (.\input (decoder_1_out0), .switch(decoder_2_out15), .\output (out_10));
  _16_bit_AND u_16_bit_and_16 (.\input (decoder_1_out0), .switch(decoder_2_out14), .\output (out_20));
  _16_bit_AND u_16_bit_and_17 (.\input (decoder_1_out0), .switch(decoder_2_out16), .\output (out_21));
  _16_bit_AND u_16_bit_and_18 (.\input (decoder_1_out0), .switch(decoder_2_out17), .\output (out_11));
  _16_bit_AND u_16_bit_and_19 (.\input (decoder_1_out0), .switch(decoder_2_out19), .\output (out_12));
  _16_bit_AND u_16_bit_and_20 (.\input (decoder_1_out0), .switch(decoder_2_out18), .\output (out_22));
  _16_bit_AND u_16_bit_and_21 (.\input (decoder_1_out0), .switch(decoder_2_out20), .\output (out_23));
endmodule

module maps (
  input  [20:0] in_1,
  input  [20:0] in_2,
  input  [20:0] in_3,
  input  [20:0] in_4,
  input  [20:0] in_5,
  input  [20:0] in_6,
  input  [20:0] in_7,
  input  [20:0] in_8,
  input  [20:0] in_9,
  input  [20:0] in_10,
  input  [20:0] in_11
);

  DotMatrix #(.matrixcols(21), .matrixrows(21)) dotmatrix_1 (
    .col0(in_1), .col1(in_2), .col2(in_3), .col3(in_4), .col4(in_5), .col5(in_6), .col6(in_7), .col7(in_8),
    .col8(in_9), .col9(in_10), .col10(in_11), .col11(in_10), .col12(in_9), .col13(in_8), .col14(in_7),
    .col15(in_6), .col16(in_5), .col17(in_4), .col18(in_3), .col19(in_2), .col20(in_1));
  // Probe on in_1
  // Probe on in_2
  // Probe on in_3
  // Probe on in_4
  // Probe on in_5
  // Probe on in_6
  // Probe on in_7
  // Probe on in_8
  // Probe on in_9
  // Probe on in_10
endmodule
