// Logisim project alt_snake_1.5 (2).circ as structural Verilog
// 1
module main (
  input  in_1,
  input  in_2
);

  wire and_3_out, and_4_out, and_5_out, and_6_out, and_7_out, and_8_out, and_9_out, and_10_out, AppleClear,
       cdm_8_mark5_1_data_inst, clock_1_out, clr, code, comparator_2_eq, comparator_3_eq,
       controlled_buffer_2_out, counter2_1_out_3, counter2_1_out_4, counter2_1_out_5, counter2_1_out_6,
       counter2_1_out_7, counter2_1_out_8, counter2_1_out_9, counter2_1_out_10, counter2_1_out_11,
       counter2_1_out_12, counter2_1_out_13, counter2_1_out_14, counter2_1_out_15, counter2_1_out_16,
       counter2_1_out_17, counter2_1_out_18, counter_2_carry, counter_4_out_3, counter_4_out_4,
       counter_4_out_5, counter_4_out_6, counter_4_out_7, counter_4_out_8, counter_4_out_9, counter_4_out_10,
       counter_4_out_11, counter_4_out_12, counter_4_out_13, counter_4_out_14, counter_4_out_15,
       counter_4_out_16, counter_4_out_17, counter_4_out_18, CYCLE, d_ff_1_q, data, decoder_2_out1,
       decoder_3_out1, decoder_4_out1, Del_tick, Delete, down, first_tacktk, golod, hz, I_Osel, left, lose,
       mem, nand_1_out, not_1_out, not_2_out, not_3_out, or_1_out, or_4_out, or_5_out, or_6_out, or_7_out,
       or_8_out, or_9_out, OVF1, OVF2, RAM, rd_wr_prime, right, takt, up, win, \Перекус ;
  wire [1:0] Move;
  wire [3:0] cdm_8_mark5_1_ps, inc_dec_1_r, inc_dec_2_r;
  wire [6:0] \input ;
  wire [7:0] adder_1_out, adr, Apple_coord, cdm_8_mark5_1_data_out, cdm_8_mark5_1_pc, cdm_8_mark5_1_r0,
       cdm_8_mark5_1_r1, cdm_8_mark5_1_r2, cdm_8_mark5_1_r3, cdm_8_mark5_1_sp, controlled_buffer_1_out,
       controlled_buffer_4_out, Cords, counter_3_q, head, I_Odata, negator_1_out, or_2_out, register_2_q,
       register_3_q, register_4_q, register_5_q;
  wire [15:0] vivod_matrix_1_out_13, vivod_matrix_1_out_18, vivod_matrix_1_out_23, vivod_matrix_1_out_28,
       vivod_matrix_1_out_33, vivod_matrix_1_out_37, vivod_matrix_1_out_40, vivod_matrix_1_out_45,
       vivod_matrix_1_out_50, vivod_matrix_1_out_55, vivod_matrix_1_out_59, vivod_matrix_1_out_62,
       vivod_matrix_1_out_67, vivod_matrix_1_out_72, vivod_matrix_1_out_77, vivod_matrix_1_out_81;
  wire [16:0] vivod_matrix_1_out_17, vivod_matrix_1_out_22, vivod_matrix_1_out_27, vivod_matrix_1_out_32,
       vivod_matrix_1_out_36, vivod_matrix_1_out_43, vivod_matrix_1_out_48, vivod_matrix_1_out_53,
       vivod_matrix_1_out_58, vivod_matrix_1_out_65, vivod_matrix_1_out_70, vivod_matrix_1_out_75,
       vivod_matrix_1_out_80, vivod_matrix_1_out_85, vivod_matrix_1_out_88, vivod_matrix_1_out_91;
  wire [17:0] vivod_matrix_1_out_16, vivod_matrix_1_out_21, vivod_matrix_1_out_26, vivod_matrix_1_out_31,
       vivod_matrix_1_out_35, vivod_matrix_1_out_42, vivod_matrix_1_out_47, vivod_matrix_1_out_52,
       vivod_matrix_1_out_57, vivod_matrix_1_out_64, vivod_matrix_1_out_69, vivod_matrix_1_out_74,
       vivod_matrix_1_out_79, vivod_matrix_1_out_84, vivod_matrix_1_out_87, vivod_matrix_1_out_90;
  wire [18:0] vivod_matrix_1_out_15, vivod_matrix_1_out_20, vivod_matrix_1_out_25, vivod_matrix_1_out_30,
       vivod_matrix_1_out_39, vivod_matrix_1_out_44, vivod_matrix_1_out_49, vivod_matrix_1_out_54,
       vivod_matrix_1_out_61, vivod_matrix_1_out_66, vivod_matrix_1_out_71, vivod_matrix_1_out_76,
       vivod_matrix_1_out_83, vivod_matrix_1_out_86, vivod_matrix_1_out_89, vivod_matrix_1_out_92;
  wire [19:0] vivod_matrix_1_out_14, vivod_matrix_1_out_19, vivod_matrix_1_out_24, vivod_matrix_1_out_29,
       vivod_matrix_1_out_34, vivod_matrix_1_out_38, vivod_matrix_1_out_41, vivod_matrix_1_out_46,
       vivod_matrix_1_out_51, vivod_matrix_1_out_56, vivod_matrix_1_out_60, vivod_matrix_1_out_63,
       vivod_matrix_1_out_68, vivod_matrix_1_out_73, vivod_matrix_1_out_78, vivod_matrix_1_out_82;
  wire [31:0] counter_1_q;

  assign controlled_buffer_1_out = first_tacktk ? 8'h88 : 8'bz;  // Controlled_Buffer controlled_buffer_1
  Pull_Resistor pull_resistor_1 (.node(controlled_buffer_1_out));
  not not_1 (not_1_out, in_1);
  Clock clock_1 (.out(clock_1_out));
  assign controlled_buffer_2_out = not_1_out ? clock_1_out : 1'bz;  // Controlled_Buffer controlled_buffer_2
  or or_1 (or_1_out, lose, win);
  Register register_1 (.D(or_2_out), .Q(head), .clk(CYCLE), .clr(clr));  // open: en
  assign or_2_out = controlled_buffer_1_out | {inc_dec_1_r, inc_dec_2_r};  // OR_Gate or_2, 8 bits wide
  // Probe on head
  golod golod_1 (.stop_golod(in_2), .clock(CYCLE), .clr(clr), .hz(hz), .golod(golod));
  and and_1 (I_Osel, not_2_out, takt, data);
  Pull_Resistor pull_resistor_2 (.node(controlled_buffer_2_out));
  Multiplexer multiplexer_1 (.in0(controlled_buffer_2_out), .in1(1'b0), .out(takt), .sel(lose));  // open: en
  or or_3 (lose, golod, d_ff_1_q);
  D_Flip_Flop d_ff_1 (.Q(d_ff_1_q), .preset(or_1_out), .reset(clr));  // open: clk, D, Qn, en
  or or_4 (or_4_out, left, right);
  or or_5 (or_5_out, clr, hz);
  Negator negator_1 (.in(head), .out(negator_1_out));
  inc_dec inc_dec_1 (.X(head[7:4]), .on_off(or_4_out), .inc_dec(right), .R(inc_dec_1_r), .OFL(OVF1));
  inc_dec inc_dec_2 (.X(head[3:0]), .on_off(or_6_out), .inc_dec(up), .R(inc_dec_2_r), .OFL(OVF2));
  // Probe on Apple_coord
  Random #(.seed(8)) random_1 (.clk(or_5_out), .out(Apple_coord));  // open: next, clr
  Adder adder_1 (.a(Apple_coord), .b(negator_1_out), .out(adder_1_out));  // open: cin, cout
  // Probe on cdm_8_mark5_1_r3
  // Probe on cdm_8_mark5_1_r2
  // Probe on cdm_8_mark5_1_r1
  // Probe on cdm_8_mark5_1_r0
  not not_2 (not_2_out, nand_1_out);
  nand nand_1 (nand_1_out, adr[4], adr[5], adr[6], adr[7]);
  and and_2 (RAM, nand_1_out, data);
  or or_6 (or_6_out, up, down);
  nor nor_1 (hz, adder_1_out[0], adder_1_out[1], adder_1_out[2], adder_1_out[3], adder_1_out[4], adder_1_out[5], adder_1_out[6], adder_1_out[7]);
  movement movement_1 (
    .Clear(clr), .out_4(up), .out_5(down), .out_6(left), .out_7(right), .Move(Move), .\input (\input ));
  // Probe on cdm_8_mark5_1_pc
  // Probe on cdm_8_mark5_1_sp
  // Probe on cdm_8_mark5_1_ps
  CdM_8_mark5 cdm_8_mark5_1 (
    .clock(takt), .addr(adr), .mem_read(rd_wr_prime), .mem_cycle(mem), .data_inst(cdm_8_mark5_1_data_inst),
    .data_out(cdm_8_mark5_1_data_out), .data_in(controlled_buffer_4_out), .r0(cdm_8_mark5_1_r0),
    .r1(cdm_8_mark5_1_r1), .r2(cdm_8_mark5_1_r2), .r3(cdm_8_mark5_1_r3), .PC(cdm_8_mark5_1_pc),
    .SP(cdm_8_mark5_1_sp), .PS(cdm_8_mark5_1_ps));
  Counter #(.width(32), .max('hffffffff)) counter_1 (
    .Q(counter_1_q), .clk(CYCLE), .clr(clr));  // open: load, D, count, carry
  or or_7 (or_7_out, hz, or_8_out, clr);
  or or_8 (or_8_out, lose, lose, win);
  Decoder #(.disabled(0)) decoder_1 (.out0(code), .out1(data), .sel(cdm_8_mark5_1_data_inst), .en(mem));
  not not_3 (not_3_out, rd_wr_prime);
  assign I_Odata = not_3_out ? cdm_8_mark5_1_data_out : 8'bz;  // Controlled_Buffer controlled_buffer_3
  assign controlled_buffer_4_out = rd_wr_prime ? I_Odata : 8'bz;  // Controlled_Buffer controlled_buffer_4
  Comparator #(.width(32), .mode("unsigned")) comparator_1 (
    .a({32{1'b0}}), .b(counter_1_q), .eq(first_tacktk));  // open: gt, lt
  sec_matrix_disp sec_matrix_disp_1 (
    .X(Apple_coord[7:4]), .clock(takt), .Y(Apple_coord[3:0]), .clear(or_7_out));  // open: out_5, out_6, out_7, out_8, out_9, out_10, out_11, out_12, out_13, out_14, out_15, out_16, out_17, out_18, out_19, out_20
  Pull_Resistor pull_resistor_3 (.node(adr[0]));
  Pull_Resistor pull_resistor_4 (.node(adr[1]));
  Pull_Resistor pull_resistor_5 (.node(adr[2]));
  Pull_Resistor pull_resistor_6 (.node(adr[3]));
  Pull_Resistor pull_resistor_7 (.node(adr[4]));
  Pull_Resistor pull_resistor_8 (.node(adr[5]));
  Pull_Resistor pull_resistor_9 (.node(adr[6]));
  Pull_Resistor pull_resistor_10 (.node(adr[7]));
  Counter #(.max('ha)) counter_2 (.carry(counter_2_carry), .clk(hz), .clr(clr));  // open: load, D, count, Q
  Register register_2 (.D(Cords), .Q(register_2_q), .clk(takt));  // open: en, clr
  vivod_matrix vivod_matrix_1 (
    .snake_coord(Cords), .apple_coord(Apple_coord), .paus(in_1), .win(win), .lose(lose), .takt(takt),
    .clr(clr), .vivod(Del_tick), .cycle(CYCLE), .apple(hz), .out_15(vivod_matrix_1_out_15),
    .out_16(vivod_matrix_1_out_16), .out_17(vivod_matrix_1_out_17), .out_13(vivod_matrix_1_out_13),
    .out_20(vivod_matrix_1_out_20), .out_21(vivod_matrix_1_out_21), .out_22(vivod_matrix_1_out_22),
    .out_18(vivod_matrix_1_out_18), .out_25(vivod_matrix_1_out_25), .out_26(vivod_matrix_1_out_26),
    .out_27(vivod_matrix_1_out_27), .out_23(vivod_matrix_1_out_23), .out_30(vivod_matrix_1_out_30),
    .out_31(vivod_matrix_1_out_31), .out_32(vivod_matrix_1_out_32), .out_28(vivod_matrix_1_out_28),
    .out_35(vivod_matrix_1_out_35), .out_36(vivod_matrix_1_out_36), .out_33(vivod_matrix_1_out_33),
    .out_39(vivod_matrix_1_out_39), .out_42(vivod_matrix_1_out_42), .out_43(vivod_matrix_1_out_43),
    .out_37(vivod_matrix_1_out_37), .out_44(vivod_matrix_1_out_44), .out_47(vivod_matrix_1_out_47),
    .out_48(vivod_matrix_1_out_48), .out_40(vivod_matrix_1_out_40), .out_49(vivod_matrix_1_out_49),
    .out_52(vivod_matrix_1_out_52), .out_53(vivod_matrix_1_out_53), .out_45(vivod_matrix_1_out_45),
    .out_54(vivod_matrix_1_out_54), .out_57(vivod_matrix_1_out_57), .out_58(vivod_matrix_1_out_58),
    .out_50(vivod_matrix_1_out_50), .out_61(vivod_matrix_1_out_61), .out_64(vivod_matrix_1_out_64),
    .out_65(vivod_matrix_1_out_65), .out_55(vivod_matrix_1_out_55), .out_66(vivod_matrix_1_out_66),
    .out_69(vivod_matrix_1_out_69), .out_70(vivod_matrix_1_out_70), .out_59(vivod_matrix_1_out_59),
    .out_71(vivod_matrix_1_out_71), .out_74(vivod_matrix_1_out_74), .out_75(vivod_matrix_1_out_75),
    .out_62(vivod_matrix_1_out_62), .out_76(vivod_matrix_1_out_76), .out_79(vivod_matrix_1_out_79),
    .out_80(vivod_matrix_1_out_80), .out_67(vivod_matrix_1_out_67), .out_83(vivod_matrix_1_out_83),
    .out_84(vivod_matrix_1_out_84), .out_85(vivod_matrix_1_out_85), .out_72(vivod_matrix_1_out_72),
    .out_86(vivod_matrix_1_out_86), .out_87(vivod_matrix_1_out_87), .out_88(vivod_matrix_1_out_88),
    .out_77(vivod_matrix_1_out_77), .out_89(vivod_matrix_1_out_89), .out_90(vivod_matrix_1_out_90),
    .out_91(vivod_matrix_1_out_91), .out_81(vivod_matrix_1_out_81), .out_92(vivod_matrix_1_out_92),
    .head_coord(head), .Delete(Delete), .out_14(vivod_matrix_1_out_14), .out_19(vivod_matrix_1_out_19),
    .out_24(vivod_matrix_1_out_24), .out_29(vivod_matrix_1_out_29), .out_34(vivod_matrix_1_out_34),
    .out_38(vivod_matrix_1_out_38), .out_41(vivod_matrix_1_out_41), .out_46(vivod_matrix_1_out_46),
    .out_51(vivod_matrix_1_out_51), .out_56(vivod_matrix_1_out_56), .out_60(vivod_matrix_1_out_60),
    .out_63(vivod_matrix_1_out_63), .out_68(vivod_matrix_1_out_68), .out_73(vivod_matrix_1_out_73),
    .out_78(vivod_matrix_1_out_78), .out_82(vivod_matrix_1_out_82));
  D_Flip_Flop d_ff_2 (.Q(win), .preset(counter_2_carry), .reset(clr));  // open: clk, D, Qn, en
  Comparator comparator_2 (.a(head), .b(register_2_q), .eq(comparator_2_eq));  // open: gt, lt
  ROM rom_1 (.addr(adr), .data(I_Odata), .sel(code));
  RAM ram_1 (.addr(adr), .data(I_Odata), .sel(RAM), .clk(takt), .ld(rd_wr_prime));  // open: clr
  Counter counter_3 (.Q(counter_3_q), .clk(comparator_2_eq), .clr(CYCLE));  // open: load, D, count, carry
  and and_3 (and_3_out, I_Osel, adr[0], adr[1], ~adr[2], ~adr[3]);  // AND_Gate
  assign I_Odata = decoder_2_out1 ? register_3_q : 8'bz;  // Controlled_Buffer controlled_buffer_5
  Register register_3 (.D({{6{1'b0}}, Move}), .Q(register_3_q), .clk(takt));  // open: en, clr
  D_Flip_Flop d_ff_3 (.Q(\Перекус ), .preset(comparator_3_eq), .reset(clr));  // open: clk, D, Qn, en
  Comparator comparator_3 (.a(counter_3_q), .b(8'h2), .eq(comparator_3_eq));  // open: gt, lt
  Decoder #(.disabled(0)) decoder_2 (.out1(decoder_2_out1), .sel(rd_wr_prime), .en(and_3_out));  // open: out0
  DotMatrix #(.inputtype("row"), .matrixcols(17), .matrixrows(16)) dotmatrix_1 (
    .row0(vivod_matrix_1_out_17), .row1(vivod_matrix_1_out_22), .row2(vivod_matrix_1_out_27),
    .row3(vivod_matrix_1_out_32), .row4(vivod_matrix_1_out_36), .row5(vivod_matrix_1_out_43),
    .row6(vivod_matrix_1_out_48), .row7(vivod_matrix_1_out_53), .row8(vivod_matrix_1_out_58),
    .row9(vivod_matrix_1_out_65), .row10(vivod_matrix_1_out_70), .row11(vivod_matrix_1_out_75),
    .row12(vivod_matrix_1_out_80), .row13(vivod_matrix_1_out_85), .row14(vivod_matrix_1_out_88),
    .row15(vivod_matrix_1_out_91));
  DotMatrix #(.inputtype("row"), .matrixcols(19), .matrixrows(16)) dotmatrix_2 (
    .row0(vivod_matrix_1_out_15), .row1(vivod_matrix_1_out_20), .row2(vivod_matrix_1_out_25),
    .row3(vivod_matrix_1_out_30), .row4(vivod_matrix_1_out_39), .row5(vivod_matrix_1_out_44),
    .row6(vivod_matrix_1_out_49), .row7(vivod_matrix_1_out_54), .row8(vivod_matrix_1_out_61),
    .row9(vivod_matrix_1_out_66), .row10(vivod_matrix_1_out_71), .row11(vivod_matrix_1_out_76),
    .row12(vivod_matrix_1_out_83), .row13(vivod_matrix_1_out_86), .row14(vivod_matrix_1_out_89),
    .row15(vivod_matrix_1_out_92));
  DotMatrix #(.inputtype("row"), .matrixcols(20), .matrixrows(16)) dotmatrix_3 (
    .row0(vivod_matrix_1_out_14), .row1(vivod_matrix_1_out_19), .row2(vivod_matrix_1_out_24),
    .row3(vivod_matrix_1_out_29), .row4(vivod_matrix_1_out_34), .row5(vivod_matrix_1_out_38),
    .row6(vivod_matrix_1_out_41), .row7(vivod_matrix_1_out_46), .row8(vivod_matrix_1_out_51),
    .row9(vivod_matrix_1_out_56), .row10(vivod_matrix_1_out_60), .row11(vivod_matrix_1_out_63),
    .row12(vivod_matrix_1_out_68), .row13(vivod_matrix_1_out_73), .row14(vivod_matrix_1_out_78),
    .row15(vivod_matrix_1_out_82));
  DotMatrix #(.inputtype("row"), .matrixcols(18), .matrixrows(16)) dotmatrix_4 (
    .row0(vivod_matrix_1_out_16), .row1(vivod_matrix_1_out_21), .row2(vivod_matrix_1_out_26),
    .row3(vivod_matrix_1_out_31), .row4(vivod_matrix_1_out_35), .row5(vivod_matrix_1_out_42),
    .row6(vivod_matrix_1_out_47), .row7(vivod_matrix_1_out_52), .row8(vivod_matrix_1_out_57),
    .row9(vivod_matrix_1_out_64), .row10(vivod_matrix_1_out_69), .row11(vivod_matrix_1_out_74),
    .row12(vivod_matrix_1_out_79), .row13(vivod_matrix_1_out_84), .row14(vivod_matrix_1_out_87),
    .row15(vivod_matrix_1_out_90));
  and and_4 (and_4_out, CYCLE, in_2);
  Keyboard keyboard_1 (.clk(takt), .clr(clr), .data(\input ));  // open: re, avail
  Register register_4 (.D(head), .Q(register_4_q), .clk(takt));  // open: en, clr
  counter counter_4 (
    .clock(hz), .clear(clr), .out_11(counter_4_out_11), .out_12(counter_4_out_12), .out_13(counter_4_out_13),
    .out_14(counter_4_out_14), .out_15(counter_4_out_15), .out_16(counter_4_out_16),
    .out_17(counter_4_out_17), .out_18(counter_4_out_18), .out_3(counter_4_out_3), .out_4(counter_4_out_4),
    .out_5(counter_4_out_5), .out_6(counter_4_out_6), .out_7(counter_4_out_7), .out_8(counter_4_out_8),
    .out_9(counter_4_out_9), .out_10(counter_4_out_10));
  _7_Segment_Display u_7_segment_display_1 (
    .g(counter_4_out_3), .f(counter_4_out_4), .a(counter_4_out_5), .b(counter_4_out_6), .e(counter_4_out_11),
    .d(counter_4_out_12), .c(counter_4_out_13), .dp(counter_4_out_14));
  DotMatrix #(.inputtype("row"), .matrixcols(16), .matrixrows(16)) dotmatrix_5 (
    .row0(vivod_matrix_1_out_13), .row1(vivod_matrix_1_out_18), .row2(vivod_matrix_1_out_23),
    .row3(vivod_matrix_1_out_28), .row4(vivod_matrix_1_out_33), .row5(vivod_matrix_1_out_37),
    .row6(vivod_matrix_1_out_40), .row7(vivod_matrix_1_out_45), .row8(vivod_matrix_1_out_50),
    .row9(vivod_matrix_1_out_55), .row10(vivod_matrix_1_out_59), .row11(vivod_matrix_1_out_62),
    .row12(vivod_matrix_1_out_67), .row13(vivod_matrix_1_out_72), .row14(vivod_matrix_1_out_77),
    .row15(vivod_matrix_1_out_81));
  _7_Segment_Display u_7_segment_display_2 (
    .g(counter2_1_out_3), .f(counter2_1_out_4), .a(counter2_1_out_5), .b(counter2_1_out_6),
    .e(counter2_1_out_11), .d(counter2_1_out_12), .c(counter2_1_out_13), .dp(counter2_1_out_14));
  counter2 counter2_1 (
    .clock(and_4_out), .clear(or_9_out), .out_11(counter2_1_out_11), .out_12(counter2_1_out_12),
    .out_13(counter2_1_out_13), .out_14(counter2_1_out_14), .out_15(counter2_1_out_15),
    .out_16(counter2_1_out_16), .out_17(counter2_1_out_17), .out_18(counter2_1_out_18),
    .out_3(counter2_1_out_3), .out_4(counter2_1_out_4), .out_5(counter2_1_out_5), .out_6(counter2_1_out_6),
    .out_7(counter2_1_out_7), .out_8(counter2_1_out_8), .out_9(counter2_1_out_9), .out_10(counter2_1_out_10));
  assign I_Odata = decoder_3_out1 ? register_4_q : 8'bz;  // Controlled_Buffer controlled_buffer_6
  _7_Segment_Display u_7_segment_display_3 (
    .g(counter_4_out_7), .f(counter_4_out_8), .a(counter_4_out_9), .b(counter_4_out_10),
    .e(counter_4_out_15), .d(counter_4_out_16), .c(counter_4_out_17), .dp(counter_4_out_18));
  _7_Segment_Display u_7_segment_display_4 (
    .g(counter2_1_out_7), .f(counter2_1_out_8), .a(counter2_1_out_9), .b(counter2_1_out_10),
    .e(counter2_1_out_15), .d(counter2_1_out_16), .c(counter2_1_out_17), .dp(counter2_1_out_18));
  or or_9 (or_9_out, clr, hz);
  and and_5 (and_5_out, I_Osel, adr[0], ~adr[1], adr[2], ~adr[3]);  // AND_Gate
  Decoder #(.disabled(0)) decoder_3 (.out1(decoder_3_out1), .sel(rd_wr_prime), .en(and_5_out));  // open: out0
  Button button_1 (.out(clr));
  assign I_Odata = decoder_4_out1 ? register_5_q : 8'bz;  // Controlled_Buffer controlled_buffer_7
  Register register_5 (.D({{7{1'b0}}, hz}), .Q(register_5_q), .clk(hz), .clr(AppleClear));  // open: en
  and and_6 (and_6_out, I_Osel, ~adr[0], adr[1], adr[2], ~adr[3]);  // AND_Gate
  Decoder #(.disabled(0)) decoder_4 (.out1(decoder_4_out1), .sel(rd_wr_prime), .en(and_6_out));  // open: out0
  Pull_Resistor pull_resistor_11 (.node(AppleClear));
  assign AppleClear = and_7_out ? 1'b1 : 1'bz;  // Controlled_Buffer controlled_buffer_8
  and and_7 (and_7_out, adr[0], adr[1], adr[2], ~adr[3], adr[4], adr[5], adr[6], adr[7]);  // AND_Gate
  and and_8 (and_8_out, adr[0], ~adr[1], ~adr[2], ~adr[3], adr[4], adr[5], ~adr[6], adr[7]);  // AND_Gate
  assign Cords = and_8_out ? I_Odata : 8'bz;  // Controlled_Buffer controlled_buffer_9
  and and_9 (and_9_out, ~adr[0], ~adr[1], ~adr[2], adr[3], adr[4], adr[5], adr[6], adr[7]);  // AND_Gate
  Register #(.width(1)) register_6 (.D(Del_tick), .Q(Delete), .clk(takt), .clr(CYCLE));  // open: en
  assign Del_tick = and_10_out ? 1'b1 : 1'bz;  // Controlled_Buffer controlled_buffer_10
  and and_10 (and_10_out, adr[0], adr[1], adr[2], adr[3], adr[4], adr[5], adr[6], adr[7]);
  Pull_Resistor pull_resistor_12 (.node(CYCLE));
  assign CYCLE = and_9_out ? 1'b1 : 1'bz;  // Controlled_Buffer controlled_buffer_11

  // Other names for the same wires on the sheet: I_Oadr[3:0] = adr[3:0]; porty[3:0] = Apple_coord[7:4]; paus = in_1;
  //   portx[3:0] = Apple_coord[3:0]; stop_golod = in_2

  // Notes on the sheet:
  //   contents of rom_1 (hex, n*v repeats v):
  //   cd f0 d1 2 c1 d1 b5 d0 87 a4 d0 f8 b0 d0 f5 b0 d1 b1 a4 d0 f3 b0 d1 b4 b6 a4 78 e1 24 cb 0 bd 8d ad
  //   ee 2c 6*20 8c c0 d0 f6 b0 0 e1 83 d0 ef b1 89 a1 d0 3f 41 e1 4f c8 0 d1 f0 31 85 c6 8c 5 e0 4e b3 a2
  //   8c e 89 ee 45 a2 d0 b5 b1 d3 ff bf d3 b1 ad d3 ef bf d2 c0 4e 6*92 a e1 6b d3 1 ee 7e d3 1 7b e1 74
  //   d3 ff ee 7e 8f 7b e1 7c d3 f0 ee 7e d3 10 d1 b5 b6 1e a6 d0 f7 b0 d0 f8 b0 ee d
  //   Получение направления
  //   Количество яблочек
  //   Получение координат головы
  //   1 - пауза 0 играем
  //   1 - есть 0 - нет голода
  //   Бит съеденного яблока
  //   Координаты змейки
  //   Бит конца цикла процессора
  //   Бит удаления
  //   Бит конца цикла процессора
endmodule

module _16_bit_AND (
  input  [15:0] \input ,
  input  switch,
  output [16:0] \output 
);

  assign \output [15:0] = \input  & {16{switch}};  // AND_Gate and_1, 16 bits wide

  assign \output [16] = 1'b0;
endmodule

module inc_dec (
  input  [3:0] X,
  input  on_off,
  input  inc_dec,
  output [3:0] R,
  output OFL
);

  wire and_2_out, and_3_out, and_4_out, and_5_out, nor_1_out, nor_2_out;
  wire [3:0] and_1_out, xor_1_out, xor_2_out, xor_3_out;
  wire [3:3] decoder_1_out0, decoder_1_out1;

  Decoder #(.enable("false")) decoder_1 (.out0(decoder_1_out0[3]), .out1(decoder_1_out1[3]), .sel(inc_dec));
  assign xor_1_out = {4{decoder_1_out0[3]}} ^ X;  // XOR_Gate xor_1, 4 bits wide
  assign xor_2_out = {4{decoder_1_out1[3]}} ^ xor_3_out;  // XOR_Gate xor_2, 4 bits wide
  assign and_1_out = xor_1_out & xor_2_out;  // AND_Gate and_1, 4 bits wide
  assign xor_3_out = X ^ {and_1_out[2:0], 1'b1};  // XOR_Gate xor_3, 4 bits wide
  Multiplexer #(.width(4), .enable("false")) multiplexer_1 (.in0(X), .in1(xor_3_out), .out(R), .sel(on_off));
  and and_2 (and_2_out, X[0], X[1], X[2], X[3]);
  nor nor_1 (nor_1_out, R[0], R[1], R[2], R[3]);
  and and_3 (and_3_out, R[0], R[1], R[2], R[3]);
  nor nor_2 (nor_2_out, X[0], X[1], X[2], X[3]);
  and and_4 (and_4_out, and_2_out, nor_1_out);
  and and_5 (and_5_out, and_3_out, nor_2_out);
  or or_1 (OFL, and_4_out, and_5_out);

  // Other names for the same wires on the sheet: O[3:0] = R
endmodule

module granca_detection (
  input  Up,
  input  Down,
  input  [7:0] in_3,
  input  Left,
  input  Right,
  output out_6
);

  wire and_1_out, and_2_out, nor_1_out, nor_2_out;

  Pull_Resistor pull_resistor_1 (.node(Up));
  Pull_Resistor pull_resistor_2 (.node(Down));
  Pull_Resistor pull_resistor_3 (.node(Left));
  Pull_Resistor pull_resistor_4 (.node(Right));
  and and_1 (and_1_out, Up, in_3[3], in_3[2], in_3[1], in_3[0]);
  and and_2 (and_2_out, in_3[7], in_3[6], in_3[5], in_3[4], Right);
  nor nor_1 (nor_1_out, ~Down, in_3[0], in_3[1], in_3[2], in_3[3]);  // NOR_Gate
  nor nor_2 (nor_2_out, in_3[4], in_3[5], in_3[6], in_3[7], ~Left);  // NOR_Gate
  or or_1 (out_6, and_1_out, nor_1_out, nor_2_out, and_2_out);
endmodule

// управление
module movement (
  input  [6:0] \input ,
  input  Clear,
  output [1:0] Move,
  output out_4,
  output out_5,
  output out_6,
  output out_7
);

  wire and_1_out, comparator_1_eq, comparator_2_eq, comparator_3_eq, comparator_4_eq, comparator_5_eq,
       comparator_6_eq, comparator_7_eq, comparator_8_eq, or_1_out, or_2_out, or_3_out, or_4_out, or_7_out,
       xnor_1_out, xor_1_out;
  wire [1:0] or_5_out, register_1_q, register_2_q;

  Comparator #(.width(7)) comparator_1 (.a(\input ), .b(7'b1100100), .eq(comparator_1_eq));  // open: gt, lt
  Comparator #(.width(7)) comparator_2 (.a(\input ), .b(7'b0110010), .eq(comparator_2_eq));  // open: gt, lt
  Comparator #(.width(7)) comparator_3 (.a(\input ), .b(7'b1110011), .eq(comparator_3_eq));  // open: gt, lt
  Comparator #(.width(7)) comparator_4 (.a(\input ), .b(7'b1001011), .eq(comparator_4_eq));  // open: gt, lt
  Comparator #(.width(7)) comparator_5 (.a(\input ), .b(7'b1100001), .eq(comparator_5_eq));  // open: gt, lt
  Comparator #(.width(7)) comparator_6 (.a(\input ), .b(7'b1000100), .eq(comparator_6_eq));  // open: gt, lt
  Comparator #(.width(7)) comparator_7 (.a(\input ), .b(7'b1110111), .eq(comparator_7_eq));  // open: gt, lt
  Comparator #(.width(7)) comparator_8 (.a(\input ), .b(7'b1000110), .eq(comparator_8_eq));  // open: gt, lt
  or or_1 (or_1_out, comparator_1_eq, comparator_2_eq);
  or or_2 (or_2_out, comparator_3_eq, comparator_4_eq);
  or or_3 (or_3_out, comparator_5_eq, comparator_6_eq);
  or or_4 (or_4_out, comparator_7_eq, comparator_8_eq);
  or or_5 (or_5_out[0], or_2_out, or_1_out);
  or or_6 (or_5_out[1], or_1_out, or_3_out);
  or or_7 (or_7_out, or_1_out, or_2_out, or_3_out, or_4_out);
  Register #(.width(2)) register_1 (.D(or_5_out), .Q(register_1_q), .clk(or_7_out), .clr(Clear));  // open: en
  Register #(.width(2)) register_2 (.D(Move), .Q(register_2_q), .clk(or_7_out), .clr(Clear));  // open: en
  xnor xnor_1 (xnor_1_out, register_2_q[1], register_1_q[1]);
  xor xor_1 (xor_1_out, register_2_q[0], register_1_q[0]);
  Multiplexer #(.width(2)) multiplexer_1 (
    .in0(register_1_q), .in1(register_2_q), .out(Move), .sel(and_1_out));  // open: en
  and and_1 (and_1_out, xnor_1_out, xor_1_out);
  Demultiplexer #(.select(2)) demultiplexer_1 (
    .out0(out_4), .out1(out_5), .out2(out_6), .out3(out_7), .in(1'b1), .sel(Move));  // open: en

  // Notes on the sheet:
  //   новое направление
  //   текушее направление
endmodule

module pseudo_reg (
  input  [3:0] in_1,
  input  [3:0] in_2,
  output [16:0] out_3,
  output [16:0] out_4,
  output [16:0] out_5,
  output [16:0] out_6,
  output [16:0] out_7,
  output [16:0] out_8,
  output [16:0] out_9,
  output [16:0] out_10,
  output [16:0] out_11,
  output [16:0] out_12,
  output [16:0] out_13,
  output [16:0] out_14,
  output [16:0] out_15,
  output [16:0] out_16,
  output [16:0] out_17,
  output [16:0] out_18
);

  wire decoder_2_out0, decoder_2_out1, decoder_2_out2, decoder_2_out3, decoder_2_out4, decoder_2_out5,
       decoder_2_out6, decoder_2_out7, decoder_2_out8, decoder_2_out9, decoder_2_out10, decoder_2_out11,
       decoder_2_out12, decoder_2_out13, decoder_2_out14, decoder_2_out15;
  wire [15:0] decoder_1_out0;

  Decoder #(.select(4), .disabled(0), .enable("false")) decoder_1 (
    .out0(decoder_1_out0[0]), .out1(decoder_1_out0[1]), .out2(decoder_1_out0[2]), .out3(decoder_1_out0[3]),
    .out4(decoder_1_out0[4]), .out5(decoder_1_out0[5]), .out6(decoder_1_out0[6]), .out7(decoder_1_out0[7]),
    .out8(decoder_1_out0[8]), .out9(decoder_1_out0[9]), .out10(decoder_1_out0[10]),
    .out11(decoder_1_out0[11]), .out12(decoder_1_out0[12]), .out13(decoder_1_out0[13]),
    .out14(decoder_1_out0[14]), .out15(decoder_1_out0[15]), .sel(in_1));
  _16_bit_AND u_16_bit_and_1 (.\input (decoder_1_out0), .switch(decoder_2_out0), .\output (out_11));
  _16_bit_AND u_16_bit_and_2 (.\input (decoder_1_out0), .switch(decoder_2_out1), .\output (out_3));
  _16_bit_AND u_16_bit_and_3 (.\input (decoder_1_out0), .switch(decoder_2_out2), .\output (out_12));
  _16_bit_AND u_16_bit_and_4 (.\input (decoder_1_out0), .switch(decoder_2_out3), .\output (out_4));
  Decoder #(.select(4), .disabled(0), .enable("false")) decoder_2 (
    .out0(decoder_2_out0), .out1(decoder_2_out1), .out2(decoder_2_out2), .out3(decoder_2_out3),
    .out4(decoder_2_out4), .out5(decoder_2_out5), .out6(decoder_2_out6), .out7(decoder_2_out7),
    .out8(decoder_2_out8), .out9(decoder_2_out9), .out10(decoder_2_out10), .out11(decoder_2_out11),
    .out12(decoder_2_out12), .out13(decoder_2_out13), .out14(decoder_2_out14), .out15(decoder_2_out15),
    .sel(in_2));
  _16_bit_AND u_16_bit_and_5 (.\input (decoder_1_out0), .switch(decoder_2_out5), .\output (out_5));
  _16_bit_AND u_16_bit_and_6 (.\input (decoder_1_out0), .switch(decoder_2_out4), .\output (out_13));
  _16_bit_AND u_16_bit_and_7 (.\input (decoder_1_out0), .switch(decoder_2_out7), .\output (out_6));
  _16_bit_AND u_16_bit_and_8 (.\input (decoder_1_out0), .switch(decoder_2_out6), .\output (out_14));
  _16_bit_AND u_16_bit_and_9 (.\input (decoder_1_out0), .switch(decoder_2_out8), .\output (out_15));
  _16_bit_AND u_16_bit_and_10 (.\input (decoder_1_out0), .switch(decoder_2_out9), .\output (out_7));
  _16_bit_AND u_16_bit_and_11 (.\input (decoder_1_out0), .switch(decoder_2_out10), .\output (out_16));
  _16_bit_AND u_16_bit_and_12 (.\input (decoder_1_out0), .switch(decoder_2_out11), .\output (out_8));
  _16_bit_AND u_16_bit_and_13 (.\input (decoder_1_out0), .switch(decoder_2_out13), .\output (out_9));
  _16_bit_AND u_16_bit_and_14 (.\input (decoder_1_out0), .switch(decoder_2_out12), .\output (out_17));
  _16_bit_AND u_16_bit_and_15 (.\input (decoder_1_out0), .switch(decoder_2_out15), .\output (out_10));
  _16_bit_AND u_16_bit_and_16 (.\input (decoder_1_out0), .switch(decoder_2_out14), .\output (out_18));
endmodule

module golod (
  input  stop_golod,
  input  clock,
  input  clr,
  input  hz,
  output golod
);

  wire and_1_out, comparator_1_eq, comparator_1_gt, comparator_2_gt, or_1_out, or_2_out;
  wire [9:0] counter_1_q, counter_2_q;

  and and_1 (and_1_out, clock, stop_golod);
  Counter #(.width(10), .max('h3ff)) counter_1 (
    .Q(counter_1_q), .clk(and_1_out), .clr(or_1_out));  // open: load, D, count, carry
  or or_1 (or_1_out, clr, hz);
  or or_2 (or_2_out, comparator_1_gt, comparator_1_eq);
  Comparator #(.width(10), .mode("unsigned")) comparator_1 (
    .a(counter_1_q), .b(10'h14), .gt(comparator_1_gt), .eq(comparator_1_eq));  // open: lt
  Counter #(.width(10), .max('h3ff)) counter_2 (
    .Q(counter_2_q), .clk(or_2_out), .clr(clr));  // open: load, D, count, carry
  Comparator #(.width(10), .mode("unsigned")) comparator_2 (
    .a(counter_2_q), .b({10{1'b0}}), .gt(comparator_2_gt));  // open: eq, lt
  and and_2 (golod, stop_golod, comparator_2_gt);

  // Notes on the sheet:
  //   тут 0f1 это константа после такого количества clockов в голод пойдет 1 которая остановит такты
endmodule

module Apple_Detection (
  input  clr,
  input  [7:0] head,
  input  [1:0] \Static_Направление ,
  input  [7:0] Apple_coord,
  output BIT_FOR_evGENII_KIRILLOV
);

  wire comparator_1_eq, comparator_1_gt, comparator_2_eq, comparator_2_gt;
  wire [3:0] inc_dec_1_r, inc_dec_2_r, inc_dec_3_r, inc_dec_4_r;
  wire [7:0] adder_1_out, negator_1_out;

  Comparator #(.width(2), .mode("unsigned")) comparator_1 (
    .a(\Static_Направление ), .b(2'b10), .gt(comparator_1_gt), .eq(comparator_1_eq));  // open: lt
  Comparator #(.width(2), .mode("unsigned")) comparator_2 (
    .a(2'b01), .b(\Static_Направление ), .gt(comparator_2_gt), .eq(comparator_2_eq));  // open: lt
  inc_dec inc_dec_1 (.X(head[3:0]), .on_off(comparator_1_eq), .inc_dec(comparator_1_eq), .R(inc_dec_1_r));  // open: OFL
  inc_dec inc_dec_2 (.X(head[7:4]), .on_off(comparator_2_gt), .inc_dec(comparator_2_gt), .R(inc_dec_2_r));  // open: OFL
  inc_dec inc_dec_3 (
    .X(inc_dec_1_r), .on_off(comparator_1_gt), .inc_dec(comparator_1_eq), .R(inc_dec_3_r));  // open: OFL
  inc_dec inc_dec_4 (
    .X(inc_dec_2_r), .on_off(comparator_2_eq), .inc_dec(comparator_2_gt), .R(inc_dec_4_r));  // open: OFL
  Negator negator_1 (.in(Apple_coord), .out(negator_1_out));
  Adder adder_1 (.a({inc_dec_4_r, inc_dec_3_r}), .b(negator_1_out), .out(adder_1_out));  // open: cin, cout
  nor nor_1 (BIT_FOR_evGENII_KIRILLOV, adder_1_out[0], adder_1_out[1], adder_1_out[2], adder_1_out[3], adder_1_out[4], adder_1_out[5], adder_1_out[6], adder_1_out[7]);

  // Notes on the sheet:
  //   Эта штука добавляет в счетчик когда следующая клетка после головы это яблоко и мы идем в его сторону
  //   Нужно придумать при какой ситуации будем очищать счетчик 
endmodule

module disp_snake (
  input  [3:0] X,
  input  clock,
  input  [3:0] Y,
  input  clear,
  input  Del,
  output [15:0] out_6,
  output [15:0] out_7,
  output [15:0] out_8,
  output [15:0] out_9,
  output [15:0] out_10,
  output [15:0] out_11,
  output [15:0] out_12,
  output [15:0] out_13,
  output [15:0] out_14,
  output [15:0] out_15,
  output [15:0] out_16,
  output [15:0] out_17,
  output [15:0] out_18,
  output [15:0] out_19,
  output [15:0] out_20,
  output [15:0] out_21
);

  wire demultiplexer_1_out0, demultiplexer_1_out1, demultiplexer_1_out2, demultiplexer_1_out3,
       demultiplexer_1_out4, demultiplexer_1_out5, demultiplexer_1_out6, demultiplexer_1_out7,
       demultiplexer_1_out8, demultiplexer_1_out9, demultiplexer_1_out10, demultiplexer_1_out11,
       demultiplexer_1_out12, demultiplexer_1_out13, demultiplexer_1_out14, demultiplexer_1_out15;
  wire [15:0] dispriadok_snake_1_riadok, dispriadok_snake_2_riadok, dispriadok_snake_3_riadok,
       dispriadok_snake_4_riadok, dispriadok_snake_5_riadok, dispriadok_snake_6_riadok,
       dispriadok_snake_7_riadok, dispriadok_snake_8_riadok, dispriadok_snake_9_riadok,
       dispriadok_snake_10_riadok, dispriadok_snake_11_riadok, dispriadok_snake_12_riadok,
       dispriadok_snake_13_riadok, dispriadok_snake_14_riadok, dispriadok_snake_15_riadok,
       dispriadok_snake_16_riadok;

  Demultiplexer #(.select(4)) demultiplexer_1 (
    .out0(demultiplexer_1_out0), .out1(demultiplexer_1_out1), .out2(demultiplexer_1_out2),
    .out3(demultiplexer_1_out3), .out4(demultiplexer_1_out4), .out5(demultiplexer_1_out5),
    .out6(demultiplexer_1_out6), .out7(demultiplexer_1_out7), .out8(demultiplexer_1_out8),
    .out9(demultiplexer_1_out9), .out10(demultiplexer_1_out10), .out11(demultiplexer_1_out11),
    .out12(demultiplexer_1_out12), .out13(demultiplexer_1_out13), .out14(demultiplexer_1_out14),
    .out15(demultiplexer_1_out15), .in(clock), .sel(Y));  // open: en
  dispriadok_snake dispriadok_snake_1 (
    .clock(demultiplexer_1_out15), .hodn(clock), .X(X), .riadok(dispriadok_snake_1_riadok), .clear(clear));
  dispriadok_snake dispriadok_snake_2 (
    .clock(demultiplexer_1_out14), .hodn(clock), .X(X), .riadok(dispriadok_snake_2_riadok), .clear(clear));
  dispriadok_snake dispriadok_snake_3 (
    .clock(demultiplexer_1_out13), .hodn(clock), .X(X), .riadok(dispriadok_snake_3_riadok), .clear(clear));
  dispriadok_snake dispriadok_snake_4 (
    .clock(demultiplexer_1_out12), .hodn(clock), .X(X), .riadok(dispriadok_snake_4_riadok), .clear(clear));
  dispriadok_snake dispriadok_snake_5 (
    .clock(demultiplexer_1_out11), .hodn(clock), .X(X), .riadok(dispriadok_snake_5_riadok), .clear(clear));
  dispriadok_snake dispriadok_snake_6 (
    .clock(demultiplexer_1_out10), .hodn(clock), .X(X), .riadok(dispriadok_snake_6_riadok), .clear(clear));
  dispriadok_snake dispriadok_snake_7 (
    .clock(demultiplexer_1_out9), .hodn(clock), .X(X), .riadok(dispriadok_snake_7_riadok), .clear(clear));
  dispriadok_snake dispriadok_snake_8 (
    .clock(demultiplexer_1_out8), .hodn(clock), .X(X), .riadok(dispriadok_snake_8_riadok), .clear(clear));
  dispriadok_snake dispriadok_snake_9 (
    .clock(demultiplexer_1_out7), .hodn(clock), .X(X), .riadok(dispriadok_snake_9_riadok), .clear(clear));
  dispriadok_snake dispriadok_snake_10 (
    .clock(demultiplexer_1_out6), .hodn(clock), .X(X), .riadok(dispriadok_snake_10_riadok), .clear(clear));
  dispriadok_snake dispriadok_snake_11 (
    .clock(demultiplexer_1_out5), .hodn(clock), .X(X), .riadok(dispriadok_snake_11_riadok), .clear(clear));
  dispriadok_snake dispriadok_snake_12 (
    .clock(demultiplexer_1_out4), .hodn(clock), .X(X), .riadok(dispriadok_snake_12_riadok), .clear(clear));
  dispriadok_snake dispriadok_snake_13 (
    .clock(demultiplexer_1_out3), .hodn(clock), .X(X), .riadok(dispriadok_snake_13_riadok), .clear(clear));
  dispriadok_snake dispriadok_snake_14 (
    .clock(demultiplexer_1_out2), .hodn(clock), .X(X), .riadok(dispriadok_snake_14_riadok), .clear(clear));
  dispriadok_snake dispriadok_snake_15 (
    .clock(demultiplexer_1_out1), .hodn(clock), .X(X), .riadok(dispriadok_snake_15_riadok), .clear(clear));
  dispriadok_snake dispriadok_snake_16 (
    .clock(demultiplexer_1_out0), .hodn(clock), .X(X), .riadok(dispriadok_snake_16_riadok), .clear(clear));
  reg_delete_snake reg_delete_snake_1 (.Input(dispriadok_snake_1_riadok), .Output(out_6), .Del(Del));
  reg_delete_snake reg_delete_snake_2 (.Input(dispriadok_snake_2_riadok), .Output(out_7), .Del(Del));
  reg_delete_snake reg_delete_snake_3 (.Input(dispriadok_snake_3_riadok), .Output(out_8), .Del(Del));
  reg_delete_snake reg_delete_snake_4 (.Input(dispriadok_snake_4_riadok), .Output(out_9), .Del(Del));
  reg_delete_snake reg_delete_snake_5 (.Input(dispriadok_snake_5_riadok), .Output(out_10), .Del(Del));
  reg_delete_snake reg_delete_snake_6 (.Input(dispriadok_snake_6_riadok), .Output(out_11), .Del(Del));
  reg_delete_snake reg_delete_snake_7 (.Input(dispriadok_snake_7_riadok), .Output(out_12), .Del(Del));
  reg_delete_snake reg_delete_snake_8 (.Input(dispriadok_snake_8_riadok), .Output(out_13), .Del(Del));
  reg_delete_snake reg_delete_snake_9 (.Input(dispriadok_snake_9_riadok), .Output(out_14), .Del(Del));
  reg_delete_snake reg_delete_snake_10 (.Input(dispriadok_snake_10_riadok), .Output(out_15), .Del(Del));
  reg_delete_snake reg_delete_snake_11 (.Input(dispriadok_snake_11_riadok), .Output(out_16), .Del(Del));
  reg_delete_snake reg_delete_snake_12 (.Input(dispriadok_snake_12_riadok), .Output(out_17), .Del(Del));
  reg_delete_snake reg_delete_snake_13 (.Input(dispriadok_snake_13_riadok), .Output(out_18), .Del(Del));
  reg_delete_snake reg_delete_snake_14 (.Input(dispriadok_snake_14_riadok), .Output(out_19), .Del(Del));
  reg_delete_snake reg_delete_snake_15 (.Input(dispriadok_snake_15_riadok), .Output(out_20), .Del(Del));
  reg_delete_snake reg_delete_snake_16 (.Input(dispriadok_snake_16_riadok), .Output(out_21), .Del(Del));
endmodule

module dispriadok_snake (
  input  clock,
  input  hodn,
  input  [3:0] X,
  input  clear,
  output [15:0] riadok
);

  wire demultiplexer_1_out0, demultiplexer_1_out1, demultiplexer_1_out2, demultiplexer_1_out3,
       demultiplexer_1_out4, demultiplexer_1_out5, demultiplexer_1_out6, demultiplexer_1_out7,
       demultiplexer_1_out8, demultiplexer_1_out9, demultiplexer_1_out10, demultiplexer_1_out11,
       demultiplexer_1_out12, demultiplexer_1_out13, demultiplexer_1_out14, demultiplexer_1_out15;

  Demultiplexer #(.select(4)) demultiplexer_1 (
    .out0(demultiplexer_1_out0), .out1(demultiplexer_1_out1), .out2(demultiplexer_1_out2),
    .out3(demultiplexer_1_out3), .out4(demultiplexer_1_out4), .out5(demultiplexer_1_out5),
    .out6(demultiplexer_1_out6), .out7(demultiplexer_1_out7), .out8(demultiplexer_1_out8),
    .out9(demultiplexer_1_out9), .out10(demultiplexer_1_out10), .out11(demultiplexer_1_out11),
    .out12(demultiplexer_1_out12), .out13(demultiplexer_1_out13), .out14(demultiplexer_1_out14),
    .out15(demultiplexer_1_out15), .in(clock), .sel(X));  // open: en
  D_Flip_Flop d_ff_1 (.clk(demultiplexer_1_out0), .D(hodn), .Q(riadok[15]), .reset(clear));  // open: Qn, preset, en
  D_Flip_Flop d_ff_2 (.clk(demultiplexer_1_out1), .D(hodn), .Q(riadok[14]), .reset(clear));  // open: Qn, preset, en
  D_Flip_Flop d_ff_3 (.clk(demultiplexer_1_out2), .D(hodn), .Q(riadok[13]), .reset(clear));  // open: Qn, preset, en
  D_Flip_Flop d_ff_4 (.clk(demultiplexer_1_out3), .D(hodn), .Q(riadok[12]), .reset(clear));  // open: Qn, preset, en
  D_Flip_Flop d_ff_5 (.clk(demultiplexer_1_out4), .D(hodn), .Q(riadok[11]), .reset(clear));  // open: Qn, preset, en
  D_Flip_Flop d_ff_6 (.clk(demultiplexer_1_out6), .D(hodn), .Q(riadok[9]), .reset(clear));  // open: Qn, preset, en
  D_Flip_Flop d_ff_7 (.clk(demultiplexer_1_out5), .D(hodn), .Q(riadok[10]), .reset(clear));  // open: Qn, preset, en
  D_Flip_Flop d_ff_8 (.clk(demultiplexer_1_out7), .D(hodn), .Q(riadok[8]), .reset(clear));  // open: Qn, preset, en
  D_Flip_Flop d_ff_9 (.clk(demultiplexer_1_out8), .D(hodn), .Q(riadok[7]), .reset(clear));  // open: Qn, preset, en
  D_Flip_Flop d_ff_10 (.clk(demultiplexer_1_out9), .D(hodn), .Q(riadok[6]), .reset(clear));  // open: Qn, preset, en
  D_Flip_Flop d_ff_11 (.clk(demultiplexer_1_out10), .D(hodn), .Q(riadok[5]), .reset(clear));  // open: Qn, preset, en
  D_Flip_Flop d_ff_12 (.clk(demultiplexer_1_out11), .D(hodn), .Q(riadok[4]), .reset(clear));  // open: Qn, preset, en
  D_Flip_Flop d_ff_13 (.clk(demultiplexer_1_out12), .D(hodn), .Q(riadok[3]), .reset(clear));  // open: Qn, preset, en
  D_Flip_Flop d_ff_14 (.clk(demultiplexer_1_out14), .D(hodn), .Q(riadok[1]), .reset(clear));  // open: Qn, preset, en
  D_Flip_Flop d_ff_15 (.clk(demultiplexer_1_out13), .D(hodn), .Q(riadok[2]), .reset(clear));  // open: Qn, preset, en
  D_Flip_Flop d_ff_16 (.clk(demultiplexer_1_out15), .D(hodn), .Q(riadok[0]), .reset(clear));  // open: Qn, preset, en
endmodule

module reg_delete_snake (
  input  [15:0] Input,
  input  Del,
  output [15:0] Output
);

  wire not_2_out, not_3_out, not_4_out, not_5_out, not_6_out, not_7_out, not_8_out, not_9_out, not_10_out,
       not_11_out, not_12_out, not_13_out, not_14_out, or_1_out;
  wire [15:0] and_1_out, controlled_buffer_1_out, controlled_buffer_2_out, demultiplexer_1_out0,
       demultiplexer_1_out1, not_1_out, or_2_out;

  or or_1 (or_1_out, Input[0], Input[1], Input[2], Input[3], Input[4], Input[5], Input[6], Input[7], Input[8], Input[9], Input[10], Input[11], Input[12], Input[13], Input[14], Input[15]);
  assign controlled_buffer_1_out = or_1_out ? Input : 16'bz;  // Controlled_Buffer controlled_buffer_1
  Demultiplexer #(.width(16)) demultiplexer_1 (
    .out0(demultiplexer_1_out0), .out1(demultiplexer_1_out1), .in(controlled_buffer_1_out), .sel(Del));  // open: en
  assign not_1_out = ~demultiplexer_1_out1;  // NOT_Gate not_1, 16 bits wide
  not not_2 (not_2_out, or_1_out);
  not not_3 (not_3_out, not_2_out);
  not not_4 (not_4_out, not_3_out);
  assign or_2_out = Output | demultiplexer_1_out0;  // OR_Gate or_2, 16 bits wide
  assign and_1_out = not_1_out & Output;  // AND_Gate and_1, 16 bits wide
  not not_5 (not_5_out, not_7_out);
  not not_6 (not_6_out, not_4_out);
  not not_7 (not_7_out, not_6_out);
  not not_8 (not_8_out, not_5_out);
  assign controlled_buffer_2_out = not_9_out ? or_2_out : 16'bz;  // Controlled_Buffer controlled_buffer_2
  not not_9 (not_9_out, Del);
  assign controlled_buffer_2_out = Del ? and_1_out : 16'bz;  // Controlled_Buffer controlled_buffer_3
  not not_10 (not_10_out, not_11_out);
  not not_11 (not_11_out, not_12_out);
  not not_12 (not_12_out, not_8_out);
  not not_13 (not_13_out, not_10_out);
  Register #(.width(16)) register_1 (.D(controlled_buffer_2_out), .Q(Output), .clk(not_14_out));  // open: en, clr
  not not_14 (not_14_out, not_13_out);

  // Notes on the sheet:
  //   Проверка на 0
  //   Если 0, то ничего не делаем
  //   Режим: Удаление или добавление
  //   Добавление пикселя
  //   Удаление пикселя
endmodule

module sec_matrixdispriadok (
  input  clock,
  input  hodn,
  input  [3:0] X,
  input  clear,
  output [16:0] riadok
);

  wire demultiplexer_1_out0, demultiplexer_1_out1, demultiplexer_1_out2, demultiplexer_1_out3,
       demultiplexer_1_out4, demultiplexer_1_out5, demultiplexer_1_out6, demultiplexer_1_out7,
       demultiplexer_1_out8, demultiplexer_1_out9, demultiplexer_1_out10, demultiplexer_1_out11,
       demultiplexer_1_out12, demultiplexer_1_out13, demultiplexer_1_out14, demultiplexer_1_out15;

  Demultiplexer #(.select(4)) demultiplexer_1 (
    .out0(demultiplexer_1_out0), .out1(demultiplexer_1_out1), .out2(demultiplexer_1_out2),
    .out3(demultiplexer_1_out3), .out4(demultiplexer_1_out4), .out5(demultiplexer_1_out5),
    .out6(demultiplexer_1_out6), .out7(demultiplexer_1_out7), .out8(demultiplexer_1_out8),
    .out9(demultiplexer_1_out9), .out10(demultiplexer_1_out10), .out11(demultiplexer_1_out11),
    .out12(demultiplexer_1_out12), .out13(demultiplexer_1_out13), .out14(demultiplexer_1_out14),
    .out15(demultiplexer_1_out15), .in(clock), .sel(X));  // open: en
  D_Flip_Flop d_ff_1 (.clk(demultiplexer_1_out0), .D(hodn), .Q(riadok[15]), .reset(clear));  // open: Qn, preset, en
  D_Flip_Flop d_ff_2 (.clk(demultiplexer_1_out1), .D(hodn), .Q(riadok[14]), .reset(clear));  // open: Qn, preset, en
  D_Flip_Flop d_ff_3 (.clk(demultiplexer_1_out2), .D(hodn), .Q(riadok[13]), .reset(clear));  // open: Qn, preset, en
  D_Flip_Flop d_ff_4 (.clk(demultiplexer_1_out3), .D(hodn), .Q(riadok[12]), .reset(clear));  // open: Qn, preset, en
  D_Flip_Flop d_ff_5 (.clk(demultiplexer_1_out5), .D(hodn), .Q(riadok[10]), .reset(clear));  // open: Qn, preset, en
  D_Flip_Flop d_ff_6 (.clk(demultiplexer_1_out4), .D(hodn), .Q(riadok[11]), .reset(clear));  // open: Qn, preset, en
  D_Flip_Flop d_ff_7 (.clk(demultiplexer_1_out6), .D(hodn), .Q(riadok[9]), .reset(clear));  // open: Qn, preset, en
  D_Flip_Flop d_ff_8 (.clk(demultiplexer_1_out7), .D(hodn), .Q(riadok[8]), .reset(clear));  // open: Qn, preset, en
  D_Flip_Flop d_ff_9 (.clk(demultiplexer_1_out8), .D(hodn), .Q(riadok[7]), .reset(clear));  // open: Qn, preset, en
  D_Flip_Flop d_ff_10 (.clk(demultiplexer_1_out9), .D(hodn), .Q(riadok[6]), .reset(clear));  // open: Qn, preset, en
  D_Flip_Flop d_ff_11 (.clk(demultiplexer_1_out10), .D(hodn), .Q(riadok[5]), .reset(clear));  // open: Qn, preset, en
  D_Flip_Flop d_ff_12 (.clk(demultiplexer_1_out11), .D(hodn), .Q(riadok[4]), .reset(clear));  // open: Qn, preset, en
  D_Flip_Flop d_ff_13 (.clk(demultiplexer_1_out12), .D(hodn), .Q(riadok[3]), .reset(clear));  // open: Qn, preset, en
  D_Flip_Flop d_ff_14 (.clk(demultiplexer_1_out13), .D(hodn), .Q(riadok[2]), .reset(clear));  // open: Qn, preset, en
  D_Flip_Flop d_ff_15 (.clk(demultiplexer_1_out14), .D(hodn), .Q(riadok[1]), .reset(clear));  // open: Qn, preset, en
  D_Flip_Flop d_ff_16 (.clk(demultiplexer_1_out15), .D(hodn), .Q(riadok[0]), .reset(clear));  // open: Qn, preset, en

  assign riadok[16] = 1'b0;
endmodule

module sec_matrix_disp (
  input  [3:0] X,
  input  clock,
  input  [3:0] Y,
  input  clear,
  output [16:0] out_5,
  output [16:0] out_6,
  output [16:0] out_7,
  output [16:0] out_8,
  output [16:0] out_9,
  output [16:0] out_10,
  output [16:0] out_11,
  output [16:0] out_12,
  output [16:0] out_13,
  output [16:0] out_14,
  output [16:0] out_15,
  output [16:0] out_16,
  output [16:0] out_17,
  output [16:0] out_18,
  output [16:0] out_19,
  output [16:0] out_20
);

  wire demultiplexer_1_out0, demultiplexer_1_out1, demultiplexer_1_out2, demultiplexer_1_out3,
       demultiplexer_1_out4, demultiplexer_1_out5, demultiplexer_1_out6, demultiplexer_1_out7,
       demultiplexer_1_out8, demultiplexer_1_out9, demultiplexer_1_out10, demultiplexer_1_out11,
       demultiplexer_1_out12, demultiplexer_1_out13, demultiplexer_1_out14, demultiplexer_1_out15;

  Demultiplexer #(.select(4)) demultiplexer_1 (
    .out0(demultiplexer_1_out0), .out1(demultiplexer_1_out1), .out2(demultiplexer_1_out2),
    .out3(demultiplexer_1_out3), .out4(demultiplexer_1_out4), .out5(demultiplexer_1_out5),
    .out6(demultiplexer_1_out6), .out7(demultiplexer_1_out7), .out8(demultiplexer_1_out8),
    .out9(demultiplexer_1_out9), .out10(demultiplexer_1_out10), .out11(demultiplexer_1_out11),
    .out12(demultiplexer_1_out12), .out13(demultiplexer_1_out13), .out14(demultiplexer_1_out14),
    .out15(demultiplexer_1_out15), .in(clock), .sel(Y));  // open: en
  sec_matrixdispriadok sec_matrixdispriadok_1 (
    .clock(clock), .hodn(demultiplexer_1_out15), .X(X), .riadok(out_5), .clear(clear));
  sec_matrixdispriadok sec_matrixdispriadok_2 (
    .clock(clock), .hodn(demultiplexer_1_out14), .X(X), .riadok(out_6), .clear(clear));
  sec_matrixdispriadok sec_matrixdispriadok_3 (
    .clock(clock), .hodn(demultiplexer_1_out13), .X(X), .riadok(out_7), .clear(clear));
  sec_matrixdispriadok sec_matrixdispriadok_4 (
    .clock(clock), .hodn(demultiplexer_1_out12), .X(X), .riadok(out_8), .clear(clear));
  sec_matrixdispriadok sec_matrixdispriadok_5 (
    .clock(clock), .hodn(demultiplexer_1_out11), .X(X), .riadok(out_9), .clear(clear));
  sec_matrixdispriadok sec_matrixdispriadok_6 (
    .clock(clock), .hodn(demultiplexer_1_out10), .X(X), .riadok(out_10), .clear(clear));
  sec_matrixdispriadok sec_matrixdispriadok_7 (
    .clock(clock), .hodn(demultiplexer_1_out9), .X(X), .riadok(out_11), .clear(clear));
  sec_matrixdispriadok sec_matrixdispriadok_8 (
    .clock(clock), .hodn(demultiplexer_1_out8), .X(X), .riadok(out_12), .clear(clear));
  sec_matrixdispriadok sec_matrixdispriadok_9 (
    .clock(clock), .hodn(demultiplexer_1_out7), .X(X), .riadok(out_13), .clear(clear));
  sec_matrixdispriadok sec_matrixdispriadok_10 (
    .clock(clock), .hodn(demultiplexer_1_out6), .X(X), .riadok(out_14), .clear(clear));
  sec_matrixdispriadok sec_matrixdispriadok_11 (
    .clock(clock), .hodn(demultiplexer_1_out5), .X(X), .riadok(out_15), .clear(clear));
  sec_matrixdispriadok sec_matrixdispriadok_12 (
    .clock(clock), .hodn(demultiplexer_1_out4), .X(X), .riadok(out_16), .clear(clear));
  sec_matrixdispriadok sec_matrixdispriadok_13 (
    .clock(clock), .hodn(demultiplexer_1_out3), .X(X), .riadok(out_17), .clear(clear));
  sec_matrixdispriadok sec_matrixdispriadok_14 (
    .clock(clock), .hodn(demultiplexer_1_out2), .X(X), .riadok(out_18), .clear(clear));
  sec_matrixdispriadok sec_matrixdispriadok_15 (
    .clock(clock), .hodn(demultiplexer_1_out1), .X(X), .riadok(out_19), .clear(clear));
  sec_matrixdispriadok sec_matrixdispriadok_16 (
    .clock(clock), .hodn(demultiplexer_1_out0), .X(X), .riadok(out_20), .clear(clear));
endmodule

module counter (
  input  clock,
  input  clear,
  output out_3,
  output out_4,
  output out_5,
  output out_6,
  output out_7,
  output out_8,
  output out_9,
  output out_10,
  output out_11,
  output out_12,
  output out_13,
  output out_14,
  output out_15,
  output out_16,
  output out_17,
  output out_18
);

  wire counter_1_carry;
  wire [7:0] counter_1_q, counter_2_q;

  Counter #(.max('ha)) counter_1 (
    .Q(counter_1_q), .carry(counter_1_carry), .clk(clock), .clr(clear));  // open: load, D, count
  Counter #(.max('ha)) counter_2 (.Q(counter_2_q), .clk(counter_1_carry), .clr(clear));  // open: load, D, count, carry
  ROM rom_1 (.addr(counter_1_q), .data({out_7, out_8, out_9, out_10, out_18, out_17, out_16, out_15}));  // open: sel
  ROM rom_2 (.addr(counter_2_q), .data({out_3, out_4, out_5, out_6, out_14, out_13, out_12, out_11}));  // open: sel

  // Other names for the same wires on the sheet: _1_1 = out_15; _1_2 = out_16; _1_3 = out_17; _1_4 = out_18;
  //   _1_5 = out_10; _1_6 = out_9; _1_7 = out_8; _1_8 = out_7; _2_1 = out_11; _2_2 = out_12; _2_3 = out_13;
  //   _2_4 = out_14; _2_5 = out_6; _2_6 = out_5; _2_7 = out_4; _2_8 = out_3

  // Notes on the sheet:
  //   contents of rom_1 (hex, n*v repeats v):
  //   77 14 b3 b6 d4 e6 e7 34 f7 f6 77
  //   contents of rom_2 (hex, n*v repeats v):
  //   77 14 b3 b6 d4 e6 e7 34 f7 f6 77
endmodule

module MAIN (
);


  // Notes on the sheet:
  //   КАК ИДЕЯ МОЖНО ПРОСТО СЮДА ВЫНЕСТИ ВСЕ ОТДЕЛЬНЫЕ 
  //   ВХОДЫ ВЗАИМОДЕЙСТВУЮЩИЕ С ПОЛЬЗОВАТЕЛЕМ И ВЫНЕСТИ ПОЛЕ
endmodule

module win (
  input  lose,
  input  win,
  input  pause,
  output [17:0] _1,
  output [17:0] _2,
  output [17:0] _3,
  output [17:0] _4,
  output [17:0] _5,
  output [17:0] _6,
  output [17:0] _7,
  output [17:0] _8,
  output [17:0] _9,
  output [17:0] _10,
  output [17:0] _11,
  output [17:0] _12,
  output [17:0] _13,
  output [17:0] _14,
  output [17:0] _15,
  output [17:0] _16
);

  wire [15:0] _5l, _5p, _5w, _6l, _6p, _6w, _7l, _7p, _7w, _8l, _8p, _8w, _9l, _9p, _9w, _10l, _10p, _10w,
       _11l, _11p, _11w, or_1_out, or_2_out, or_3_out, or_4_out, or_5_out, or_6_out, or_7_out;

  assign _5p = pause ? 16'h200 : 16'bz;  // Controlled_Buffer controlled_buffer_1
  assign _6p = pause ? 16'h300 : 16'bz;  // Controlled_Buffer controlled_buffer_2
  assign _7p = pause ? 16'h380 : 16'bz;  // Controlled_Buffer controlled_buffer_3
  assign _8p = pause ? 16'h3c0 : 16'bz;  // Controlled_Buffer controlled_buffer_4
  Pull_Resistor pull_resistor_1 (.node(_9p));
  assign _9p = pause ? 16'h380 : 16'bz;  // Controlled_Buffer controlled_buffer_5
  assign _10p = pause ? 16'h300 : 16'bz;  // Controlled_Buffer controlled_buffer_6
  Pull_Resistor pull_resistor_2 (.node(_10p));
  Pull_Resistor pull_resistor_3 (.node(_11p));
  assign _11p = pause ? 16'h200 : 16'bz;  // Controlled_Buffer controlled_buffer_7
  assign _5w = win ? {16{1'b0}} : 16'bz;  // Controlled_Buffer controlled_buffer_8
  assign _6w = win ? 16'h4542 : 16'bz;  // Controlled_Buffer controlled_buffer_9
  assign _7w = win ? 16'h4462 : 16'bz;  // Controlled_Buffer controlled_buffer_10
  assign _8w = win ? 16'h4552 : 16'bz;  // Controlled_Buffer controlled_buffer_11
  assign _9w = win ? 16'h554a : 16'bz;  // Controlled_Buffer controlled_buffer_12
  Pull_Resistor pull_resistor_4 (.node(_9w));
  assign _10w = win ? 16'h6d46 : 16'bz;  // Controlled_Buffer controlled_buffer_13
  Pull_Resistor pull_resistor_5 (.node(_10w));
  assign _11w = win ? 16'h4542 : 16'bz;  // Controlled_Buffer controlled_buffer_14
  Pull_Resistor pull_resistor_6 (.node(_11w));
  assign _5l = lose ? {16{1'b0}} : 16'bz;  // Controlled_Buffer controlled_buffer_15
  assign _6l = lose ? 16'h4ef6 : 16'bz;  // Controlled_Buffer controlled_buffer_16
  assign _7l = lose ? 16'h4a84 : 16'bz;  // Controlled_Buffer controlled_buffer_17
  assign _8l = lose ? 16'h4ac4 : 16'bz;  // Controlled_Buffer controlled_buffer_18
  Pull_Resistor pull_resistor_7 (.node(_9l));
  assign _9l = lose ? 16'h4a66 : 16'bz;  // Controlled_Buffer controlled_buffer_19
  assign _10l = lose ? 16'h4a34 : 16'bz;  // Controlled_Buffer controlled_buffer_20
  Pull_Resistor pull_resistor_8 (.node(_10l));
  assign _11l = lose ? 16'h6ef6 : 16'bz;  // Controlled_Buffer controlled_buffer_21
  Pull_Resistor pull_resistor_9 (.node(_11l));
  Pull_Resistor pull_resistor_10 (.node(_5p));
  Pull_Resistor pull_resistor_11 (.node(_6p));
  Pull_Resistor pull_resistor_12 (.node(_7p));
  Pull_Resistor pull_resistor_13 (.node(_8p));
  Pull_Resistor pull_resistor_14 (.node(_5w));
  Pull_Resistor pull_resistor_15 (.node(_6w));
  Pull_Resistor pull_resistor_16 (.node(_7w));
  Pull_Resistor pull_resistor_17 (.node(_8w));
  Pull_Resistor pull_resistor_18 (.node(_5l));
  Pull_Resistor pull_resistor_19 (.node(_6l));
  Pull_Resistor pull_resistor_20 (.node(_7l));
  Pull_Resistor pull_resistor_21 (.node(_8l));
  assign or_1_out = _5p | _5w | _5l;  // OR_Gate or_1, 16 bits wide
  helper_1 helper_1_1 (.in(or_1_out), .out(_5));
  assign or_2_out = _6p | _6w | _6l;  // OR_Gate or_2, 16 bits wide
  helper_1 helper_1_2 (.in(or_2_out), .out(_6));
  assign or_3_out = _7p | _7w | _7l;  // OR_Gate or_3, 16 bits wide
  helper_1 helper_1_3 (.in(or_3_out), .out(_7));
  assign or_4_out = _8p | _8w | _8l;  // OR_Gate or_4, 16 bits wide
  helper_1 helper_1_4 (.in(or_4_out), .out(_8));
  assign or_5_out = _9p | _9w | _9l;  // OR_Gate or_5, 16 bits wide
  helper_1 helper_1_5 (.in(or_5_out), .out(_9));
  assign or_6_out = _10p | _10w | _10l;  // OR_Gate or_6, 16 bits wide
  helper_1 helper_1_6 (.in(or_6_out), .out(_10));
  assign or_7_out = _11p | _11w | _11l;  // OR_Gate or_7, 16 bits wide
  helper_1 helper_1_7 (.in(or_7_out), .out(_11));

  assign _1 = {18{1'b0}};
  assign _2 = {18{1'b0}};
  assign _3 = {18{1'b0}};
  assign _4 = {18{1'b0}};
  assign _12 = {18{1'b0}};
  assign _13 = {18{1'b0}};
  assign _14 = {18{1'b0}};
  assign _15 = {18{1'b0}};
  assign _16 = {18{1'b0}};

  // Other names for the same wires on the sheet: paus = pause
endmodule

module vivod_matrix (
  input  [7:0] snake_coord,
  input  [7:0] apple_coord,
  input  [7:0] head_coord,
  input  Delete,
  input  paus,
  input  win,
  input  lose,
  input  takt,
  input  clr,
  input  vivod,
  input  cycle,
  input  apple,
  output [15:0] out_13,
  output [19:0] out_14,
  output [18:0] out_15,
  output [17:0] out_16,
  output [16:0] out_17,
  output [15:0] out_18,
  output [19:0] out_19,
  output [18:0] out_20,
  output [17:0] out_21,
  output [16:0] out_22,
  output [15:0] out_23,
  output [19:0] out_24,
  output [18:0] out_25,
  output [17:0] out_26,
  output [16:0] out_27,
  output [15:0] out_28,
  output [19:0] out_29,
  output [18:0] out_30,
  output [17:0] out_31,
  output [16:0] out_32,
  output [15:0] out_33,
  output [19:0] out_34,
  output [17:0] out_35,
  output [16:0] out_36,
  output [15:0] out_37,
  output [19:0] out_38,
  output [18:0] out_39,
  output [15:0] out_40,
  output [19:0] out_41,
  output [17:0] out_42,
  output [16:0] out_43,
  output [18:0] out_44,
  output [15:0] out_45,
  output [19:0] out_46,
  output [17:0] out_47,
  output [16:0] out_48,
  output [18:0] out_49,
  output [15:0] out_50,
  output [19:0] out_51,
  output [17:0] out_52,
  output [16:0] out_53,
  output [18:0] out_54,
  output [15:0] out_55,
  output [19:0] out_56,
  output [17:0] out_57,
  output [16:0] out_58,
  output [15:0] out_59,
  output [19:0] out_60,
  output [18:0] out_61,
  output [15:0] out_62,
  output [19:0] out_63,
  output [17:0] out_64,
  output [16:0] out_65,
  output [18:0] out_66,
  output [15:0] out_67,
  output [19:0] out_68,
  output [17:0] out_69,
  output [16:0] out_70,
  output [18:0] out_71,
  output [15:0] out_72,
  output [19:0] out_73,
  output [17:0] out_74,
  output [16:0] out_75,
  output [18:0] out_76,
  output [15:0] out_77,
  output [19:0] out_78,
  output [17:0] out_79,
  output [16:0] out_80,
  output [15:0] out_81,
  output [19:0] out_82,
  output [18:0] out_83,
  output [17:0] out_84,
  output [16:0] out_85,
  output [18:0] out_86,
  output [17:0] out_87,
  output [16:0] out_88,
  output [18:0] out_89,
  output [17:0] out_90,
  output [16:0] out_91,
  output [18:0] out_92
);

  wire or_1_out, or_2_out, or_4_out, or_5_out, rest;
  wire [15:0] _1s, _2s, _3s, _4s, _5s, _6s, _7s, _8s, _9s, _10s, _11s, _12s, _13s, _14s, _15s, _16s;

  Pull_Resistor pull_resistor_1 (.node(vivod));
  or or_1 (or_1_out, vivod, clr);
  or or_2 (or_2_out, lose, cycle, win);
  or or_3 (rest, or_1_out, or_2_out);
  disp_snake disp_snake_1 (
    .X(snake_coord[7:4]), .out_6(_1s), .clock(takt), .Y(snake_coord[3:0]), .out_7(_2s), .out_8(_3s),
    .out_9(_4s), .out_10(_5s), .out_11(_6s), .out_12(_7s), .out_13(_8s), .out_14(_9s), .out_15(_10s),
    .out_16(_11s), .out_17(_12s), .out_18(_13s), .out_19(_14s), .out_20(_15s), .out_21(_16s), .clear(rest),
    .Del(Delete));
  or or_4 (or_4_out, lose, win);
  sec_matrix_disp sec_matrix_disp_1 (
    .X(apple_coord[7:4]), .clock(takt), .Y(apple_coord[3:0]), .out_5(out_17), .out_6(out_22), .out_7(out_27),
    .out_8(out_32), .out_9(out_36), .out_10(out_43), .out_11(out_48), .out_12(out_53), .out_13(out_58),
    .out_14(out_65), .out_15(out_70), .out_16(out_75), .out_17(out_80), .out_18(out_85), .out_19(out_88),
    .out_20(out_91), .clear(or_5_out));
  or or_5 (or_5_out, apple, or_4_out, clr);
  trans trans_1 (.in16(_1s), .in17(out_17), .out19(out_15), .in18(out_16));
  trans trans_2 (.in16(_2s), .in17(out_22), .out19(out_20), .in18(out_21));
  trans trans_3 (.in16(_3s), .in17(out_27), .out19(out_25), .in18(out_26));
  trans trans_4 (.in16(_4s), .in17(out_32), .out19(out_30), .in18(out_31));
  trans trans_5 (.in16(_5s), .in17(out_36), .out19(out_39), .in18(out_35));
  trans trans_6 (.in16(_6s), .in17(out_43), .out19(out_44), .in18(out_42));
  trans trans_7 (.in16(_7s), .in17(out_48), .out19(out_49), .in18(out_47));
  trans trans_8 (.in16(_8s), .in17(out_53), .out19(out_54), .in18(out_52));
  trans trans_9 (.in16(_9s), .in17(out_58), .out19(out_61), .in18(out_57));
  trans trans_10 (.in16(_10s), .in17(out_65), .out19(out_66), .in18(out_64));
  trans trans_11 (.in16(_11s), .in17(out_70), .out19(out_71), .in18(out_69));
  trans trans_12 (.in16(_12s), .in17(out_75), .out19(out_76), .in18(out_74));
  trans trans_13 (.in16(_13s), .in17(out_80), .out19(out_83), .in18(out_79));
  trans trans_14 (.in16(_14s), .in17(out_85), .out19(out_86), .in18(out_84));
  trans trans_15 (.in16(_15s), .in17(out_88), .out19(out_89), .in18(out_87));
  trans trans_16 (.in16(_16s), .in17(out_91), .out19(out_92), .in18(out_90));
  win win_1 (
    .lose(lose), .win(win), .pause(paus), ._1(out_16), ._2(out_21), ._3(out_26), ._4(out_31), ._5(out_35),
    ._6(out_42), ._7(out_47), ._8(out_52), ._9(out_57), ._10(out_64), ._11(out_69), ._12(out_74),
    ._13(out_79), ._14(out_84), ._15(out_87), ._16(out_90));
  headdisp headdisp_1 (
    .X(head_coord[7:4]), .clock(takt), .Y(head_coord[3:0]), .clear(rest), .out_5(out_14), .out_6(out_19),
    .out_7(out_24), .out_8(out_29), .out_9(out_34), .out_10(out_38), .out_11(out_41), .out_12(out_46),
    .out_13(out_51), .out_14(out_56), .out_15(out_60), .out_16(out_63), .out_17(out_68), .out_18(out_73),
    .out_19(out_78), .out_20(out_82));
  _16_20NOAND u_16_20noand_1 (._16in(_1s), ._20in(out_14), ._16out(out_13));
  _16_20NOAND u_16_20noand_2 (._16in(_2s), ._20in(out_19), ._16out(out_18));
  _16_20NOAND u_16_20noand_3 (._16in(_3s), ._20in(out_24), ._16out(out_23));
  _16_20NOAND u_16_20noand_4 (._16in(_4s), ._20in(out_29), ._16out(out_28));
  _16_20NOAND u_16_20noand_5 (._16in(_5s), ._20in(out_34), ._16out(out_33));
  _16_20NOAND u_16_20noand_6 (._16in(_6s), ._20in(out_38), ._16out(out_37));
  _16_20NOAND u_16_20noand_7 (._16in(_7s), ._20in(out_41), ._16out(out_40));
  _16_20NOAND u_16_20noand_8 (._16in(_8s), ._20in(out_46), ._16out(out_45));
  _16_20NOAND u_16_20noand_9 (._16in(_9s), ._20in(out_51), ._16out(out_50));
  _16_20NOAND u_16_20noand_10 (._16in(_10s), ._20in(out_56), ._16out(out_55));
  _16_20NOAND u_16_20noand_11 (._16in(_11s), ._20in(out_60), ._16out(out_59));
  _16_20NOAND u_16_20noand_12 (._16in(_12s), ._20in(out_63), ._16out(out_62));
  _16_20NOAND u_16_20noand_13 (._16in(_13s), ._20in(out_68), ._16out(out_67));
  _16_20NOAND u_16_20noand_14 (._16in(_14s), ._20in(out_73), ._16out(out_72));
  _16_20NOAND u_16_20noand_15 (._16in(_15s), ._20in(out_78), ._16out(out_77));
  _16_20NOAND u_16_20noand_16 (._16in(_16s), ._20in(out_82), ._16out(out_81));

  // Other names for the same wires on the sheet: _1[17:0] = out_16; _1a[16:0] = out_17; _1h[19:0] = out_14;
  //   _1h4[19:0] = out_73; _2[17:0] = out_21; _2a[16:0] = out_22; _3[17:0] = out_26; _3a[16:0] = out_27;
  //   _3h[19:0] = out_24; _4[17:0] = out_31; _4a[16:0] = out_32; _4h[19:0] = out_29; _5[17:0] = out_35;
  //   _5a[16:0] = out_36; _5h[19:0] = out_34; _6[17:0] = out_42; _6a[16:0] = out_43; _6h[19:0] = out_38;
  //   _7[17:0] = out_47; _7a[16:0] = out_48; _7h[19:0] = out_41; _8[17:0] = out_52; _8a[16:0] = out_53;
  //   _8h[19:0] = out_46; _9[17:0] = out_57; _9a[16:0] = out_58; _9h[19:0] = out_51; _10[17:0] = out_64;
  //   _10a[16:0] = out_65; _10h[19:0] = out_56; _11[17:0] = out_69; _11a[16:0] = out_70; _11h[19:0] = out_60;
  //   _12[17:0] = out_74; _12a[16:0] = out_75; _12h[19:0] = out_63; _13[17:0] = out_79; _13a[16:0] = out_80;
  //   _13h[19:0] = out_68; _14[17:0] = out_84; _14a[16:0] = out_85; _15[17:0] = out_87; _15a[16:0] = out_88;
  //   _15h[19:0] = out_78; _16[17:0] = out_90; _16a[16:0] = out_91; _16h[19:0] = out_82; h2[19:0] = out_19
endmodule

module trans (
  input  [15:0] in16,
  input  [16:0] in17,
  input  [17:0] in18,
  output [18:0] out19
);

  assign out19[15:0] = in16 | in17[15:0] | in18[15:0];  // OR_Gate or_1, 16 bits wide

  assign out19[18:16] = 3'b111;
endmodule

module counter2 (
  input  clock,
  input  clear,
  output out_3,
  output out_4,
  output out_5,
  output out_6,
  output out_7,
  output out_8,
  output out_9,
  output out_10,
  output out_11,
  output out_12,
  output out_13,
  output out_14,
  output out_15,
  output out_16,
  output out_17,
  output out_18
);

  wire comparator_1_eq;
  wire [7:0] counter_1_q, counter_2_q;

  Counter #(.max('h14)) counter_1 (.Q(counter_1_q), .clk(clock), .clr(clear));  // open: load, D, count, carry
  Counter #(.max('h5)) counter_2 (.Q(counter_2_q), .clk(comparator_1_eq), .clr(clear));  // open: load, D, count, carry
  ROM rom_1 (.addr(counter_1_q), .data({out_7, out_8, out_9, out_10, out_18, out_17, out_16, out_15}));  // open: sel
  ROM rom_2 (.addr(counter_2_q), .data({out_3, out_4, out_5, out_6, out_14, out_13, out_12, out_11}));  // open: sel
  Comparator comparator_1 (
    .a(8'hf6), .b({out_7, out_8, out_9, out_10, out_18, out_17, out_16, out_15}), .eq(comparator_1_eq));  // open: gt, lt

  // Other names for the same wires on the sheet: _1_1 = out_15; _1_2 = out_16; _1_3 = out_17; _1_4 = out_18;
  //   _1_5 = out_10; _1_6 = out_9; _1_7 = out_8; _1_8 = out_7; _2_1 = out_11; _2_2 = out_12; _2_3 = out_13;
  //   _2_4 = out_14; _2_5 = out_6; _2_6 = out_5; _2_7 = out_4; _2_8 = out_3

  // Notes on the sheet:
  //   contents of rom_1 (hex, n*v repeats v):
  //   77 f6 f7 34 e7 e6 d4 b6 b3 14 77 f6 f7 34 e7 e6 d4 b6 b3 14 77
  //   contents of rom_2 (hex, n*v repeats v):
  //   b3 14 77
endmodule

module helper_1 (
  input  [15:0] in,
  output [17:0] out
);


  assign out = {2'b00, in};
endmodule

module headdispriadok (
  input  clock,
  input  hodn,
  input  [3:0] X,
  input  clear,
  output [19:0] riadok
);

  wire demultiplexer_1_out0, demultiplexer_1_out1, demultiplexer_1_out2, demultiplexer_1_out3,
       demultiplexer_1_out4, demultiplexer_1_out5, demultiplexer_1_out6, demultiplexer_1_out7,
       demultiplexer_1_out8, demultiplexer_1_out9, demultiplexer_1_out10, demultiplexer_1_out11,
       demultiplexer_1_out12, demultiplexer_1_out13, demultiplexer_1_out14, demultiplexer_1_out15;

  Demultiplexer #(.select(4)) demultiplexer_1 (
    .out0(demultiplexer_1_out0), .out1(demultiplexer_1_out1), .out2(demultiplexer_1_out2),
    .out3(demultiplexer_1_out3), .out4(demultiplexer_1_out4), .out5(demultiplexer_1_out5),
    .out6(demultiplexer_1_out6), .out7(demultiplexer_1_out7), .out8(demultiplexer_1_out8),
    .out9(demultiplexer_1_out9), .out10(demultiplexer_1_out10), .out11(demultiplexer_1_out11),
    .out12(demultiplexer_1_out12), .out13(demultiplexer_1_out13), .out14(demultiplexer_1_out14),
    .out15(demultiplexer_1_out15), .in(clock), .sel(X));  // open: en
  D_Flip_Flop d_ff_1 (.clk(demultiplexer_1_out0), .D(hodn), .Q(riadok[15]), .reset(clear));  // open: Qn, preset, en
  D_Flip_Flop d_ff_2 (.clk(demultiplexer_1_out1), .D(hodn), .Q(riadok[14]), .reset(clear));  // open: Qn, preset, en
  D_Flip_Flop d_ff_3 (.clk(demultiplexer_1_out2), .D(hodn), .Q(riadok[13]), .reset(clear));  // open: Qn, preset, en
  D_Flip_Flop d_ff_4 (.clk(demultiplexer_1_out3), .D(hodn), .Q(riadok[12]), .reset(clear));  // open: Qn, preset, en
  D_Flip_Flop d_ff_5 (.clk(demultiplexer_1_out4), .D(hodn), .Q(riadok[11]), .reset(clear));  // open: Qn, preset, en
  D_Flip_Flop d_ff_6 (.clk(demultiplexer_1_out5), .D(hodn), .Q(riadok[10]), .reset(clear));  // open: Qn, preset, en
  D_Flip_Flop d_ff_7 (.clk(demultiplexer_1_out6), .D(hodn), .Q(riadok[9]), .reset(clear));  // open: Qn, preset, en
  D_Flip_Flop d_ff_8 (.clk(demultiplexer_1_out7), .D(hodn), .Q(riadok[8]), .reset(clear));  // open: Qn, preset, en
  D_Flip_Flop d_ff_9 (.clk(demultiplexer_1_out8), .D(hodn), .Q(riadok[7]), .reset(clear));  // open: Qn, preset, en
  D_Flip_Flop d_ff_10 (.clk(demultiplexer_1_out9), .D(hodn), .Q(riadok[6]), .reset(clear));  // open: Qn, preset, en
  D_Flip_Flop d_ff_11 (.clk(demultiplexer_1_out10), .D(hodn), .Q(riadok[5]), .reset(clear));  // open: Qn, preset, en
  D_Flip_Flop d_ff_12 (.clk(demultiplexer_1_out11), .D(hodn), .Q(riadok[4]), .reset(clear));  // open: Qn, preset, en
  D_Flip_Flop d_ff_13 (.clk(demultiplexer_1_out13), .D(hodn), .Q(riadok[2]), .reset(clear));  // open: Qn, preset, en
  D_Flip_Flop d_ff_14 (.clk(demultiplexer_1_out12), .D(hodn), .Q(riadok[3]), .reset(clear));  // open: Qn, preset, en
  D_Flip_Flop d_ff_15 (.clk(demultiplexer_1_out14), .D(hodn), .Q(riadok[1]), .reset(clear));  // open: Qn, preset, en
  D_Flip_Flop d_ff_16 (.clk(demultiplexer_1_out15), .D(hodn), .Q(riadok[0]), .reset(clear));  // open: Qn, preset, en

  assign riadok[19:16] = 4'b0000;
endmodule

module headdisp (
  input  [3:0] X,
  input  clock,
  input  [3:0] Y,
  input  clear,
  output [19:0] out_5,
  output [19:0] out_6,
  output [19:0] out_7,
  output [19:0] out_8,
  output [19:0] out_9,
  output [19:0] out_10,
  output [19:0] out_11,
  output [19:0] out_12,
  output [19:0] out_13,
  output [19:0] out_14,
  output [19:0] out_15,
  output [19:0] out_16,
  output [19:0] out_17,
  output [19:0] out_18,
  output [19:0] out_19,
  output [19:0] out_20
);

  wire demultiplexer_1_out0, demultiplexer_1_out1, demultiplexer_1_out2, demultiplexer_1_out3,
       demultiplexer_1_out4, demultiplexer_1_out5, demultiplexer_1_out6, demultiplexer_1_out7,
       demultiplexer_1_out8, demultiplexer_1_out9, demultiplexer_1_out10, demultiplexer_1_out11,
       demultiplexer_1_out12, demultiplexer_1_out13, demultiplexer_1_out14, demultiplexer_1_out15;

  Demultiplexer #(.select(4)) demultiplexer_1 (
    .out0(demultiplexer_1_out0), .out1(demultiplexer_1_out1), .out2(demultiplexer_1_out2),
    .out3(demultiplexer_1_out3), .out4(demultiplexer_1_out4), .out5(demultiplexer_1_out5),
    .out6(demultiplexer_1_out6), .out7(demultiplexer_1_out7), .out8(demultiplexer_1_out8),
    .out9(demultiplexer_1_out9), .out10(demultiplexer_1_out10), .out11(demultiplexer_1_out11),
    .out12(demultiplexer_1_out12), .out13(demultiplexer_1_out13), .out14(demultiplexer_1_out14),
    .out15(demultiplexer_1_out15), .in(clock), .sel(Y));  // open: en
  headdispriadok headdispriadok_1 (.clock(demultiplexer_1_out15), .hodn(clock), .X(X), .clear(clear), .riadok(out_5));
  headdispriadok headdispriadok_2 (.clock(demultiplexer_1_out14), .hodn(clock), .X(X), .clear(clear), .riadok(out_6));
  headdispriadok headdispriadok_3 (.clock(demultiplexer_1_out13), .hodn(clock), .X(X), .clear(clear), .riadok(out_7));
  headdispriadok headdispriadok_4 (.clock(demultiplexer_1_out12), .hodn(clock), .X(X), .clear(clear), .riadok(out_8));
  headdispriadok headdispriadok_5 (.clock(demultiplexer_1_out11), .hodn(clock), .X(X), .clear(clear), .riadok(out_9));
  headdispriadok headdispriadok_6 (.clock(demultiplexer_1_out10), .hodn(clock), .X(X), .clear(clear), .riadok(out_10));
  headdispriadok headdispriadok_7 (.clock(demultiplexer_1_out9), .hodn(clock), .X(X), .clear(clear), .riadok(out_11));
  headdispriadok headdispriadok_8 (.clock(demultiplexer_1_out8), .hodn(clock), .X(X), .clear(clear), .riadok(out_12));
  headdispriadok headdispriadok_9 (.clock(demultiplexer_1_out7), .hodn(clock), .X(X), .clear(clear), .riadok(out_13));
  headdispriadok headdispriadok_10 (.clock(demultiplexer_1_out6), .hodn(clock), .X(X), .clear(clear), .riadok(out_14));
  headdispriadok headdispriadok_11 (.clock(demultiplexer_1_out5), .hodn(clock), .X(X), .clear(clear), .riadok(out_15));
  headdispriadok headdispriadok_12 (.clock(demultiplexer_1_out4), .hodn(clock), .X(X), .clear(clear), .riadok(out_16));
  headdispriadok headdispriadok_13 (.clock(demultiplexer_1_out3), .hodn(clock), .X(X), .clear(clear), .riadok(out_17));
  headdispriadok headdispriadok_14 (.clock(demultiplexer_1_out2), .hodn(clock), .X(X), .clear(clear), .riadok(out_18));
  headdispriadok headdispriadok_15 (.clock(demultiplexer_1_out1), .hodn(clock), .X(X), .clear(clear), .riadok(out_19));
  headdispriadok headdispriadok_16 (.clock(demultiplexer_1_out0), .hodn(clock), .X(X), .clear(clear), .riadok(out_20));
endmodule

module _16_20NOAND (
  input  [15:0] _16in,
  input  [19:0] _20in,
  output [15:0] _16out
);

  assign _16out = _16in & ~_20in[15:0];  // AND_Gate and_1, 16 bits wide
endmodule
