// Logisim project alt_snake_3.6.circ as structural Verilog
// 1
module main (
  input  in_1,
  input  in_2
);

  wire and_3_out, and_4_out, and_5_out, and_6_out, and_7_out, and_8_out, and_9_out, and_11_out, and_12_out,
       and_13_out, and_14_out, and_15_out, AppleClear, cdm_8_mark5_1_data_inst, ChangeHead, clock_1_out, clr,
       code, comparator_2_eq, comparator_3_eq, controlled_buffer_2_out, controlled_buffer_6_out,
       counter2_1_out_3, counter2_1_out_4, counter2_1_out_5, counter2_1_out_6, counter2_1_out_7,
       counter2_1_out_8, counter2_1_out_9, counter2_1_out_10, counter2_1_out_11, counter2_1_out_12,
       counter2_1_out_13, counter2_1_out_14, counter2_1_out_15, counter2_1_out_16, counter2_1_out_17,
       counter2_1_out_18, counter_2_carry, counter_4_out_3, counter_4_out_4, counter_4_out_5,
       counter_4_out_6, counter_4_out_7, counter_4_out_8, counter_4_out_9, counter_4_out_10,
       counter_4_out_11, counter_4_out_12, counter_4_out_13, counter_4_out_14, counter_4_out_15,
       counter_4_out_16, counter_4_out_17, counter_4_out_18, CYCLE, d_ff_1_q, data, decoder_3_out1,
       decoder_4_out1, Del_tick, Delete, down, first_tacktk, golod, hz, I_Osel, keyboard_1_avail, left, lose,
       mem, nand_1_out, nor_2_out, nor_3_out, nor_4_out, nor_5_out, not_1_out, not_2_out, not_3_out,
       not_4_out, not_5_out, or_1_out, or_3_out, or_4_out, or_6_out, or_7_out, or_8_out, or_9_out, OVF1,
       OVF2, RAM, rd_wr_prime, resp, right, takt, up, wall, win, \Перекус ;
  wire [1:0] Move;
  wire [3:0] cdm_8_mark5_1_ps, inc_dec_1_r, inc_dec_2_r;
  wire [6:0] \input ;
  wire [7:0] adder_1_out, adr, Apple_coord, cdm_8_mark5_1_data_out, cdm_8_mark5_1_pc, cdm_8_mark5_1_r0,
       cdm_8_mark5_1_r1, cdm_8_mark5_1_r2, cdm_8_mark5_1_r3, cdm_8_mark5_1_sp, controlled_buffer_4_out,
       Cords, counter_3_q, head, I_Odata, negator_1_out, or_2_out, pull_resistor_1_node, register_2_q,
       register_3_q;
  wire [15:0] vivod_matrix_1_out_14, vivod_matrix_1_out_19, vivod_matrix_1_out_24, vivod_matrix_1_out_29,
       vivod_matrix_1_out_34, vivod_matrix_1_out_38, vivod_matrix_1_out_41, vivod_matrix_1_out_46,
       vivod_matrix_1_out_51, vivod_matrix_1_out_56, vivod_matrix_1_out_60, vivod_matrix_1_out_63,
       vivod_matrix_1_out_68, vivod_matrix_1_out_73, vivod_matrix_1_out_78, vivod_matrix_1_out_82;
  wire [16:0] vivod_matrix_1_out_18, vivod_matrix_1_out_23, vivod_matrix_1_out_28, vivod_matrix_1_out_33,
       vivod_matrix_1_out_37, vivod_matrix_1_out_44, vivod_matrix_1_out_49, vivod_matrix_1_out_54,
       vivod_matrix_1_out_59, vivod_matrix_1_out_66, vivod_matrix_1_out_71, vivod_matrix_1_out_76,
       vivod_matrix_1_out_81, vivod_matrix_1_out_86, vivod_matrix_1_out_89, vivod_matrix_1_out_92;
  wire [17:0] vivod_matrix_1_out_17, vivod_matrix_1_out_22, vivod_matrix_1_out_27, vivod_matrix_1_out_32,
       vivod_matrix_1_out_36, vivod_matrix_1_out_43, vivod_matrix_1_out_48, vivod_matrix_1_out_53,
       vivod_matrix_1_out_58, vivod_matrix_1_out_65, vivod_matrix_1_out_70, vivod_matrix_1_out_75,
       vivod_matrix_1_out_80, vivod_matrix_1_out_85, vivod_matrix_1_out_88, vivod_matrix_1_out_91;
  wire [18:0] vivod_matrix_1_out_16, vivod_matrix_1_out_21, vivod_matrix_1_out_26, vivod_matrix_1_out_31,
       vivod_matrix_1_out_40, vivod_matrix_1_out_45, vivod_matrix_1_out_50, vivod_matrix_1_out_55,
       vivod_matrix_1_out_62, vivod_matrix_1_out_67, vivod_matrix_1_out_72, vivod_matrix_1_out_77,
       vivod_matrix_1_out_84, vivod_matrix_1_out_87, vivod_matrix_1_out_90, vivod_matrix_1_out_93;
  wire [19:0] vivod_matrix_1_out_15, vivod_matrix_1_out_20, vivod_matrix_1_out_25, vivod_matrix_1_out_30,
       vivod_matrix_1_out_35, vivod_matrix_1_out_39, vivod_matrix_1_out_42, vivod_matrix_1_out_47,
       vivod_matrix_1_out_52, vivod_matrix_1_out_57, vivod_matrix_1_out_61, vivod_matrix_1_out_64,
       vivod_matrix_1_out_69, vivod_matrix_1_out_74, vivod_matrix_1_out_79, vivod_matrix_1_out_83;
  wire [31:0] counter_1_q;

  Pull_Resistor pull_resistor_1 (.node(pull_resistor_1_node));
  assign pull_resistor_1_node = first_tacktk ? 8'h88 : 8'bz;  // Controlled_Buffer controlled_buffer_1
  not not_1 (not_1_out, in_1);
  Clock clock_1 (.out(clock_1_out));
  assign controlled_buffer_2_out = not_1_out ? clock_1_out : 1'bz;  // Controlled_Buffer controlled_buffer_2
  or or_1 (or_1_out, lose, win);
  Register register_1 (.D(or_2_out), .Q(head), .clk(CYCLE), .clr(clr));  // open: en
  assign or_2_out = pull_resistor_1_node | {inc_dec_1_r, inc_dec_2_r};  // OR_Gate or_2, 8 bits wide
  // Probe on head
  golod golod_1 (.stop_golod(in_2), .clock(CYCLE), .clr(clr), .hz(hz), .golod(golod));
  and and_1 (I_Osel, not_2_out, takt, data);
  Pull_Resistor pull_resistor_2 (.node(controlled_buffer_2_out));
  Multiplexer multiplexer_1 (.in0(controlled_buffer_2_out), .in1(1'b0), .out(takt), .sel(d_ff_1_q));  // open: en
  D_Flip_Flop d_ff_1 (.Q(d_ff_1_q), .preset(or_1_out), .reset(clr));  // open: clk, D, Qn, en
  or or_3 (or_3_out, left, right);
  or or_4 (or_4_out, clr, resp, hz);
  Negator negator_1 (.in(head), .out(negator_1_out));
  inc_dec inc_dec_1 (.X(head[7:4]), .on_off(or_3_out), .inc_dec(right), .R(inc_dec_1_r), .OFL(OVF1));
  inc_dec inc_dec_2 (.X(head[3:0]), .on_off(or_6_out), .inc_dec(up), .R(inc_dec_2_r), .OFL(OVF2));
  // Probe on Apple_coord
  Random #(.seed(8)) random_1 (.clk(or_4_out), .out(Apple_coord));  // open: next, clr
  Adder adder_1 (.a(Apple_coord), .b(negator_1_out), .out(adder_1_out));  // open: cin, cout
  // Probe on cdm_8_mark5_1_r3
  // Probe on cdm_8_mark5_1_r2
  // Probe on cdm_8_mark5_1_r1
  // Probe on cdm_8_mark5_1_r0
  not not_2 (not_2_out, nand_1_out);
  nand nand_1 (nand_1_out, adr[4], adr[5], adr[6], adr[7]);
  and and_2 (RAM, nand_1_out, data);
  or or_5 (lose, golod, wall, \Перекус );
  or or_6 (or_6_out, up, down);
  nor nor_1 (hz, adder_1_out[0], adder_1_out[1], adder_1_out[2], adder_1_out[3], adder_1_out[4], adder_1_out[5], adder_1_out[6], adder_1_out[7]);
  // Probe on cdm_8_mark5_1_sp
  // Probe on cdm_8_mark5_1_pc
  // Probe on cdm_8_mark5_1_ps
  CdM_8_mark5 cdm_8_mark5_1 (
    .clock(takt), .addr(adr), .mem_read(rd_wr_prime), .mem_cycle(mem), .data_inst(cdm_8_mark5_1_data_inst),
    .data_out(cdm_8_mark5_1_data_out), .data_in(controlled_buffer_4_out), .r0(cdm_8_mark5_1_r0),
    .r1(cdm_8_mark5_1_r1), .r2(cdm_8_mark5_1_r2), .r3(cdm_8_mark5_1_r3), .PC(cdm_8_mark5_1_pc),
    .SP(cdm_8_mark5_1_sp), .PS(cdm_8_mark5_1_ps));
  Counter #(.width(32), .max('hffffffff)) counter_1 (
    .Q(counter_1_q), .clk(CYCLE), .clr(clr));  // open: load, D, count, carry
  Decoder #(.disabled(0)) decoder_1 (.out0(code), .out1(data), .sel(cdm_8_mark5_1_data_inst), .en(mem));
  not not_3 (not_3_out, rd_wr_prime);
  assign I_Odata = not_3_out ? cdm_8_mark5_1_data_out : 8'bz;  // Controlled_Buffer controlled_buffer_3
  assign controlled_buffer_4_out = rd_wr_prime ? I_Odata : 8'bz;  // Controlled_Buffer controlled_buffer_4
  Comparator #(.width(32), .mode("unsigned")) comparator_1 (
    .a({32{1'b0}}), .b(counter_1_q), .eq(first_tacktk));  // open: gt, lt
  Pull_Resistor pull_resistor_3 (.node(adr[0]));
  Pull_Resistor pull_resistor_4 (.node(adr[1]));
  Pull_Resistor pull_resistor_5 (.node(adr[2]));
  Pull_Resistor pull_resistor_6 (.node(adr[3]));
  Pull_Resistor pull_resistor_7 (.node(adr[4]));
  Pull_Resistor pull_resistor_8 (.node(adr[5]));
  Pull_Resistor pull_resistor_9 (.node(adr[6]));
  Pull_Resistor pull_resistor_10 (.node(adr[7]));
  Counter #(.max('ha)) counter_2 (.carry(counter_2_carry), .clk(hz), .clr(clr));  // open: load, D, count, Q
  Register register_2 (.D(Cords), .Q(register_2_q), .clk(takt));  // open: en, clr
  vivod_matrix vivod_matrix_1 (
    .snake_coord(Cords), .apple_coord(Apple_coord), .paus(in_1), .win(win), .lose(lose), .takt(takt),
    .clr(clr), .vivod(Del_tick), .cycle(CYCLE), .apple(hz), .out_16(vivod_matrix_1_out_16),
    .out_17(vivod_matrix_1_out_17), .out_18(vivod_matrix_1_out_18), .out_14(vivod_matrix_1_out_14),
    .out_21(vivod_matrix_1_out_21), .out_22(vivod_matrix_1_out_22), .out_23(vivod_matrix_1_out_23),
    .out_19(vivod_matrix_1_out_19), .out_26(vivod_matrix_1_out_26), .out_27(vivod_matrix_1_out_27),
    .out_28(vivod_matrix_1_out_28), .out_24(vivod_matrix_1_out_24), .out_31(vivod_matrix_1_out_31),
    .out_32(vivod_matrix_1_out_32), .out_33(vivod_matrix_1_out_33), .out_29(vivod_matrix_1_out_29),
    .out_36(vivod_matrix_1_out_36), .out_37(vivod_matrix_1_out_37), .out_34(vivod_matrix_1_out_34),
    .out_40(vivod_matrix_1_out_40), .out_43(vivod_matrix_1_out_43), .out_44(vivod_matrix_1_out_44),
    .out_38(vivod_matrix_1_out_38), .out_45(vivod_matrix_1_out_45), .out_48(vivod_matrix_1_out_48),
    .out_49(vivod_matrix_1_out_49), .out_41(vivod_matrix_1_out_41), .out_50(vivod_matrix_1_out_50),
    .out_53(vivod_matrix_1_out_53), .out_54(vivod_matrix_1_out_54), .out_46(vivod_matrix_1_out_46),
    .out_55(vivod_matrix_1_out_55), .out_58(vivod_matrix_1_out_58), .out_59(vivod_matrix_1_out_59),
    .out_51(vivod_matrix_1_out_51), .out_62(vivod_matrix_1_out_62), .out_65(vivod_matrix_1_out_65),
    .out_66(vivod_matrix_1_out_66), .out_56(vivod_matrix_1_out_56), .out_67(vivod_matrix_1_out_67),
    .out_70(vivod_matrix_1_out_70), .out_71(vivod_matrix_1_out_71), .out_60(vivod_matrix_1_out_60),
    .out_72(vivod_matrix_1_out_72), .out_75(vivod_matrix_1_out_75), .out_76(vivod_matrix_1_out_76),
    .out_63(vivod_matrix_1_out_63), .out_77(vivod_matrix_1_out_77), .out_80(vivod_matrix_1_out_80),
    .out_81(vivod_matrix_1_out_81), .out_68(vivod_matrix_1_out_68), .out_84(vivod_matrix_1_out_84),
    .out_85(vivod_matrix_1_out_85), .out_86(vivod_matrix_1_out_86), .out_73(vivod_matrix_1_out_73),
    .out_87(vivod_matrix_1_out_87), .out_88(vivod_matrix_1_out_88), .out_89(vivod_matrix_1_out_89),
    .out_78(vivod_matrix_1_out_78), .out_90(vivod_matrix_1_out_90), .out_91(vivod_matrix_1_out_91),
    .out_92(vivod_matrix_1_out_92), .out_82(vivod_matrix_1_out_82), .out_93(vivod_matrix_1_out_93),
    .head_coord(head), .Delete(Delete), .out_15(vivod_matrix_1_out_15), .out_20(vivod_matrix_1_out_20),
    .out_25(vivod_matrix_1_out_25), .out_30(vivod_matrix_1_out_30), .out_35(vivod_matrix_1_out_35),
    .out_39(vivod_matrix_1_out_39), .out_42(vivod_matrix_1_out_42), .out_47(vivod_matrix_1_out_47),
    .out_52(vivod_matrix_1_out_52), .out_57(vivod_matrix_1_out_57), .out_61(vivod_matrix_1_out_61),
    .out_64(vivod_matrix_1_out_64), .out_69(vivod_matrix_1_out_69), .out_74(vivod_matrix_1_out_74),
    .out_79(vivod_matrix_1_out_79), .out_83(vivod_matrix_1_out_83), .resp(resp));
  D_Flip_Flop d_ff_2 (.Q(win), .preset(counter_2_carry), .reset(clr));  // open: clk, D, Qn, en
  Comparator comparator_2 (.a(head), .b(register_2_q), .eq(comparator_2_eq));  // open: gt, lt
  ROM rom_1 (.addr(adr), .data(I_Odata), .sel(code));
  RAM ram_1 (.addr(adr), .data(I_Odata), .sel(RAM), .clk(takt), .ld(rd_wr_prime));  // open: clr
  assign I_Odata = not_4_out ? {{6{1'b0}}, Move} : 8'bz;  // Controlled_Buffer controlled_buffer_5
  Counter counter_3 (.Q(counter_3_q), .clk(comparator_2_eq), .clr(CYCLE));  // open: load, D, count, carry
  and and_3 (and_3_out, I_Osel, adr[0], adr[1], ~adr[2], ~adr[3]);  // AND_Gate
  not not_4 (not_4_out, not_5_out);
  not not_5 (not_5_out, ChangeHead);
  D_Flip_Flop d_ff_3 (.Q(\Перекус ), .preset(comparator_3_eq), .reset(clr));  // open: clk, D, Qn, en
  Comparator comparator_3 (.a(counter_3_q), .b(8'h2), .eq(comparator_3_eq));  // open: gt, lt
  Decoder #(.disabled(0)) decoder_2 (.out1(ChangeHead), .sel(rd_wr_prime), .en(and_3_out));  // open: out0
  _7_Segment_Display u_7_segment_display_1 (
    .g(counter_4_out_3), .f(counter_4_out_4), .a(counter_4_out_5), .b(counter_4_out_6), .e(counter_4_out_11),
    .d(counter_4_out_12), .c(counter_4_out_13), .dp(counter_4_out_14));
  counter counter_4 (
    .clock(hz), .clear(clr), .out_11(counter_4_out_11), .out_12(counter_4_out_12), .out_13(counter_4_out_13),
    .out_14(counter_4_out_14), .out_15(counter_4_out_15), .out_16(counter_4_out_16),
    .out_17(counter_4_out_17), .out_18(counter_4_out_18), .out_3(counter_4_out_3), .out_4(counter_4_out_4),
    .out_5(counter_4_out_5), .out_6(counter_4_out_6), .out_7(counter_4_out_7), .out_8(counter_4_out_8),
    .out_9(counter_4_out_9), .out_10(counter_4_out_10));
  DotMatrix #(.inputtype("row"), .matrixcols(17), .matrixrows(16)) dotmatrix_1 (
    .row0(vivod_matrix_1_out_18), .row1(vivod_matrix_1_out_23), .row2(vivod_matrix_1_out_28),
    .row3(vivod_matrix_1_out_33), .row4(vivod_matrix_1_out_37), .row5(vivod_matrix_1_out_44),
    .row6(vivod_matrix_1_out_49), .row7(vivod_matrix_1_out_54), .row8(vivod_matrix_1_out_59),
    .row9(vivod_matrix_1_out_66), .row10(vivod_matrix_1_out_71), .row11(vivod_matrix_1_out_76),
    .row12(vivod_matrix_1_out_81), .row13(vivod_matrix_1_out_86), .row14(vivod_matrix_1_out_89),
    .row15(vivod_matrix_1_out_92));
  DotMatrix #(.inputtype("row"), .matrixcols(19), .matrixrows(16)) dotmatrix_2 (
    .row0(vivod_matrix_1_out_16), .row1(vivod_matrix_1_out_21), .row2(vivod_matrix_1_out_26),
    .row3(vivod_matrix_1_out_31), .row4(vivod_matrix_1_out_40), .row5(vivod_matrix_1_out_45),
    .row6(vivod_matrix_1_out_50), .row7(vivod_matrix_1_out_55), .row8(vivod_matrix_1_out_62),
    .row9(vivod_matrix_1_out_67), .row10(vivod_matrix_1_out_72), .row11(vivod_matrix_1_out_77),
    .row12(vivod_matrix_1_out_84), .row13(vivod_matrix_1_out_87), .row14(vivod_matrix_1_out_90),
    .row15(vivod_matrix_1_out_93));
  DotMatrix #(.inputtype("row"), .matrixcols(18), .matrixrows(16)) dotmatrix_3 (
    .row0(vivod_matrix_1_out_17), .row1(vivod_matrix_1_out_22), .row2(vivod_matrix_1_out_27),
    .row3(vivod_matrix_1_out_32), .row4(vivod_matrix_1_out_36), .row5(vivod_matrix_1_out_43),
    .row6(vivod_matrix_1_out_48), .row7(vivod_matrix_1_out_53), .row8(vivod_matrix_1_out_58),
    .row9(vivod_matrix_1_out_65), .row10(vivod_matrix_1_out_70), .row11(vivod_matrix_1_out_75),
    .row12(vivod_matrix_1_out_80), .row13(vivod_matrix_1_out_85), .row14(vivod_matrix_1_out_88),
    .row15(vivod_matrix_1_out_91));
  DotMatrix #(.inputtype("row"), .matrixcols(20), .matrixrows(16)) dotmatrix_4 (
    .row0(vivod_matrix_1_out_15), .row1(vivod_matrix_1_out_20), .row2(vivod_matrix_1_out_25),
    .row3(vivod_matrix_1_out_30), .row4(vivod_matrix_1_out_35), .row5(vivod_matrix_1_out_39),
    .row6(vivod_matrix_1_out_42), .row7(vivod_matrix_1_out_47), .row8(vivod_matrix_1_out_52),
    .row9(vivod_matrix_1_out_57), .row10(vivod_matrix_1_out_61), .row11(vivod_matrix_1_out_64),
    .row12(vivod_matrix_1_out_69), .row13(vivod_matrix_1_out_74), .row14(vivod_matrix_1_out_79),
    .row15(vivod_matrix_1_out_83));
  DotMatrix #(.matrixcols(4), .matrixrows(17)) dotmatrix_5 (
    .col0(17'haaaa), .col1(17'haaaa), .col2(17'haaaa), .col3(17'haaaa));
  assign controlled_buffer_6_out = keyboard_1_avail ? takt : 1'bz;  // Controlled_Buffer controlled_buffer_6
  and and_4 (and_4_out, CYCLE, in_2);
  _7_Segment_Display u_7_segment_display_2 (
    .g(counter_4_out_7), .f(counter_4_out_8), .a(counter_4_out_9), .b(counter_4_out_10),
    .e(counter_4_out_15), .d(counter_4_out_16), .c(counter_4_out_17), .dp(counter_4_out_18));
  DotMatrix #(.inputtype("row"), .matrixcols(16), .matrixrows(16)) dotmatrix_6 (
    .row0(vivod_matrix_1_out_14), .row1(vivod_matrix_1_out_19), .row2(vivod_matrix_1_out_24),
    .row3(vivod_matrix_1_out_29), .row4(vivod_matrix_1_out_34), .row5(vivod_matrix_1_out_38),
    .row6(vivod_matrix_1_out_41), .row7(vivod_matrix_1_out_46), .row8(vivod_matrix_1_out_51),
    .row9(vivod_matrix_1_out_56), .row10(vivod_matrix_1_out_60), .row11(vivod_matrix_1_out_63),
    .row12(vivod_matrix_1_out_68), .row13(vivod_matrix_1_out_73), .row14(vivod_matrix_1_out_78),
    .row15(vivod_matrix_1_out_82));
  Keyboard keyboard_1 (.clk(controlled_buffer_6_out), .clr(clr), .avail(keyboard_1_avail), .data(\input ));  // open: re
  assign I_Odata = decoder_3_out1 ? head : 8'bz;  // Controlled_Buffer controlled_buffer_7
  _7_Segment_Display u_7_segment_display_3 (
    .g(counter2_1_out_3), .f(counter2_1_out_4), .a(counter2_1_out_5), .b(counter2_1_out_6),
    .e(counter2_1_out_11), .d(counter2_1_out_12), .c(counter2_1_out_13), .dp(counter2_1_out_14));
  counter2 counter2_1 (
    .clock(and_4_out), .clear(or_7_out), .out_11(counter2_1_out_11), .out_12(counter2_1_out_12),
    .out_13(counter2_1_out_13), .out_14(counter2_1_out_14), .out_15(counter2_1_out_15),
    .out_16(counter2_1_out_16), .out_17(counter2_1_out_17), .out_18(counter2_1_out_18),
    .out_3(counter2_1_out_3), .out_4(counter2_1_out_4), .out_5(counter2_1_out_5), .out_6(counter2_1_out_6),
    .out_7(counter2_1_out_7), .out_8(counter2_1_out_8), .out_9(counter2_1_out_9), .out_10(counter2_1_out_10));
  _7_Segment_Display u_7_segment_display_4 (
    .g(counter2_1_out_7), .f(counter2_1_out_8), .a(counter2_1_out_9), .b(counter2_1_out_10),
    .e(counter2_1_out_15), .d(counter2_1_out_16), .c(counter2_1_out_17), .dp(counter2_1_out_18));
  movement movement_1 (
    .\input (\input ), .Clear(clr), .Move(Move), .up(up), .right(right), .down(down), .left(left),
    .Clk(ChangeHead));
  and and_5 (and_5_out, I_Osel, adr[0], ~adr[1], adr[2], ~adr[3]);  // AND_Gate
  Decoder #(.disabled(0)) decoder_3 (.out1(decoder_3_out1), .sel(rd_wr_prime), .en(and_5_out));  // open: out0
  or or_7 (or_7_out, clr, hz);
  Button button_1 (.out(clr));
  and and_6 (and_6_out, head[4], head[5], head[6], head[7]);
  and and_7 (and_7_out, head[0], head[1], head[2], head[3]);
  nor nor_2 (nor_2_out, head[4], head[5], head[6], head[7]);
  nor nor_3 (nor_3_out, head[0], head[1], head[2], head[3]);
  and and_8 (and_8_out, Apple_coord[0], Apple_coord[1], Apple_coord[2], Apple_coord[3]);
  and and_9 (and_9_out, Apple_coord[4], Apple_coord[5], Apple_coord[6], Apple_coord[7]);
  nor nor_4 (nor_4_out, Apple_coord[0], Apple_coord[1], Apple_coord[2], Apple_coord[3]);
  nor nor_5 (nor_5_out, Apple_coord[4], Apple_coord[5], Apple_coord[6], Apple_coord[7]);
  assign I_Odata = decoder_4_out1 ? register_3_q : 8'bz;  // Controlled_Buffer controlled_buffer_8
  Register register_3 (.D({{7{1'b0}}, hz}), .Q(register_3_q), .clk(hz), .clr(AppleClear));  // open: en
  Counter #(.width(1), .max('h1), .ongoal("stay")) counter_5 (
    .carry(wall), .clk(or_8_out), .clr(clr));  // open: load, D, count, Q
  or or_8 (or_8_out, and_6_out, and_7_out, nor_2_out, nor_3_out);
  or or_9 (or_9_out, and_8_out, and_9_out, nor_4_out, nor_5_out);
  and and_10 (resp, or_9_out, takt);
  and and_11 (and_11_out, I_Osel, ~adr[0], adr[1], adr[2], ~adr[3]);  // AND_Gate
  Decoder #(.disabled(0)) decoder_4 (.out1(decoder_4_out1), .sel(rd_wr_prime), .en(and_11_out));  // open: out0
  Pull_Resistor pull_resistor_11 (.node(AppleClear));
  assign AppleClear = and_12_out ? 1'b1 : 1'bz;  // Controlled_Buffer controlled_buffer_9
  and and_12 (and_12_out, adr[0], adr[1], adr[2], ~adr[3], adr[4], adr[5], adr[6], adr[7]);  // AND_Gate
  and and_13 (and_13_out, adr[0], ~adr[1], ~adr[2], ~adr[3], adr[4], adr[5], ~adr[6], adr[7]);  // AND_Gate
  assign Cords = and_13_out ? I_Odata : 8'bz;  // Controlled_Buffer controlled_buffer_10
  and and_14 (and_14_out, ~adr[0], ~adr[1], ~adr[2], adr[3], adr[4], adr[5], adr[6], adr[7]);  // AND_Gate
  Register #(.width(1)) register_4 (.D(Del_tick), .Q(Delete), .clk(takt), .clr(CYCLE));  // open: en
  assign Del_tick = and_15_out ? 1'b1 : 1'bz;  // Controlled_Buffer controlled_buffer_11
  and and_15 (and_15_out, adr[0], adr[1], adr[2], adr[3], adr[4], adr[5], adr[6], adr[7]);
  Pull_Resistor pull_resistor_12 (.node(CYCLE));
  assign CYCLE = and_14_out ? 1'b1 : 1'bz;  // Controlled_Buffer controlled_buffer_12

  // Other names for the same wires on the sheet: I_Oadr[3:0] = adr[3:0]; x[3:0] = head[3:0]; paus = in_1;
  //   stop_golod = in_2; y[3:0] = head[7:4]

  // Notes on the sheet:
  //   contents of rom_1 (hex, n*v repeats v):
  //   cd f0 d1 3 c1 d1 b5 d0 87 a4 d0 f8 b0 d0 f5 b0 d1 b1 a4 d0 f3 b0 d1 b4 b6 a4 78 e1 24 cb 0 bd 8d ad
  //   ee 2c 6*20 8c c0 d0 f6 b0 0 e1 79 d0 ef b1 89 a1 d0 3f 41 e1 4f c8 0 d1 f0 31 85 c6 8c 5 e0 4e b3 a2
  //   8c e 89 ee 45 a2 d3 ef bf d2 c0 d0 40 4e e1 5d d3 1 ee 6e 78 e1 64 d3 10 ee 6e 20 78 e1 6c d3 ff ee
  //   6e d3 f0 d0 b5 b1 d2 ff ba d2 b1 a9 17 a3 d0 f7 b0 d0 f8 b0 ee d
  //   Получение направления
  //   Количество яблочек
  //   Получение координат головы
  //   Голод
  //   1 - пауза 0 играем
  //   1 - есть 0 - нет голода
  //   Бит съеденного яблока
  //   Координаты змейки
  //   Бит очищения яблочка
  //   Бит удаления
  //   Бит конца цикла процессора
endmodule

module _16_bit_AND (
  input  [15:0] \input ,
  input  switch,
  output [16:0] \output 
);

  assign \output [15:0] = \input  & {16{switch}};  // AND_Gate and_1, 16 bits wide

  assign \output [16] = 1'b0;
endmodule

module inc_dec (
  input  [3:0] X,
  input  on_off,
  input  inc_dec,
  output [3:0] R,
  output OFL
);

  wire and_2_out, and_3_out, and_4_out, and_5_out, nor_1_out, nor_2_out;
  wire [3:0] and_1_out, xor_1_out, xor_2_out, xor_3_out;
  wire [3:3] decoder_1_out0, decoder_1_out1;

  Decoder #(.enable("false")) decoder_1 (.out0(decoder_1_out0[3]), .out1(decoder_1_out1[3]), .sel(inc_dec));
  assign xor_1_out = {4{decoder_1_out0[3]}} ^ X;  // XOR_Gate xor_1, 4 bits wide
  assign xor_2_out = {4{decoder_1_out1[3]}} ^ xor_3_out;  // XOR_Gate xor_2, 4 bits wide
  assign and_1_out = xor_1_out & xor_2_out;  // AND_Gate and_1, 4 bits wide
  assign xor_3_out = X ^ {and_1_out[2:0], 1'b1};  // XOR_Gate xor_3, 4 bits wide
  Multiplexer #(.width(4), .enable("false")) multiplexer_1 (.in0(X), .in1(xor_3_out), .out(R), .sel(on_off));
  and and_2 (and_2_out, X[0], X[1], X[2], X[3]);
  nor nor_1 (nor_1_out, R[0], R[1], R[2], R[3]);
  and and_3 (and_3_out, R[0], R[1], R[2], R[3]);
  nor nor_2 (nor_2_out, X[0], X[1], X[2], X[3]);
  and and_4 (and_4_out, and_2_out, nor_1_out);
  and and_5 (and_5_out, and_3_out, nor_2_out);
  or or_1 (OFL, and_4_out, and_5_out);

  // Other names for the same wires on the sheet: O[3:0] = R
endmodule

module granca_detection (
  input  Up,
  input  Down,
  input  [7:0] in_3,
  input  Left,
  input  Right,
  output out_6
);

  wire and_1_out, and_2_out, nor_1_out, nor_2_out;

  Pull_Resistor pull_resistor_1 (.node(Up));
  Pull_Resistor pull_resistor_2 (.node(Down));
  Pull_Resistor pull_resistor_3 (.node(Left));
  Pull_Resistor pull_resistor_4 (.node(Right));
  and and_1 (and_1_out, Up, in_3[3], in_3[2], in_3[1], in_3[0]);
  and and_2 (and_2_out, in_3[7], in_3[6], in_3[5], in_3[4], Right);
  nor nor_1 (nor_1_out, ~Down, in_3[0], in_3[1], in_3[2], in_3[3]);  // NOR_Gate
  nor nor_2 (nor_2_out, in_3[4], in_3[5], in_3[6], in_3[7], ~Left);  // NOR_Gate
  or or_1 (out_6, and_1_out, nor_1_out, nor_2_out, and_2_out);
endmodule

module movement (
  input  Clk,
  input  [6:0] \input ,
  input  Clear,
  output [1:0] Move,
  output up,
  output right,
  output down,
  output left
);

  wire comparator_1_eq, comparator_2_eq, comparator_3_eq, comparator_4_eq, not_1_out, not_2_out, not_3_out,
       not_4_out, not_5_out, not_6_out, not_7_out, not_8_out, not_9_out, not_10_out, not_11_out, not_12_out,
       not_13_out, not_14_out, not_15_out, not_16_out, not_17_out, not_18_out, not_19_out, not_20_out,
       not_21_out, not_23_out, not_24_out, or_1_out, or_2_out, or_5_out, takt;
  wire [1:0] adder_1_out, choose, demultiplexer_1_out1, demultiplexer_1_out3, multiplexer_1_out, or_3_out,
       register_1_q, subtractor_1_out;

  Register #(.width(2)) register_1 (.D(multiplexer_1_out), .Q(register_1_q), .clk(takt), .clr(Clear));  // open: en
  Multiplexer #(.select(2), .width(2), .enable("false")) multiplexer_1 (
    .in1(adder_1_out), .in3(subtractor_1_out), .out(multiplexer_1_out), .sel(choose));  // open: in0, in2
  Comparator #(.width(7)) comparator_1 (.a(\input ), .b(7'b1100100), .eq(comparator_1_eq));  // open: gt, lt
  Comparator #(.width(7)) comparator_2 (.a(\input ), .b(7'b0110010), .eq(comparator_2_eq));  // open: gt, lt
  Comparator #(.width(7)) comparator_3 (.a(\input ), .b(7'b1100001), .eq(comparator_3_eq));  // open: gt, lt
  Comparator #(.width(7)) comparator_4 (.a(\input ), .b(7'b1000100), .eq(comparator_4_eq));  // open: gt, lt
  Demultiplexer #(.select(2), .width(2), .enable("false")) demultiplexer_1 (
    .out1(demultiplexer_1_out1), .out3(demultiplexer_1_out3), .in(register_1_q), .sel(choose));  // open: out0, out2
  or or_1 (or_1_out, comparator_1_eq, comparator_2_eq);
  or or_2 (or_2_out, comparator_3_eq, comparator_4_eq);
  Adder #(.width(2)) adder_1 (.a(2'b01), .b(demultiplexer_1_out1), .out(adder_1_out));  // open: cin, cout
  Subtractor #(.width(2)) subtractor_1 (
    .a(demultiplexer_1_out3), .b(2'b01), .out(subtractor_1_out));  // open: bin, bout
  Register #(.width(2)) register_2 (.D(register_1_q), .Q(Move), .clk(Clk), .clr(Clear));  // open: en
  or or_3 (or_3_out[0], or_1_out, or_2_out);
  or or_4 (or_3_out[1], or_2_out, or_2_out);
  or or_5 (or_5_out, or_1_out, or_2_out);
  not not_1 (not_1_out, or_5_out);
  not not_2 (not_2_out, not_11_out);
  not not_3 (not_3_out, not_2_out);
  not not_4 (not_4_out, not_3_out);
  Demultiplexer #(.select(2), .enable("false")) demultiplexer_2 (
    .out0(up), .out1(right), .out2(down), .out3(left), .in(1'b1), .sel(Move));
  Register #(.width(2)) register_3 (.D(or_3_out), .Q(choose), .clk(or_5_out), .clr(Clear));  // open: en
  not not_5 (not_5_out, not_7_out);
  not not_6 (not_6_out, not_8_out);
  not not_7 (not_7_out, not_1_out);
  not not_8 (not_8_out, not_5_out);
  not not_9 (not_9_out, not_12_out);
  not not_10 (not_10_out, not_20_out);
  not not_11 (not_11_out, not_9_out);
  not not_12 (not_12_out, not_10_out);
  not not_13 (not_13_out, not_14_out);
  not not_14 (not_14_out, not_4_out);
  not not_15 (not_15_out, not_16_out);
  not not_16 (not_16_out, not_13_out);
  not not_17 (not_17_out, not_6_out);
  not not_18 (not_18_out, not_19_out);
  not not_19 (not_19_out, not_17_out);
  not not_20 (not_20_out, not_21_out);
  not not_21 (not_21_out, not_18_out);
  not not_22 (takt, not_24_out);
  not not_23 (not_23_out, not_15_out);
  not not_24 (not_24_out, not_23_out);

  // Other names for the same wires on the sheet: clr = Clear

  // Notes on the sheet:
  //   отвечает за формирование направления (01 - right  11 - left)
  //   суммируем по модулю 4, для того чтобы зациклить направления
endmodule

module pseudo_reg (
  input  [3:0] in_1,
  input  [3:0] in_2,
  output [16:0] out_3,
  output [16:0] out_4,
  output [16:0] out_5,
  output [16:0] out_6,
  output [16:0] out_7,
  output [16:0] out_8,
  output [16:0] out_9,
  output [16:0] out_10,
  output [16:0] out_11,
  output [16:0] out_12,
  output [16:0] out_13,
  output [16:0] out_14,
  output [16:0] out_15,
  output [16:0] out_16,
  output [16:0] out_17,
  output [16:0] out_18
);

  wire decoder_2_out0, decoder_2_out1, decoder_2_out2, decoder_2_out3, decoder_2_out4, decoder_2_out5,
       decoder_2_out6, decoder_2_out7, decoder_2_out8, decoder_2_out9, decoder_2_out10, decoder_2_out11,
       decoder_2_out12, decoder_2_out13, decoder_2_out14, decoder_2_out15;
  wire [15:0] decoder_1_out0;

  Decoder #(.select(4), .disabled(0), .enable("false")) decoder_1 (
    .out0(decoder_1_out0[0]), .out1(decoder_1_out0[1]), .out2(decoder_1_out0[2]), .out3(decoder_1_out0[3]),
    .out4(decoder_1_out0[4]), .out5(decoder_1_out0[5]), .out6(decoder_1_out0[6]), .out7(decoder_1_out0[7]),
    .out8(decoder_1_out0[8]), .out9(decoder_1_out0[9]), .out10(decoder_1_out0[10]),
    .out11(decoder_1_out0[11]), .out12(decoder_1_out0[12]), .out13(decoder_1_out0[13]),
    .out14(decoder_1_out0[14]), .out15(decoder_1_out0[15]), .sel(in_1));
  _16_bit_AND u_16_bit_and_1 (.\input (decoder_1_out0), .switch(decoder_2_out0), .\output (out_11));
  _16_bit_AND u_16_bit_and_2 (.\input (decoder_1_out0), .switch(decoder_2_out1), .\output (out_3));
  _16_bit_AND u_16_bit_and_3 (.\input (decoder_1_out0), .switch(decoder_2_out3), .\output (out_4));
  _16_bit_AND u_16_bit_and_4 (.\input (decoder_1_out0), .switch(decoder_2_out2), .\output (out_12));
  Decoder #(.select(4), .disabled(0), .enable("false")) decoder_2 (
    .out0(decoder_2_out0), .out1(decoder_2_out1), .out2(decoder_2_out2), .out3(decoder_2_out3),
    .out4(decoder_2_out4), .out5(decoder_2_out5), .out6(decoder_2_out6), .out7(decoder_2_out7),
    .out8(decoder_2_out8), .out9(decoder_2_out9), .out10(decoder_2_out10), .out11(decoder_2_out11),
    .out12(decoder_2_out12), .out13(decoder_2_out13), .out14(decoder_2_out14), .out15(decoder_2_out15),
    .sel(in_2));
  _16_bit_AND u_16_bit_and_5 (.\input (decoder_1_out0), .switch(decoder_2_out4), .\output (out_13));
  _16_bit_AND u_16_bit_and_6 (.\input (decoder_1_out0), .switch(decoder_2_out5), .\output (out_5));
  _16_bit_AND u_16_bit_and_7 (.\input (decoder_1_out0), .switch(decoder_2_out7), .\output (out_6));
  _16_bit_AND u_16_bit_and_8 (.\input (decoder_1_out0), .switch(decoder_2_out6), .\output (out_14));
  _16_bit_AND u_16_bit_and_9 (.\input (decoder_1_out0), .switch(decoder_2_out8), .\output (out_15));
  _16_bit_AND u_16_bit_and_10 (.\input (decoder_1_out0), .switch(decoder_2_out9), .\output (out_7));
  _16_bit_AND u_16_bit_and_11 (.\input (decoder_1_out0), .switch(decoder_2_out11), .\output (out_8));
  _16_bit_AND u_16_bit_and_12 (.\input (decoder_1_out0), .switch(decoder_2_out10), .\output (out_16));
  _16_bit_AND u_16_bit_and_13 (.\input (decoder_1_out0), .switch(decoder_2_out13), .\output (out_9));
  _16_bit_AND u_16_bit_and_14 (.\input (decoder_1_out0), .switch(decoder_2_out12), .\output (out_17));
  _16_bit_AND u_16_bit_and_15 (.\input (decoder_1_out0), .switch(decoder_2_out14), .\output (out_18));
  _16_bit_AND u_16_bit_and_16 (.\input (decoder_1_out0), .switch(decoder_2_out15), .\output (out_10));
endmodule

module golod (
  input  stop_golod,
  input  clock,
  input  clr,
  input  hz,
  output golod
);

  wire and_1_out, comparator_1_eq, comparator_1_gt, comparator_2_gt, or_1_out, or_2_out;
  wire [9:0] counter_1_q, counter_2_q;

  and and_1 (and_1_out, clock, stop_golod);
  Counter #(.width(10), .max('h3ff)) counter_1 (
    .Q(counter_1_q), .clk(and_1_out), .clr(or_1_out));  // open: load, D, count, carry
  or or_1 (or_1_out, clr, hz);
  Comparator #(.width(10), .mode("unsigned")) comparator_1 (
    .a(counter_1_q), .b(10'h14), .gt(comparator_1_gt), .eq(comparator_1_eq));  // open: lt
  or or_2 (or_2_out, comparator_1_gt, comparator_1_eq);
  Counter #(.width(10), .max('h3ff)) counter_2 (
    .Q(counter_2_q), .clk(or_2_out), .clr(clr));  // open: load, D, count, carry
  Comparator #(.width(10), .mode("unsigned")) comparator_2 (
    .a(counter_2_q), .b({10{1'b0}}), .gt(comparator_2_gt));  // open: eq, lt
  and and_2 (golod, stop_golod, comparator_2_gt);

  // Notes on the sheet:
  //   тут 0f1 это константа после такого количества clockов в голод пойдет 1 которая остановит такты
endmodule

module Apple_Detection (
  input  clr,
  input  [7:0] head,
  input  [1:0] \Static_Направление ,
  input  [7:0] Apple_coord,
  output BIT_FOR_evGENII_KIRILLOV
);

  wire comparator_1_eq, comparator_1_gt, comparator_2_eq, comparator_2_gt;
  wire [3:0] inc_dec_1_r, inc_dec_2_r, inc_dec_3_r, inc_dec_4_r;
  wire [7:0] adder_1_out, negator_1_out;

  Comparator #(.width(2), .mode("unsigned")) comparator_1 (
    .a(\Static_Направление ), .b(2'b10), .gt(comparator_1_gt), .eq(comparator_1_eq));  // open: lt
  Comparator #(.width(2), .mode("unsigned")) comparator_2 (
    .a(2'b01), .b(\Static_Направление ), .gt(comparator_2_gt), .eq(comparator_2_eq));  // open: lt
  inc_dec inc_dec_1 (.X(head[3:0]), .on_off(comparator_1_eq), .inc_dec(comparator_1_eq), .R(inc_dec_1_r));  // open: OFL
  inc_dec inc_dec_2 (.X(head[7:4]), .on_off(comparator_2_gt), .inc_dec(comparator_2_gt), .R(inc_dec_2_r));  // open: OFL
  inc_dec inc_dec_3 (
    .X(inc_dec_1_r), .on_off(comparator_1_gt), .inc_dec(comparator_1_eq), .R(inc_dec_3_r));  // open: OFL
  inc_dec inc_dec_4 (
    .X(inc_dec_2_r), .on_off(comparator_2_eq), .inc_dec(comparator_2_gt), .R(inc_dec_4_r));  // open: OFL
  Negator negator_1 (.in(Apple_coord), .out(negator_1_out));
  Adder adder_1 (.a({inc_dec_4_r, inc_dec_3_r}), .b(negator_1_out), .out(adder_1_out));  // open: cin, cout
  nor nor_1 (BIT_FOR_evGENII_KIRILLOV, adder_1_out[0], adder_1_out[1], adder_1_out[2], adder_1_out[3], adder_1_out[4], adder_1_out[5], adder_1_out[6], adder_1_out[7]);

  // Notes on the sheet:
  //   Эта штука добавляет в счетчик когда следующая клетка после головы это яблоко и мы идем в его сторону
  //   Нужно придумать при какой ситуации будем очищать счетчик 
endmodule

module disp_snake (
  input  [3:0] X,
  input  clock,
  input  [3:0] Y,
  input  clear,
  input  Del,
  output [15:0] out_6,
  output [15:0] out_7,
  output [15:0] out_8,
  output [15:0] out_9,
  output [15:0] out_10,
  output [15:0] out_11,
  output [15:0] out_12,
  output [15:0] out_13,
  output [15:0] out_14,
  output [15:0] out_15,
  output [15:0] out_16,
  output [15:0] out_17,
  output [15:0] out_18,
  output [15:0] out_19,
  output [15:0] out_20,
  output [15:0] out_21
);

  wire demultiplexer_1_out0, demultiplexer_1_out1, demultiplexer_1_out2, demultiplexer_1_out3,
       demultiplexer_1_out4, demultiplexer_1_out5, demultiplexer_1_out6, demultiplexer_1_out7,
       demultiplexer_1_out8, demultiplexer_1_out9, demultiplexer_1_out10, demultiplexer_1_out11,
       demultiplexer_1_out12, demultiplexer_1_out13, demultiplexer_1_out14, demultiplexer_1_out15;
  wire [15:0] dispriadok_snake_1_riadok, dispriadok_snake_2_riadok, dispriadok_snake_3_riadok,
       dispriadok_snake_4_riadok, dispriadok_snake_5_riadok, dispriadok_snake_6_riadok,
       dispriadok_snake_7_riadok, dispriadok_snake_8_riadok, dispriadok_snake_9_riadok,
       dispriadok_snake_10_riadok, dispriadok_snake_11_riadok, dispriadok_snake_12_riadok,
       dispriadok_snake_13_riadok, dispriadok_snake_14_riadok, dispriadok_snake_15_riadok,
       dispriadok_snake_16_riadok;

  Demultiplexer #(.select(4)) demultiplexer_1 (
    .out0(demultiplexer_1_out0), .out1(demultiplexer_1_out1), .out2(demultiplexer_1_out2),
    .out3(demultiplexer_1_out3), .out4(demultiplexer_1_out4), .out5(demultiplexer_1_out5),
    .out6(demultiplexer_1_out6), .out7(demultiplexer_1_out7), .out8(demultiplexer_1_out8),
    .out9(demultiplexer_1_out9), .out10(demultiplexer_1_out10), .out11(demultiplexer_1_out11),
    .out12(demultiplexer_1_out12), .out13(demultiplexer_1_out13), .out14(demultiplexer_1_out14),
    .out15(demultiplexer_1_out15), .in(clock), .sel(Y));  // open: en
  dispriadok_snake dispriadok_snake_1 (
    .clock(demultiplexer_1_out15), .hodn(clock), .X(X), .riadok(dispriadok_snake_1_riadok), .clear(clear));
  dispriadok_snake dispriadok_snake_2 (
    .clock(demultiplexer_1_out14), .hodn(clock), .X(X), .riadok(dispriadok_snake_2_riadok), .clear(clear));
  dispriadok_snake dispriadok_snake_3 (
    .clock(demultiplexer_1_out13), .hodn(clock), .X(X), .riadok(dispriadok_snake_3_riadok), .clear(clear));
  dispriadok_snake dispriadok_snake_4 (
    .clock(demultiplexer_1_out12), .hodn(clock), .X(X), .riadok(dispriadok_snake_4_riadok), .clear(clear));
  dispriadok_snake dispriadok_snake_5 (
    .clock(demultiplexer_1_out11), .hodn(clock), .X(X), .riadok(dispriadok_snake_5_riadok), .clear(clear));
  dispriadok_snake dispriadok_snake_6 (
    .clock(demultiplexer_1_out10), .hodn(clock), .X(X), .riadok(dispriadok_snake_6_riadok), .clear(clear));
  dispriadok_snake dispriadok_snake_7 (
    .clock(demultiplexer_1_out9), .hodn(clock), .X(X), .riadok(dispriadok_snake_7_riadok), .clear(clear));
  dispriadok_snake dispriadok_snake_8 (
    .clock(demultiplexer_1_out8), .hodn(clock), .X(X), .riadok(dispriadok_snake_8_riadok), .clear(clear));
  dispriadok_snake dispriadok_snake_9 (
    .clock(demultiplexer_1_out7), .hodn(clock), .X(X), .riadok(dispriadok_snake_9_riadok), .clear(clear));
  dispriadok_snake dispriadok_snake_10 (
    .clock(demultiplexer_1_out6), .hodn(clock), .X(X), .riadok(dispriadok_snake_10_riadok), .clear(clear));
  dispriadok_snake dispriadok_snake_11 (
    .clock(demultiplexer_1_out5), .hodn(clock), .X(X), .riadok(dispriadok_snake_11_riadok), .clear(clear));
  dispriadok_snake dispriadok_snake_12 (
    .clock(demultiplexer_1_out4), .hodn(clock), .X(X), .riadok(dispriadok_snake_12_riadok), .clear(clear));
  dispriadok_snake dispriadok_snake_13 (
    .clock(demultiplexer_1_out3), .hodn(clock), .X(X), .riadok(dispriadok_snake_13_riadok), .clear(clear));
  dispriadok_snake dispriadok_snake_14 (
    .clock(demultiplexer_1_out2), .hodn(clock), .X(X), .riadok(dispriadok_snake_14_riadok), .clear(clear));
  dispriadok_snake dispriadok_snake_15 (
    .clock(demultiplexer_1_out1), .hodn(clock), .X(X), .riadok(dispriadok_snake_15_riadok), .clear(clear));
  dispriadok_snake dispriadok_snake_16 (
    .clock(demultiplexer_1_out0), .hodn(clock), .X(X), .riadok(dispriadok_snake_16_riadok), .clear(clear));
  reg_delete_snake reg_delete_snake_1 (.Input(dispriadok_snake_1_riadok), .Output(out_6), .Del(Del));
  reg_delete_snake reg_delete_snake_2 (.Input(dispriadok_snake_2_riadok), .Output(out_7), .Del(Del));
  reg_delete_snake reg_delete_snake_3 (.Input(dispriadok_snake_3_riadok), .Output(out_8), .Del(Del));
  reg_delete_snake reg_delete_snake_4 (.Input(dispriadok_snake_4_riadok), .Output(out_9), .Del(Del));
  reg_delete_snake reg_delete_snake_5 (.Input(dispriadok_snake_5_riadok), .Output(out_10), .Del(Del));
  reg_delete_snake reg_delete_snake_6 (.Input(dispriadok_snake_6_riadok), .Output(out_11), .Del(Del));
  reg_delete_snake reg_delete_snake_7 (.Input(dispriadok_snake_7_riadok), .Output(out_12), .Del(Del));
  reg_delete_snake reg_delete_snake_8 (.Input(dispriadok_snake_8_riadok), .Output(out_13), .Del(Del));
  reg_delete_snake reg_delete_snake_9 (.Input(dispriadok_snake_9_riadok), .Output(out_14), .Del(Del));
  reg_delete_snake reg_delete_snake_10 (.Input(dispriadok_snake_10_riadok), .Output(out_15), .Del(Del));
  reg_delete_snake reg_delete_snake_11 (.Input(dispriadok_snake_11_riadok), .Output(out_16), .Del(Del));
  reg_delete_snake reg_delete_snake_12 (.Input(dispriadok_snake_12_riadok), .Output(out_17), .Del(Del));
  reg_delete_snake reg_delete_snake_13 (.Input(dispriadok_snake_13_riadok), .Output(out_18), .Del(Del));
  reg_delete_snake reg_delete_snake_14 (.Input(dispriadok_snake_14_riadok), .Output(out_19), .Del(Del));
  reg_delete_snake reg_delete_snake_15 (.Input(dispriadok_snake_15_riadok), .Output(out_20), .Del(Del));
  reg_delete_snake reg_delete_snake_16 (.Input(dispriadok_snake_16_riadok), .Output(out_21), .Del(Del));
endmodule

module dispriadok_snake (
  input  clock,
  input  hodn,
  input  [3:0] X,
  input  clear,
  output [15:0] riadok
);

  wire demultiplexer_1_out0, demultiplexer_1_out1, demultiplexer_1_out2, demultiplexer_1_out3,
       demultiplexer_1_out4, demultiplexer_1_out5, demultiplexer_1_out6, demultiplexer_1_out7,
       demultiplexer_1_out8, demultiplexer_1_out9, demultiplexer_1_out10, demultiplexer_1_out11,
       demultiplexer_1_out12, demultiplexer_1_out13, demultiplexer_1_out14, demultiplexer_1_out15;

  Demultiplexer #(.select(4)) demultiplexer_1 (
    .out0(demultiplexer_1_out0), .out1(demultiplexer_1_out1), .out2(demultiplexer_1_out2),
    .out3(demultiplexer_1_out3), .out4(demultiplexer_1_out4), .out5(demultiplexer_1_out5),
    .out6(demultiplexer_1_out6), .out7(demultiplexer_1_out7), .out8(demultiplexer_1_out8),
    .out9(demultiplexer_1_out9), .out10(demultiplexer_1_out10), .out11(demultiplexer_1_out11),
    .out12(demultiplexer_1_out12), .out13(demultiplexer_1_out13), .out14(demultiplexer_1_out14),
    .out15(demultiplexer_1_out15), .in(clock), .sel(X));  // open: en
  D_Flip_Flop d_ff_1 (.clk(demultiplexer_1_out0), .D(hodn), .Q(riadok[15]), .reset(clear));  // open: Qn, preset, en
  D_Flip_Flop d_ff_2 (.clk(demultiplexer_1_out1), .D(hodn), .Q(riadok[14]), .reset(clear));  // open: Qn, preset, en
  D_Flip_Flop d_ff_3 (.clk(demultiplexer_1_out2), .D(hodn), .Q(riadok[13]), .reset(clear));  // open: Qn, preset, en
  D_Flip_Flop d_ff_4 (.clk(demultiplexer_1_out3), .D(hodn), .Q(riadok[12]), .reset(clear));  // open: Qn, preset, en
  D_Flip_Flop d_ff_5 (.clk(demultiplexer_1_out4), .D(hodn), .Q(riadok[11]), .reset(clear));  // open: Qn, preset, en
  D_Flip_Flop d_ff_6 (.clk(demultiplexer_1_out6), .D(hodn), .Q(riadok[9]), .reset(clear));  // open: Qn, preset, en
  D_Flip_Flop d_ff_7 (.clk(demultiplexer_1_out5), .D(hodn), .Q(riadok[10]), .reset(clear));  // open: Qn, preset, en
  D_Flip_Flop d_ff_8 (.clk(demultiplexer_1_out7), .D(hodn), .Q(riadok[8]), .reset(clear));  // open: Qn, preset, en
  D_Flip_Flop d_ff_9 (.clk(demultiplexer_1_out8), .D(hodn), .Q(riadok[7]), .reset(clear));  // open: Qn, preset, en
  D_Flip_Flop d_ff_10 (.clk(demultiplexer_1_out9), .D(hodn), .Q(riadok[6]), .reset(clear));  // open: Qn, preset, en
  D_Flip_Flop d_ff_11 (.clk(demultiplexer_1_out10), .D(hodn), .Q(riadok[5]), .reset(clear));  // open: Qn, preset, en
  D_Flip_Flop d_ff_12 (.clk(demultiplexer_1_out11), .D(hodn), .Q(riadok[4]), .reset(clear));  // open: Qn, preset, en
  D_Flip_Flop d_ff_13 (.clk(demultiplexer_1_out12), .D(hodn), .Q(riadok[3]), .reset(clear));  // open: Qn, preset, en
  D_Flip_Flop d_ff_14 (.clk(demultiplexer_1_out13), .D(hodn), .Q(riadok[2]), .reset(clear));  // open: Qn, preset, en
  D_Flip_Flop d_ff_15 (.clk(demultiplexer_1_out14), .D(hodn), .Q(riadok[1]), .reset(clear));  // open: Qn, preset, en
  D_Flip_Flop d_ff_16 (.clk(demultiplexer_1_out15), .D(hodn), .Q(riadok[0]), .reset(clear));  // open: Qn, preset, en
endmodule

module reg_delete_snake (
  input  [15:0] Input,
  input  Del,
  output [15:0] Output
);

  wire not_2_out, not_3_out, not_4_out, not_5_out, not_6_out, not_7_out, not_8_out, not_9_out, not_10_out,
       not_11_out, not_12_out, not_13_out, not_14_out, or_1_out;
  wire [15:0] and_1_out, controlled_buffer_1_out, controlled_buffer_2_out, demultiplexer_1_out0,
       demultiplexer_1_out1, not_1_out, or_2_out;

  or or_1 (or_1_out, Input[0], Input[1], Input[2], Input[3], Input[4], Input[5], Input[6], Input[7], Input[8], Input[9], Input[10], Input[11], Input[12], Input[13], Input[14], Input[15]);
  assign controlled_buffer_1_out = or_1_out ? Input : 16'bz;  // Controlled_Buffer controlled_buffer_1
  Demultiplexer #(.width(16)) demultiplexer_1 (
    .out0(demultiplexer_1_out0), .out1(demultiplexer_1_out1), .in(controlled_buffer_1_out), .sel(Del));  // open: en
  assign not_1_out = ~demultiplexer_1_out1;  // NOT_Gate not_1, 16 bits wide
  not not_2 (not_2_out, not_3_out);
  not not_3 (not_3_out, not_4_out);
  not not_4 (not_4_out, or_1_out);
  assign or_2_out = Output | demultiplexer_1_out0;  // OR_Gate or_2, 16 bits wide
  assign and_1_out = not_1_out & Output;  // AND_Gate and_1, 16 bits wide
  not not_5 (not_5_out, not_7_out);
  not not_6 (not_6_out, not_5_out);
  not not_7 (not_7_out, not_2_out);
  not not_8 (not_8_out, not_6_out);
  assign controlled_buffer_2_out = not_9_out ? or_2_out : 16'bz;  // Controlled_Buffer controlled_buffer_2
  not not_9 (not_9_out, Del);
  assign controlled_buffer_2_out = Del ? and_1_out : 16'bz;  // Controlled_Buffer controlled_buffer_3
  not not_10 (not_10_out, not_12_out);
  not not_11 (not_11_out, not_10_out);
  not not_12 (not_12_out, not_8_out);
  not not_13 (not_13_out, not_11_out);
  Register #(.width(16)) register_1 (.D(controlled_buffer_2_out), .Q(Output), .clk(not_14_out));  // open: en, clr
  not not_14 (not_14_out, not_13_out);

  // Notes on the sheet:
  //   Проверка на 0
  //   Если 0, то ничего не делаем
  //   Режим: Удаление или добавление
  //   Добавление пикселя
  //   Удаление пикселя
endmodule

module sec_matrixdispriadok (
  input  clock,
  input  hodn,
  input  [3:0] X,
  input  clear,
  output [16:0] riadok
);

  wire demultiplexer_1_out0, demultiplexer_1_out1, demultiplexer_1_out2, demultiplexer_1_out3,
       demultiplexer_1_out4, demultiplexer_1_out5, demultiplexer_1_out6, demultiplexer_1_out7,
       demultiplexer_1_out8, demultiplexer_1_out9, demultiplexer_1_out10, demultiplexer_1_out11,
       demultiplexer_1_out12, demultiplexer_1_out13, demultiplexer_1_out14, demultiplexer_1_out15;

  Demultiplexer #(.select(4)) demultiplexer_1 (
    .out0(demultiplexer_1_out0), .out1(demultiplexer_1_out1), .out2(demultiplexer_1_out2),
    .out3(demultiplexer_1_out3), .out4(demultiplexer_1_out4), .out5(demultiplexer_1_out5),
    .out6(demultiplexer_1_out6), .out7(demultiplexer_1_out7), .out8(demultiplexer_1_out8),
    .out9(demultiplexer_1_out9), .out10(demultiplexer_1_out10), .out11(demultiplexer_1_out11),
    .out12(demultiplexer_1_out12), .out13(demultiplexer_1_out13), .out14(demultiplexer_1_out14),
    .out15(demultiplexer_1_out15), .in(clock), .sel(X));  // open: en
  D_Flip_Flop d_ff_1 (.clk(demultiplexer_1_out0), .D(hodn), .Q(riadok[15]), .reset(clear));  // open: Qn, preset, en
  D_Flip_Flop d_ff_2 (.clk(demultiplexer_1_out1), .D(hodn), .Q(riadok[14]), .reset(clear));  // open: Qn, preset, en
  D_Flip_Flop d_ff_3 (.clk(demultiplexer_1_out2), .D(hodn), .Q(riadok[13]), .reset(clear));  // open: Qn, preset, en
  D_Flip_Flop d_ff_4 (.clk(demultiplexer_1_out3), .D(hodn), .Q(riadok[12]), .reset(clear));  // open: Qn, preset, en
  D_Flip_Flop d_ff_5 (.clk(demultiplexer_1_out5), .D(hodn), .Q(riadok[10]), .reset(clear));  // open: Qn, preset, en
  D_Flip_Flop d_ff_6 (.clk(demultiplexer_1_out4), .D(hodn), .Q(riadok[11]), .reset(clear));  // open: Qn, preset, en
  D_Flip_Flop d_ff_7 (.clk(demultiplexer_1_out6), .D(hodn), .Q(riadok[9]), .reset(clear));  // open: Qn, preset, en
  D_Flip_Flop d_ff_8 (.clk(demultiplexer_1_out7), .D(hodn), .Q(riadok[8]), .reset(clear));  // open: Qn, preset, en
  D_Flip_Flop d_ff_9 (.clk(demultiplexer_1_out8), .D(hodn), .Q(riadok[7]), .reset(clear));  // open: Qn, preset, en
  D_Flip_Flop d_ff_10 (.clk(demultiplexer_1_out9), .D(hodn), .Q(riadok[6]), .reset(clear));  // open: Qn, preset, en
  D_Flip_Flop d_ff_11 (.clk(demultiplexer_1_out10), .D(hodn), .Q(riadok[5]), .reset(clear));  // open: Qn, preset, en
  D_Flip_Flop d_ff_12 (.clk(demultiplexer_1_out11), .D(hodn), .Q(riadok[4]), .reset(clear));  // open: Qn, preset, en
  D_Flip_Flop d_ff_13 (.clk(demultiplexer_1_out12), .D(hodn), .Q(riadok[3]), .reset(clear));  // open: Qn, preset, en
  D_Flip_Flop d_ff_14 (.clk(demultiplexer_1_out13), .D(hodn), .Q(riadok[2]), .reset(clear));  // open: Qn, preset, en
  D_Flip_Flop d_ff_15 (.clk(demultiplexer_1_out14), .D(hodn), .Q(riadok[1]), .reset(clear));  // open: Qn, preset, en
  D_Flip_Flop d_ff_16 (.clk(demultiplexer_1_out15), .D(hodn), .Q(riadok[0]), .reset(clear));  // open: Qn, preset, en

  assign riadok[16] = 1'b0;
endmodule

module sec_matrix_disp (
  input  [3:0] X,
  input  clock,
  input  [3:0] Y,
  input  clear,
  output [16:0] out_5,
  output [16:0] out_6,
  output [16:0] out_7,
  output [16:0] out_8,
  output [16:0] out_9,
  output [16:0] out_10,
  output [16:0] out_11,
  output [16:0] out_12,
  output [16:0] out_13,
  output [16:0] out_14,
  output [16:0] out_15,
  output [16:0] out_16,
  output [16:0] out_17,
  output [16:0] out_18,
  output [16:0] out_19,
  output [16:0] out_20
);

  wire demultiplexer_1_out0, demultiplexer_1_out1, demultiplexer_1_out2, demultiplexer_1_out3,
       demultiplexer_1_out4, demultiplexer_1_out5, demultiplexer_1_out6, demultiplexer_1_out7,
       demultiplexer_1_out8, demultiplexer_1_out9, demultiplexer_1_out10, demultiplexer_1_out11,
       demultiplexer_1_out12, demultiplexer_1_out13, demultiplexer_1_out14, demultiplexer_1_out15;

  Demultiplexer #(.select(4)) demultiplexer_1 (
    .out0(demultiplexer_1_out0), .out1(demultiplexer_1_out1), .out2(demultiplexer_1_out2),
    .out3(demultiplexer_1_out3), .out4(demultiplexer_1_out4), .out5(demultiplexer_1_out5),
    .out6(demultiplexer_1_out6), .out7(demultiplexer_1_out7), .out8(demultiplexer_1_out8),
    .out9(demultiplexer_1_out9), .out10(demultiplexer_1_out10), .out11(demultiplexer_1_out11),
    .out12(demultiplexer_1_out12), .out13(demultiplexer_1_out13), .out14(demultiplexer_1_out14),
    .out15(demultiplexer_1_out15), .in(clock), .sel(Y));  // open: en
  sec_matrixdispriadok sec_matrixdispriadok_1 (
    .clock(clock), .hodn(demultiplexer_1_out15), .X(X), .riadok(out_5), .clear(clear));
  sec_matrixdispriadok sec_matrixdispriadok_2 (
    .clock(clock), .hodn(demultiplexer_1_out14), .X(X), .riadok(out_6), .clear(clear));
  sec_matrixdispriadok sec_matrixdispriadok_3 (
    .clock(clock), .hodn(demultiplexer_1_out13), .X(X), .riadok(out_7), .clear(clear));
  sec_matrixdispriadok sec_matrixdispriadok_4 (
    .clock(clock), .hodn(demultiplexer_1_out12), .X(X), .riadok(out_8), .clear(clear));
  sec_matrixdispriadok sec_matrixdispriadok_5 (
    .clock(clock), .hodn(demultiplexer_1_out11), .X(X), .riadok(out_9), .clear(clear));
  sec_matrixdispriadok sec_matrixdispriadok_6 (
    .clock(clock), .hodn(demultiplexer_1_out10), .X(X), .riadok(out_10), .clear(clear));
  sec_matrixdispriadok sec_matrixdispriadok_7 (
    .clock(clock), .hodn(demultiplexer_1_out9), .X(X), .riadok(out_11), .clear(clear));
  sec_matrixdispriadok sec_matrixdispriadok_8 (
    .clock(clock), .hodn(demultiplexer_1_out8), .X(X), .riadok(out_12), .clear(clear));
  sec_matrixdispriadok sec_matrixdispriadok_9 (
    .clock(clock), .hodn(demultiplexer_1_out7), .X(X), .riadok(out_13), .clear(clear));
  sec_matrixdispriadok sec_matrixdispriadok_10 (
    .clock(clock), .hodn(demultiplexer_1_out6), .X(X), .riadok(out_14), .clear(clear));
  sec_matrixdispriadok sec_matrixdispriadok_11 (
    .clock(clock), .hodn(demultiplexer_1_out5), .X(X), .riadok(out_15), .clear(clear));
  sec_matrixdispriadok sec_matrixdispriadok_12 (
    .clock(clock), .hodn(demultiplexer_1_out4), .X(X), .riadok(out_16), .clear(clear));
  sec_matrixdispriadok sec_matrixdispriadok_13 (
    .clock(clock), .hodn(demultiplexer_1_out3), .X(X), .riadok(out_17), .clear(clear));
  sec_matrixdispriadok sec_matrixdispriadok_14 (
    .clock(clock), .hodn(demultiplexer_1_out2), .X(X), .riadok(out_18), .clear(clear));
  sec_matrixdispriadok sec_matrixdispriadok_15 (
    .clock(clock), .hodn(demultiplexer_1_out1), .X(X), .riadok(out_19), .clear(clear));
  sec_matrixdispriadok sec_matrixdispriadok_16 (
    .clock(clock), .hodn(demultiplexer_1_out0), .X(X), .riadok(out_20), .clear(clear));
endmodule

module counter (
  input  clock,
  input  clear,
  output out_3,
  output out_4,
  output out_5,
  output out_6,
  output out_7,
  output out_8,
  output out_9,
  output out_10,
  output out_11,
  output out_12,
  output out_13,
  output out_14,
  output out_15,
  output out_16,
  output out_17,
  output out_18
);

  wire counter_1_carry;
  wire [7:0] counter_1_q, counter_2_q;

  Counter #(.max('ha)) counter_1 (
    .Q(counter_1_q), .carry(counter_1_carry), .clk(clock), .clr(clear));  // open: load, D, count
  Counter #(.max('ha)) counter_2 (.Q(counter_2_q), .clk(counter_1_carry), .clr(clear));  // open: load, D, count, carry
  ROM rom_1 (.addr(counter_1_q), .data({out_7, out_8, out_9, out_10, out_18, out_17, out_16, out_15}));  // open: sel
  ROM rom_2 (.addr(counter_2_q), .data({out_3, out_4, out_5, out_6, out_14, out_13, out_12, out_11}));  // open: sel

  // Other names for the same wires on the sheet: _1_1 = out_15; _1_2 = out_16; _1_3 = out_17; _1_4 = out_18;
  //   _1_5 = out_10; _1_6 = out_9; _1_7 = out_8; _1_8 = out_7; _2_1 = out_11; _2_2 = out_12; _2_3 = out_13;
  //   _2_4 = out_14; _2_5 = out_6; _2_6 = out_5; _2_7 = out_4; _2_8 = out_3

  // Notes on the sheet:
  //   contents of rom_1 (hex, n*v repeats v):
  //   77 14 b3 b6 d4 e6 e7 34 f7 f6 77
  //   contents of rom_2 (hex, n*v repeats v):
  //   77 14 b3 b6 d4 e6 e7 34 f7 f6 77
endmodule

module MAIN (
);


  // Notes on the sheet:
  //   КАК ИДЕЯ МОЖНО ПРОСТО СЮДА ВЫНЕСТИ ВСЕ ОТДЕЛЬНЫЕ 
  //   ВХОДЫ ВЗАИМОДЕЙСТВУЮЩИЕ С ПОЛЬЗОВАТЕЛЕМ И ВЫНЕСТИ ПОЛЕ
endmodule

module win (
  input  lose,
  input  win,
  input  pause,
  output [17:0] _1,
  output [17:0] _2,
  output [17:0] _3,
  output [17:0] _4,
  output [17:0] _5,
  output [17:0] _6,
  output [17:0] _7,
  output [17:0] _8,
  output [17:0] _9,
  output [17:0] _10,
  output [17:0] _11,
  output [17:0] _12,
  output [17:0] _13,
  output [17:0] _14,
  output [17:0] _15,
  output [17:0] _16
);

  wire wall;
  wire [15:0] _5_t, _5l, _5p, _5w, _6l, _6p, _6w, _7l, _7p, _7w, _8l, _8p, _8w, _9l, _9p, _9w, _10l, _10p,
       _10w, _11l, _11p, _11w, or_1_out, or_2_out, or_3_out, or_4_out, or_5_out, or_6_out, or_7_out;

  assign _5p = pause ? 16'h200 : 16'bz;  // Controlled_Buffer controlled_buffer_1
  assign _6p = pause ? 16'h300 : 16'bz;  // Controlled_Buffer controlled_buffer_2
  assign _7p = pause ? 16'h380 : 16'bz;  // Controlled_Buffer controlled_buffer_3
  assign _8p = pause ? 16'h3c0 : 16'bz;  // Controlled_Buffer controlled_buffer_4
  assign _9p = pause ? 16'h380 : 16'bz;  // Controlled_Buffer controlled_buffer_5
  Pull_Resistor pull_resistor_1 (.node(_9p));
  assign _10p = pause ? 16'h300 : 16'bz;  // Controlled_Buffer controlled_buffer_6
  Pull_Resistor pull_resistor_2 (.node(_10p));
  Pull_Resistor pull_resistor_3 (.node(_11p));
  assign _11p = pause ? 16'h200 : 16'bz;  // Controlled_Buffer controlled_buffer_7
  assign _5w = win ? {16{1'b0}} : 16'bz;  // Controlled_Buffer controlled_buffer_8
  assign _6w = win ? 16'h4542 : 16'bz;  // Controlled_Buffer controlled_buffer_9
  assign _7w = win ? 16'h4462 : 16'bz;  // Controlled_Buffer controlled_buffer_10
  assign _8w = win ? 16'h4552 : 16'bz;  // Controlled_Buffer controlled_buffer_11
  Pull_Resistor pull_resistor_4 (.node(_9w));
  assign _9w = win ? 16'h554a : 16'bz;  // Controlled_Buffer controlled_buffer_12
  assign _10w = win ? 16'h6d46 : 16'bz;  // Controlled_Buffer controlled_buffer_13
  Pull_Resistor pull_resistor_5 (.node(_10w));
  Pull_Resistor pull_resistor_6 (.node(_11w));
  assign _11w = win ? 16'h4542 : 16'bz;  // Controlled_Buffer controlled_buffer_14
  assign _5l = lose ? {16{1'b0}} : 16'bz;  // Controlled_Buffer controlled_buffer_15
  assign _6l = lose ? 16'h4ef6 : 16'bz;  // Controlled_Buffer controlled_buffer_16
  assign _7l = lose ? 16'h4a84 : 16'bz;  // Controlled_Buffer controlled_buffer_17
  assign _8l = lose ? 16'h4ac4 : 16'bz;  // Controlled_Buffer controlled_buffer_18
  assign _9l = lose ? 16'h4a66 : 16'bz;  // Controlled_Buffer controlled_buffer_19
  Pull_Resistor pull_resistor_7 (.node(_9l));
  Pull_Resistor pull_resistor_8 (.node(_10l));
  assign _10l = lose ? 16'h4a34 : 16'bz;  // Controlled_Buffer controlled_buffer_20
  Pull_Resistor pull_resistor_9 (.node(_11l));
  assign _11l = lose ? 16'h6ef6 : 16'bz;  // Controlled_Buffer controlled_buffer_21
  assign _5_t = wall ? 16'h8001 : 16'bz;  // Controlled_Buffer controlled_buffer_22
  Pull_Resistor pull_resistor_10 (.node(_5_t));
  Pull_Resistor pull_resistor_11 (.node(_5p));
  Pull_Resistor pull_resistor_12 (.node(_6p));
  Pull_Resistor pull_resistor_13 (.node(_7p));
  Pull_Resistor pull_resistor_14 (.node(_8p));
  Pull_Resistor pull_resistor_15 (.node(_5w));
  Pull_Resistor pull_resistor_16 (.node(_6w));
  Pull_Resistor pull_resistor_17 (.node(_7w));
  Pull_Resistor pull_resistor_18 (.node(_8w));
  Pull_Resistor pull_resistor_19 (.node(_5l));
  Pull_Resistor pull_resistor_20 (.node(_6l));
  Pull_Resistor pull_resistor_21 (.node(_7l));
  Pull_Resistor pull_resistor_22 (.node(_8l));
  nor nor_1 (wall, lose, win);
  Pull_Resistor pull_resistor_23 (.node(_1));
  assign _1 = wall ? 18'hffff : 18'bz;  // Controlled_Buffer controlled_buffer_23
  Pull_Resistor pull_resistor_24 (.node(_2));
  assign _2 = wall ? 18'h8001 : 18'bz;  // Controlled_Buffer controlled_buffer_24
  helper_1 helper_1_1 (.in(or_1_out), .out(_5));
  assign or_1_out = _5_t | _5p | _5w | _5l;  // OR_Gate or_1, 16 bits wide
  assign or_2_out = _5_t | _6p | _6w | _6l;  // OR_Gate or_2, 16 bits wide
  helper_1 helper_1_2 (.in(or_2_out), .out(_6));
  helper_1 helper_1_3 (.in(or_3_out), .out(_7));
  assign or_3_out = _5_t | _7p | _7w | _7l;  // OR_Gate or_3, 16 bits wide
  helper_1 helper_1_4 (.in(or_4_out), .out(_8));
  assign or_4_out = _5_t | _8p | _8w | _8l;  // OR_Gate or_4, 16 bits wide
  assign or_5_out = _5_t | _9p | _9w | _9l;  // OR_Gate or_5, 16 bits wide
  helper_1 helper_1_5 (.in(or_5_out), .out(_9));
  assign or_6_out = _5_t | _10p | _10w | _10l;  // OR_Gate or_6, 16 bits wide
  helper_1 helper_1_6 (.in(or_6_out), .out(_10));
  helper_1 helper_1_7 (.in(or_7_out), .out(_11));
  assign or_7_out = _5_t | _11p | _11l | _11w;  // OR_Gate or_7, 16 bits wide
  Pull_Resistor pull_resistor_25 (.node(_12));
  assign _12 = wall ? 18'h8001 : 18'bz;  // Controlled_Buffer controlled_buffer_25
  assign _16 = wall ? 18'hffff : 18'bz;  // Controlled_Buffer controlled_buffer_26
  Pull_Resistor pull_resistor_26 (.node(_16));

  assign _3 = _2;
  assign _4 = _2;
  assign _13 = _12;
  assign _14 = _12;
  assign _15 = _12;

  // Other names for the same wires on the sheet: _6_t[15:0] = _5_t; _7_t[15:0] = _5_t; _8_t[15:0] = _5_t;
  //   _9_t[15:0] = _5_t; _10_t[15:0] = _5_t; _11_t[15:0] = _5_t; paus = pause
endmodule

module vivod_matrix (
  input  [7:0] snake_coord,
  input  [7:0] apple_coord,
  input  [7:0] head_coord,
  input  Delete,
  input  paus,
  input  win,
  input  lose,
  input  takt,
  input  clr,
  input  vivod,
  input  cycle,
  input  apple,
  input  resp,
  output [15:0] out_14,
  output [19:0] out_15,
  output [18:0] out_16,
  output [17:0] out_17,
  output [16:0] out_18,
  output [15:0] out_19,
  output [19:0] out_20,
  output [18:0] out_21,
  output [17:0] out_22,
  output [16:0] out_23,
  output [15:0] out_24,
  output [19:0] out_25,
  output [18:0] out_26,
  output [17:0] out_27,
  output [16:0] out_28,
  output [15:0] out_29,
  output [19:0] out_30,
  output [18:0] out_31,
  output [17:0] out_32,
  output [16:0] out_33,
  output [15:0] out_34,
  output [19:0] out_35,
  output [17:0] out_36,
  output [16:0] out_37,
  output [15:0] out_38,
  output [19:0] out_39,
  output [18:0] out_40,
  output [15:0] out_41,
  output [19:0] out_42,
  output [17:0] out_43,
  output [16:0] out_44,
  output [18:0] out_45,
  output [15:0] out_46,
  output [19:0] out_47,
  output [17:0] out_48,
  output [16:0] out_49,
  output [18:0] out_50,
  output [15:0] out_51,
  output [19:0] out_52,
  output [17:0] out_53,
  output [16:0] out_54,
  output [18:0] out_55,
  output [15:0] out_56,
  output [19:0] out_57,
  output [17:0] out_58,
  output [16:0] out_59,
  output [15:0] out_60,
  output [19:0] out_61,
  output [18:0] out_62,
  output [15:0] out_63,
  output [19:0] out_64,
  output [17:0] out_65,
  output [16:0] out_66,
  output [18:0] out_67,
  output [15:0] out_68,
  output [19:0] out_69,
  output [17:0] out_70,
  output [16:0] out_71,
  output [18:0] out_72,
  output [15:0] out_73,
  output [19:0] out_74,
  output [17:0] out_75,
  output [16:0] out_76,
  output [18:0] out_77,
  output [15:0] out_78,
  output [19:0] out_79,
  output [17:0] out_80,
  output [16:0] out_81,
  output [15:0] out_82,
  output [19:0] out_83,
  output [18:0] out_84,
  output [17:0] out_85,
  output [16:0] out_86,
  output [18:0] out_87,
  output [17:0] out_88,
  output [16:0] out_89,
  output [18:0] out_90,
  output [17:0] out_91,
  output [16:0] out_92,
  output [18:0] out_93
);

  wire or_1_out, or_2_out, or_4_out, or_5_out, rest;
  wire [15:0] _1s, _2s, _3s, _4s, _5s, _6s, _7s, _8s, _9s, _10s, _11s, _12s, _13s, _14s, _15s, _16s;

  Pull_Resistor pull_resistor_1 (.node(vivod));
  or or_1 (or_1_out, vivod, clr);
  or or_2 (or_2_out, lose, cycle, win);
  or or_3 (rest, or_1_out, or_2_out);
  disp_snake disp_snake_1 (
    .X(snake_coord[7:4]), .out_6(_1s), .clock(takt), .Y(snake_coord[3:0]), .out_7(_2s), .out_8(_3s),
    .out_9(_4s), .out_10(_5s), .out_11(_6s), .out_12(_7s), .out_13(_8s), .out_14(_9s), .out_15(_10s),
    .out_16(_11s), .out_17(_12s), .out_18(_13s), .out_19(_14s), .out_20(_15s), .out_21(_16s), .clear(rest),
    .Del(Delete));
  or or_4 (or_4_out, lose, win);
  sec_matrix_disp sec_matrix_disp_1 (
    .X(apple_coord[7:4]), .clock(takt), .Y(apple_coord[3:0]), .out_5(out_18), .out_6(out_23), .out_7(out_28),
    .out_8(out_33), .out_9(out_37), .out_10(out_44), .out_11(out_49), .out_12(out_54), .out_13(out_59),
    .out_14(out_66), .out_15(out_71), .out_16(out_76), .out_17(out_81), .out_18(out_86), .out_19(out_89),
    .out_20(out_92), .clear(or_5_out));
  or or_5 (or_5_out, apple, or_4_out, clr, resp);
  trans trans_1 (.in16(_1s), .in17(out_18), .out19(out_16), .in18(out_17));
  trans trans_2 (.in16(_2s), .in17(out_23), .out19(out_21), .in18(out_22));
  trans trans_3 (.in16(_3s), .in17(out_28), .out19(out_26), .in18(out_27));
  trans trans_4 (.in16(_4s), .in17(out_33), .out19(out_31), .in18(out_32));
  trans trans_5 (.in16(_5s), .in17(out_37), .out19(out_40), .in18(out_36));
  trans trans_6 (.in16(_6s), .in17(out_44), .out19(out_45), .in18(out_43));
  trans trans_7 (.in16(_7s), .in17(out_49), .out19(out_50), .in18(out_48));
  trans trans_8 (.in16(_8s), .in17(out_54), .out19(out_55), .in18(out_53));
  trans trans_9 (.in16(_9s), .in17(out_59), .out19(out_62), .in18(out_58));
  trans trans_10 (.in16(_10s), .in17(out_66), .out19(out_67), .in18(out_65));
  trans trans_11 (.in16(_11s), .in17(out_71), .out19(out_72), .in18(out_70));
  trans trans_12 (.in16(_12s), .in17(out_76), .out19(out_77), .in18(out_75));
  trans trans_13 (.in16(_13s), .in17(out_81), .out19(out_84), .in18(out_80));
  trans trans_14 (.in16(_14s), .in17(out_86), .out19(out_87), .in18(out_85));
  trans trans_15 (.in16(_15s), .in17(out_89), .out19(out_90), .in18(out_88));
  trans trans_16 (.in16(_16s), .in17(out_92), .out19(out_93), .in18(out_91));
  win win_1 (
    .lose(lose), .win(win), .pause(paus), ._1(out_17), ._2(out_22), ._3(out_27), ._4(out_32), ._5(out_36),
    ._6(out_43), ._7(out_48), ._8(out_53), ._9(out_58), ._10(out_65), ._11(out_70), ._12(out_75),
    ._13(out_80), ._14(out_85), ._15(out_88), ._16(out_91));
  headdisp headdisp_1 (
    .X(head_coord[7:4]), .clock(takt), .Y(head_coord[3:0]), .clear(rest), .out_5(out_15), .out_6(out_20),
    .out_7(out_25), .out_8(out_30), .out_9(out_35), .out_10(out_39), .out_11(out_42), .out_12(out_47),
    .out_13(out_52), .out_14(out_57), .out_15(out_61), .out_16(out_64), .out_17(out_69), .out_18(out_74),
    .out_19(out_79), .out_20(out_83));
  _16_20NOAND u_16_20noand_1 (._16in(_1s), ._20in(out_15), ._16out(out_14));
  _16_20NOAND u_16_20noand_2 (._16in(_2s), ._20in(out_20), ._16out(out_19));
  _16_20NOAND u_16_20noand_3 (._16in(_3s), ._20in(out_25), ._16out(out_24));
  _16_20NOAND u_16_20noand_4 (._16in(_4s), ._20in(out_30), ._16out(out_29));
  _16_20NOAND u_16_20noand_5 (._16in(_5s), ._20in(out_35), ._16out(out_34));
  _16_20NOAND u_16_20noand_6 (._16in(_6s), ._20in(out_39), ._16out(out_38));
  _16_20NOAND u_16_20noand_7 (._16in(_7s), ._20in(out_42), ._16out(out_41));
  _16_20NOAND u_16_20noand_8 (._16in(_8s), ._20in(out_47), ._16out(out_46));
  _16_20NOAND u_16_20noand_9 (._16in(_9s), ._20in(out_52), ._16out(out_51));
  _16_20NOAND u_16_20noand_10 (._16in(_10s), ._20in(out_57), ._16out(out_56));
  _16_20NOAND u_16_20noand_11 (._16in(_11s), ._20in(out_61), ._16out(out_60));
  _16_20NOAND u_16_20noand_12 (._16in(_12s), ._20in(out_64), ._16out(out_63));
  _16_20NOAND u_16_20noand_13 (._16in(_13s), ._20in(out_69), ._16out(out_68));
  _16_20NOAND u_16_20noand_14 (._16in(_14s), ._20in(out_74), ._16out(out_73));
  _16_20NOAND u_16_20noand_15 (._16in(_15s), ._20in(out_79), ._16out(out_78));
  _16_20NOAND u_16_20noand_16 (._16in(_16s), ._20in(out_83), ._16out(out_82));

  // Other names for the same wires on the sheet: _1[17:0] = out_17; _1a[16:0] = out_18; _1h[19:0] = out_15;
  //   _1h4[19:0] = out_74; _2[17:0] = out_22; _2a[16:0] = out_23; _3[17:0] = out_27; _3a[16:0] = out_28;
  //   _3h[19:0] = out_25; _4[17:0] = out_32; _4a[16:0] = out_33; _4h[19:0] = out_30; _5[17:0] = out_36;
  //   _5a[16:0] = out_37; _5h[19:0] = out_35; _6[17:0] = out_43; _6a[16:0] = out_44; _6h[19:0] = out_39;
  //   _7[17:0] = out_48; _7a[16:0] = out_49; _7h[19:0] = out_42; _8[17:0] = out_53; _8a[16:0] = out_54;
  //   _8h[19:0] = out_47; _9[17:0] = out_58; _9a[16:0] = out_59; _9h[19:0] = out_52; _10[17:0] = out_65;
  //   _10a[16:0] = out_66; _10h[19:0] = out_57; _11[17:0] = out_70; _11a[16:0] = out_71; _11h[19:0] = out_61;
  //   _12[17:0] = out_75; _12a[16:0] = out_76; _12h[19:0] = out_64; _13[17:0] = out_80; _13a[16:0] = out_81;
  //   _13h[19:0] = out_69; _14[17:0] = out_85; _14a[16:0] = out_86; _15[17:0] = out_88; _15a[16:0] = out_89;
  //   _15h[19:0] = out_79; _16[17:0] = out_91; _16a[16:0] = out_92; _16h[19:0] = out_83; h2[19:0] = out_20
endmodule

module trans (
  input  [15:0] in16,
  input  [16:0] in17,
  input  [17:0] in18,
  output [18:0] out19
);

  assign out19[15:0] = in16 | in17[15:0] | in18[15:0];  // OR_Gate or_1, 16 bits wide

  assign out19[18:16] = 3'b111;
endmodule

module counter2 (
  input  clock,
  input  clear,
  output out_3,
  output out_4,
  output out_5,
  output out_6,
  output out_7,
  output out_8,
  output out_9,
  output out_10,
  output out_11,
  output out_12,
  output out_13,
  output out_14,
  output out_15,
  output out_16,
  output out_17,
  output out_18
);

  wire comparator_1_eq;
  wire [7:0] counter_1_q, counter_2_q;

  Counter #(.max('h14)) counter_1 (.Q(counter_1_q), .clk(clock), .clr(clear));  // open: load, D, count, carry
  Counter #(.max('h5)) counter_2 (.Q(counter_2_q), .clk(comparator_1_eq), .clr(clear));  // open: load, D, count, carry
  ROM rom_1 (.addr(counter_1_q), .data({out_7, out_8, out_9, out_10, out_18, out_17, out_16, out_15}));  // open: sel
  ROM rom_2 (.addr(counter_2_q), .data({out_3, out_4, out_5, out_6, out_14, out_13, out_12, out_11}));  // open: sel
  Comparator comparator_1 (
    .a(8'hf6), .b({out_7, out_8, out_9, out_10, out_18, out_17, out_16, out_15}), .eq(comparator_1_eq));  // open: gt, lt

  // Other names for the same wires on the sheet: _1_1 = out_15; _1_2 = out_16; _1_3 = out_17; _1_4 = out_18;
  //   _1_5 = out_10; _1_6 = out_9; _1_7 = out_8; _1_8 = out_7; _2_1 = out_11; _2_2 = out_12; _2_3 = out_13;
  //   _2_4 = out_14; _2_5 = out_6; _2_6 = out_5; _2_7 = out_4; _2_8 = out_3

  // Notes on the sheet:
  //   contents of rom_1 (hex, n*v repeats v):
  //   77 f6 f7 34 e7 e6 d4 b6 b3 14 77 f6 f7 34 e7 e6 d4 b6 b3 14 77
  //   contents of rom_2 (hex, n*v repeats v):
  //   b3 14 77
endmodule

module helper_1 (
  input  [15:0] in,
  output [17:0] out
);


  assign out = {2'b00, in};
endmodule

module headdispriadok (
  input  clock,
  input  hodn,
  input  [3:0] X,
  input  clear,
  output [19:0] riadok
);

  wire demultiplexer_1_out0, demultiplexer_1_out1, demultiplexer_1_out2, demultiplexer_1_out3,
       demultiplexer_1_out4, demultiplexer_1_out5, demultiplexer_1_out6, demultiplexer_1_out7,
       demultiplexer_1_out8, demultiplexer_1_out9, demultiplexer_1_out10, demultiplexer_1_out11,
       demultiplexer_1_out12, demultiplexer_1_out13, demultiplexer_1_out14, demultiplexer_1_out15;

  Demultiplexer #(.select(4)) demultiplexer_1 (
    .out0(demultiplexer_1_out0), .out1(demultiplexer_1_out1), .out2(demultiplexer_1_out2),
    .out3(demultiplexer_1_out3), .out4(demultiplexer_1_out4), .out5(demultiplexer_1_out5),
    .out6(demultiplexer_1_out6), .out7(demultiplexer_1_out7), .out8(demultiplexer_1_out8),
    .out9(demultiplexer_1_out9), .out10(demultiplexer_1_out10), .out11(demultiplexer_1_out11),
    .out12(demultiplexer_1_out12), .out13(demultiplexer_1_out13), .out14(demultiplexer_1_out14),
    .out15(demultiplexer_1_out15), .in(clock), .sel(X));  // open: en
  D_Flip_Flop d_ff_1 (.clk(demultiplexer_1_out0), .D(hodn), .Q(riadok[15]), .reset(clear));  // open: Qn, preset, en
  D_Flip_Flop d_ff_2 (.clk(demultiplexer_1_out1), .D(hodn), .Q(riadok[14]), .reset(clear));  // open: Qn, preset, en
  D_Flip_Flop d_ff_3 (.clk(demultiplexer_1_out2), .D(hodn), .Q(riadok[13]), .reset(clear));  // open: Qn, preset, en
  D_Flip_Flop d_ff_4 (.clk(demultiplexer_1_out3), .D(hodn), .Q(riadok[12]), .reset(clear));  // open: Qn, preset, en
  D_Flip_Flop d_ff_5 (.clk(demultiplexer_1_out5), .D(hodn), .Q(riadok[10]), .reset(clear));  // open: Qn, preset, en
  D_Flip_Flop d_ff_6 (.clk(demultiplexer_1_out4), .D(hodn), .Q(riadok[11]), .reset(clear));  // open: Qn, preset, en
  D_Flip_Flop d_ff_7 (.clk(demultiplexer_1_out6), .D(hodn), .Q(riadok[9]), .reset(clear));  // open: Qn, preset, en
  D_Flip_Flop d_ff_8 (.clk(demultiplexer_1_out7), .D(hodn), .Q(riadok[8]), .reset(clear));  // open: Qn, preset, en
  D_Flip_Flop d_ff_9 (.clk(demultiplexer_1_out8), .D(hodn), .Q(riadok[7]), .reset(clear));  // open: Qn, preset, en
  D_Flip_Flop d_ff_10 (.clk(demultiplexer_1_out9), .D(hodn), .Q(riadok[6]), .reset(clear));  // open: Qn, preset, en
  D_Flip_Flop d_ff_11 (.clk(demultiplexer_1_out10), .D(hodn), .Q(riadok[5]), .reset(clear));  // open: Qn, preset, en
  D_Flip_Flop d_ff_12 (.clk(demultiplexer_1_out11), .D(hodn), .Q(riadok[4]), .reset(clear));  // open: Qn, preset, en
  D_Flip_Flop d_ff_13 (.clk(demultiplexer_1_out12), .D(hodn), .Q(riadok[3]), .reset(clear));  // open: Qn, preset, en
  D_Flip_Flop d_ff_14 (.clk(demultiplexer_1_out13), .D(hodn), .Q(riadok[2]), .reset(clear));  // open: Qn, preset, en
  D_Flip_Flop d_ff_15 (.clk(demultiplexer_1_out14), .D(hodn), .Q(riadok[1]), .reset(clear));  // open: Qn, preset, en
  D_Flip_Flop d_ff_16 (.clk(demultiplexer_1_out15), .D(hodn), .Q(riadok[0]), .reset(clear));  // open: Qn, preset, en

  assign riadok[19:16] = 4'b0000;
endmodule

module headdisp (
  input  [3:0] X,
  input  clock,
  input  [3:0] Y,
  input  clear,
  output [19:0] out_5,
  output [19:0] out_6,
  output [19:0] out_7,
  output [19:0] out_8,
  output [19:0] out_9,
  output [19:0] out_10,
  output [19:0] out_11,
  output [19:0] out_12,
  output [19:0] out_13,
  output [19:0] out_14,
  output [19:0] out_15,
  output [19:0] out_16,
  output [19:0] out_17,
  output [19:0] out_18,
  output [19:0] out_19,
  output [19:0] out_20
);

  wire demultiplexer_1_out0, demultiplexer_1_out1, demultiplexer_1_out2, demultiplexer_1_out3,
       demultiplexer_1_out4, demultiplexer_1_out5, demultiplexer_1_out6, demultiplexer_1_out7,
       demultiplexer_1_out8, demultiplexer_1_out9, demultiplexer_1_out10, demultiplexer_1_out11,
       demultiplexer_1_out12, demultiplexer_1_out13, demultiplexer_1_out14, demultiplexer_1_out15;

  Demultiplexer #(.select(4)) demultiplexer_1 (
    .out0(demultiplexer_1_out0), .out1(demultiplexer_1_out1), .out2(demultiplexer_1_out2),
    .out3(demultiplexer_1_out3), .out4(demultiplexer_1_out4), .out5(demultiplexer_1_out5),
    .out6(demultiplexer_1_out6), .out7(demultiplexer_1_out7), .out8(demultiplexer_1_out8),
    .out9(demultiplexer_1_out9), .out10(demultiplexer_1_out10), .out11(demultiplexer_1_out11),
    .out12(demultiplexer_1_out12), .out13(demultiplexer_1_out13), .out14(demultiplexer_1_out14),
    .out15(demultiplexer_1_out15), .in(clock), .sel(Y));  // open: en
  headdispriadok headdispriadok_1 (.clock(demultiplexer_1_out15), .hodn(clock), .X(X), .clear(clear), .riadok(out_5));
  headdispriadok headdispriadok_2 (.clock(demultiplexer_1_out14), .hodn(clock), .X(X), .clear(clear), .riadok(out_6));
  headdispriadok headdispriadok_3 (.clock(demultiplexer_1_out13), .hodn(clock), .X(X), .clear(clear), .riadok(out_7));
  headdispriadok headdispriadok_4 (.clock(demultiplexer_1_out12), .hodn(clock), .X(X), .clear(clear), .riadok(out_8));
  headdispriadok headdispriadok_5 (.clock(demultiplexer_1_out11), .hodn(clock), .X(X), .clear(clear), .riadok(out_9));
  headdispriadok headdispriadok_6 (.clock(demultiplexer_1_out10), .hodn(clock), .X(X), .clear(clear), .riadok(out_10));
  headdispriadok headdispriadok_7 (.clock(demultiplexer_1_out9), .hodn(clock), .X(X), .clear(clear), .riadok(out_11));
  headdispriadok headdispriadok_8 (.clock(demultiplexer_1_out8), .hodn(clock), .X(X), .clear(clear), .riadok(out_12));
  headdispriadok headdispriadok_9 (.clock(demultiplexer_1_out7), .hodn(clock), .X(X), .clear(clear), .riadok(out_13));
  headdispriadok headdispriadok_10 (.clock(demultiplexer_1_out6), .hodn(clock), .X(X), .clear(clear), .riadok(out_14));
  headdispriadok headdispriadok_11 (.clock(demultiplexer_1_out5), .hodn(clock), .X(X), .clear(clear), .riadok(out_15));
  headdispriadok headdispriadok_12 (.clock(demultiplexer_1_out4), .hodn(clock), .X(X), .clear(clear), .riadok(out_16));
  headdispriadok headdispriadok_13 (.clock(demultiplexer_1_out3), .hodn(clock), .X(X), .clear(clear), .riadok(out_17));
  headdispriadok headdispriadok_14 (.clock(demultiplexer_1_out2), .hodn(clock), .X(X), .clear(clear), .riadok(out_18));
  headdispriadok headdispriadok_15 (.clock(demultiplexer_1_out1), .hodn(clock), .X(X), .clear(clear), .riadok(out_19));
  headdispriadok headdispriadok_16 (.clock(demultiplexer_1_out0), .hodn(clock), .X(X), .clear(clear), .riadok(out_20));
endmodule

module _16_20NOAND (
  input  [15:0] _16in,
  input  [19:0] _20in,
  output [15:0] _16out
);

  assign _16out = _16in & ~_20in[15:0];  // AND_Gate and_1, 16 bits wide
endmodule
