// Logisim project alt_snake_4.9.circ as structural Verilog
// 1
module main (
  input  \ПАУЗА ,
  input  \ГОЛОД ,
  input  in_3,
  input  in_4
);

  wire and_1_out, and_2_out, and_3_out, and_4_out, and_8_out, and_9_out, and_10_out, and_11_out, and_13_out,
       and_14_out, and_15_out, and_16_out, and_17_out, apple, AppleClear, applecol, button_1_out,
       cdm_8_mark5_1_data_inst, Change, ChangeMove, clock_1_out, clr, code, controlled_buffer_2_out,
       controlled_buffer_8_out, counter_0_1_out_3, counter_0_1_out_4, counter_0_1_out_5, counter_0_1_out_6,
       counter_0_1_out_7, counter_0_1_out_8, counter_0_1_out_9, counter_0_1_out_10, counter_0_1_out_11,
       counter_0_1_out_12, counter_0_1_out_13, counter_0_1_out_14, counter_0_1_out_15, counter_0_1_out_16,
       counter_0_1_out_17, counter_0_1_out_18, counter_1_1_out_3, counter_1_1_out_4, counter_1_1_out_5,
       counter_1_1_out_6, counter_1_1_out_7, counter_1_1_out_8, counter_1_1_out_9, counter_1_1_out_10,
       counter_1_1_out_11, counter_1_1_out_12, counter_1_1_out_13, counter_1_1_out_14, counter_1_1_out_15,
       counter_1_1_out_16, counter_1_1_out_17, counter_1_1_out_18, counter_3_carry, cpu_clr, CYCLE, d_ff_1_q,
       d_ff_2_q, data, decoder_4_out1, decoder_5_out1, Del_tick, Delete, down, first_tacktk, golod, I_Osel,
       keyboard_1_avail, keyboard_2_avail, left, lose, mem, nand_1_out, nor_1_out, nor_2_out, nor_3_out,
       nor_4_out, not_1_out, not_2_out, not_3_out, not_4_out, not_5_out, not_6_out, not_7_out, or_1_out,
       or_3_out, or_4_out, or_5_out, or_6_out, or_7_out, or_9_out, output_matrix_1_clk,
       output_matrix_1_clk_apple, output_matrix_1_clr_apple, output_matrix_1_clr_kbd,
       output_matrix_1_hunger_clk, output_matrix_1_hunger_clr, RAM, rd_wr_prime, resp, RESTART_out, right,
       takt, up, wall, win, \ГОЛОД_out_3 , \ГОЛОД_out_4 , \ГОЛОД_out_5 , \ГОЛОД_out_6 , \ГОЛОД_out_7 ,
       \ГОЛОД_out_8 , \ГОЛОД_out_9 , \ГОЛОД_out_10 , \ГОЛОД_out_11 , \ГОЛОД_out_12 , \ГОЛОД_out_13 ,
       \ГОЛОД_out_14 , \ГОЛОД_out_15 , \ГОЛОД_out_16 , \ГОЛОД_out_17 , \ГОЛОД_out_18 , \КОЛ_ВО_ЯБЛОК_out_3 ,
       \КОЛ_ВО_ЯБЛОК_out_4 , \КОЛ_ВО_ЯБЛОК_out_5 , \КОЛ_ВО_ЯБЛОК_out_6 , \КОЛ_ВО_ЯБЛОК_out_7 ,
       \КОЛ_ВО_ЯБЛОК_out_8 , \КОЛ_ВО_ЯБЛОК_out_9 , \КОЛ_ВО_ЯБЛОК_out_10 , \КОЛ_ВО_ЯБЛОК_out_11 ,
       \КОЛ_ВО_ЯБЛОК_out_12 , \КОЛ_ВО_ЯБЛОК_out_13 , \КОЛ_ВО_ЯБЛОК_out_14 , \КОЛ_ВО_ЯБЛОК_out_15 ,
       \КОЛ_ВО_ЯБЛОК_out_16 , \КОЛ_ВО_ЯБЛОК_out_17 , \КОЛ_ВО_ЯБЛОК_out_18 , \Перекус ;
  wire [1:0] Move;
  wire [3:0] cdm_8_mark5_1_ps;
  wire [6:0] \input , keyboard_1_data;
  wire [7:0] adder_1_out, adr, Apple_coord, cdm_8_mark5_1_data_out, cdm_8_mark5_1_pc, cdm_8_mark5_1_r0,
       cdm_8_mark5_1_r1, cdm_8_mark5_1_r2, cdm_8_mark5_1_r3, cdm_8_mark5_1_sp, controlled_buffer_1_out,
       controlled_buffer_5_out, Cords, head, I_Odata, inc_dec_2_r, negator_1_out, or_2_out, register_2_q,
       register_3_q;
  wire [15:0] output_matrix_1_out_12, output_matrix_1_out_17, output_matrix_1_out_22, output_matrix_1_out_27,
       output_matrix_1_out_32, output_matrix_1_out_36, output_matrix_1_out_39, output_matrix_1_out_44,
       output_matrix_1_out_49, output_matrix_1_out_54, output_matrix_1_out_58, output_matrix_1_out_61,
       output_matrix_1_out_66, output_matrix_1_out_71, output_matrix_1_out_76, output_matrix_1_out_80;
  wire [16:0] output_matrix_1_out_16, output_matrix_1_out_21, output_matrix_1_out_26, output_matrix_1_out_31,
       output_matrix_1_out_35, output_matrix_1_out_42, output_matrix_1_out_47, output_matrix_1_out_52,
       output_matrix_1_out_57, output_matrix_1_out_64, output_matrix_1_out_69, output_matrix_1_out_74,
       output_matrix_1_out_79, output_matrix_1_out_84, output_matrix_1_out_87, output_matrix_1_out_90,
       undriven;
  wire [17:0] output_matrix_1_out_15, output_matrix_1_out_20, output_matrix_1_out_25, output_matrix_1_out_30,
       output_matrix_1_out_34, output_matrix_1_out_41, output_matrix_1_out_46, output_matrix_1_out_51,
       output_matrix_1_out_56, output_matrix_1_out_63, output_matrix_1_out_68, output_matrix_1_out_73,
       output_matrix_1_out_78, output_matrix_1_out_83, output_matrix_1_out_86, output_matrix_1_out_89;
  wire [18:0] output_matrix_1_out_14, output_matrix_1_out_19, output_matrix_1_out_24, output_matrix_1_out_29,
       output_matrix_1_out_38, output_matrix_1_out_43, output_matrix_1_out_48, output_matrix_1_out_53,
       output_matrix_1_out_60, output_matrix_1_out_65, output_matrix_1_out_70, output_matrix_1_out_75,
       output_matrix_1_out_82, output_matrix_1_out_85, output_matrix_1_out_88, output_matrix_1_out_91;
  wire [19:0] output_matrix_1_out_13, output_matrix_1_out_18, output_matrix_1_out_23, output_matrix_1_out_28,
       output_matrix_1_out_33, output_matrix_1_out_37, output_matrix_1_out_40, output_matrix_1_out_45,
       output_matrix_1_out_50, output_matrix_1_out_55, output_matrix_1_out_59, output_matrix_1_out_62,
       output_matrix_1_out_67, output_matrix_1_out_72, output_matrix_1_out_77, output_matrix_1_out_81;
  wire [31:0] counter_2_q;

  assign controlled_buffer_1_out = first_tacktk ? 8'h88 : 8'bz;  // Controlled_Buffer controlled_buffer_1
  Pull_Resistor pull_resistor_1 (.node(controlled_buffer_1_out));
  or or_1 (or_1_out, clr, applecol, resp, apple);
  assign or_2_out = controlled_buffer_1_out | inc_dec_2_r;  // OR_Gate or_2, 8 bits wide
  Register register_1 (.D(or_2_out), .Q(head), .clk(CYCLE), .clr(clr));  // open: en
  // Probe on Apple_coord
  Random #(.seed(8)) random_1 (.clk(or_1_out), .out(Apple_coord));  // open: next, clr
  // Probe on head
  output_matrix output_matrix_1 (
    .out_14(output_matrix_1_out_14), .out_15(output_matrix_1_out_15), .out_16(output_matrix_1_out_16),
    .out_12(output_matrix_1_out_12), .out_19(output_matrix_1_out_19), .out_20(output_matrix_1_out_20),
    .out_21(output_matrix_1_out_21), .out_17(output_matrix_1_out_17), .out_24(output_matrix_1_out_24),
    .out_25(output_matrix_1_out_25), .out_26(output_matrix_1_out_26), .out_22(output_matrix_1_out_22),
    .out_29(output_matrix_1_out_29), .out_30(output_matrix_1_out_30), .out_31(output_matrix_1_out_31),
    .out_27(output_matrix_1_out_27), .out_34(output_matrix_1_out_34), .out_35(output_matrix_1_out_35),
    .out_32(output_matrix_1_out_32), .out_38(output_matrix_1_out_38), .out_41(output_matrix_1_out_41),
    .out_42(output_matrix_1_out_42), .out_36(output_matrix_1_out_36), .out_43(output_matrix_1_out_43),
    .out_46(output_matrix_1_out_46), .out_47(output_matrix_1_out_47), .out_39(output_matrix_1_out_39),
    .out_48(output_matrix_1_out_48), .out_51(output_matrix_1_out_51), .out_52(output_matrix_1_out_52),
    .out_44(output_matrix_1_out_44), .out_53(output_matrix_1_out_53), .out_56(output_matrix_1_out_56),
    .out_57(output_matrix_1_out_57), .out_49(output_matrix_1_out_49), .out_60(output_matrix_1_out_60),
    .out_63(output_matrix_1_out_63), .out_64(output_matrix_1_out_64), .out_54(output_matrix_1_out_54),
    .out_65(output_matrix_1_out_65), .out_68(output_matrix_1_out_68), .out_69(output_matrix_1_out_69),
    .out_58(output_matrix_1_out_58), .out_70(output_matrix_1_out_70), .out_73(output_matrix_1_out_73),
    .out_74(output_matrix_1_out_74), .out_61(output_matrix_1_out_61), .out_75(output_matrix_1_out_75),
    .out_78(output_matrix_1_out_78), .out_79(output_matrix_1_out_79), .out_66(output_matrix_1_out_66),
    .out_82(output_matrix_1_out_82), .out_83(output_matrix_1_out_83), .out_84(output_matrix_1_out_84),
    .out_71(output_matrix_1_out_71), .out_85(output_matrix_1_out_85), .out_86(output_matrix_1_out_86),
    .out_87(output_matrix_1_out_87), .out_76(output_matrix_1_out_76), .out_88(output_matrix_1_out_88),
    .out_89(output_matrix_1_out_89), .out_90(output_matrix_1_out_90), .out_80(output_matrix_1_out_80),
    .out_91(output_matrix_1_out_91), .out_13(output_matrix_1_out_13), .out_18(output_matrix_1_out_18),
    .out_23(output_matrix_1_out_23), .out_28(output_matrix_1_out_28), .out_33(output_matrix_1_out_33),
    .out_37(output_matrix_1_out_37), .out_40(output_matrix_1_out_40), .out_45(output_matrix_1_out_45),
    .out_50(output_matrix_1_out_50), .out_55(output_matrix_1_out_55), .out_59(output_matrix_1_out_59),
    .out_62(output_matrix_1_out_62), .out_67(output_matrix_1_out_67), .out_72(output_matrix_1_out_72),
    .out_77(output_matrix_1_out_77), .out_81(output_matrix_1_out_81), .Paus(\ПАУЗА ),
    .clr_button(RESTART_out), .golod(\ГОЛОД ), .clk(output_matrix_1_clk), .\input (keyboard_1_data),
    .clr_kbd(output_matrix_1_clr_kbd), .available(keyboard_1_avail), .clk_apple(output_matrix_1_clk_apple),
    .clr_apple(output_matrix_1_clr_apple), .hunger_clk(output_matrix_1_hunger_clk),
    .hunger_clr(output_matrix_1_hunger_clr));
  or or_3 (or_3_out, left, right);
  or or_4 (or_4_out, down, up);
  Adder adder_1 (.a(Apple_coord), .b(negator_1_out), .out(adder_1_out));  // open: cin, cout
  Negator negator_1 (.in(head), .out(negator_1_out));
  and and_1 (and_1_out, head[4], head[5], head[6], head[7]);
  and and_2 (and_2_out, head[0], head[1], head[2], head[3]);
  nor nor_1 (nor_1_out, head[4], head[5], head[6], head[7]);
  nor nor_2 (nor_2_out, head[0], head[1], head[2], head[3]);
  and and_3 (and_3_out, Apple_coord[0], Apple_coord[1], Apple_coord[2], Apple_coord[3]);
  and and_4 (and_4_out, Apple_coord[4], Apple_coord[5], Apple_coord[6], Apple_coord[7]);
  nor nor_3 (nor_3_out, Apple_coord[0], Apple_coord[1], Apple_coord[2], Apple_coord[3]);
  nor nor_4 (nor_4_out, Apple_coord[4], Apple_coord[5], Apple_coord[6], Apple_coord[7]);
  inc_dec inc_dec_1 (.X(head[7:4]), .on_off(or_3_out), .inc_dec(right), .R(inc_dec_2_r[7:4]));
  inc_dec inc_dec_2 (.X(head[3:0]), .on_off(or_4_out), .inc_dec(up), .R(inc_dec_2_r[3:0]));
  or or_5 (or_5_out, and_1_out, and_2_out, nor_1_out, nor_2_out);
  or or_6 (or_6_out, and_3_out, and_4_out, nor_3_out, nor_4_out);
  not not_1 (not_1_out, in_3);
  Clock clock_1 (.out(clock_1_out));
  assign controlled_buffer_2_out = not_1_out ? clock_1_out : 1'bz;  // Controlled_Buffer controlled_buffer_2
  or or_7 (or_7_out, lose, win);
  nor nor_5 (apple, adder_1_out[0], adder_1_out[1], adder_1_out[2], adder_1_out[3], adder_1_out[4], adder_1_out[5], adder_1_out[6], adder_1_out[7]);
  Counter #(.width(1), .max('h1), .ongoal("stay")) counter_1 (
    .carry(wall), .clk(or_5_out), .clr(clr));  // open: load, D, count, Q
  and and_5 (resp, or_6_out, takt);
  Pull_Resistor pull_resistor_2 (.node(controlled_buffer_2_out));
  Multiplexer multiplexer_1 (.in0(controlled_buffer_2_out), .in1(1'b0), .out(takt), .sel(d_ff_1_q));  // open: en
  D_Flip_Flop d_ff_1 (.Q(d_ff_1_q), .preset(or_7_out), .reset(clr));  // open: clk, D, Qn, en
  Counter #(.width(32), .max('hffffffff)) counter_2 (
    .Q(counter_2_q), .clk(CYCLE), .clr(clr));  // open: load, D, count, carry
  and and_6 (I_Osel, not_3_out, takt, data);
  assign I_Odata = not_2_out ? {{6{1'b0}}, Move} : 8'bz;  // Controlled_Buffer controlled_buffer_3
  not not_2 (not_2_out, not_4_out);
  D_Flip_Flop d_ff_2 (.Q(d_ff_2_q), .preset(\Перекус ), .reset(clr));  // open: clk, D, Qn, en
  Comparator #(.width(32), .mode("unsigned")) comparator_1 (
    .a({32{1'b0}}), .b(counter_2_q), .eq(first_tacktk));  // open: gt, lt
  granica_1 granica_1_1 ();
  // Probe on cdm_8_mark5_1_r1
  // Probe on cdm_8_mark5_1_r0
  not not_3 (not_3_out, nand_1_out);
  and and_7 (RAM, nand_1_out, data);
  not not_4 (not_4_out, ChangeMove);
  or or_8 (lose, golod, wall, d_ff_2_q);
  Counter #(.max('ha)) counter_3 (.carry(counter_3_carry), .clk(apple), .clr(clr));  // open: load, D, count, Q
  // Probe on cdm_8_mark5_1_r3
  // Probe on cdm_8_mark5_1_r2
  // Probe on cdm_8_mark5_1_sp
  // Probe on cdm_8_mark5_1_pc
  nand nand_1 (nand_1_out, adr[4], adr[5], adr[6], adr[7]);
  and and_8 (and_8_out, I_Osel, adr[0], adr[1], ~adr[2], ~adr[3]);  // AND_Gate
  Decoder #(.disabled(0)) decoder_1 (.out1(ChangeMove), .sel(rd_wr_prime), .en(and_8_out));  // open: out0
  D_Flip_Flop d_ff_3 (.Q(win), .preset(counter_3_carry), .reset(clr));  // open: clk, D, Qn, en
  // Probe on cdm_8_mark5_1_ps
  Decoder #(.disabled(0)) decoder_2 (.out0(code), .out1(data), .sel(cdm_8_mark5_1_data_inst), .en(mem));
  CdM_8_mark5 cdm_8_mark5_1 (
    .clock(takt), .addr(adr), .mem_read(rd_wr_prime), .mem_cycle(mem), .data_inst(cdm_8_mark5_1_data_inst),
    .data_out(cdm_8_mark5_1_data_out), .data_in(controlled_buffer_5_out), .r0(cdm_8_mark5_1_r0),
    .r1(cdm_8_mark5_1_r1), .r2(cdm_8_mark5_1_r2), .r3(cdm_8_mark5_1_r3), .PC(cdm_8_mark5_1_pc),
    .SP(cdm_8_mark5_1_sp), .PS(cdm_8_mark5_1_ps));
  not not_5 (not_5_out, rd_wr_prime);
  assign I_Odata = not_5_out ? cdm_8_mark5_1_data_out : 8'bz;  // Controlled_Buffer controlled_buffer_4
  assign controlled_buffer_5_out = rd_wr_prime ? I_Odata : 8'bz;  // Controlled_Buffer controlled_buffer_5
  assign I_Odata = Change ? head : 8'bz;  // Controlled_Buffer controlled_buffer_6
  _7_Segment_Display u_7_segment_display_1 (
    .g(\КОЛ_ВО_ЯБЛОК_out_3 ), .f(\КОЛ_ВО_ЯБЛОК_out_4 ), .a(\КОЛ_ВО_ЯБЛОК_out_5 ), .b(\КОЛ_ВО_ЯБЛОК_out_6 ),
    .e(\КОЛ_ВО_ЯБЛОК_out_11 ), .d(\КОЛ_ВО_ЯБЛОК_out_12 ), .c(\КОЛ_ВО_ЯБЛОК_out_13 ),
    .dp(\КОЛ_ВО_ЯБЛОК_out_14 ));
  _7_Segment_Display u_7_segment_display_2 (
    .g(\КОЛ_ВО_ЯБЛОК_out_7 ), .f(\КОЛ_ВО_ЯБЛОК_out_8 ), .a(\КОЛ_ВО_ЯБЛОК_out_9 ), .b(\КОЛ_ВО_ЯБЛОК_out_10 ),
    .e(\КОЛ_ВО_ЯБЛОК_out_15 ), .d(\КОЛ_ВО_ЯБЛОК_out_16 ), .c(\КОЛ_ВО_ЯБЛОК_out_17 ),
    .dp(\КОЛ_ВО_ЯБЛОК_out_18 ));
  counter_0 \u_КОЛ_ВО_ЯБЛОК  (
    .clock(output_matrix_1_clk_apple), .clear(output_matrix_1_clr_apple), .out_11(\КОЛ_ВО_ЯБЛОК_out_11 ),
    .out_12(\КОЛ_ВО_ЯБЛОК_out_12 ), .out_13(\КОЛ_ВО_ЯБЛОК_out_13 ), .out_14(\КОЛ_ВО_ЯБЛОК_out_14 ),
    .out_15(\КОЛ_ВО_ЯБЛОК_out_15 ), .out_16(\КОЛ_ВО_ЯБЛОК_out_16 ), .out_17(\КОЛ_ВО_ЯБЛОК_out_17 ),
    .out_18(\КОЛ_ВО_ЯБЛОК_out_18 ), .out_3(\КОЛ_ВО_ЯБЛОК_out_3 ), .out_4(\КОЛ_ВО_ЯБЛОК_out_4 ),
    .out_5(\КОЛ_ВО_ЯБЛОК_out_5 ), .out_6(\КОЛ_ВО_ЯБЛОК_out_6 ), .out_7(\КОЛ_ВО_ЯБЛОК_out_7 ),
    .out_8(\КОЛ_ВО_ЯБЛОК_out_8 ), .out_9(\КОЛ_ВО_ЯБЛОК_out_9 ), .out_10(\КОЛ_ВО_ЯБЛОК_out_10 ));
  DotMatrix #(.inputtype("row"), .matrixcols(20), .matrixrows(16)) dotmatrix_1 (
    .row0(output_matrix_1_out_13), .row1(output_matrix_1_out_18), .row2(output_matrix_1_out_23),
    .row3(output_matrix_1_out_28), .row4(output_matrix_1_out_33), .row5(output_matrix_1_out_37),
    .row6(output_matrix_1_out_40), .row7(output_matrix_1_out_45), .row8(output_matrix_1_out_50),
    .row9(output_matrix_1_out_55), .row10(output_matrix_1_out_59), .row11(output_matrix_1_out_62),
    .row12(output_matrix_1_out_67), .row13(output_matrix_1_out_72), .row14(output_matrix_1_out_77),
    .row15(output_matrix_1_out_81));
  DotMatrix #(.inputtype("row"), .matrixcols(19), .matrixrows(16)) dotmatrix_2 (
    .row0(output_matrix_1_out_14), .row1(output_matrix_1_out_19), .row2(output_matrix_1_out_24),
    .row3(output_matrix_1_out_29), .row4(output_matrix_1_out_38), .row5(output_matrix_1_out_43),
    .row6(output_matrix_1_out_48), .row7(output_matrix_1_out_53), .row8(output_matrix_1_out_60),
    .row9(output_matrix_1_out_65), .row10(output_matrix_1_out_70), .row11(output_matrix_1_out_75),
    .row12(output_matrix_1_out_82), .row13(output_matrix_1_out_85), .row14(output_matrix_1_out_88),
    .row15(output_matrix_1_out_91));
  DotMatrix #(.inputtype("row"), .matrixcols(16), .matrixrows(16)) dotmatrix_3 (
    .row0(output_matrix_1_out_12), .row1(output_matrix_1_out_17), .row2(output_matrix_1_out_22),
    .row3(output_matrix_1_out_27), .row4(output_matrix_1_out_32), .row5(output_matrix_1_out_36),
    .row6(output_matrix_1_out_39), .row7(output_matrix_1_out_44), .row8(output_matrix_1_out_49),
    .row9(output_matrix_1_out_54), .row10(output_matrix_1_out_58), .row11(output_matrix_1_out_61),
    .row12(output_matrix_1_out_66), .row13(output_matrix_1_out_71), .row14(output_matrix_1_out_76),
    .row15(output_matrix_1_out_80));
  DotMatrix #(.inputtype("row"), .matrixcols(18), .matrixrows(16)) dotmatrix_4 (
    .row0(output_matrix_1_out_15), .row1(output_matrix_1_out_20), .row2(output_matrix_1_out_25),
    .row3(output_matrix_1_out_30), .row4(output_matrix_1_out_34), .row5(output_matrix_1_out_41),
    .row6(output_matrix_1_out_46), .row7(output_matrix_1_out_51), .row8(output_matrix_1_out_56),
    .row9(output_matrix_1_out_63), .row10(output_matrix_1_out_68), .row11(output_matrix_1_out_73),
    .row12(output_matrix_1_out_78), .row13(output_matrix_1_out_83), .row14(output_matrix_1_out_86),
    .row15(output_matrix_1_out_89));
  DotMatrix #(.inputtype("row"), .matrixcols(17), .matrixrows(16)) dotmatrix_5 (
    .row0(output_matrix_1_out_16), .row1(output_matrix_1_out_21), .row2(output_matrix_1_out_26),
    .row3(output_matrix_1_out_31), .row4(output_matrix_1_out_35), .row5(output_matrix_1_out_42),
    .row6(output_matrix_1_out_47), .row7(output_matrix_1_out_52), .row8(output_matrix_1_out_57),
    .row9(output_matrix_1_out_64), .row10(output_matrix_1_out_69), .row11(output_matrix_1_out_74),
    .row12(output_matrix_1_out_79), .row13(output_matrix_1_out_84), .row14(output_matrix_1_out_87),
    .row15(output_matrix_1_out_90));
  DotMatrix #(.matrixcols(4), .matrixrows(17)) dotmatrix_6 (.col1(undriven), .col2(undriven));  // open: col0, col3
  Keyboard keyboard_1 (
    .clk(output_matrix_1_clk), .clr(output_matrix_1_clr_kbd), .avail(keyboard_1_avail), .data(keyboard_1_data));  // open: re
  golod golod_1 (.stop_golod(in_4), .clock(CYCLE), .clr(clr), .apple(apple), .golod(golod));
  counter_1 \u_ГОЛОД  (
    .clock(output_matrix_1_hunger_clk), .clear(output_matrix_1_hunger_clr), .out_11(\ГОЛОД_out_11 ),
    .out_12(\ГОЛОД_out_12 ), .out_13(\ГОЛОД_out_13 ), .out_14(\ГОЛОД_out_14 ), .out_15(\ГОЛОД_out_15 ),
    .out_16(\ГОЛОД_out_16 ), .out_17(\ГОЛОД_out_17 ), .out_18(\ГОЛОД_out_18 ), .out_3(\ГОЛОД_out_3 ),
    .out_4(\ГОЛОД_out_4 ), .out_5(\ГОЛОД_out_5 ), .out_6(\ГОЛОД_out_6 ), .out_7(\ГОЛОД_out_7 ),
    .out_8(\ГОЛОД_out_8 ), .out_9(\ГОЛОД_out_9 ), .out_10(\ГОЛОД_out_10 ));
  _7_Segment_Display u_7_segment_display_3 (
    .g(\ГОЛОД_out_3 ), .f(\ГОЛОД_out_4 ), .a(\ГОЛОД_out_5 ), .b(\ГОЛОД_out_6 ), .e(\ГОЛОД_out_11 ),
    .d(\ГОЛОД_out_12 ), .c(\ГОЛОД_out_13 ), .dp(\ГОЛОД_out_14 ));
  Pull_Resistor pull_resistor_3 (.node(adr[0]));
  Pull_Resistor pull_resistor_4 (.node(adr[1]));
  Pull_Resistor pull_resistor_5 (.node(adr[2]));
  Pull_Resistor pull_resistor_6 (.node(adr[3]));
  Pull_Resistor pull_resistor_7 (.node(adr[4]));
  Pull_Resistor pull_resistor_8 (.node(adr[5]));
  Pull_Resistor pull_resistor_9 (.node(adr[6]));
  Pull_Resistor pull_resistor_10 (.node(adr[7]));
  and and_9 (and_9_out, I_Osel, adr[0], ~adr[1], adr[2], ~adr[3]);  // AND_Gate
  Decoder #(.disabled(0)) decoder_3 (.out1(Change), .sel(rd_wr_prime), .en(and_9_out));  // open: out0
  _7_Segment_Display u_7_segment_display_4 (
    .g(\ГОЛОД_out_7 ), .f(\ГОЛОД_out_8 ), .a(\ГОЛОД_out_9 ), .b(\ГОЛОД_out_10 ), .e(\ГОЛОД_out_15 ),
    .d(\ГОЛОД_out_16 ), .c(\ГОЛОД_out_17 ), .dp(\ГОЛОД_out_18 ));
  Button RESTART (.out(RESTART_out));
  ROM rom_1 (.addr(adr), .data(I_Odata), .sel(code));
  RAM ram_1 (.addr(adr), .data(I_Odata), .sel(RAM), .clk(takt), .ld(rd_wr_prime), .clr(clr));
  movement movement_1 (
    .\input (\input ), .Clear(clr), .Move(Move), .up(up), .right(right), .down(down), .left(left),
    .Clk(ChangeMove));
  Register register_2 (.D({{7{1'b0}}, apple}), .Q(register_2_q), .clk(apple), .clr(AppleClear));  // open: en
  _7_Segment_Display u_7_segment_display_5 (
    .g(counter_0_1_out_3), .f(counter_0_1_out_4), .a(counter_0_1_out_5), .b(counter_0_1_out_6),
    .e(counter_0_1_out_11), .d(counter_0_1_out_12), .c(counter_0_1_out_13), .dp(counter_0_1_out_14));
  counter_0 counter_0_1 (
    .clock(apple), .clear(clr), .out_11(counter_0_1_out_11), .out_12(counter_0_1_out_12),
    .out_13(counter_0_1_out_13), .out_14(counter_0_1_out_14), .out_15(counter_0_1_out_15),
    .out_16(counter_0_1_out_16), .out_17(counter_0_1_out_17), .out_18(counter_0_1_out_18),
    .out_3(counter_0_1_out_3), .out_4(counter_0_1_out_4), .out_5(counter_0_1_out_5),
    .out_6(counter_0_1_out_6), .out_7(counter_0_1_out_7), .out_8(counter_0_1_out_8),
    .out_9(counter_0_1_out_9), .out_10(counter_0_1_out_10));
  DotMatrix #(.inputtype("row"), .matrixcols(18), .matrixrows(16)) dotmatrix_7 ();  // open: row0, row1, row2, row3, row4, row5, row6, row7, row8, row9, row10, row11, row12, row13, row14, row15
  DotMatrix #(.inputtype("row"), .matrixcols(20), .matrixrows(16)) dotmatrix_8 ();  // open: row0, row1, row2, row3, row4, row5, row6, row7, row8, row9, row10, row11, row12, row13, row14, row15
  DotMatrix #(.inputtype("row"), .matrixcols(19), .matrixrows(16)) dotmatrix_9 ();  // open: row0, row1, row2, row3, row4, row5, row6, row7, row8, row9, row10, row11, row12, row13, row14, row15
  assign I_Odata = decoder_4_out1 ? register_2_q : 8'bz;  // Controlled_Buffer controlled_buffer_7
  and and_10 (and_10_out, CYCLE, in_4);
  _7_Segment_Display u_7_segment_display_6 (
    .g(counter_0_1_out_7), .f(counter_0_1_out_8), .a(counter_0_1_out_9), .b(counter_0_1_out_10),
    .e(counter_0_1_out_15), .d(counter_0_1_out_16), .c(counter_0_1_out_17), .dp(counter_0_1_out_18));
  DotMatrix #(.inputtype("row"), .matrixcols(16), .matrixrows(16)) dotmatrix_10 ();  // open: row0, row1, row2, row3, row4, row5, row6, row7, row8, row9, row10, row11, row12, row13, row14, row15
  DotMatrix #(.inputtype("row"), .matrixcols(17), .matrixrows(16)) dotmatrix_11 ();  // open: row0, row1, row2, row3, row4, row5, row6, row7, row8, row9, row10, row11, row12, row13, row14, row15
  Keyboard keyboard_2 (.clk(controlled_buffer_8_out), .clr(clr), .avail(keyboard_2_avail), .data(\input ));  // open: re
  assign controlled_buffer_8_out = keyboard_2_avail ? takt : 1'bz;  // Controlled_Buffer controlled_buffer_8
  and and_11 (and_11_out, I_Osel, ~adr[0], adr[1], adr[2], ~adr[3]);  // AND_Gate
  _7_Segment_Display u_7_segment_display_7 (
    .g(counter_1_1_out_7), .f(counter_1_1_out_8), .a(counter_1_1_out_9), .b(counter_1_1_out_10),
    .e(counter_1_1_out_15), .d(counter_1_1_out_16), .c(counter_1_1_out_17), .dp(counter_1_1_out_18));
  counter_1 counter_1_1 (
    .clock(and_10_out), .clear(or_9_out), .out_11(counter_1_1_out_11), .out_12(counter_1_1_out_12),
    .out_13(counter_1_1_out_13), .out_14(counter_1_1_out_14), .out_15(counter_1_1_out_15),
    .out_16(counter_1_1_out_16), .out_17(counter_1_1_out_17), .out_18(counter_1_1_out_18),
    .out_3(counter_1_1_out_3), .out_4(counter_1_1_out_4), .out_5(counter_1_1_out_5),
    .out_6(counter_1_1_out_6), .out_7(counter_1_1_out_7), .out_8(counter_1_1_out_8),
    .out_9(counter_1_1_out_9), .out_10(counter_1_1_out_10));
  _7_Segment_Display u_7_segment_display_8 (
    .g(counter_1_1_out_3), .f(counter_1_1_out_4), .a(counter_1_1_out_5), .b(counter_1_1_out_6),
    .e(counter_1_1_out_11), .d(counter_1_1_out_12), .c(counter_1_1_out_13), .dp(counter_1_1_out_14));
  Decoder #(.disabled(0)) decoder_4 (.out1(decoder_4_out1), .sel(rd_wr_prime), .en(and_11_out));  // open: out0
  or or_9 (or_9_out, clr, apple);
  Button button_1 (.out(button_1_out));
  and and_12 (cpu_clr, ~adr[0], adr[1], ~adr[2], adr[3], adr[4], adr[5], adr[6], adr[7]);  // AND_Gate
  Pull_Resistor pull_resistor_11 (.node(AppleClear));
  assign AppleClear = and_13_out ? 1'b1 : 1'bz;  // Controlled_Buffer controlled_buffer_9
  and and_13 (and_13_out, adr[0], adr[1], adr[2], ~adr[3], adr[4], adr[5], adr[6], adr[7]);  // AND_Gate
  not not_6 (not_6_out, not_7_out);
  not not_7 (not_7_out, clr);
  or or_10 (clr, button_1_out, cpu_clr);
  assign I_Odata = decoder_5_out1 ? register_3_q : 8'bz;  // Controlled_Buffer controlled_buffer_10
  Register register_3 (.D({{7{1'b0}}, clr}), .Q(register_3_q), .clk(not_6_out), .clr(cpu_clr));  // open: en
  and and_14 (and_14_out, I_Osel, adr[0], ~adr[1], ~adr[2], adr[3]);  // AND_Gate
  and and_15 (and_15_out, ~adr[0], ~adr[1], ~adr[2], adr[3], adr[4], adr[5], adr[6], adr[7]);  // AND_Gate
  and and_16 (and_16_out, adr[0], adr[1], adr[2], adr[3], adr[4], adr[5], adr[6], adr[7]);
  Decoder #(.disabled(0)) decoder_5 (.out1(decoder_5_out1), .sel(rd_wr_prime), .en(and_14_out));  // open: out0
  Pull_Resistor pull_resistor_12 (.node(CYCLE));
  assign CYCLE = and_15_out ? 1'b1 : 1'bz;  // Controlled_Buffer controlled_buffer_11
  Register #(.width(1)) register_4 (.D(Del_tick), .Q(Delete), .clk(takt), .clr(CYCLE));  // open: en
  assign Del_tick = and_16_out ? 1'b1 : 1'bz;  // Controlled_Buffer controlled_buffer_12
  and and_17 (and_17_out, adr[0], ~adr[1], ~adr[2], ~adr[3], adr[4], adr[5], ~adr[6], adr[7]);  // AND_Gate
  assign Cords = and_17_out ? I_Odata : 8'bz;  // Controlled_Buffer controlled_buffer_13

  // Other names for the same wires on the sheet: I_Oadr[3:0] = adr[3:0]; paus = in_3; stop_golod = in_4;
  //   x[3:0] = head[3:0]; y[3:0] = head[7:4]

  // Notes on the sheet:
  //   Получение направления
  //   Получение координат головы
  //   contents of rom_1 (hex, n*v repeats v):
  //   d0 fa b0 cd f0 d1 3 c1 d1 b5 d0 87 a4 d0 f8 b0 d0 f9 b0 0 e0 18 ee 0 d0 f5 b0 d1 b1 a4 d0 f3 b0 d1
  //   b4 b6 a4 78 e1 2f cb 0 bd 8d ad ee 37 6*20 8c c0 d0 f6 b0 0 e1 84 d0 ef b1 89 a1 d0 3f 41 e1 5a c8 0
  //   d1 f0 31 85 c6 8c 5 e0 59 b3 a2 8c e 89 ee 50 a2 d3 ef bf d2 c0 d0 40 4e e1 68 d3 1 ee 79 78 e1 6f
  //   d3 10 ee 79 20 78 e1 77 d3 ff ee 79 d3 f0 d0 b5 b1 d2 ff ba d2 b1 a9 17 a3 d0 f7 b0 d0 f8 b0 ee 10
  //   Бит съеденного яблока
  //   Количество яблочек
  //   Голод
  //   Очищение
  //   Бит очищения яблочка
  //   1 - пауза 0 играем
  //   1 - есть 0 - нет голода
  //   Бит удаления
  //   Флаг очищения
  //   Бит конца цикла процессора
  //   Координаты змейки
endmodule

module output_matrix (
  input  Paus,
  input  available,
  input  clr_button,
  input  golod,
  input  [6:0] \input ,
  output clk,
  output clk_apple,
  output clr_apple,
  output clr_kbd,
  output hunger_clk,
  output hunger_clr,
  output [15:0] out_12,
  output [19:0] out_13,
  output [18:0] out_14,
  output [17:0] out_15,
  output [16:0] out_16,
  output [15:0] out_17,
  output [19:0] out_18,
  output [18:0] out_19,
  output [17:0] out_20,
  output [16:0] out_21,
  output [15:0] out_22,
  output [19:0] out_23,
  output [18:0] out_24,
  output [17:0] out_25,
  output [16:0] out_26,
  output [15:0] out_27,
  output [19:0] out_28,
  output [18:0] out_29,
  output [17:0] out_30,
  output [16:0] out_31,
  output [15:0] out_32,
  output [19:0] out_33,
  output [17:0] out_34,
  output [16:0] out_35,
  output [15:0] out_36,
  output [19:0] out_37,
  output [18:0] out_38,
  output [15:0] out_39,
  output [19:0] out_40,
  output [17:0] out_41,
  output [16:0] out_42,
  output [18:0] out_43,
  output [15:0] out_44,
  output [19:0] out_45,
  output [17:0] out_46,
  output [16:0] out_47,
  output [18:0] out_48,
  output [15:0] out_49,
  output [19:0] out_50,
  output [17:0] out_51,
  output [16:0] out_52,
  output [18:0] out_53,
  output [15:0] out_54,
  output [19:0] out_55,
  output [17:0] out_56,
  output [16:0] out_57,
  output [15:0] out_58,
  output [19:0] out_59,
  output [18:0] out_60,
  output [15:0] out_61,
  output [19:0] out_62,
  output [17:0] out_63,
  output [16:0] out_64,
  output [18:0] out_65,
  output [15:0] out_66,
  output [19:0] out_67,
  output [17:0] out_68,
  output [16:0] out_69,
  output [18:0] out_70,
  output [15:0] out_71,
  output [19:0] out_72,
  output [17:0] out_73,
  output [16:0] out_74,
  output [18:0] out_75,
  output [15:0] out_76,
  output [19:0] out_77,
  output [17:0] out_78,
  output [16:0] out_79,
  output [15:0] out_80,
  output [19:0] out_81,
  output [18:0] out_82,
  output [17:0] out_83,
  output [16:0] out_84,
  output [18:0] out_85,
  output [17:0] out_86,
  output [16:0] out_87,
  output [18:0] out_88,
  output [17:0] out_89,
  output [16:0] out_90,
  output [18:0] out_91
);

  wire and_1_out, and_2_out, and_3_out, and_4_out, and_9_out, and_10_out, and_11_out, and_13_out, and_14_out,
       and_15_out, and_16_out, and_17_out, AppleClear, applecpl, cdm_8_mark5_1_data_inst, Change, ChangeMove,
       clock_1_out, code, controlled_buffer_3_out, counter_3_carry, cpu_clr, CYCLE, Cycle_t, cycle_t_t,
       d_ff_1_q, d_ff_2_q, data, decoder_4_out1, decoder_5_out1, Del_tick, Delete, down, first_tacktk,
       golod_t, I_Osel, left, lose, mem, nand_1_out, nor_1_out, nor_2_out, nor_3_out, nor_4_out, not_1_out,
       not_2_out, not_3_out, not_4_out, not_5_out, not_6_out, not_7_out, not_8_out, not_9_out, not_10_out,
       not_11_out, or_3_out, or_4_out, or_5_out, or_6_out, or_7_out, or_8_out, or_11_out, or_12_out,
       or_13_out, or_15_out, or_16_out, RAM, rd_wr_prime, resp, rest, right, takt, up, vivod, wall, win,
       \колиз_ябл , \перекус ;
  wire [1:0] Move;
  wire [3:0] cdm_8_mark5_1_ps;
  wire [7:0] adder_1_out, adr, Apple_coord, cdm_8_mark5_1_data_out, cdm_8_mark5_1_pc, cdm_8_mark5_1_r0,
       cdm_8_mark5_1_r1, cdm_8_mark5_1_r2, cdm_8_mark5_1_r3, cdm_8_mark5_1_sp, controlled_buffer_1_out,
       controlled_buffer_6_out, Cords, head, I_Odata, inc_dec_1_r, negator_1_out, or_2_out, register_2_q,
       register_3_q;
  wire [15:0] _1s, _2s, _3s, _4s, _5s, _6s, _7s, _8s, _9s, _10s, _11s, _12s, _13s, _14s, _15s, _16s,
       n17_16and_1__16out, n17_16and_2__16out, n17_16and_3__16out, n17_16and_4__16out, n17_16and_5__16out,
       n17_16and_6__16out, n17_16and_7__16out, n17_16and_8__16out, n17_16and_9__16out, n17_16and_10__16out,
       n17_16and_11__16out, n17_16and_12__16out, n17_16and_13__16out, n17_16and_14__16out,
       n17_16and_15__16out, n17_16and_16__16out, n20_16and_1__16out, n20_16and_2__16out, n20_16and_3__16out,
       n20_16and_4__16out, n20_16and_5__16out, n20_16and_6__16out, n20_16and_7__16out, n20_16and_8__16out,
       n20_16and_9__16out, n20_16and_10__16out, n20_16and_11__16out, n20_16and_12__16out,
       n20_16and_13__16out, n20_16and_14__16out, n20_16and_15__16out, n20_16and_16__16out, or_17_out,
       or_19_out, register_5_q, register_6_q, register_7_q, register_8_q, register_9_q, register_10_q,
       register_11_q, register_12_q, register_13_q, register_14_q, register_15_q, register_16_q,
       register_17_q, register_18_q, register_19_q, register_20_q;
  wire [31:0] counter_2_q;

  assign controlled_buffer_1_out = first_tacktk ? 8'h88 : 8'bz;  // Controlled_Buffer controlled_buffer_1
  or or_1 (clr_apple, clr_button, cpu_clr);
  Pull_Resistor pull_resistor_1 (.node(controlled_buffer_1_out));
  Register register_1 (.D(or_2_out), .Q(head), .clk(CYCLE), .clr(clr_apple));  // open: en
  assign or_2_out = controlled_buffer_1_out | inc_dec_1_r;  // OR_Gate or_2, 8 bits wide
  or or_3 (or_3_out, clr_apple, \колиз_ябл , resp, clk_apple);
  Random #(.seed(8)) random_1 (.clk(or_3_out), .out(Apple_coord));  // open: next, clr
  // Probe on head
  // Probe on Apple_coord
  Negator negator_1 (.in(head), .out(negator_1_out));
  and and_1 (and_1_out, head[4], head[5], head[6], head[7]);
  and and_2 (and_2_out, head[0], head[1], head[2], head[3]);
  nor nor_1 (nor_1_out, head[4], head[5], head[6], head[7]);
  nor nor_2 (nor_2_out, head[0], head[1], head[2], head[3]);
  and and_3 (and_3_out, Apple_coord[0], Apple_coord[1], Apple_coord[2], Apple_coord[3]);
  and and_4 (and_4_out, Apple_coord[4], Apple_coord[5], Apple_coord[6], Apple_coord[7]);
  nor nor_3 (nor_3_out, Apple_coord[0], Apple_coord[1], Apple_coord[2], Apple_coord[3]);
  nor nor_4 (nor_4_out, Apple_coord[4], Apple_coord[5], Apple_coord[6], Apple_coord[7]);
  or or_4 (or_4_out, left, right);
  inc_dec inc_dec_1 (.X(head[7:4]), .on_off(or_4_out), .inc_dec(right), .R(inc_dec_1_r[7:4]));
  inc_dec inc_dec_2 (.X(head[3:0]), .on_off(or_5_out), .inc_dec(up), .R(inc_dec_1_r[3:0]));
  or or_5 (or_5_out, down, up);
  Adder adder_1 (.a(Apple_coord), .b(negator_1_out), .out(adder_1_out));  // open: cin, cout
  assign clk = available ? takt : 1'bz;  // Controlled_Buffer controlled_buffer_2
  Clock clock_1 (.out(clock_1_out));
  Counter #(.width(1), .max('h1), .ongoal("stay")) counter_1 (
    .carry(wall), .clk(or_6_out), .clr(clr_apple));  // open: load, D, count, Q
  or or_6 (or_6_out, and_1_out, and_2_out, nor_1_out, nor_2_out);
  or or_7 (or_7_out, and_3_out, and_4_out, nor_3_out, nor_4_out);
  not not_1 (not_1_out, Paus);
  assign controlled_buffer_3_out = not_1_out ? clock_1_out : 1'bz;  // Controlled_Buffer controlled_buffer_3
  Pull_Resistor pull_resistor_2 (.node(controlled_buffer_3_out));
  D_Flip_Flop d_ff_1 (.Q(d_ff_1_q), .preset(or_8_out), .reset(clr_apple));  // open: clk, D, Qn, en
  or or_8 (or_8_out, lose, win);
  nor nor_5 (clk_apple, adder_1_out[0], adder_1_out[1], adder_1_out[2], adder_1_out[3], adder_1_out[4], adder_1_out[5], adder_1_out[6], adder_1_out[7]);
  and and_5 (resp, or_7_out, takt);
  Multiplexer multiplexer_1 (.in0(controlled_buffer_3_out), .in1(1'b0), .out(takt), .sel(d_ff_1_q));  // open: en
  Counter #(.width(32), .max('hffffffff)) counter_2 (
    .Q(counter_2_q), .clk(CYCLE), .clr(clr_apple));  // open: load, D, count, carry
  and and_6 (I_Osel, not_4_out, takt, data);
  assign I_Odata = not_3_out ? {{6{1'b0}}, Move} : 8'bz;  // Controlled_Buffer controlled_buffer_4
  and and_7 (hunger_clk, CYCLE, golod);
  or or_9 (hunger_clr, clk_apple, clr_apple);
  D_Flip_Flop d_ff_2 (.Q(d_ff_2_q), .preset(\перекус ), .reset(clr_apple));  // open: clk, D, Qn, en
  Comparator #(.width(32), .mode("unsigned")) comparator_1 (
    .a({32{1'b0}}), .b(counter_2_q), .eq(first_tacktk));  // open: gt, lt
  granica_1 granica_1_1 ();
  not not_2 (not_2_out, ChangeMove);
  not not_3 (not_3_out, not_2_out);
  or or_10 (lose, golod_t, wall, d_ff_2_q);
  // Probe on cdm_8_mark5_1_r3
  // Probe on cdm_8_mark5_1_r2
  // Probe on cdm_8_mark5_1_r1
  // Probe on cdm_8_mark5_1_r0
  not not_4 (not_4_out, nand_1_out);
  nand nand_1 (nand_1_out, adr[4], adr[5], adr[6], adr[7]);
  and and_8 (RAM, nand_1_out, data);
  and and_9 (and_9_out, I_Osel, adr[0], adr[1], ~adr[2], ~adr[3]);  // AND_Gate
  Counter #(.max('ha)) counter_3 (
    .carry(counter_3_carry), .clk(clk_apple), .clr(clr_apple));  // open: load, D, count, Q
  // Probe on cdm_8_mark5_1_sp
  // Probe on cdm_8_mark5_1_pc
  // Probe on cdm_8_mark5_1_ps
  CdM_8_mark5 cdm_8_mark5_1 (
    .clock(takt), .addr(adr), .mem_read(rd_wr_prime), .mem_cycle(mem), .data_inst(cdm_8_mark5_1_data_inst),
    .data_out(cdm_8_mark5_1_data_out), .data_in(controlled_buffer_6_out), .r0(cdm_8_mark5_1_r0),
    .r1(cdm_8_mark5_1_r1), .r2(cdm_8_mark5_1_r2), .r3(cdm_8_mark5_1_r3), .PC(cdm_8_mark5_1_pc),
    .SP(cdm_8_mark5_1_sp), .PS(cdm_8_mark5_1_ps));
  Decoder #(.disabled(0)) decoder_1 (.out1(ChangeMove), .sel(rd_wr_prime), .en(and_9_out));  // open: out0
  D_Flip_Flop d_ff_3 (.Q(win), .preset(counter_3_carry), .reset(clr_apple));  // open: clk, D, Qn, en
  Decoder #(.disabled(0)) decoder_2 (.out0(code), .out1(data), .sel(cdm_8_mark5_1_data_inst), .en(mem));
  not not_5 (not_5_out, rd_wr_prime);
  assign I_Odata = not_5_out ? cdm_8_mark5_1_data_out : 8'bz;  // Controlled_Buffer controlled_buffer_5
  assign controlled_buffer_6_out = rd_wr_prime ? I_Odata : 8'bz;  // Controlled_Buffer controlled_buffer_6
  assign I_Odata = Change ? head : 8'bz;  // Controlled_Buffer controlled_buffer_7
  golod golod_1 (.stop_golod(golod), .clock(CYCLE), .clr(clr_apple), .apple(clk_apple), .golod(golod_t));
  and and_10 (and_10_out, I_Osel, adr[0], ~adr[1], adr[2], ~adr[3]);  // AND_Gate
  Pull_Resistor pull_resistor_3 (.node(adr[0]));
  Pull_Resistor pull_resistor_4 (.node(adr[1]));
  Pull_Resistor pull_resistor_5 (.node(adr[2]));
  Pull_Resistor pull_resistor_6 (.node(adr[3]));
  Pull_Resistor pull_resistor_7 (.node(adr[4]));
  Pull_Resistor pull_resistor_8 (.node(adr[5]));
  Pull_Resistor pull_resistor_9 (.node(adr[6]));
  Pull_Resistor pull_resistor_10 (.node(adr[7]));
  Decoder #(.disabled(0)) decoder_3 (.out1(Change), .sel(rd_wr_prime), .en(and_10_out));  // open: out0
  ROM rom_1 (.addr(adr), .data(I_Odata), .sel(code));
  RAM ram_1 (.addr(adr), .data(I_Odata), .sel(RAM), .clk(takt), .ld(rd_wr_prime), .clr(clr_apple));
  movement movement_1 (
    .\input (\input ), .Clear(clr_apple), .Move(Move), .up(up), .right(right), .down(down), .left(left),
    .Clk(ChangeMove));
  assign I_Odata = decoder_4_out1 ? register_2_q : 8'bz;  // Controlled_Buffer controlled_buffer_8
  Register register_2 (.D({{7{1'b0}}, clk_apple}), .Q(register_2_q), .clk(clk_apple), .clr(AppleClear));  // open: en
  and and_11 (and_11_out, I_Osel, ~adr[0], adr[1], adr[2], ~adr[3]);  // AND_Gate
  Decoder #(.disabled(0)) decoder_4 (.out1(decoder_4_out1), .sel(rd_wr_prime), .en(and_11_out));  // open: out0
  and and_12 (cpu_clr, ~adr[0], adr[1], ~adr[2], adr[3], adr[4], adr[5], adr[6], adr[7]);  // AND_Gate
  and and_13 (and_13_out, adr[0], adr[1], adr[2], ~adr[3], adr[4], adr[5], adr[6], adr[7]);  // AND_Gate
  Pull_Resistor pull_resistor_11 (.node(AppleClear));
  assign AppleClear = and_13_out ? 1'b1 : 1'bz;  // Controlled_Buffer controlled_buffer_9
  assign I_Odata = decoder_5_out1 ? register_3_q : 8'bz;  // Controlled_Buffer controlled_buffer_10
  Register register_3 (.D({{7{1'b0}}, clr_apple}), .Q(register_3_q), .clk(not_6_out), .clr(cpu_clr));  // open: en
  not not_6 (not_6_out, not_7_out);
  not not_7 (not_7_out, clr_apple);
  and and_14 (and_14_out, I_Osel, adr[0], ~adr[1], ~adr[2], adr[3]);  // AND_Gate
  Decoder #(.disabled(0)) decoder_5 (.out1(decoder_5_out1), .sel(rd_wr_prime), .en(and_14_out));  // open: out0
  Pull_Resistor pull_resistor_12 (.node(CYCLE));
  assign CYCLE = and_15_out ? 1'b1 : 1'bz;  // Controlled_Buffer controlled_buffer_11
  and and_15 (and_15_out, ~adr[0], ~adr[1], ~adr[2], adr[3], adr[4], adr[5], adr[6], adr[7]);  // AND_Gate
  assign Del_tick = and_16_out ? 1'b1 : 1'bz;  // Controlled_Buffer controlled_buffer_12
  and and_16 (and_16_out, adr[0], adr[1], adr[2], adr[3], adr[4], adr[5], adr[6], adr[7]);
  Register #(.width(1)) register_4 (.D(Del_tick), .Q(Delete), .clk(takt), .clr(CYCLE));  // open: en
  and and_17 (and_17_out, adr[0], ~adr[1], ~adr[2], ~adr[3], adr[4], adr[5], ~adr[6], adr[7]);  // AND_Gate
  assign Cords = and_17_out ? I_Odata : 8'bz;  // Controlled_Buffer controlled_buffer_13
  Pull_Resistor pull_resistor_13 (.node(vivod));
  or or_11 (or_11_out, win, clr_apple, lose);
  or or_12 (or_12_out, vivod, clr_apple);
  or or_13 (or_13_out, lose, Cycle_t);
  helper_0 helper_0_1 (.in16(_1s), .in17(out_16), .out19(out_14), .in18(out_15));
  helper_0 helper_0_2 (.in16(_2s), .in17(out_21), .out19(out_19), .in18(out_20));
  helper_0 helper_0_3 (.in16(_3s), .in17(out_26), .out19(out_24), .in18(out_25));
  helper_0 helper_0_4 (.in16(_4s), .in17(out_31), .out19(out_29), .in18(out_30));
  helper_0 helper_0_5 (.in16(_5s), .in17(out_35), .out19(out_38), .in18(out_34));
  helper_0 helper_0_6 (.in16(_6s), .in17(out_42), .out19(out_43), .in18(out_41));
  helper_0 helper_0_7 (.in16(_7s), .in17(out_47), .out19(out_48), .in18(out_46));
  helper_0 helper_0_8 (.in16(_8s), .in17(out_52), .out19(out_53), .in18(out_51));
  helper_0 helper_0_9 (.in16(_9s), .in17(out_57), .out19(out_60), .in18(out_56));
  helper_0 helper_0_10 (.in16(_10s), .in17(out_64), .out19(out_65), .in18(out_63));
  helper_0 helper_0_11 (.in16(_11s), .in17(out_69), .out19(out_70), .in18(out_68));
  helper_0 helper_0_12 (.in16(_12s), .in17(out_74), .out19(out_75), .in18(out_73));
  helper_0 helper_0_13 (.in16(_13s), .in17(out_79), .out19(out_82), .in18(out_78));
  helper_0 helper_0_14 (.in16(_14s), .in17(out_84), .out19(out_85), .in18(out_83));
  helper_0 helper_0_15 (.in16(_15s), .in17(out_87), .out19(out_88), .in18(out_86));
  helper_0 helper_0_16 (.in16(_16s), .in17(out_90), .out19(out_91), .in18(out_89));
  _16bit_register_1 u_16bit_register_1_1 (
    .X(Cords[7:4]), .out_7(_1s), .clock(takt), .Y(Cords[3:0]), .out_8(_2s), .out_9(_3s), .out_10(_4s),
    .out_11(_5s), .out_12(_6s), .out_13(_7s), .out_14(_8s), .out_15(_9s), .out_16(_10s), .out_17(_11s),
    .out_18(_12s), .out_19(_13s), .out_20(_14s), .out_21(_15s), .out_22(_16s), .clear(rest), .Del(Delete),
    .\end (or_11_out));
  or or_14 (rest, or_12_out, or_13_out);
  or or_15 (or_15_out, lose, win);
  or or_16 (or_16_out, clk_apple, applecpl, or_15_out, clr_apple, resp);
  _17bit_register_1 u_17bit_register_1_1 (
    .X(Apple_coord[7:4]), .clock(takt), .Y(Apple_coord[3:0]), .out_5(out_16), .out_6(out_21), .out_7(out_26),
    .out_8(out_31), .out_9(out_35), .out_10(out_42), .out_11(out_47), .out_12(out_52), .out_13(out_57),
    .out_14(out_64), .out_15(out_69), .out_16(out_74), .out_17(out_79), .out_18(out_84), .out_19(out_87),
    .out_20(out_90), .clear(or_16_out));
  _16_20NOAND u_16_20noand_1 (._16in(_1s), ._20in(out_13), ._16out(out_12));
  _16_20NOAND u_16_20noand_2 (._16in(_2s), ._20in(out_18), ._16out(out_17));
  _16_20NOAND u_16_20noand_3 (._16in(_3s), ._20in(out_23), ._16out(out_22));
  _16_20NOAND u_16_20noand_4 (._16in(_4s), ._20in(out_28), ._16out(out_27));
  _16_20NOAND u_16_20noand_5 (._16in(_5s), ._20in(out_33), ._16out(out_32));
  _16_20NOAND u_16_20noand_6 (._16in(_6s), ._20in(out_37), ._16out(out_36));
  _16_20NOAND u_16_20noand_7 (._16in(_7s), ._20in(out_40), ._16out(out_39));
  _16_20NOAND u_16_20noand_8 (._16in(_8s), ._20in(out_45), ._16out(out_44));
  _16_20NOAND u_16_20noand_9 (._16in(_9s), ._20in(out_50), ._16out(out_49));
  _16_20NOAND u_16_20noand_10 (._16in(_10s), ._20in(out_55), ._16out(out_54));
  _16_20NOAND u_16_20noand_11 (._16in(_11s), ._20in(out_59), ._16out(out_58));
  _16_20NOAND u_16_20noand_12 (._16in(_12s), ._20in(out_62), ._16out(out_61));
  _16_20NOAND u_16_20noand_13 (._16in(_13s), ._20in(out_67), ._16out(out_66));
  _16_20NOAND u_16_20noand_14 (._16in(_14s), ._20in(out_72), ._16out(out_71));
  _16_20NOAND u_16_20noand_15 (._16in(_15s), ._20in(out_77), ._16out(out_76));
  _16_20NOAND u_16_20noand_16 (._16in(_16s), ._20in(out_81), ._16out(out_80));
  _17_16AND u_17_16and_1 (._16in(out_12), ._17in(out_16), ._16out(n17_16and_1__16out));
  _17_16AND u_17_16and_2 (._16in(out_17), ._17in(out_21), ._16out(n17_16and_2__16out));
  _17_16AND u_17_16and_3 (._16in(out_22), ._17in(out_26), ._16out(n17_16and_3__16out));
  _17_16AND u_17_16and_4 (._16in(out_27), ._17in(out_31), ._16out(n17_16and_4__16out));
  _17_16AND u_17_16and_5 (._16in(out_32), ._17in(out_35), ._16out(n17_16and_5__16out));
  _17_16AND u_17_16and_6 (._16in(out_36), ._17in(out_42), ._16out(n17_16and_6__16out));
  _17_16AND u_17_16and_7 (._16in(out_39), ._17in(out_47), ._16out(n17_16and_7__16out));
  _17_16AND u_17_16and_8 (._16in(out_44), ._17in(out_52), ._16out(n17_16and_8__16out));
  _17_16AND u_17_16and_9 (._16in(out_49), ._17in(out_57), ._16out(n17_16and_9__16out));
  _17_16AND u_17_16and_10 (._16in(out_54), ._17in(out_64), ._16out(n17_16and_10__16out));
  _17_16AND u_17_16and_11 (._16in(out_58), ._17in(out_69), ._16out(n17_16and_11__16out));
  _17_16AND u_17_16and_12 (._16in(out_61), ._17in(out_74), ._16out(n17_16and_12__16out));
  _17_16AND u_17_16and_13 (._16in(out_66), ._17in(out_79), ._16out(n17_16and_13__16out));
  _17_16AND u_17_16and_14 (._16in(out_71), ._17in(out_84), ._16out(n17_16and_14__16out));
  _17_16AND u_17_16and_15 (._16in(out_76), ._17in(out_87), ._16out(n17_16and_15__16out));
  _17_16AND u_17_16and_16 (._16in(out_80), ._17in(out_90), ._16out(n17_16and_16__16out));
  win_lose_pause win_lose_pause_1 (
    .lose(lose), .win(win), .pause(Paus), ._1(out_15), ._2(out_20), ._3(out_25), ._4(out_30), ._5(out_34),
    ._6(out_41), ._7(out_46), ._8(out_51), ._9(out_56), ._10(out_63), ._11(out_68), ._12(out_73),
    ._13(out_78), ._14(out_83), ._15(out_86), ._16(out_89));
  assign or_17_out = n17_16and_1__16out | n17_16and_2__16out | n17_16and_3__16out | n17_16and_4__16out | n17_16and_5__16out | n17_16and_6__16out | n17_16and_7__16out | n17_16and_8__16out | n17_16and_9__16out | n17_16and_10__16out | n17_16and_11__16out | n17_16and_12__16out | n17_16and_13__16out | n17_16and_14__16out | n17_16and_15__16out | n17_16and_16__16out;  // OR_Gate or_17, 16 bits wide
  or or_18 (\колиз_ябл , or_17_out[0], or_17_out[1], or_17_out[2], or_17_out[3], or_17_out[4], or_17_out[5], or_17_out[6], or_17_out[7], or_17_out[9], or_17_out[10], or_17_out[11], or_17_out[12], or_17_out[13], or_17_out[14], or_17_out[15], or_17_out[8]);
  _20bit_register_1 u_20bit_register_1_1 (
    .X(head[7:4]), .clock(takt), .Y(head[3:0]), .clear(rest), .out_5(out_13), .out_6(out_18), .out_7(out_23),
    .out_8(out_28), .out_9(out_33), .out_10(out_37), .out_11(out_40), .out_12(out_45), .out_13(out_50),
    .out_14(out_55), .out_15(out_59), .out_16(out_62), .out_17(out_67), .out_18(out_72), .out_19(out_77),
    .out_20(out_81));
  Register #(.width(16)) register_5 (.D(_1s), .Q(register_5_q), .clk(not_11_out));  // open: en, clr
  Register #(.width(16)) register_6 (.D(_2s), .Q(register_6_q), .clk(not_11_out));  // open: en, clr
  Register #(.width(16)) register_7 (.D(_3s), .Q(register_7_q), .clk(not_11_out));  // open: en, clr
  Register #(.width(16)) register_8 (.D(_4s), .Q(register_8_q), .clk(not_11_out));  // open: en, clr
  Register #(.width(16)) register_9 (.D(_5s), .Q(register_9_q), .clk(not_11_out));  // open: en, clr
  Register #(.width(16)) register_10 (.D(_6s), .Q(register_10_q), .clk(not_11_out));  // open: en, clr
  Register #(.width(16)) register_11 (.D(_7s), .Q(register_11_q), .clk(not_11_out));  // open: en, clr
  Register #(.width(16)) register_12 (.D(_8s), .Q(register_12_q), .clk(not_11_out));  // open: en, clr
  Register #(.width(16)) register_13 (.D(_9s), .Q(register_13_q), .clk(not_11_out));  // open: en, clr
  Register #(.width(16)) register_14 (.D(_10s), .Q(register_14_q), .clk(not_11_out));  // open: en, clr
  Register #(.width(16)) register_15 (.D(_11s), .Q(register_15_q), .clk(not_11_out));  // open: en, clr
  Register #(.width(16)) register_16 (.D(_12s), .Q(register_16_q), .clk(not_11_out));  // open: en, clr
  Register #(.width(16)) register_17 (.D(_13s), .Q(register_17_q), .clk(not_11_out));  // open: en, clr
  Register #(.width(16)) register_18 (.D(_14s), .Q(register_18_q), .clk(not_11_out));  // open: en, clr
  Register #(.width(16)) register_19 (.D(_15s), .Q(register_19_q), .clk(not_11_out));  // open: en, clr
  Register #(.width(16)) register_20 (.D(_16s), .Q(register_20_q), .clk(not_11_out));  // open: en, clr
  not not_8 (not_8_out, not_9_out);
  not not_9 (not_9_out, not_10_out);
  not not_10 (not_10_out, cycle_t_t);
  not not_11 (not_11_out, not_8_out);
  _20_16AND u_20_16and_1 (._16in(register_5_q), ._20in(out_13), ._16out(n20_16and_1__16out));
  _20_16AND u_20_16and_2 (._16in(register_6_q), ._20in(out_18), ._16out(n20_16and_2__16out));
  _20_16AND u_20_16and_3 (._16in(register_7_q), ._20in(out_23), ._16out(n20_16and_3__16out));
  _20_16AND u_20_16and_4 (._16in(register_8_q), ._20in(out_28), ._16out(n20_16and_4__16out));
  _20_16AND u_20_16and_5 (._16in(register_9_q), ._20in(out_33), ._16out(n20_16and_5__16out));
  _20_16AND u_20_16and_6 (._16in(register_10_q), ._20in(out_37), ._16out(n20_16and_6__16out));
  _20_16AND u_20_16and_7 (._16in(register_11_q), ._20in(out_40), ._16out(n20_16and_7__16out));
  _20_16AND u_20_16and_8 (._16in(register_12_q), ._20in(out_45), ._16out(n20_16and_8__16out));
  _20_16AND u_20_16and_9 (._16in(register_13_q), ._20in(out_50), ._16out(n20_16and_9__16out));
  _20_16AND u_20_16and_10 (._16in(register_14_q), ._20in(out_55), ._16out(n20_16and_10__16out));
  _20_16AND u_20_16and_11 (._16in(register_15_q), ._20in(out_59), ._16out(n20_16and_11__16out));
  _20_16AND u_20_16and_12 (._16in(register_16_q), ._20in(out_62), ._16out(n20_16and_12__16out));
  _20_16AND u_20_16and_13 (._16in(register_17_q), ._20in(out_67), ._16out(n20_16and_13__16out));
  _20_16AND u_20_16and_14 (._16in(register_18_q), ._20in(out_72), ._16out(n20_16and_14__16out));
  _20_16AND u_20_16and_15 (._16in(register_19_q), ._20in(out_77), ._16out(n20_16and_15__16out));
  _20_16AND u_20_16and_16 (._16in(register_20_q), ._20in(out_81), ._16out(n20_16and_16__16out));
  assign or_19_out = n20_16and_1__16out | n20_16and_2__16out | n20_16and_3__16out | n20_16and_4__16out | n20_16and_5__16out | n20_16and_6__16out | n20_16and_7__16out | n20_16and_8__16out | n20_16and_9__16out | n20_16and_10__16out | n20_16and_11__16out | n20_16and_12__16out | n20_16and_13__16out | n20_16and_14__16out | n20_16and_15__16out | n20_16and_16__16out;  // OR_Gate or_19, 16 bits wide
  or or_20 (\перекус , or_19_out[0], or_19_out[1], or_19_out[2], or_19_out[3], or_19_out[4], or_19_out[5], or_19_out[6], or_19_out[7], or_19_out[9], or_19_out[10], or_19_out[11], or_19_out[12], or_19_out[13], or_19_out[14], or_19_out[15], or_19_out[8]);

  assign clr_kbd = clr_apple;

  // Other names for the same wires on the sheet: apple = clk_apple; clr = clr_apple; y[3:0] = head[7:4];
  //   x[3:0] = head[3:0]; _1[17:0] = out_15; _1a[16:0] = out_16; _1h[19:0] = out_13; _1h4[19:0] = out_72;
  //   _2[17:0] = out_20; _2a[16:0] = out_21; _3[17:0] = out_25; _3a[16:0] = out_26; _3h[19:0] = out_23;
  //   _4[17:0] = out_30; _4a[16:0] = out_31; _4h[19:0] = out_28; _5[17:0] = out_34; _5a[16:0] = out_35;
  //   _5h[19:0] = out_33; _6[17:0] = out_41; _6a[16:0] = out_42; _6h[19:0] = out_37; _7[17:0] = out_46;
  //   _7a[16:0] = out_47; _7h[19:0] = out_40; _8[17:0] = out_51; _8a[16:0] = out_52; _8h[19:0] = out_45;
  //   _9[17:0] = out_56; _9a[16:0] = out_57; _9h[19:0] = out_50; _10[17:0] = out_63; _10a[16:0] = out_64;
  //   _10h[19:0] = out_55; _11[17:0] = out_68; _11a[16:0] = out_69; _11h[19:0] = out_59; _12[17:0] = out_73;
  //   _12a[16:0] = out_74; _12h[19:0] = out_62; _13[17:0] = out_78; _13a[16:0] = out_79; _13h[19:0] = out_67;
  //   _14[17:0] = out_83; _14a[16:0] = out_84; _15[17:0] = out_86; _15a[16:0] = out_87; _15h[19:0] = out_77;
  //   _16[17:0] = out_89; _16a[16:0] = out_90; _16h[19:0] = out_81; I_Oadr[3:0] = adr[3:0]; h2[19:0] = out_18;
  //   stop_golod = golod

  // Notes on the sheet:
  //   Получение направления
  //   Получение координат головы
  //   contents of rom_1 (hex, n*v repeats v):
  //   d0 fa b0 cd f0 d1 3 c1 d1 b5 d0 87 a4 d0 f8 b0 d0 f9 b0 0 e0 18 ee 0 d0 f5 b0 d1 b1 a4 d0 f3 b0 d1
  //   b4 b6 a4 78 e1 2f cb 0 bd 8d ad ee 37 6*20 8c c0 d0 f6 b0 0 e1 84 d0 ef b1 89 a1 d0 3f 41 e1 5a c8 0
  //   d1 f0 31 85 c6 8c 5 e0 59 b3 a2 8c e 89 ee 50 a2 d3 ef bf d2 c0 d0 40 4e e1 68 d3 1 ee 79 78 e1 6f
  //   d3 10 ee 79 20 78 e1 77 d3 ff ee 79 d3 f0 d0 b5 b1 d2 ff ba d2 b1 a9 17 a3 d0 f7 b0 d0 f8 b0 ee 10
  //   Бит съеденного яблока
  //   Очищение
  //   Бит очищения яблочка
  //   Флаг очищения
  //   Бит конца цикла процессора
  //   Бит удаления
  //   Координаты змейки
  //   матрица 20 бит
  //   Вывод тела змеи
  //   матрица 19 бит
  //   матрица 18 бит
  //   вывод яблока
  //   матрица 17 бит
  //   вывод паузы, lose, win
  //   яблоко и змейка
  //   вывод головы
  //   само перекус
endmodule

module inc_dec (
  input  [3:0] X,
  input  on_off,
  input  inc_dec,
  output [3:0] R
);

  wire [3:0] and_1_out, xor_1_out, xor_2_out, xor_3_out;
  wire [3:3] decoder_1_out0, decoder_1_out1;

  Decoder #(.enable("false")) decoder_1 (.out0(decoder_1_out0[3]), .out1(decoder_1_out1[3]), .sel(inc_dec));
  assign xor_1_out = {4{decoder_1_out0[3]}} ^ X;  // XOR_Gate xor_1, 4 bits wide
  assign xor_2_out = {4{decoder_1_out1[3]}} ^ xor_3_out;  // XOR_Gate xor_2, 4 bits wide
  assign and_1_out = xor_1_out & xor_2_out;  // AND_Gate and_1, 4 bits wide
  assign xor_3_out = X ^ {and_1_out[2:0], 1'b1};  // XOR_Gate xor_3, 4 bits wide
  Multiplexer #(.width(4), .enable("false")) multiplexer_1 (.in0(X), .in1(xor_3_out), .out(R), .sel(on_off));
endmodule

module movement (
  input  Clk,
  input  [6:0] \input ,
  input  Clear,
  output [1:0] Move,
  output up,
  output right,
  output down,
  output left
);

  wire comparator_1_eq, comparator_2_eq, comparator_3_eq, comparator_4_eq, not_1_out, not_2_out, not_3_out,
       not_4_out, not_5_out, not_6_out, not_7_out, not_8_out, not_9_out, not_10_out, not_11_out, not_12_out,
       not_13_out, not_14_out, not_15_out, not_16_out, not_17_out, not_18_out, not_19_out, not_20_out,
       not_21_out, not_22_out, not_23_out, or_1_out, or_2_out, or_5_out, takt;
  wire [1:0] adder_1_out, choose, demultiplexer_1_out1, demultiplexer_1_out3, multiplexer_1_out, or_3_out,
       register_1_q, subtractor_1_out;

  Register #(.width(2)) register_1 (.D(multiplexer_1_out), .Q(register_1_q), .clk(takt), .clr(Clear));  // open: en
  Multiplexer #(.select(2), .width(2), .enable("false")) multiplexer_1 (
    .in1(adder_1_out), .in3(subtractor_1_out), .out(multiplexer_1_out), .sel(choose));  // open: in0, in2
  Comparator #(.width(7)) comparator_1 (.a(\input ), .b(7'b1100100), .eq(comparator_1_eq));  // open: gt, lt
  Comparator #(.width(7)) comparator_2 (.a(\input ), .b(7'b0110010), .eq(comparator_2_eq));  // open: gt, lt
  Comparator #(.width(7)) comparator_3 (.a(\input ), .b(7'b1100001), .eq(comparator_3_eq));  // open: gt, lt
  Comparator #(.width(7)) comparator_4 (.a(\input ), .b(7'b1000100), .eq(comparator_4_eq));  // open: gt, lt
  Demultiplexer #(.select(2), .width(2), .enable("false")) demultiplexer_1 (
    .out1(demultiplexer_1_out1), .out3(demultiplexer_1_out3), .in(register_1_q), .sel(choose));  // open: out0, out2
  or or_1 (or_1_out, comparator_1_eq, comparator_2_eq);
  or or_2 (or_2_out, comparator_3_eq, comparator_4_eq);
  Adder #(.width(2)) adder_1 (.a(2'b01), .b(demultiplexer_1_out1), .out(adder_1_out));  // open: cin, cout
  Subtractor #(.width(2)) subtractor_1 (
    .a(demultiplexer_1_out3), .b(2'b01), .out(subtractor_1_out));  // open: bin, bout
  Register #(.width(2)) register_2 (.D(register_1_q), .Q(Move), .clk(Clk), .clr(Clear));  // open: en
  or or_3 (or_3_out[0], or_1_out, or_2_out);
  or or_4 (or_3_out[1], or_2_out, or_2_out);
  or or_5 (or_5_out, or_1_out, or_2_out);
  not not_1 (not_1_out, or_5_out);
  not not_2 (not_2_out, not_9_out);
  not not_3 (not_3_out, not_2_out);
  not not_4 (not_4_out, not_3_out);
  Demultiplexer #(.select(2), .enable("false")) demultiplexer_2 (
    .out0(up), .out1(right), .out2(down), .out3(left), .in(1'b1), .sel(Move));
  Register #(.width(2)) register_3 (.D(or_3_out), .Q(choose), .clk(or_5_out), .clr(Clear));  // open: en
  not not_5 (not_5_out, not_7_out);
  not not_6 (not_6_out, not_1_out);
  not not_7 (not_7_out, not_6_out);
  not not_8 (not_8_out, not_5_out);
  not not_9 (not_9_out, not_11_out);
  not not_10 (not_10_out, not_21_out);
  not not_11 (not_11_out, not_12_out);
  not not_12 (not_12_out, not_10_out);
  not not_13 (not_13_out, not_15_out);
  not not_14 (not_14_out, not_4_out);
  not not_15 (not_15_out, not_16_out);
  not not_16 (not_16_out, not_14_out);
  not not_17 (not_17_out, not_18_out);
  not not_18 (not_18_out, not_19_out);
  not not_19 (not_19_out, not_8_out);
  not not_20 (not_20_out, not_17_out);
  not not_21 (not_21_out, not_20_out);
  not not_22 (not_22_out, not_13_out);
  not not_23 (not_23_out, not_22_out);
  not not_24 (takt, not_23_out);

  // Other names for the same wires on the sheet: clr = Clear

  // Notes on the sheet:
  //   отвечает за формирование направления (01 - right  11 - left)
  //   суммируем по модулю 4, для того чтобы зациклить направления
endmodule

module golod (
  input  stop_golod,
  input  clock,
  input  clr,
  input  apple,
  output golod
);

  wire and_1_out, comparator_1_eq, comparator_1_gt, d_ff_1_q, or_1_out, or_2_out;
  wire [9:0] counter_1_q;

  Counter #(.width(10), .max('h3ff)) counter_1 (
    .Q(counter_1_q), .clk(and_1_out), .clr(or_1_out));  // open: load, D, count, carry
  and and_1 (and_1_out, clock, stop_golod);
  or or_1 (or_1_out, clr, apple);
  Comparator #(.width(10), .mode("unsigned")) comparator_1 (
    .a(counter_1_q), .b(10'h14), .gt(comparator_1_gt), .eq(comparator_1_eq));  // open: lt
  D_Flip_Flop d_ff_1 (.Q(d_ff_1_q), .preset(or_2_out), .reset(clr));  // open: clk, D, Qn, en
  or or_2 (or_2_out, comparator_1_gt, comparator_1_eq);
  and and_2 (golod, stop_golod, d_ff_1_q);
endmodule

module win_lose_pause (
  input  lose,
  input  win,
  input  pause,
  output [17:0] _1,
  output [17:0] _2,
  output [17:0] _3,
  output [17:0] _4,
  output [17:0] _5,
  output [17:0] _6,
  output [17:0] _7,
  output [17:0] _8,
  output [17:0] _9,
  output [17:0] _10,
  output [17:0] _11,
  output [17:0] _12,
  output [17:0] _13,
  output [17:0] _14,
  output [17:0] _15,
  output [17:0] _16
);

  wire wall;
  wire [15:0] _5_t, _5l, _5p, _5w, _6l, _6p, _6w, _7l, _7p, _7w, _8l, _8p, _8w, _9l, _9p, _9w, _10l, _10p,
       _10w, _11l, _11p, _11w, or_1_out, or_2_out, or_3_out, or_4_out, or_5_out, or_6_out, or_7_out;

  assign _5p = pause ? 16'h200 : 16'bz;  // Controlled_Buffer controlled_buffer_1
  assign _6p = pause ? 16'h300 : 16'bz;  // Controlled_Buffer controlled_buffer_2
  assign _7p = pause ? 16'h380 : 16'bz;  // Controlled_Buffer controlled_buffer_3
  assign _8p = pause ? 16'h3c0 : 16'bz;  // Controlled_Buffer controlled_buffer_4
  Pull_Resistor pull_resistor_1 (.node(_9p));
  assign _9p = pause ? 16'h380 : 16'bz;  // Controlled_Buffer controlled_buffer_5
  assign _10p = pause ? 16'h300 : 16'bz;  // Controlled_Buffer controlled_buffer_6
  Pull_Resistor pull_resistor_2 (.node(_10p));
  assign _11p = pause ? 16'h200 : 16'bz;  // Controlled_Buffer controlled_buffer_7
  Pull_Resistor pull_resistor_3 (.node(_11p));
  assign _5w = win ? {16{1'b0}} : 16'bz;  // Controlled_Buffer controlled_buffer_8
  assign _6w = win ? 16'h4542 : 16'bz;  // Controlled_Buffer controlled_buffer_9
  assign _7w = win ? 16'h4462 : 16'bz;  // Controlled_Buffer controlled_buffer_10
  assign _8w = win ? 16'h4552 : 16'bz;  // Controlled_Buffer controlled_buffer_11
  assign _9w = win ? 16'h554a : 16'bz;  // Controlled_Buffer controlled_buffer_12
  Pull_Resistor pull_resistor_4 (.node(_9w));
  Pull_Resistor pull_resistor_5 (.node(_10w));
  assign _10w = win ? 16'h6d46 : 16'bz;  // Controlled_Buffer controlled_buffer_13
  Pull_Resistor pull_resistor_6 (.node(_11w));
  assign _11w = win ? 16'h4542 : 16'bz;  // Controlled_Buffer controlled_buffer_14
  assign _5l = lose ? {16{1'b0}} : 16'bz;  // Controlled_Buffer controlled_buffer_15
  assign _6l = lose ? 16'h4ef6 : 16'bz;  // Controlled_Buffer controlled_buffer_16
  assign _7l = lose ? 16'h4a84 : 16'bz;  // Controlled_Buffer controlled_buffer_17
  assign _8l = lose ? 16'h4ac4 : 16'bz;  // Controlled_Buffer controlled_buffer_18
  assign _9l = lose ? 16'h4a66 : 16'bz;  // Controlled_Buffer controlled_buffer_19
  Pull_Resistor pull_resistor_7 (.node(_9l));
  assign _10l = lose ? 16'h4a34 : 16'bz;  // Controlled_Buffer controlled_buffer_20
  Pull_Resistor pull_resistor_8 (.node(_10l));
  assign _11l = lose ? 16'h6ef6 : 16'bz;  // Controlled_Buffer controlled_buffer_21
  Pull_Resistor pull_resistor_9 (.node(_11l));
  Pull_Resistor pull_resistor_10 (.node(_5_t));
  assign _5_t = wall ? 16'h8001 : 16'bz;  // Controlled_Buffer controlled_buffer_22
  Pull_Resistor pull_resistor_11 (.node(_5p));
  Pull_Resistor pull_resistor_12 (.node(_6p));
  Pull_Resistor pull_resistor_13 (.node(_7p));
  Pull_Resistor pull_resistor_14 (.node(_8p));
  Pull_Resistor pull_resistor_15 (.node(_5w));
  Pull_Resistor pull_resistor_16 (.node(_6w));
  Pull_Resistor pull_resistor_17 (.node(_7w));
  Pull_Resistor pull_resistor_18 (.node(_8w));
  Pull_Resistor pull_resistor_19 (.node(_5l));
  Pull_Resistor pull_resistor_20 (.node(_6l));
  Pull_Resistor pull_resistor_21 (.node(_7l));
  Pull_Resistor pull_resistor_22 (.node(_8l));
  nor nor_1 (wall, lose, win);
  assign _1 = wall ? 18'hffff : 18'bz;  // Controlled_Buffer controlled_buffer_23
  Pull_Resistor pull_resistor_23 (.node(_1));
  Pull_Resistor pull_resistor_24 (.node(_2));
  assign _2 = wall ? 18'h8001 : 18'bz;  // Controlled_Buffer controlled_buffer_24
  assign or_1_out = _5_t | _5p | _5w | _5l;  // OR_Gate or_1, 16 bits wide
  helper_1 helper_1_1 (.in(or_1_out), .out(_5));
  assign or_2_out = _5_t | _6p | _6w | _6l;  // OR_Gate or_2, 16 bits wide
  helper_1 helper_1_2 (.in(or_2_out), .out(_6));
  assign or_3_out = _5_t | _7p | _7w | _7l;  // OR_Gate or_3, 16 bits wide
  helper_1 helper_1_3 (.in(or_3_out), .out(_7));
  assign or_4_out = _5_t | _8p | _8w | _8l;  // OR_Gate or_4, 16 bits wide
  helper_1 helper_1_4 (.in(or_4_out), .out(_8));
  helper_1 helper_1_5 (.in(or_5_out), .out(_9));
  assign or_5_out = _5_t | _9p | _9w | _9l;  // OR_Gate or_5, 16 bits wide
  helper_1 helper_1_6 (.in(or_6_out), .out(_10));
  assign or_6_out = _5_t | _10p | _10w | _10l;  // OR_Gate or_6, 16 bits wide
  helper_1 helper_1_7 (.in(or_7_out), .out(_11));
  assign or_7_out = _5_t | _11p | _11l | _11w;  // OR_Gate or_7, 16 bits wide
  assign _12 = wall ? 18'h8001 : 18'bz;  // Controlled_Buffer controlled_buffer_25
  Pull_Resistor pull_resistor_25 (.node(_12));
  Pull_Resistor pull_resistor_26 (.node(_16));
  assign _16 = wall ? 18'hffff : 18'bz;  // Controlled_Buffer controlled_buffer_26

  assign _3 = _2;
  assign _4 = _2;
  assign _13 = _12;
  assign _14 = _12;
  assign _15 = _12;

  // Other names for the same wires on the sheet: _6_t[15:0] = _5_t; _7_t[15:0] = _5_t; _8_t[15:0] = _5_t;
  //   _9_t[15:0] = _5_t; _10_t[15:0] = _5_t; _11_t[15:0] = _5_t; paus = pause
endmodule

module helper_0 (
  input  [15:0] in16,
  input  [16:0] in17,
  input  [17:0] in18,
  output [18:0] out19
);

  assign out19[15:0] = in16 | in17[15:0] | in18[15:0];  // OR_Gate or_1, 16 bits wide

  assign out19[18:16] = 3'b111;
endmodule

module helper_1 (
  input  [15:0] in,
  output [17:0] out
);


  assign out = {2'b00, in};
endmodule

module counter_0 (
  input  clock,
  input  clear,
  output out_3,
  output out_4,
  output out_5,
  output out_6,
  output out_7,
  output out_8,
  output out_9,
  output out_10,
  output out_11,
  output out_12,
  output out_13,
  output out_14,
  output out_15,
  output out_16,
  output out_17,
  output out_18
);

  wire counter_1_carry;
  wire [7:0] counter_1_q, counter_2_q;

  Counter #(.max('ha)) counter_1 (
    .Q(counter_1_q), .carry(counter_1_carry), .clk(clock), .clr(clear));  // open: load, D, count
  Counter #(.max('ha)) counter_2 (.Q(counter_2_q), .clk(counter_1_carry), .clr(clear));  // open: load, D, count, carry
  ROM rom_1 (.addr(counter_1_q), .data({out_7, out_8, out_9, out_10, out_18, out_17, out_16, out_15}));  // open: sel
  ROM rom_2 (.addr(counter_2_q), .data({out_3, out_4, out_5, out_6, out_14, out_13, out_12, out_11}));  // open: sel

  // Other names for the same wires on the sheet: _1_1 = out_15; _1_2 = out_16; _1_3 = out_17; _1_4 = out_18;
  //   _1_5 = out_10; _1_6 = out_9; _1_7 = out_8; _1_8 = out_7; _2_1 = out_11; _2_2 = out_12; _2_3 = out_13;
  //   _2_4 = out_14; _2_5 = out_6; _2_6 = out_5; _2_7 = out_4; _2_8 = out_3

  // Notes on the sheet:
  //   contents of rom_1 (hex, n*v repeats v):
  //   77 14 b3 b6 d4 e6 e7 34 f7 f6 77
  //   contents of rom_2 (hex, n*v repeats v):
  //   77 14 b3 b6 d4 e6 e7 34 f7 f6 77
endmodule

module counter_1 (
  input  clock,
  input  clear,
  output out_3,
  output out_4,
  output out_5,
  output out_6,
  output out_7,
  output out_8,
  output out_9,
  output out_10,
  output out_11,
  output out_12,
  output out_13,
  output out_14,
  output out_15,
  output out_16,
  output out_17,
  output out_18
);

  wire comparator_1_eq;
  wire [7:0] counter_1_q, counter_2_q;

  Counter #(.max('h14)) counter_1 (.Q(counter_1_q), .clk(clock), .clr(clear));  // open: load, D, count, carry
  Counter #(.max('h5)) counter_2 (.Q(counter_2_q), .clk(comparator_1_eq), .clr(clear));  // open: load, D, count, carry
  ROM rom_1 (.addr(counter_1_q), .data({out_7, out_8, out_9, out_10, out_18, out_17, out_16, out_15}));  // open: sel
  ROM rom_2 (.addr(counter_2_q), .data({out_3, out_4, out_5, out_6, out_14, out_13, out_12, out_11}));  // open: sel
  Comparator comparator_1 (
    .a(8'hf6), .b({out_7, out_8, out_9, out_10, out_18, out_17, out_16, out_15}), .eq(comparator_1_eq));  // open: gt, lt

  // Other names for the same wires on the sheet: _1_1 = out_15; _1_2 = out_16; _1_3 = out_17; _1_4 = out_18;
  //   _1_5 = out_10; _1_6 = out_9; _1_7 = out_8; _1_8 = out_7; _2_1 = out_11; _2_2 = out_12; _2_3 = out_13;
  //   _2_4 = out_14; _2_5 = out_6; _2_6 = out_5; _2_7 = out_4; _2_8 = out_3

  // Notes on the sheet:
  //   contents of rom_1 (hex, n*v repeats v):
  //   77 f6 f7 34 e7 e6 d4 b6 b3 14 77 f6 f7 34 e7 e6 d4 b6 b3 14 77
  //   contents of rom_2 (hex, n*v repeats v):
  //   b3 14 77
endmodule

module _16_20NOAND (
  input  [15:0] _16in,
  input  [19:0] _20in,
  output [15:0] _16out
);

  assign _16out = _16in & ~_20in[15:0];  // AND_Gate and_1, 16 bits wide
endmodule

module _20_16AND (
  input  [15:0] _16in,
  input  [19:0] _20in,
  output [15:0] _16out
);

  assign _16out = _16in & _20in[15:0];  // AND_Gate and_1, 16 bits wide
endmodule

module _17_16AND (
  input  [15:0] _16in,
  input  [16:0] _17in,
  output [15:0] _16out
);

  assign _16out = _16in & _17in[15:0];  // AND_Gate and_1, 16 bits wide
endmodule

module _16bit_register_0 (
  input  clock,
  input  update,
  input  [3:0] X,
  input  clear,
  output [15:0] \output 
);

  wire demultiplexer_1_out0, demultiplexer_1_out1, demultiplexer_1_out2, demultiplexer_1_out3,
       demultiplexer_1_out4, demultiplexer_1_out5, demultiplexer_1_out6, demultiplexer_1_out7,
       demultiplexer_1_out8, demultiplexer_1_out9, demultiplexer_1_out10, demultiplexer_1_out11,
       demultiplexer_1_out12, demultiplexer_1_out13, demultiplexer_1_out14, demultiplexer_1_out15;

  Demultiplexer #(.select(4)) demultiplexer_1 (
    .out0(demultiplexer_1_out0), .out1(demultiplexer_1_out1), .out2(demultiplexer_1_out2),
    .out3(demultiplexer_1_out3), .out4(demultiplexer_1_out4), .out5(demultiplexer_1_out5),
    .out6(demultiplexer_1_out6), .out7(demultiplexer_1_out7), .out8(demultiplexer_1_out8),
    .out9(demultiplexer_1_out9), .out10(demultiplexer_1_out10), .out11(demultiplexer_1_out11),
    .out12(demultiplexer_1_out12), .out13(demultiplexer_1_out13), .out14(demultiplexer_1_out14),
    .out15(demultiplexer_1_out15), .in(clock), .sel(X));  // open: en
  D_Flip_Flop d_ff_1 (.clk(demultiplexer_1_out0), .D(update), .Q(\output [15]), .reset(clear));  // open: Qn, preset, en
  D_Flip_Flop d_ff_2 (.clk(demultiplexer_1_out1), .D(update), .Q(\output [14]), .reset(clear));  // open: Qn, preset, en
  D_Flip_Flop d_ff_3 (.clk(demultiplexer_1_out2), .D(update), .Q(\output [13]), .reset(clear));  // open: Qn, preset, en
  D_Flip_Flop d_ff_4 (.clk(demultiplexer_1_out3), .D(update), .Q(\output [12]), .reset(clear));  // open: Qn, preset, en
  D_Flip_Flop d_ff_5 (.clk(demultiplexer_1_out4), .D(update), .Q(\output [11]), .reset(clear));  // open: Qn, preset, en
  D_Flip_Flop d_ff_6 (.clk(demultiplexer_1_out6), .D(update), .Q(\output [9]), .reset(clear));  // open: Qn, preset, en
  D_Flip_Flop d_ff_7 (.clk(demultiplexer_1_out5), .D(update), .Q(\output [10]), .reset(clear));  // open: Qn, preset, en
  D_Flip_Flop d_ff_8 (.clk(demultiplexer_1_out7), .D(update), .Q(\output [8]), .reset(clear));  // open: Qn, preset, en
  D_Flip_Flop d_ff_9 (.clk(demultiplexer_1_out8), .D(update), .Q(\output [7]), .reset(clear));  // open: Qn, preset, en
  D_Flip_Flop d_ff_10 (.clk(demultiplexer_1_out9), .D(update), .Q(\output [6]), .reset(clear));  // open: Qn, preset, en
  D_Flip_Flop d_ff_11 (
    .clk(demultiplexer_1_out10), .D(update), .Q(\output [5]), .reset(clear));  // open: Qn, preset, en
  D_Flip_Flop d_ff_12 (
    .clk(demultiplexer_1_out11), .D(update), .Q(\output [4]), .reset(clear));  // open: Qn, preset, en
  D_Flip_Flop d_ff_13 (
    .clk(demultiplexer_1_out12), .D(update), .Q(\output [3]), .reset(clear));  // open: Qn, preset, en
  D_Flip_Flop d_ff_14 (
    .clk(demultiplexer_1_out13), .D(update), .Q(\output [2]), .reset(clear));  // open: Qn, preset, en
  D_Flip_Flop d_ff_15 (
    .clk(demultiplexer_1_out14), .D(update), .Q(\output [1]), .reset(clear));  // open: Qn, preset, en
  D_Flip_Flop d_ff_16 (
    .clk(demultiplexer_1_out15), .D(update), .Q(\output [0]), .reset(clear));  // open: Qn, preset, en
endmodule

module _16bit_register_1 (
  input  [3:0] X,
  input  clock,
  input  [3:0] Y,
  input  clear,
  input  Del,
  input  \end ,
  output [15:0] out_7,
  output [15:0] out_8,
  output [15:0] out_9,
  output [15:0] out_10,
  output [15:0] out_11,
  output [15:0] out_12,
  output [15:0] out_13,
  output [15:0] out_14,
  output [15:0] out_15,
  output [15:0] out_16,
  output [15:0] out_17,
  output [15:0] out_18,
  output [15:0] out_19,
  output [15:0] out_20,
  output [15:0] out_21,
  output [15:0] out_22
);

  wire demultiplexer_1_out0, demultiplexer_1_out1, demultiplexer_1_out2, demultiplexer_1_out3,
       demultiplexer_1_out4, demultiplexer_1_out5, demultiplexer_1_out6, demultiplexer_1_out7,
       demultiplexer_1_out8, demultiplexer_1_out9, demultiplexer_1_out10, demultiplexer_1_out11,
       demultiplexer_1_out12, demultiplexer_1_out13, demultiplexer_1_out14, demultiplexer_1_out15;
  wire [15:0] n16bit_register_0_1_output, n16bit_register_0_2_output, n16bit_register_0_3_output,
       n16bit_register_0_4_output, n16bit_register_0_5_output, n16bit_register_0_6_output,
       n16bit_register_0_7_output, n16bit_register_0_8_output, n16bit_register_0_9_output,
       n16bit_register_0_10_output, n16bit_register_0_11_output, n16bit_register_0_12_output,
       n16bit_register_0_13_output, n16bit_register_0_14_output, n16bit_register_0_15_output,
       n16bit_register_0_16_output;

  Demultiplexer #(.select(4)) demultiplexer_1 (
    .out0(demultiplexer_1_out0), .out1(demultiplexer_1_out1), .out2(demultiplexer_1_out2),
    .out3(demultiplexer_1_out3), .out4(demultiplexer_1_out4), .out5(demultiplexer_1_out5),
    .out6(demultiplexer_1_out6), .out7(demultiplexer_1_out7), .out8(demultiplexer_1_out8),
    .out9(demultiplexer_1_out9), .out10(demultiplexer_1_out10), .out11(demultiplexer_1_out11),
    .out12(demultiplexer_1_out12), .out13(demultiplexer_1_out13), .out14(demultiplexer_1_out14),
    .out15(demultiplexer_1_out15), .in(clock), .sel(Y));  // open: en
  _16bit_register_0 u_16bit_register_0_1 (
    .clock(demultiplexer_1_out15), .update(clock), .X(X), .\output (n16bit_register_0_1_output), .clear(clear));
  reg_delete_snake reg_delete_snake_1 (.Input(n16bit_register_0_1_output), .Output(out_7), .Del(Del), .clr(\end ));
  _16bit_register_0 u_16bit_register_0_2 (
    .clock(demultiplexer_1_out14), .update(clock), .X(X), .\output (n16bit_register_0_2_output), .clear(clear));
  reg_delete_snake reg_delete_snake_2 (.Input(n16bit_register_0_2_output), .Output(out_8), .Del(Del), .clr(\end ));
  _16bit_register_0 u_16bit_register_0_3 (
    .clock(demultiplexer_1_out13), .update(clock), .X(X), .\output (n16bit_register_0_3_output), .clear(clear));
  reg_delete_snake reg_delete_snake_3 (.Input(n16bit_register_0_3_output), .Output(out_9), .Del(Del), .clr(\end ));
  _16bit_register_0 u_16bit_register_0_4 (
    .clock(demultiplexer_1_out12), .update(clock), .X(X), .\output (n16bit_register_0_4_output), .clear(clear));
  reg_delete_snake reg_delete_snake_4 (.Input(n16bit_register_0_4_output), .Output(out_10), .Del(Del), .clr(\end ));
  _16bit_register_0 u_16bit_register_0_5 (
    .clock(demultiplexer_1_out11), .update(clock), .X(X), .\output (n16bit_register_0_5_output), .clear(clear));
  reg_delete_snake reg_delete_snake_5 (.Input(n16bit_register_0_5_output), .Output(out_11), .Del(Del), .clr(\end ));
  _16bit_register_0 u_16bit_register_0_6 (
    .clock(demultiplexer_1_out10), .update(clock), .X(X), .\output (n16bit_register_0_6_output), .clear(clear));
  reg_delete_snake reg_delete_snake_6 (.Input(n16bit_register_0_6_output), .Output(out_12), .Del(Del), .clr(\end ));
  _16bit_register_0 u_16bit_register_0_7 (
    .clock(demultiplexer_1_out9), .update(clock), .X(X), .\output (n16bit_register_0_7_output), .clear(clear));
  reg_delete_snake reg_delete_snake_7 (.Input(n16bit_register_0_7_output), .Output(out_13), .Del(Del), .clr(\end ));
  _16bit_register_0 u_16bit_register_0_8 (
    .clock(demultiplexer_1_out8), .update(clock), .X(X), .\output (n16bit_register_0_8_output), .clear(clear));
  reg_delete_snake reg_delete_snake_8 (.Input(n16bit_register_0_8_output), .Output(out_14), .Del(Del), .clr(\end ));
  _16bit_register_0 u_16bit_register_0_9 (
    .clock(demultiplexer_1_out7), .update(clock), .X(X), .\output (n16bit_register_0_9_output), .clear(clear));
  reg_delete_snake reg_delete_snake_9 (.Input(n16bit_register_0_9_output), .Output(out_15), .Del(Del), .clr(\end ));
  _16bit_register_0 u_16bit_register_0_10 (
    .clock(demultiplexer_1_out6), .update(clock), .X(X), .\output (n16bit_register_0_10_output), .clear(clear));
  reg_delete_snake reg_delete_snake_10 (.Input(n16bit_register_0_10_output), .Output(out_16), .Del(Del), .clr(\end ));
  _16bit_register_0 u_16bit_register_0_11 (
    .clock(demultiplexer_1_out5), .update(clock), .X(X), .\output (n16bit_register_0_11_output), .clear(clear));
  reg_delete_snake reg_delete_snake_11 (.Input(n16bit_register_0_11_output), .Output(out_17), .Del(Del), .clr(\end ));
  _16bit_register_0 u_16bit_register_0_12 (
    .clock(demultiplexer_1_out4), .update(clock), .X(X), .\output (n16bit_register_0_12_output), .clear(clear));
  reg_delete_snake reg_delete_snake_12 (.Input(n16bit_register_0_12_output), .Output(out_18), .Del(Del), .clr(\end ));
  _16bit_register_0 u_16bit_register_0_13 (
    .clock(demultiplexer_1_out3), .update(clock), .X(X), .\output (n16bit_register_0_13_output), .clear(clear));
  reg_delete_snake reg_delete_snake_13 (.Input(n16bit_register_0_13_output), .Output(out_19), .Del(Del), .clr(\end ));
  _16bit_register_0 u_16bit_register_0_14 (
    .clock(demultiplexer_1_out2), .update(clock), .X(X), .\output (n16bit_register_0_14_output), .clear(clear));
  reg_delete_snake reg_delete_snake_14 (.Input(n16bit_register_0_14_output), .Output(out_20), .Del(Del), .clr(\end ));
  _16bit_register_0 u_16bit_register_0_15 (
    .clock(demultiplexer_1_out1), .update(clock), .X(X), .\output (n16bit_register_0_15_output), .clear(clear));
  reg_delete_snake reg_delete_snake_15 (.Input(n16bit_register_0_15_output), .Output(out_21), .Del(Del), .clr(\end ));
  _16bit_register_0 u_16bit_register_0_16 (
    .clock(demultiplexer_1_out0), .update(clock), .X(X), .\output (n16bit_register_0_16_output), .clear(clear));
  reg_delete_snake reg_delete_snake_16 (.Input(n16bit_register_0_16_output), .Output(out_22), .Del(Del), .clr(\end ));
endmodule

module reg_delete_snake (
  input  [15:0] Input,
  input  clr,
  input  Del,
  output [15:0] Output
);

  wire not_1_out, not_2_out, not_3_out, not_4_out, not_5_out, not_6_out, not_7_out, not_8_out, not_9_out,
       not_10_out, not_11_out, or_1_out;
  wire [15:0] and_1_out, controlled_buffer_1_out, controlled_buffer_2_out, demultiplexer_1_out0,
       demultiplexer_1_out1, or_2_out;

  assign controlled_buffer_1_out = or_1_out ? Input : 16'bz;  // Controlled_Buffer controlled_buffer_1
  or or_1 (or_1_out, Input[7], Input[0], Input[1], Input[2], Input[3], Input[4], Input[5], Input[6], Input[8], Input[9], Input[10], Input[11], Input[12], Input[13], Input[14], Input[15]);
  Demultiplexer #(.width(16)) demultiplexer_1 (
    .out0(demultiplexer_1_out0), .out1(demultiplexer_1_out1), .in(controlled_buffer_1_out), .sel(Del));  // open: en
  not not_1 (not_1_out, not_2_out);
  not not_2 (not_2_out, not_3_out);
  not not_3 (not_3_out, or_1_out);
  assign or_2_out = Output | demultiplexer_1_out0;  // OR_Gate or_2, 16 bits wide
  assign and_1_out = ~demultiplexer_1_out1 & Output;  // AND_Gate and_1, 16 bits wide
  not not_4 (not_4_out, not_1_out);
  not not_5 (not_5_out, not_4_out);
  not not_6 (not_6_out, not_5_out);
  not not_7 (not_7_out, not_6_out);
  assign controlled_buffer_2_out = not_8_out ? or_2_out : 16'bz;  // Controlled_Buffer controlled_buffer_2
  not not_8 (not_8_out, Del);
  assign controlled_buffer_2_out = Del ? and_1_out : 16'bz;  // Controlled_Buffer controlled_buffer_3
  not not_9 (not_9_out, not_7_out);
  not not_10 (not_10_out, not_11_out);
  not not_11 (not_11_out, not_9_out);
  Register #(.width(16)) register_1 (.D(controlled_buffer_2_out), .Q(Output), .clk(not_10_out), .clr(clr));  // open: en

  // Notes on the sheet:
  //   Проверка на 0
  //   Если 0, то ничего не делаем
  //   Режим: Удаление или добавление
  //   Добавление пикселя
  //   Удаление пикселя
endmodule

module _17bit_register_0 (
  input  clock,
  input  update,
  input  [3:0] X,
  input  clear,
  output [16:0] \output 
);

  wire demultiplexer_1_out0, demultiplexer_1_out1, demultiplexer_1_out2, demultiplexer_1_out3,
       demultiplexer_1_out4, demultiplexer_1_out5, demultiplexer_1_out6, demultiplexer_1_out7,
       demultiplexer_1_out8, demultiplexer_1_out9, demultiplexer_1_out10, demultiplexer_1_out11,
       demultiplexer_1_out12, demultiplexer_1_out13, demultiplexer_1_out14, demultiplexer_1_out15;

  Demultiplexer #(.select(4)) demultiplexer_1 (
    .out0(demultiplexer_1_out0), .out1(demultiplexer_1_out1), .out2(demultiplexer_1_out2),
    .out3(demultiplexer_1_out3), .out4(demultiplexer_1_out4), .out5(demultiplexer_1_out5),
    .out6(demultiplexer_1_out6), .out7(demultiplexer_1_out7), .out8(demultiplexer_1_out8),
    .out9(demultiplexer_1_out9), .out10(demultiplexer_1_out10), .out11(demultiplexer_1_out11),
    .out12(demultiplexer_1_out12), .out13(demultiplexer_1_out13), .out14(demultiplexer_1_out14),
    .out15(demultiplexer_1_out15), .in(clock), .sel(X));  // open: en
  D_Flip_Flop d_ff_1 (.clk(demultiplexer_1_out0), .D(update), .Q(\output [15]), .reset(clear));  // open: Qn, preset, en
  D_Flip_Flop d_ff_2 (.clk(demultiplexer_1_out1), .D(update), .Q(\output [14]), .reset(clear));  // open: Qn, preset, en
  D_Flip_Flop d_ff_3 (.clk(demultiplexer_1_out2), .D(update), .Q(\output [13]), .reset(clear));  // open: Qn, preset, en
  D_Flip_Flop d_ff_4 (.clk(demultiplexer_1_out3), .D(update), .Q(\output [12]), .reset(clear));  // open: Qn, preset, en
  D_Flip_Flop d_ff_5 (.clk(demultiplexer_1_out5), .D(update), .Q(\output [10]), .reset(clear));  // open: Qn, preset, en
  D_Flip_Flop d_ff_6 (.clk(demultiplexer_1_out4), .D(update), .Q(\output [11]), .reset(clear));  // open: Qn, preset, en
  D_Flip_Flop d_ff_7 (.clk(demultiplexer_1_out6), .D(update), .Q(\output [9]), .reset(clear));  // open: Qn, preset, en
  D_Flip_Flop d_ff_8 (.clk(demultiplexer_1_out7), .D(update), .Q(\output [8]), .reset(clear));  // open: Qn, preset, en
  D_Flip_Flop d_ff_9 (.clk(demultiplexer_1_out8), .D(update), .Q(\output [7]), .reset(clear));  // open: Qn, preset, en
  D_Flip_Flop d_ff_10 (.clk(demultiplexer_1_out9), .D(update), .Q(\output [6]), .reset(clear));  // open: Qn, preset, en
  D_Flip_Flop d_ff_11 (
    .clk(demultiplexer_1_out10), .D(update), .Q(\output [5]), .reset(clear));  // open: Qn, preset, en
  D_Flip_Flop d_ff_12 (
    .clk(demultiplexer_1_out11), .D(update), .Q(\output [4]), .reset(clear));  // open: Qn, preset, en
  D_Flip_Flop d_ff_13 (
    .clk(demultiplexer_1_out13), .D(update), .Q(\output [2]), .reset(clear));  // open: Qn, preset, en
  D_Flip_Flop d_ff_14 (
    .clk(demultiplexer_1_out12), .D(update), .Q(\output [3]), .reset(clear));  // open: Qn, preset, en
  D_Flip_Flop d_ff_15 (
    .clk(demultiplexer_1_out14), .D(update), .Q(\output [1]), .reset(clear));  // open: Qn, preset, en
  D_Flip_Flop d_ff_16 (
    .clk(demultiplexer_1_out15), .D(update), .Q(\output [0]), .reset(clear));  // open: Qn, preset, en

  assign \output [16] = 1'b0;
endmodule

module _17bit_register_1 (
  input  [3:0] X,
  input  clock,
  input  [3:0] Y,
  input  clear,
  output [16:0] out_5,
  output [16:0] out_6,
  output [16:0] out_7,
  output [16:0] out_8,
  output [16:0] out_9,
  output [16:0] out_10,
  output [16:0] out_11,
  output [16:0] out_12,
  output [16:0] out_13,
  output [16:0] out_14,
  output [16:0] out_15,
  output [16:0] out_16,
  output [16:0] out_17,
  output [16:0] out_18,
  output [16:0] out_19,
  output [16:0] out_20
);

  wire demultiplexer_1_out0, demultiplexer_1_out1, demultiplexer_1_out2, demultiplexer_1_out3,
       demultiplexer_1_out4, demultiplexer_1_out5, demultiplexer_1_out6, demultiplexer_1_out7,
       demultiplexer_1_out8, demultiplexer_1_out9, demultiplexer_1_out10, demultiplexer_1_out11,
       demultiplexer_1_out12, demultiplexer_1_out13, demultiplexer_1_out14, demultiplexer_1_out15;

  Demultiplexer #(.select(4)) demultiplexer_1 (
    .out0(demultiplexer_1_out0), .out1(demultiplexer_1_out1), .out2(demultiplexer_1_out2),
    .out3(demultiplexer_1_out3), .out4(demultiplexer_1_out4), .out5(demultiplexer_1_out5),
    .out6(demultiplexer_1_out6), .out7(demultiplexer_1_out7), .out8(demultiplexer_1_out8),
    .out9(demultiplexer_1_out9), .out10(demultiplexer_1_out10), .out11(demultiplexer_1_out11),
    .out12(demultiplexer_1_out12), .out13(demultiplexer_1_out13), .out14(demultiplexer_1_out14),
    .out15(demultiplexer_1_out15), .in(clock), .sel(Y));  // open: en
  _17bit_register_0 u_17bit_register_0_1 (
    .clock(clock), .update(demultiplexer_1_out15), .X(X), .\output (out_5), .clear(clear));
  _17bit_register_0 u_17bit_register_0_2 (
    .clock(clock), .update(demultiplexer_1_out14), .X(X), .\output (out_6), .clear(clear));
  _17bit_register_0 u_17bit_register_0_3 (
    .clock(clock), .update(demultiplexer_1_out13), .X(X), .\output (out_7), .clear(clear));
  _17bit_register_0 u_17bit_register_0_4 (
    .clock(clock), .update(demultiplexer_1_out12), .X(X), .\output (out_8), .clear(clear));
  _17bit_register_0 u_17bit_register_0_5 (
    .clock(clock), .update(demultiplexer_1_out11), .X(X), .\output (out_9), .clear(clear));
  _17bit_register_0 u_17bit_register_0_6 (
    .clock(clock), .update(demultiplexer_1_out10), .X(X), .\output (out_10), .clear(clear));
  _17bit_register_0 u_17bit_register_0_7 (
    .clock(clock), .update(demultiplexer_1_out9), .X(X), .\output (out_11), .clear(clear));
  _17bit_register_0 u_17bit_register_0_8 (
    .clock(clock), .update(demultiplexer_1_out8), .X(X), .\output (out_12), .clear(clear));
  _17bit_register_0 u_17bit_register_0_9 (
    .clock(clock), .update(demultiplexer_1_out7), .X(X), .\output (out_13), .clear(clear));
  _17bit_register_0 u_17bit_register_0_10 (
    .clock(clock), .update(demultiplexer_1_out6), .X(X), .\output (out_14), .clear(clear));
  _17bit_register_0 u_17bit_register_0_11 (
    .clock(clock), .update(demultiplexer_1_out5), .X(X), .\output (out_15), .clear(clear));
  _17bit_register_0 u_17bit_register_0_12 (
    .clock(clock), .update(demultiplexer_1_out4), .X(X), .\output (out_16), .clear(clear));
  _17bit_register_0 u_17bit_register_0_13 (
    .clock(clock), .update(demultiplexer_1_out3), .X(X), .\output (out_17), .clear(clear));
  _17bit_register_0 u_17bit_register_0_14 (
    .clock(clock), .update(demultiplexer_1_out2), .X(X), .\output (out_18), .clear(clear));
  _17bit_register_0 u_17bit_register_0_15 (
    .clock(clock), .update(demultiplexer_1_out1), .X(X), .\output (out_19), .clear(clear));
  _17bit_register_0 u_17bit_register_0_16 (
    .clock(clock), .update(demultiplexer_1_out0), .X(X), .\output (out_20), .clear(clear));
endmodule

module _20bit_register_0 (
  input  clock,
  input  update,
  input  [3:0] X,
  input  clear,
  output [19:0] \output 
);

  wire demultiplexer_1_out0, demultiplexer_1_out1, demultiplexer_1_out2, demultiplexer_1_out3,
       demultiplexer_1_out4, demultiplexer_1_out5, demultiplexer_1_out6, demultiplexer_1_out7,
       demultiplexer_1_out8, demultiplexer_1_out9, demultiplexer_1_out10, demultiplexer_1_out11,
       demultiplexer_1_out12, demultiplexer_1_out13, demultiplexer_1_out14, demultiplexer_1_out15;

  Demultiplexer #(.select(4)) demultiplexer_1 (
    .out0(demultiplexer_1_out0), .out1(demultiplexer_1_out1), .out2(demultiplexer_1_out2),
    .out3(demultiplexer_1_out3), .out4(demultiplexer_1_out4), .out5(demultiplexer_1_out5),
    .out6(demultiplexer_1_out6), .out7(demultiplexer_1_out7), .out8(demultiplexer_1_out8),
    .out9(demultiplexer_1_out9), .out10(demultiplexer_1_out10), .out11(demultiplexer_1_out11),
    .out12(demultiplexer_1_out12), .out13(demultiplexer_1_out13), .out14(demultiplexer_1_out14),
    .out15(demultiplexer_1_out15), .in(clock), .sel(X));  // open: en
  D_Flip_Flop d_ff_1 (.clk(demultiplexer_1_out0), .D(update), .Q(\output [15]), .reset(clear));  // open: Qn, preset, en
  D_Flip_Flop d_ff_2 (.clk(demultiplexer_1_out1), .D(update), .Q(\output [14]), .reset(clear));  // open: Qn, preset, en
  D_Flip_Flop d_ff_3 (.clk(demultiplexer_1_out2), .D(update), .Q(\output [13]), .reset(clear));  // open: Qn, preset, en
  D_Flip_Flop d_ff_4 (.clk(demultiplexer_1_out3), .D(update), .Q(\output [12]), .reset(clear));  // open: Qn, preset, en
  D_Flip_Flop d_ff_5 (.clk(demultiplexer_1_out5), .D(update), .Q(\output [10]), .reset(clear));  // open: Qn, preset, en
  D_Flip_Flop d_ff_6 (.clk(demultiplexer_1_out4), .D(update), .Q(\output [11]), .reset(clear));  // open: Qn, preset, en
  D_Flip_Flop d_ff_7 (.clk(demultiplexer_1_out6), .D(update), .Q(\output [9]), .reset(clear));  // open: Qn, preset, en
  D_Flip_Flop d_ff_8 (.clk(demultiplexer_1_out7), .D(update), .Q(\output [8]), .reset(clear));  // open: Qn, preset, en
  D_Flip_Flop d_ff_9 (.clk(demultiplexer_1_out8), .D(update), .Q(\output [7]), .reset(clear));  // open: Qn, preset, en
  D_Flip_Flop d_ff_10 (.clk(demultiplexer_1_out9), .D(update), .Q(\output [6]), .reset(clear));  // open: Qn, preset, en
  D_Flip_Flop d_ff_11 (
    .clk(demultiplexer_1_out10), .D(update), .Q(\output [5]), .reset(clear));  // open: Qn, preset, en
  D_Flip_Flop d_ff_12 (
    .clk(demultiplexer_1_out11), .D(update), .Q(\output [4]), .reset(clear));  // open: Qn, preset, en
  D_Flip_Flop d_ff_13 (
    .clk(demultiplexer_1_out12), .D(update), .Q(\output [3]), .reset(clear));  // open: Qn, preset, en
  D_Flip_Flop d_ff_14 (
    .clk(demultiplexer_1_out13), .D(update), .Q(\output [2]), .reset(clear));  // open: Qn, preset, en
  D_Flip_Flop d_ff_15 (
    .clk(demultiplexer_1_out14), .D(update), .Q(\output [1]), .reset(clear));  // open: Qn, preset, en
  D_Flip_Flop d_ff_16 (
    .clk(demultiplexer_1_out15), .D(update), .Q(\output [0]), .reset(clear));  // open: Qn, preset, en

  assign \output [19:16] = 4'b0000;
endmodule

module _20bit_register_1 (
  input  [3:0] X,
  input  clock,
  input  [3:0] Y,
  input  clear,
  output [19:0] out_5,
  output [19:0] out_6,
  output [19:0] out_7,
  output [19:0] out_8,
  output [19:0] out_9,
  output [19:0] out_10,
  output [19:0] out_11,
  output [19:0] out_12,
  output [19:0] out_13,
  output [19:0] out_14,
  output [19:0] out_15,
  output [19:0] out_16,
  output [19:0] out_17,
  output [19:0] out_18,
  output [19:0] out_19,
  output [19:0] out_20
);

  wire demultiplexer_1_out0, demultiplexer_1_out1, demultiplexer_1_out2, demultiplexer_1_out3,
       demultiplexer_1_out4, demultiplexer_1_out5, demultiplexer_1_out6, demultiplexer_1_out7,
       demultiplexer_1_out8, demultiplexer_1_out9, demultiplexer_1_out10, demultiplexer_1_out11,
       demultiplexer_1_out12, demultiplexer_1_out13, demultiplexer_1_out14, demultiplexer_1_out15;

  Demultiplexer #(.select(4)) demultiplexer_1 (
    .out0(demultiplexer_1_out0), .out1(demultiplexer_1_out1), .out2(demultiplexer_1_out2),
    .out3(demultiplexer_1_out3), .out4(demultiplexer_1_out4), .out5(demultiplexer_1_out5),
    .out6(demultiplexer_1_out6), .out7(demultiplexer_1_out7), .out8(demultiplexer_1_out8),
    .out9(demultiplexer_1_out9), .out10(demultiplexer_1_out10), .out11(demultiplexer_1_out11),
    .out12(demultiplexer_1_out12), .out13(demultiplexer_1_out13), .out14(demultiplexer_1_out14),
    .out15(demultiplexer_1_out15), .in(clock), .sel(Y));  // open: en
  _20bit_register_0 u_20bit_register_0_1 (
    .clock(demultiplexer_1_out15), .update(clock), .X(X), .clear(clear), .\output (out_5));
  _20bit_register_0 u_20bit_register_0_2 (
    .clock(demultiplexer_1_out14), .update(clock), .X(X), .clear(clear), .\output (out_6));
  _20bit_register_0 u_20bit_register_0_3 (
    .clock(demultiplexer_1_out13), .update(clock), .X(X), .clear(clear), .\output (out_7));
  _20bit_register_0 u_20bit_register_0_4 (
    .clock(demultiplexer_1_out12), .update(clock), .X(X), .clear(clear), .\output (out_8));
  _20bit_register_0 u_20bit_register_0_5 (
    .clock(demultiplexer_1_out11), .update(clock), .X(X), .clear(clear), .\output (out_9));
  _20bit_register_0 u_20bit_register_0_6 (
    .clock(demultiplexer_1_out10), .update(clock), .X(X), .clear(clear), .\output (out_10));
  _20bit_register_0 u_20bit_register_0_7 (
    .clock(demultiplexer_1_out9), .update(clock), .X(X), .clear(clear), .\output (out_11));
  _20bit_register_0 u_20bit_register_0_8 (
    .clock(demultiplexer_1_out8), .update(clock), .X(X), .clear(clear), .\output (out_12));
  _20bit_register_0 u_20bit_register_0_9 (
    .clock(demultiplexer_1_out7), .update(clock), .X(X), .clear(clear), .\output (out_13));
  _20bit_register_0 u_20bit_register_0_10 (
    .clock(demultiplexer_1_out6), .update(clock), .X(X), .clear(clear), .\output (out_14));
  _20bit_register_0 u_20bit_register_0_11 (
    .clock(demultiplexer_1_out5), .update(clock), .X(X), .clear(clear), .\output (out_15));
  _20bit_register_0 u_20bit_register_0_12 (
    .clock(demultiplexer_1_out4), .update(clock), .X(X), .clear(clear), .\output (out_16));
  _20bit_register_0 u_20bit_register_0_13 (
    .clock(demultiplexer_1_out3), .update(clock), .X(X), .clear(clear), .\output (out_17));
  _20bit_register_0 u_20bit_register_0_14 (
    .clock(demultiplexer_1_out2), .update(clock), .X(X), .clear(clear), .\output (out_18));
  _20bit_register_0 u_20bit_register_0_15 (
    .clock(demultiplexer_1_out1), .update(clock), .X(X), .clear(clear), .\output (out_19));
  _20bit_register_0 u_20bit_register_0_16 (
    .clock(demultiplexer_1_out0), .update(clock), .X(X), .clear(clear), .\output (out_20));
endmodule

module edges (
  input  in_1,
  input  in_2,
  input  in_3,
  input  in_4
);
endmodule
