// Logisim project last_version_1.circ as structural Verilog: 7 circuits, main circuit main
// 1
module main (
);

  wire _0_b_out, _1_a_out, _2_b_prime_out, and_1_out, and_3_out, button_2_out, button_3_out, button_4_out,
       button_5_out, button_6_out, cdm_8_mark5_1_p4, cdm_8_mark5_1_p5, cdm_8_mark5_1_p7, cdm_8_mark5_1_p8,
       cdm_8_mark5_1_p9, cdm_8_mark5_1_p10, cdm_8_mark5_1_p11, cdm_8_mark5_1_p12, cdm_8_mark5_1_p13, clk,
       clock, clr, d_ff_1_qn, decoder_1_out0, decoder_1_out1, decoder_2_out0, decoder_2_out2, down,
       granca_detection_1_out_6, HZ, IAck, IO_2_out, IOsel, IRQ, left, not_1_out, not_2_out, or_1_out,
       or_2_out, or_4_out, READwrite, right, up;
  wire [1:0] nor_1_out, register_5_q;
  wire [2:0] vec;
  wire [3:0] inc_dec_1_r, inc_dec_2_r, IOaddr;
  wire [7:0] and_4_out, cdm_8_mark5_1_p16, cdm_8_mark5_1_p17, IOdat, random_1_out, register_1_q, register_4_q;
  wire [7:4] cdm_8_mark5_1_p15;
  wire [15:0] pseudo_reg_1_out_3, pseudo_reg_1_out_4, pseudo_reg_1_out_5, pseudo_reg_1_out_6,
       pseudo_reg_1_out_7, pseudo_reg_1_out_8, pseudo_reg_1_out_9, pseudo_reg_1_out_10, pseudo_reg_1_out_11,
       pseudo_reg_1_out_12, pseudo_reg_1_out_13, pseudo_reg_1_out_14, pseudo_reg_1_out_15,
       pseudo_reg_1_out_16, pseudo_reg_1_out_17, pseudo_reg_1_out_18, pseudo_reg_2_out_3, pseudo_reg_2_out_4,
       pseudo_reg_2_out_5, pseudo_reg_2_out_6, pseudo_reg_2_out_7, pseudo_reg_2_out_8, pseudo_reg_2_out_9,
       pseudo_reg_2_out_10, pseudo_reg_2_out_11, pseudo_reg_2_out_12, pseudo_reg_2_out_13,
       pseudo_reg_2_out_14, pseudo_reg_2_out_15, pseudo_reg_2_out_16, pseudo_reg_2_out_17,
       pseudo_reg_2_out_18;

  Clock clock_1 (.out(clk));
  granca_detection granca_detection_1 (
    .in_3(register_1_q), .Left(left), .Right(right), .out_6(granca_detection_1_out_6), .Up(up), .Down(down));
  Button button_1 (.out(clr));
  Register register_1 (.D({inc_dec_1_r, inc_dec_2_r}), .Q(register_1_q), .clk(and_1_out), .clr(clr));  // open: en
  and and_1 (and_1_out, clock, d_ff_1_qn);
  D_Flip_Flop d_ff_1 (.Qn(d_ff_1_qn), .preset(granca_detection_1_out_6), .reset(clr));  // open: clk, D, Q, en
  // Probe on cdm_8_mark5_1_p8
  // Probe on cdm_8_mark5_1_p7
  // Probe on cdm_8_mark5_1_p5
  // Probe on cdm_8_mark5_1_p4
  or or_1 (or_1_out, left, right);
  // Probe on cdm_8_mark5_1_p10
  // Probe on cdm_8_mark5_1_p11
  // Probe on cdm_8_mark5_1_p9
  // CdM_8_mark5 cdm_8_mark5_1: pin names not known; wires that end beside it: IRQ, vec, IAck, cdm_8_mark5_1_p4, cdm_8_mark5_1_p5, clk, cdm_8_mark5_1_p7, cdm_8_mark5_1_p8, cdm_8_mark5_1_p9, cdm_8_mark5_1_p10, cdm_8_mark5_1_p11, cdm_8_mark5_1_p12, cdm_8_mark5_1_p13, READwrite, {cdm_8_mark5_1_p15, IOaddr}, cdm_8_mark5_1_p16, cdm_8_mark5_1_p17
  inc_dec inc_dec_1 (.X(register_1_q[7:4]), .on_off(or_1_out), .inc_dec(right), .R(inc_dec_1_r));  // open: OFL
  inc_dec inc_dec_2 (.X(register_1_q[3:0]), .on_off(or_2_out), .inc_dec(up), .R(inc_dec_2_r));  // open: OFL
  and and_2 (IOsel, cdm_8_mark5_1_p15[4], cdm_8_mark5_1_p15[5], cdm_8_mark5_1_p15[6], cdm_8_mark5_1_p15[7], decoder_1_out1);
  Decoder #(.disabled(0)) decoder_1 (
    .out0(decoder_1_out0), .out1(decoder_1_out1), .sel(cdm_8_mark5_1_p12), .en(cdm_8_mark5_1_p13));
  not not_1 (not_1_out, READwrite);
  assign IOdat = not_1_out ? cdm_8_mark5_1_p16 : 8'bz;  // Controlled_Buffer controlled_buffer_1
  assign cdm_8_mark5_1_p17 = READwrite ? IOdat : 8'bz;  // Controlled_Buffer controlled_buffer_2
  Register #(.width(4)) register_2 (.D(register_1_q[7:4]), .clk(clock), .clr(clr));  // open: en, Q
  or or_2 (or_2_out, up, down);
  // Probe on {cdm_8_mark5_1_p15, IOaddr}
  and and_3 (and_3_out, decoder_1_out1, ~IOsel);  // AND_Gate
  Register #(.width(4)) register_3 (.D(register_1_q[3:0]), .clk(clock), .clr(clr));  // open: en, Q
  assign and_4_out = register_1_q & random_1_out;  // AND_Gate and_4, 8 bits wide
  or or_3 (HZ, and_4_out[7], and_4_out[6], and_4_out[5], and_4_out[4], and_4_out[3], and_4_out[2], and_4_out[1], and_4_out[0]);
  RAM ram_1 (
    .addr({cdm_8_mark5_1_p15, IOaddr}), .data(IOdat), .sel(and_3_out), .clk(not_2_out), .ld(READwrite));  // open: clr
  not not_2 (not_2_out, clk);
  ROM rom_1 (.addr({cdm_8_mark5_1_p15, IOaddr}), .data(IOdat), .sel(decoder_1_out0));
  DotMatrix #(.matrixcols(16), .matrixrows(16)) dotmatrix_1 (
    .col0(pseudo_reg_1_out_11), .col1(pseudo_reg_1_out_3), .col2(pseudo_reg_1_out_12),
    .col3(pseudo_reg_1_out_4), .col4(pseudo_reg_1_out_13), .col5(pseudo_reg_1_out_5),
    .col6(pseudo_reg_1_out_14), .col7(pseudo_reg_1_out_6), .col8(pseudo_reg_1_out_15),
    .col9(pseudo_reg_1_out_7), .col10(pseudo_reg_1_out_16), .col11(pseudo_reg_1_out_8),
    .col12(pseudo_reg_1_out_17), .col13(pseudo_reg_1_out_9), .col14(pseudo_reg_1_out_18),
    .col15(pseudo_reg_1_out_10));
  pseudo_reg pseudo_reg_1 (
    .in_1(register_1_q[3:0]), .in_2(register_1_q[7:4]), .out_11(pseudo_reg_1_out_11),
    .out_3(pseudo_reg_1_out_3), .out_4(pseudo_reg_1_out_4), .out_12(pseudo_reg_1_out_12),
    .out_5(pseudo_reg_1_out_5), .out_13(pseudo_reg_1_out_13), .out_6(pseudo_reg_1_out_6),
    .out_14(pseudo_reg_1_out_14), .out_7(pseudo_reg_1_out_7), .out_15(pseudo_reg_1_out_15),
    .out_8(pseudo_reg_1_out_8), .out_16(pseudo_reg_1_out_16), .out_9(pseudo_reg_1_out_9),
    .out_17(pseudo_reg_1_out_17), .out_10(pseudo_reg_1_out_10), .out_18(pseudo_reg_1_out_18));
  // Probe on IOdat
  Button button_2 (.out(button_2_out));
  Button button_3 (.out(button_3_out));
  Button button_4 (.out(button_4_out));
  Button button_5 (.out(button_5_out));
  movement movement_1 (
    .Right(button_3_out), .Down(button_5_out), .Left(button_4_out), .Up(button_2_out), .Clock(clock),
    .Clear(clr), .out_7(up), .out_8(down), .out_9(left), .out_10(right));
  Random #(.seed(16)) random_1 (.clk(HZ), .out(random_1_out));  // open: next, clr
  and IO_2 (IO_2_out, IOsel, ~IOaddr[0], ~IOaddr[2], ~IOaddr[3]);  // AND_Gate
  DotMatrix #(.matrixcols(16), .matrixrows(16)) dotmatrix_2 (
    .col0(pseudo_reg_2_out_11), .col1(pseudo_reg_2_out_3), .col2(pseudo_reg_2_out_12),
    .col3(pseudo_reg_2_out_4), .col4(pseudo_reg_2_out_13), .col5(pseudo_reg_2_out_5),
    .col6(pseudo_reg_2_out_14), .col7(pseudo_reg_2_out_6), .col8(pseudo_reg_2_out_15),
    .col9(pseudo_reg_2_out_7), .col10(pseudo_reg_2_out_16), .col11(pseudo_reg_2_out_8),
    .col12(pseudo_reg_2_out_17), .col13(pseudo_reg_2_out_9), .col14(pseudo_reg_2_out_18),
    .col15(pseudo_reg_2_out_10));
  pseudo_reg pseudo_reg_2 (
    .in_1(random_1_out[3:0]), .in_2(random_1_out[7:4]), .out_11(pseudo_reg_2_out_11),
    .out_3(pseudo_reg_2_out_3), .out_4(pseudo_reg_2_out_4), .out_12(pseudo_reg_2_out_12),
    .out_5(pseudo_reg_2_out_5), .out_13(pseudo_reg_2_out_13), .out_6(pseudo_reg_2_out_6),
    .out_14(pseudo_reg_2_out_14), .out_7(pseudo_reg_2_out_7), .out_15(pseudo_reg_2_out_15),
    .out_8(pseudo_reg_2_out_8), .out_16(pseudo_reg_2_out_16), .out_9(pseudo_reg_2_out_9),
    .out_17(pseudo_reg_2_out_17), .out_10(pseudo_reg_2_out_10), .out_18(pseudo_reg_2_out_18));
  DotMatrix #(.matrixcols(1), .matrixrows(8)) dotmatrix_3 (.col0(register_4_q));
  Register #(.trigger("falling")) register_4 (.D(IOdat), .en(IO_2_out), .Q(register_4_q), .clk(clk));  // open: clr
  assign vec = IAck ? 3'b001 : 3'bz;  // Controlled_Buffer controlled_buffer_3
  Decoder #(.select(2), .enable("false")) decoder_2 (
    .out0(decoder_2_out0), .out1(IRQ), .out2(decoder_2_out2), .sel(register_5_q));  // open: out3
  Button button_6 (.out(button_6_out));
  and _0_b (_0_b_out, button_6_out, decoder_2_out0);
  and _1_a (_1_a_out, IAck, IRQ);
  and _2_b_prime (_2_b_prime_out, ~button_6_out, decoder_2_out2);  // AND_Gate
  and and_5 (nor_1_out[1], register_5_q[0], ~register_5_q[1]);  // AND_Gate
  or or_4 (or_4_out, _0_b_out, _1_a_out, _2_b_prime_out);
  nor nor_1 (nor_1_out[0], register_5_q[0], register_5_q[1]);
  Register #(.width(2), .trigger("falling")) register_5 (
    .D(nor_1_out), .en(or_4_out), .Q(register_5_q), .clk(clk));  // open: clr

  // Notes on the sheet:
  //   coor X
  //   coor Y
  //   contents of rom_1 (hex, n*v repeats v):
  //   cd f0 d0 9 c0 d0 80 c0 d9 d3 10 d0 f2 3a a e1 14 2f ee 15 93 e3 19 d3 10 a3 ee e 82 d9 212*0 1c
  //   garland
  //   0->1->2->0
endmodule

module _16_bit_AND (
  input  [15:0] \input ,
  input  switch,
  output [15:0] \output 
);

  assign \output  = \input  & {16{switch}};  // AND_Gate and_1, 16 bits wide
endmodule

module column_switch (
  input  [3:0] in_1,
  input  [3:0] in_2
);
endmodule

module inc_dec (
  input  [3:0] X,
  input  on_off,
  input  inc_dec,
  output [3:0] R,
  output OFL
);

  wire and_2_out, and_3_out;
  wire [3:0] and_1_out, xor_1_out, xor_2_out, xor_3_out;
  wire [3:3] decoder_1_out0, decoder_1_out1;

  Decoder #(.enable("false")) decoder_1 (.out0(decoder_1_out0[3]), .out1(decoder_1_out1[3]), .sel(inc_dec));
  assign xor_1_out = {4{decoder_1_out0[3]}} ^ X;  // XOR_Gate xor_1, 4 bits wide
  assign xor_2_out = {4{decoder_1_out1[3]}} ^ xor_3_out;  // XOR_Gate xor_2, 4 bits wide
  assign and_1_out = xor_1_out & xor_2_out;  // AND_Gate and_1, 4 bits wide
  and and_2 (and_2_out, and_1_out[3], inc_dec);
  and and_3 (and_3_out, and_1_out[3], ~inc_dec);  // AND_Gate
  assign xor_3_out = X ^ {and_1_out[2:0], 1'b1};  // XOR_Gate xor_3, 4 bits wide
  or or_1 (OFL, and_2_out, and_3_out);
  Multiplexer #(.width(4), .enable("false")) multiplexer_1 (.in0(X), .in1(xor_3_out), .out(R), .sel(on_off));
endmodule

module granca_detection (
  input  Up,
  input  Down,
  input  [7:0] in_3,
  input  Left,
  input  Right,
  output out_6
);

  wire and_1_out, and_2_out, nor_1_out, nor_2_out;

  Pull_Resistor pull_resistor_1 (.node(Up));
  Pull_Resistor pull_resistor_2 (.node(Down));
  Pull_Resistor pull_resistor_3 (.node(Left));
  Pull_Resistor pull_resistor_4 (.node(Right));
  and and_1 (and_1_out, Up, in_3[3], in_3[2], in_3[1], in_3[0]);
  and and_2 (and_2_out, in_3[7], in_3[6], in_3[5], in_3[4], Right);
  nor nor_1 (nor_1_out, ~Down, in_3[0], in_3[1], in_3[2], in_3[3]);  // NOR_Gate
  nor nor_2 (nor_2_out, in_3[4], in_3[5], in_3[6], in_3[7], ~Left);  // NOR_Gate
  or or_1 (out_6, and_1_out, nor_1_out, nor_2_out, and_2_out);
endmodule

module movement (
  input  Right,
  input  Down,
  input  Left,
  input  Up,
  input  Clock,
  input  Clear,
  output out_7,
  output out_8,
  output out_9,
  output out_10
);

  wire and_1_out, counter_1_carry, or_3_out, xnor_1_out, xor_1_out;
  wire [1:0] multiplexer_1_out, or_1_out, register_1_q, register_2_q;

  or or_1 (or_1_out[0], Down, Right);
  or or_2 (or_1_out[1], Right, Left);
  or or_3 (or_3_out, Right, Down, Left, Up);
  Register #(.width(2)) register_1 (.D(or_1_out), .Q(register_1_q), .clk(or_3_out), .clr(Clear));  // open: en
  Register #(.width(2)) register_2 (.D(multiplexer_1_out), .Q(register_2_q), .clk(or_3_out), .clr(Clear));  // open: en
  xnor xnor_1 (xnor_1_out, register_2_q[1], register_1_q[1]);
  and and_1 (and_1_out, xnor_1_out, xor_1_out);
  xor xor_1 (xor_1_out, register_2_q[0], register_1_q[0]);
  Multiplexer #(.width(2)) multiplexer_1 (
    .in0(register_1_q), .in1(register_2_q), .out(multiplexer_1_out), .sel(and_1_out));  // open: en
  Counter #(.width(3), .max('h5)) counter_1 (
    .carry(counter_1_carry), .clk(Clock), .clr(Clear));  // open: load, D, count, Q
  Demultiplexer #(.select(2)) demultiplexer_1 (
    .out0(out_7), .out1(out_8), .out2(out_9), .out3(out_10), .in(counter_1_carry), .sel(multiplexer_1_out));  // open: en

  // Other names for the same wires on the sheet: clr = Clear

  // Notes on the sheet:
  //   новое напр.
  //   текушее напр.
endmodule

module pseudo_reg (
  input  [3:0] in_1,
  input  [3:0] in_2,
  output [15:0] out_3,
  output [15:0] out_4,
  output [15:0] out_5,
  output [15:0] out_6,
  output [15:0] out_7,
  output [15:0] out_8,
  output [15:0] out_9,
  output [15:0] out_10,
  output [15:0] out_11,
  output [15:0] out_12,
  output [15:0] out_13,
  output [15:0] out_14,
  output [15:0] out_15,
  output [15:0] out_16,
  output [15:0] out_17,
  output [15:0] out_18
);

  wire decoder_2_out0, decoder_2_out1, decoder_2_out2, decoder_2_out3, decoder_2_out4, decoder_2_out5,
       decoder_2_out6, decoder_2_out7, decoder_2_out8, decoder_2_out9, decoder_2_out10, decoder_2_out11,
       decoder_2_out12, decoder_2_out13, decoder_2_out14, decoder_2_out15;
  wire [15:0] decoder_1_out0;

  Decoder #(.select(4), .disabled(0), .enable("false")) decoder_1 (
    .out0(decoder_1_out0[0]), .out1(decoder_1_out0[1]), .out2(decoder_1_out0[2]), .out3(decoder_1_out0[3]),
    .out4(decoder_1_out0[4]), .out5(decoder_1_out0[5]), .out6(decoder_1_out0[6]), .out7(decoder_1_out0[7]),
    .out8(decoder_1_out0[8]), .out9(decoder_1_out0[9]), .out10(decoder_1_out0[10]),
    .out11(decoder_1_out0[11]), .out12(decoder_1_out0[12]), .out13(decoder_1_out0[13]),
    .out14(decoder_1_out0[14]), .out15(decoder_1_out0[15]), .sel(in_1));
  _16_bit_AND u_16_bit_and_1 (.\input (decoder_1_out0), .switch(decoder_2_out1), .\output (out_3));
  _16_bit_AND u_16_bit_and_2 (.\input (decoder_1_out0), .switch(decoder_2_out0), .\output (out_11));
  _16_bit_AND u_16_bit_and_3 (.\input (decoder_1_out0), .switch(decoder_2_out3), .\output (out_4));
  _16_bit_AND u_16_bit_and_4 (.\input (decoder_1_out0), .switch(decoder_2_out2), .\output (out_12));
  Decoder #(.select(4), .disabled(0), .enable("false")) decoder_2 (
    .out0(decoder_2_out0), .out1(decoder_2_out1), .out2(decoder_2_out2), .out3(decoder_2_out3),
    .out4(decoder_2_out4), .out5(decoder_2_out5), .out6(decoder_2_out6), .out7(decoder_2_out7),
    .out8(decoder_2_out8), .out9(decoder_2_out9), .out10(decoder_2_out10), .out11(decoder_2_out11),
    .out12(decoder_2_out12), .out13(decoder_2_out13), .out14(decoder_2_out14), .out15(decoder_2_out15),
    .sel(in_2));
  _16_bit_AND u_16_bit_and_5 (.\input (decoder_1_out0), .switch(decoder_2_out4), .\output (out_13));
  _16_bit_AND u_16_bit_and_6 (.\input (decoder_1_out0), .switch(decoder_2_out5), .\output (out_5));
  _16_bit_AND u_16_bit_and_7 (.\input (decoder_1_out0), .switch(decoder_2_out6), .\output (out_14));
  _16_bit_AND u_16_bit_and_8 (.\input (decoder_1_out0), .switch(decoder_2_out7), .\output (out_6));
  _16_bit_AND u_16_bit_and_9 (.\input (decoder_1_out0), .switch(decoder_2_out8), .\output (out_15));
  _16_bit_AND u_16_bit_and_10 (.\input (decoder_1_out0), .switch(decoder_2_out9), .\output (out_7));
  _16_bit_AND u_16_bit_and_11 (.\input (decoder_1_out0), .switch(decoder_2_out10), .\output (out_16));
  _16_bit_AND u_16_bit_and_12 (.\input (decoder_1_out0), .switch(decoder_2_out11), .\output (out_8));
  _16_bit_AND u_16_bit_and_13 (.\input (decoder_1_out0), .switch(decoder_2_out12), .\output (out_17));
  _16_bit_AND u_16_bit_and_14 (.\input (decoder_1_out0), .switch(decoder_2_out13), .\output (out_9));
  _16_bit_AND u_16_bit_and_15 (.\input (decoder_1_out0), .switch(decoder_2_out15), .\output (out_10));
  _16_bit_AND u_16_bit_and_16 (.\input (decoder_1_out0), .switch(decoder_2_out14), .\output (out_18));
endmodule
