// Logisim project last_version_12.circ as structural Verilog
// 1
module main (
  input  in_1,
  input  in_2,
  input  in_3
);

  wire _1_1, _1_2, _1_3, _1_4, _1_5, _1_6, _1_7, _1_8, _2_1, _2_2, _2_3, _2_4, _2_5, _2_6, _2_7, _2_8,
       and_1_out, and_5_out, button_1_out, button_2_out, button_3_out, button_4_out, cdm_8_mark5_1_p1,
       cdm_8_mark5_1_p2, cdm_8_mark5_1_p4, cdm_8_mark5_1_p5, cdm_8_mark5_1_p6, cdm_8_mark5_1_p7,
       cdm_8_mark5_1_p8, cdm_8_mark5_1_p9, clk, clock, clock_1_out, clr, code, controlled_buffer_1_out,
       counter_1_carry, d_ff_1_qn, data, decoder_1_out0, decoder_1_out1, down, golod,
       granca_detection_1_out_6, hz, I_Osel, In_Out_prime, left, mem, nand_1_out, nor_4_out, nor_5_out,
       not_1_out, not_2_out, not_3_out, not_4_out, not_5_out, not_6_out, not_7_out, not_8_out, not_9_out,
       not_10_out, not_11_out, or_1_out, or_2_out, or_3_out, or_4_out, port1, port2, port3, port4, port_gran,
       RAM, right, takt, transistor_1_out, up;
  wire [3:0] I_Oadr, inc_dec_1_r, inc_dec_2_r, portx, porty, register_5_q, register_5_q_2;
  wire [6:0] controlled_buffer_2_out, keyboard_1_data, undriven;
  wire [7:0] adder_1_out, cdm_8_mark5_1_p13, cdm_8_mark5_1_p14, counter_1_q, counter_2_q, head, I_Odata,
       negator_1_out, register_4_q;
  wire [7:4] cdm_8_mark5_1_p12;
  wire [7:7] s_r_ff_1_qn;
  wire [15:0] or_5_out, or_6_out, or_7_out, or_8_out, or_9_out, or_10_out, or_11_out, or_12_out, or_13_out,
       or_14_out, or_15_out, or_16_out, or_17_out, or_18_out, or_19_out, or_20_out, pseudo_reg_1_out_3,
       pseudo_reg_1_out_4, pseudo_reg_1_out_5, pseudo_reg_1_out_6, pseudo_reg_1_out_7, pseudo_reg_1_out_8,
       pseudo_reg_1_out_9, pseudo_reg_1_out_10, pseudo_reg_1_out_11, pseudo_reg_1_out_12,
       pseudo_reg_1_out_13, pseudo_reg_1_out_14, pseudo_reg_1_out_15, pseudo_reg_1_out_16,
       pseudo_reg_1_out_17, pseudo_reg_1_out_18, pseudo_reg_2_out_3, pseudo_reg_2_out_4, pseudo_reg_2_out_5,
       pseudo_reg_2_out_6, pseudo_reg_2_out_7, pseudo_reg_2_out_8, pseudo_reg_2_out_9, pseudo_reg_2_out_10,
       pseudo_reg_2_out_11, pseudo_reg_2_out_12, pseudo_reg_2_out_13, pseudo_reg_2_out_14,
       pseudo_reg_2_out_15, pseudo_reg_2_out_16, pseudo_reg_2_out_17, pseudo_reg_2_out_18;

  not not_1 (not_1_out, in_1);
  Clock clock_1 (.out(clock_1_out));
  assign controlled_buffer_1_out = not_1_out ? clock_1_out : 1'bz;  // Controlled_Buffer controlled_buffer_1
  and and_1 (and_1_out, clock, d_ff_1_qn);
  D_Flip_Flop d_ff_1 (.Qn(d_ff_1_qn), .preset(granca_detection_1_out_6), .reset(clr));  // open: clk, D, Q, en
  granca_detection granca_detection_1 (
    .in_3(head), .Left(left), .Right(right), .out_6(granca_detection_1_out_6), .Up(up), .Down(down));
  Negator negator_1 (.in(head), .out(negator_1_out));
  Pull_Resistor pull_resistor_1 (.node(controlled_buffer_1_out));
  Multiplexer multiplexer_1 (.in0(controlled_buffer_1_out), .in1(1'b0), .out(takt), .sel(golod));  // open: en
  Register register_1 (.D({inc_dec_2_r, inc_dec_1_r}), .Q(head), .clk(and_1_out), .clr(clr));  // open: en
  or or_1 (or_1_out, left, right);
  Adder adder_1 (.a({porty, portx}), .b(negator_1_out), .out(adder_1_out));  // open: cin, cout
  or or_2 (or_2_out, port1, port2, port3, port4);
  and and_2 (port_gran, or_2_out, takt);
  inc_dec inc_dec_1 (.X(head[3:0]), .on_off(or_4_out), .inc_dec(up), .R(inc_dec_1_r));  // open: OFL
  inc_dec inc_dec_2 (.X(head[7:4]), .on_off(or_1_out), .inc_dec(right), .R(inc_dec_2_r));  // open: OFL
  Random #(.seed(16)) random_1 (.clk(or_3_out), .out({porty, portx}));  // open: next, clr
  or or_3 (or_3_out, clr, port_gran, hz);
  Button button_1 (.out(button_1_out));
  Register #(.width(4)) register_2 (.D(head[7:4]), .clk(clock), .clr(clr));  // open: en, Q
  or or_4 (or_4_out, up, down);
  nor nor_1 (hz, adder_1_out[0], adder_1_out[1], adder_1_out[2], adder_1_out[3], adder_1_out[4], adder_1_out[5], adder_1_out[6], adder_1_out[7]);
  Button button_2 (.out(button_2_out));
  Transistor #(.\type ("n")) transistor_1 (.in(1'b0), .out(transistor_1_out), .gate(button_1_out));
  assign controlled_buffer_2_out = button_1_out ? 7'b1100001 : 7'bz;  // Controlled_Buffer controlled_buffer_2
  not not_2 (not_2_out, transistor_1_out);
  not not_3 (not_3_out, decoder_1_out1);
  Register #(.width(4)) register_3 (.D(head[3:0]), .clk(clock), .clr(clr));  // open: en, Q
  pseudo_reg pseudo_reg_1 (
    .in_1(head[3:0]), .in_2(head[7:4]), .out_11(pseudo_reg_1_out_11), .out_3(pseudo_reg_1_out_3),
    .out_4(pseudo_reg_1_out_4), .out_12(pseudo_reg_1_out_12), .out_5(pseudo_reg_1_out_5),
    .out_13(pseudo_reg_1_out_13), .out_6(pseudo_reg_1_out_6), .out_14(pseudo_reg_1_out_14),
    .out_7(pseudo_reg_1_out_7), .out_15(pseudo_reg_1_out_15), .out_8(pseudo_reg_1_out_8),
    .out_16(pseudo_reg_1_out_16), .out_9(pseudo_reg_1_out_9), .out_17(pseudo_reg_1_out_17),
    .out_10(pseudo_reg_1_out_10), .out_18(pseudo_reg_1_out_18));
  pseudo_reg pseudo_reg_2 (
    .in_1(portx), .in_2(porty), .out_11(pseudo_reg_2_out_11), .out_3(pseudo_reg_2_out_3),
    .out_4(pseudo_reg_2_out_4), .out_12(pseudo_reg_2_out_12), .out_5(pseudo_reg_2_out_5),
    .out_13(pseudo_reg_2_out_13), .out_6(pseudo_reg_2_out_6), .out_14(pseudo_reg_2_out_14),
    .out_7(pseudo_reg_2_out_7), .out_15(pseudo_reg_2_out_15), .out_8(pseudo_reg_2_out_8),
    .out_16(pseudo_reg_2_out_16), .out_9(pseudo_reg_2_out_9), .out_17(pseudo_reg_2_out_17),
    .out_10(pseudo_reg_2_out_10), .out_18(pseudo_reg_2_out_18));
  nor nor_2 (port1, portx[0], portx[1], portx[2], portx[3]);
  nor nor_3 (port2, porty[0], porty[1], porty[2], porty[3]);
  Button button_3 (.out(button_3_out));
  Transistor #(.\type ("n")) transistor_2 (.in(1'b0), .out(transistor_1_out), .gate(button_2_out));
  assign controlled_buffer_2_out = button_2_out ? 7'b1100010 : 7'bz;  // Controlled_Buffer controlled_buffer_3
  nor nor_4 (nor_4_out, transistor_1_out, not_2_out);
  nor nor_5 (nor_5_out, not_3_out, decoder_1_out1);
  assign or_5_out = pseudo_reg_1_out_11 | pseudo_reg_2_out_11;  // OR_Gate or_5, 16 bits wide
  Transistor #(.\type ("n")) transistor_3 (.in(1'b0), .out(transistor_1_out), .gate(button_3_out));
  assign controlled_buffer_2_out = button_3_out ? 7'b1100011 : 7'bz;  // Controlled_Buffer controlled_buffer_4
  S_R_Flip_Flop s_r_ff_1 (.S(nor_4_out), .R(nor_5_out), .Qn(s_r_ff_1_qn[7]), .en(1'b0));  // open: clk, Q, preset, reset
  DotMatrix #(.matrixcols(16), .matrixrows(16)) dotmatrix_1 (
    .col0(or_5_out), .col1(or_8_out), .col2(or_7_out), .col3(or_6_out), .col4(or_9_out), .col5(or_10_out),
    .col6(or_12_out), .col7(or_11_out), .col8(or_13_out), .col9(or_15_out), .col10(or_16_out),
    .col11(or_14_out), .col12(or_17_out), .col13(or_18_out), .col14(or_20_out), .col15(or_19_out));
  assign or_6_out = pseudo_reg_1_out_4 | pseudo_reg_2_out_4;  // OR_Gate or_6, 16 bits wide
  assign or_7_out = pseudo_reg_1_out_12 | pseudo_reg_2_out_12;  // OR_Gate or_7, 16 bits wide
  assign or_8_out = pseudo_reg_1_out_3 | pseudo_reg_2_out_3;  // OR_Gate or_8, 16 bits wide
  and and_3 (port3, portx[0], portx[1], portx[2], portx[3]);
  and and_4 (port4, porty[0], porty[1], porty[2], porty[3]);
  Pull_Resistor #(.pull(1)) pull_resistor_2 (.node(transistor_1_out));
  Button button_4 (.out(button_4_out));
  Transistor #(.\type ("n")) transistor_4 (.in(1'b0), .out(transistor_1_out), .gate(button_4_out));
  assign controlled_buffer_2_out = button_4_out ? 7'b1100100 : 7'bz;  // Controlled_Buffer controlled_buffer_5
  \рп  \u_рп_1  ();
  assign or_9_out = pseudo_reg_1_out_13 | pseudo_reg_2_out_13;  // OR_Gate or_9, 16 bits wide
  assign or_10_out = pseudo_reg_1_out_5 | pseudo_reg_2_out_5;  // OR_Gate or_10, 16 bits wide
  not not_4 (not_4_out, not_5_out);
  not not_5 (not_5_out, transistor_1_out);
  Register register_4 (.D(head), .Q(register_4_q), .clk(clk));  // open: en, clr
  assign or_11_out = pseudo_reg_1_out_6 | pseudo_reg_2_out_6;  // OR_Gate or_11, 16 bits wide
  assign or_12_out = pseudo_reg_1_out_14 | pseudo_reg_2_out_14;  // OR_Gate or_12, 16 bits wide
  assign or_13_out = pseudo_reg_1_out_15 | pseudo_reg_2_out_15;  // OR_Gate or_13, 16 bits wide
  not not_6 (not_6_out, not_4_out);
  not not_7 (not_7_out, not_6_out);
  not not_8 (not_8_out, not_7_out);
  not not_9 (not_9_out, not_8_out);
  // Probe on register_4_q
  assign or_14_out = pseudo_reg_1_out_8 | pseudo_reg_2_out_8;  // OR_Gate or_14, 16 bits wide
  assign or_15_out = pseudo_reg_1_out_7 | pseudo_reg_2_out_7;  // OR_Gate or_15, 16 bits wide
  assign or_16_out = pseudo_reg_1_out_16 | pseudo_reg_2_out_16;  // OR_Gate or_16, 16 bits wide
  assign I_Odata = decoder_1_out1 ? register_4_q : 8'bz;  // Controlled_Buffer controlled_buffer_6
  // Probe on {s_r_ff_1_qn[7], undriven}
  _7_Segment_Display u_7_segment_display_1 (
    .g(_2_8), .f(_2_7), .a(_2_6), .b(_2_5), .e(_2_1), .d(_2_2), .c(_2_3), .dp(_2_4));
  _7_Segment_Display u_7_segment_display_2 (
    .g(_1_8), .f(_1_7), .a(_1_6), .b(_1_5), .e(_1_1), .d(_1_2), .c(_1_3), .dp(_1_4));
  Keyboard keyboard_1 (.clk(takt), .data(keyboard_1_data));  // open: re, clr, avail
  assign or_17_out = pseudo_reg_1_out_17 | pseudo_reg_2_out_17;  // OR_Gate or_17, 16 bits wide
  assign or_18_out = pseudo_reg_1_out_9 | pseudo_reg_2_out_9;  // OR_Gate or_18, 16 bits wide
  movement movement_1 (
    .Clock(clock), .Clear(clr), .out_4(up), .out_5(down), .out_6(left), .out_7(right),
    .\input (keyboard_1_data));
  assign or_19_out = pseudo_reg_1_out_10 | pseudo_reg_2_out_10;  // OR_Gate or_19, 16 bits wide
  assign or_20_out = pseudo_reg_1_out_18 | pseudo_reg_2_out_18;  // OR_Gate or_20, 16 bits wide
  and and_5 (and_5_out, I_Osel, I_Oadr[0], I_Oadr[1], ~I_Oadr[2], ~I_Oadr[3]);  // AND_Gate
  Decoder #(.disabled(0)) decoder_1 (.out0(decoder_1_out0), .out1(decoder_1_out1), .sel(In_Out_prime), .en(and_5_out));
  Hex_Digit_Display hex_digit_display_1 (.value(register_5_q_2));  // open: dp
  Hex_Digit_Display hex_digit_display_2 (.value(register_5_q));  // open: dp
  Register register_5 (.Q({register_5_q_2, register_5_q}), .clk(clk));  // open: D, en, clr
  Button button_5 (.out(clr));
  Acceleratiaon acceleratiaon_1 (.takt(takt), .clr(clr), .clockout(clock), .acceleration(in_3));
  Counter #(.max('ha)) counter_1 (
    .Q(counter_1_q), .carry(counter_1_carry), .clk(hz), .clr(clr));  // open: load, D, count
  Counter #(.max('ha)) counter_2 (.Q(counter_2_q), .clk(counter_1_carry), .clr(clr));  // open: load, D, count, carry
  and and_6 (I_Osel, not_10_out, clk, data);
  golod golod_1 (.stop_golod(in_2), .clock(clock), .clr_2(clr), .hz(hz), .clr(clr), .golod(golod));
  Clock clock_2 (.out(clk));
  // Probe on cdm_8_mark5_1_p4
  // Probe on cdm_8_mark5_1_p2
  // Probe on cdm_8_mark5_1_p1
  not not_10 (not_10_out, nand_1_out);
  and and_7 (RAM, nand_1_out, data);
  ROM rom_1 (.addr(counter_1_q), .data({_1_8, _1_7, _1_6, _1_5, _1_4, _1_3, _1_2, _1_1}));  // open: sel
  ROM rom_2 (.addr(counter_2_q), .data({_2_8, _2_7, _2_6, _2_5, _2_4, _2_3, _2_2, _2_1}));  // open: sel
  // Probe on cdm_8_mark5_1_p5
  // Probe on cdm_8_mark5_1_p6
  // Probe on cdm_8_mark5_1_p8
  // Probe on cdm_8_mark5_1_p7
  nand nand_1 (nand_1_out, cdm_8_mark5_1_p12[4], cdm_8_mark5_1_p12[5], cdm_8_mark5_1_p12[6], cdm_8_mark5_1_p12[7]);
  _7_Segment_Display u_7_segment_display_3 (
    .g(_2_8), .f(_2_7), .a(_2_6), .b(_2_5), .e(_2_1), .d(_2_2), .c(_2_3), .dp(_2_4));
  Decoder #(.disabled(0)) decoder_2 (.out0(code), .out1(data), .sel(cdm_8_mark5_1_p9), .en(mem));
  // CdM_8_mark5 cdm_8_mark5_1: pin names not known; wires that end beside it: cdm_8_mark5_1_p1, cdm_8_mark5_1_p2, clk, cdm_8_mark5_1_p4, cdm_8_mark5_1_p5, cdm_8_mark5_1_p6, cdm_8_mark5_1_p7, cdm_8_mark5_1_p8, cdm_8_mark5_1_p9, mem, In_Out_prime, {cdm_8_mark5_1_p12, I_Oadr}, cdm_8_mark5_1_p13, cdm_8_mark5_1_p14
  not not_11 (not_11_out, In_Out_prime);
  assign I_Odata = not_11_out ? cdm_8_mark5_1_p13 : 8'bz;  // Controlled_Buffer controlled_buffer_7
  assign cdm_8_mark5_1_p14 = In_Out_prime ? I_Odata : 8'bz;  // Controlled_Buffer controlled_buffer_8
  _7_Segment_Display u_7_segment_display_4 (
    .g(_1_8), .f(_1_7), .a(_1_6), .b(_1_5), .e(_1_1), .d(_1_2), .c(_1_3), .dp(_1_4));
  Pull_Resistor pull_resistor_3 (.node(I_Oadr[0]));
  Pull_Resistor pull_resistor_4 (.node(I_Oadr[1]));
  Pull_Resistor pull_resistor_5 (.node(I_Oadr[2]));
  Pull_Resistor pull_resistor_6 (.node(I_Oadr[3]));
  Pull_Resistor pull_resistor_7 (.node(cdm_8_mark5_1_p12[4]));
  Pull_Resistor pull_resistor_8 (.node(cdm_8_mark5_1_p12[5]));
  Pull_Resistor pull_resistor_9 (.node(cdm_8_mark5_1_p12[6]));
  Pull_Resistor pull_resistor_10 (.node(cdm_8_mark5_1_p12[7]));
  ROM rom_3 (.addr({cdm_8_mark5_1_p12, I_Oadr}), .data(I_Odata), .sel(code));
  RAM ram_1 (.addr({cdm_8_mark5_1_p12, I_Oadr}), .data(I_Odata), .sel(RAM), .clk(clk), .ld(In_Out_prime));  // open: clr
  // OR_Gate or_21 is placed but not wired
  // OR_Gate or_22 is placed but not wired

  // Other names for the same wires on the sheet: acceleration = in_3; paus = in_1; rd_wr_prime = In_Out_prime;
  //   stop_golod = in_2

  // Notes on the sheet:
  //   coor X
  //   coor Y
  //   1 - пауза 0 играем
  //   1 - нет голода 0 - есть
  //   1 - есть ускорение 0 - нет
  //   contents of rom_1 (hex, n*v repeats v):
  //   77 14 b3 b6 d4 e6 e7 34 f7 f6 77
  //   contents of rom_2 (hex, n*v repeats v):
  //   77 14 b3 b6 d4 e6 e7 34 f7 f6 77
  //   contents of rom_3 (hex, n*v repeats v):
  //   cd f0 d0 f3 b1 5 e4 4 a1 ee 4
endmodule

module _16_bit_AND (
  input  [15:0] \input ,
  input  switch,
  output [15:0] \output 
);

  assign \output  = \input  & {16{switch}};  // AND_Gate and_1, 16 bits wide
endmodule

module column_switch (
  input  [9:0] in_1,
  input  in_2,
  output [9:0] out_3
);

  wire comparator_1_eq;
  wire [9:0] multiplexer_1_out;

  Multiplexer #(.width(10)) multiplexer_1 (
    .in0(in_1), .in1({1'b0, in_1[9:1]}), .out(multiplexer_1_out), .sel(in_2));  // open: en
  Comparator #(.width(10)) comparator_1 (.a(in_1), .b({10{1'b0}}), .eq(comparator_1_eq));  // open: gt, lt
  Multiplexer #(.width(10)) multiplexer_2 (
    .in0(multiplexer_1_out), .in1(10'h10), .out(out_3), .sel(comparator_1_eq));  // open: en
endmodule

module inc_dec (
  input  [3:0] X,
  input  on_off,
  input  inc_dec,
  output [3:0] R,
  output OFL
);

  wire and_2_out, and_3_out;
  wire [3:0] and_1_out, xor_1_out, xor_2_out, xor_3_out;
  wire [3:3] decoder_1_out0, decoder_1_out1;

  Decoder #(.enable("false")) decoder_1 (.out0(decoder_1_out0[3]), .out1(decoder_1_out1[3]), .sel(inc_dec));
  assign xor_1_out = {4{decoder_1_out0[3]}} ^ X;  // XOR_Gate xor_1, 4 bits wide
  assign xor_2_out = {4{decoder_1_out1[3]}} ^ xor_3_out;  // XOR_Gate xor_2, 4 bits wide
  assign and_1_out = xor_1_out & xor_2_out;  // AND_Gate and_1, 4 bits wide
  and and_2 (and_2_out, and_1_out[3], inc_dec);
  and and_3 (and_3_out, and_1_out[3], ~inc_dec);  // AND_Gate
  assign xor_3_out = X ^ {and_1_out[2:0], 1'b1};  // XOR_Gate xor_3, 4 bits wide
  or or_1 (OFL, and_2_out, and_3_out);
  Multiplexer #(.width(4), .enable("false")) multiplexer_1 (.in0(X), .in1(xor_3_out), .out(R), .sel(on_off));
endmodule

module granca_detection (
  input  Up,
  input  Down,
  input  [7:0] in_3,
  input  Left,
  input  Right,
  output out_6
);

  wire and_1_out, and_2_out, nor_1_out, nor_2_out;

  Pull_Resistor pull_resistor_1 (.node(Up));
  Pull_Resistor pull_resistor_2 (.node(Down));
  Pull_Resistor pull_resistor_3 (.node(Left));
  Pull_Resistor pull_resistor_4 (.node(Right));
  and and_1 (and_1_out, Up, in_3[3], in_3[2], in_3[1], in_3[0]);
  and and_2 (and_2_out, in_3[7], in_3[6], in_3[5], in_3[4], Right);
  nor nor_1 (nor_1_out, ~Down, in_3[0], in_3[1], in_3[2], in_3[3]);  // NOR_Gate
  nor nor_2 (nor_2_out, in_3[4], in_3[5], in_3[6], in_3[7], ~Left);  // NOR_Gate
  or or_1 (out_6, and_1_out, nor_1_out, nor_2_out, and_2_out);
endmodule

module movement (
  input  [6:0] \input ,
  input  Clock,
  input  Clear,
  output out_4,
  output out_5,
  output out_6,
  output out_7
);

  wire and_1_out, comparator_1_eq, comparator_2_eq, comparator_3_eq, comparator_4_eq, counter_1_carry,
       or_3_out, xnor_1_out, xor_1_out;
  wire [1:0] multiplexer_1_out, or_1_out, register_1_q, register_2_q;

  Comparator #(.width(7)) comparator_1 (.a(\input ), .b(7'b1100100), .eq(comparator_1_eq));  // open: gt, lt
  Comparator #(.width(7)) comparator_2 (.a(\input ), .b(7'b1110011), .eq(comparator_2_eq));  // open: gt, lt
  Comparator #(.width(7)) comparator_3 (.a(\input ), .b(7'b1100001), .eq(comparator_3_eq));  // open: gt, lt
  Comparator #(.width(7)) comparator_4 (.a(\input ), .b(7'b1110111), .eq(comparator_4_eq));  // open: gt, lt
  or or_1 (or_1_out[0], comparator_2_eq, comparator_1_eq);
  or or_2 (or_1_out[1], comparator_1_eq, comparator_3_eq);
  or or_3 (or_3_out, comparator_1_eq, comparator_2_eq, comparator_3_eq, comparator_4_eq);
  Register #(.width(2)) register_1 (.D(or_1_out), .Q(register_1_q), .clk(or_3_out), .clr(Clear));  // open: en
  Register #(.width(2)) register_2 (.D(multiplexer_1_out), .Q(register_2_q), .clk(or_3_out), .clr(Clear));  // open: en
  xor xor_1 (xor_1_out, register_2_q[0], register_1_q[0]);
  xnor xnor_1 (xnor_1_out, register_2_q[1], register_1_q[1]);
  and and_1 (and_1_out, xnor_1_out, xor_1_out);
  Multiplexer #(.width(2)) multiplexer_1 (
    .in0(register_1_q), .in1(register_2_q), .out(multiplexer_1_out), .sel(and_1_out));  // open: en
  Counter #(.width(3), .max('h5)) counter_1 (
    .carry(counter_1_carry), .clk(Clock), .clr(Clear));  // open: load, D, count, Q
  Demultiplexer #(.select(2)) demultiplexer_1 (
    .out0(out_4), .out1(out_5), .out2(out_6), .out3(out_7), .in(counter_1_carry), .sel(multiplexer_1_out));  // open: en

  // Other names for the same wires on the sheet: clr = Clear

  // Notes on the sheet:
  //   новое напр.
  //   текушее напр.
endmodule

module pseudo_reg (
  input  [3:0] in_1,
  input  [3:0] in_2,
  output [15:0] out_3,
  output [15:0] out_4,
  output [15:0] out_5,
  output [15:0] out_6,
  output [15:0] out_7,
  output [15:0] out_8,
  output [15:0] out_9,
  output [15:0] out_10,
  output [15:0] out_11,
  output [15:0] out_12,
  output [15:0] out_13,
  output [15:0] out_14,
  output [15:0] out_15,
  output [15:0] out_16,
  output [15:0] out_17,
  output [15:0] out_18
);

  wire decoder_2_out0, decoder_2_out1, decoder_2_out2, decoder_2_out3, decoder_2_out4, decoder_2_out5,
       decoder_2_out6, decoder_2_out7, decoder_2_out8, decoder_2_out9, decoder_2_out10, decoder_2_out11,
       decoder_2_out12, decoder_2_out13, decoder_2_out14, decoder_2_out15;
  wire [15:0] decoder_1_out0;

  Decoder #(.select(4), .disabled(0), .enable("false")) decoder_1 (
    .out0(decoder_1_out0[0]), .out1(decoder_1_out0[1]), .out2(decoder_1_out0[2]), .out3(decoder_1_out0[3]),
    .out4(decoder_1_out0[4]), .out5(decoder_1_out0[5]), .out6(decoder_1_out0[6]), .out7(decoder_1_out0[7]),
    .out8(decoder_1_out0[8]), .out9(decoder_1_out0[9]), .out10(decoder_1_out0[10]),
    .out11(decoder_1_out0[11]), .out12(decoder_1_out0[12]), .out13(decoder_1_out0[13]),
    .out14(decoder_1_out0[14]), .out15(decoder_1_out0[15]), .sel(in_1));
  _16_bit_AND u_16_bit_and_1 (.\input (decoder_1_out0), .switch(decoder_2_out1), .\output (out_3));
  _16_bit_AND u_16_bit_and_2 (.\input (decoder_1_out0), .switch(decoder_2_out0), .\output (out_11));
  _16_bit_AND u_16_bit_and_3 (.\input (decoder_1_out0), .switch(decoder_2_out3), .\output (out_4));
  _16_bit_AND u_16_bit_and_4 (.\input (decoder_1_out0), .switch(decoder_2_out2), .\output (out_12));
  Decoder #(.select(4), .disabled(0), .enable("false")) decoder_2 (
    .out0(decoder_2_out0), .out1(decoder_2_out1), .out2(decoder_2_out2), .out3(decoder_2_out3),
    .out4(decoder_2_out4), .out5(decoder_2_out5), .out6(decoder_2_out6), .out7(decoder_2_out7),
    .out8(decoder_2_out8), .out9(decoder_2_out9), .out10(decoder_2_out10), .out11(decoder_2_out11),
    .out12(decoder_2_out12), .out13(decoder_2_out13), .out14(decoder_2_out14), .out15(decoder_2_out15),
    .sel(in_2));
  _16_bit_AND u_16_bit_and_5 (.\input (decoder_1_out0), .switch(decoder_2_out5), .\output (out_5));
  _16_bit_AND u_16_bit_and_6 (.\input (decoder_1_out0), .switch(decoder_2_out4), .\output (out_13));
  _16_bit_AND u_16_bit_and_7 (.\input (decoder_1_out0), .switch(decoder_2_out6), .\output (out_14));
  _16_bit_AND u_16_bit_and_8 (.\input (decoder_1_out0), .switch(decoder_2_out7), .\output (out_6));
  _16_bit_AND u_16_bit_and_9 (.\input (decoder_1_out0), .switch(decoder_2_out9), .\output (out_7));
  _16_bit_AND u_16_bit_and_10 (.\input (decoder_1_out0), .switch(decoder_2_out8), .\output (out_15));
  _16_bit_AND u_16_bit_and_11 (.\input (decoder_1_out0), .switch(decoder_2_out11), .\output (out_8));
  _16_bit_AND u_16_bit_and_12 (.\input (decoder_1_out0), .switch(decoder_2_out10), .\output (out_16));
  _16_bit_AND u_16_bit_and_13 (.\input (decoder_1_out0), .switch(decoder_2_out13), .\output (out_9));
  _16_bit_AND u_16_bit_and_14 (.\input (decoder_1_out0), .switch(decoder_2_out12), .\output (out_17));
  _16_bit_AND u_16_bit_and_15 (.\input (decoder_1_out0), .switch(decoder_2_out14), .\output (out_18));
  _16_bit_AND u_16_bit_and_16 (.\input (decoder_1_out0), .switch(decoder_2_out15), .\output (out_10));
endmodule

module CP (
);

  wire cdm_8_mark5_1_p2, cdm_8_mark5_1_p3, cdm_8_mark5_1_p5, cdm_8_mark5_1_p6, cdm_8_mark5_1_p7,
       cdm_8_mark5_1_p8, clk, code, data, IRQ, mem, not_1_out, rd_wr, undriven;
  wire [7:0] cdm_8_mark5_1_p11, cdm_8_mark5_1_p12, cdm_8_mark5_1_p13, cdm_8_mark5_1_p14, IOdat;

  // Probe on undriven
  // Probe on undriven
  // Probe on cdm_8_mark5_1_p3
  // Probe on cdm_8_mark5_1_p2
  // Probe on cdm_8_mark5_1_p7
  // Probe on cdm_8_mark5_1_p6
  // Probe on cdm_8_mark5_1_p5
  // CdM_8_mark5 cdm_8_mark5_1: pin names not known; wires that end beside it: IRQ, cdm_8_mark5_1_p2, cdm_8_mark5_1_p3, clk, cdm_8_mark5_1_p5, cdm_8_mark5_1_p6, cdm_8_mark5_1_p7, cdm_8_mark5_1_p8, mem, rd_wr, cdm_8_mark5_1_p11, cdm_8_mark5_1_p12, cdm_8_mark5_1_p13, cdm_8_mark5_1_p14
  Clock clock_1 (.out(clk));
  Decoder decoder_1 (.out0(code), .out1(data), .sel(cdm_8_mark5_1_p8), .en(mem));
  assign IOdat = not_1_out ? cdm_8_mark5_1_p12 : 8'bz;  // Controlled_Buffer controlled_buffer_1
  not not_1 (not_1_out, rd_wr);
  assign cdm_8_mark5_1_p13 = rd_wr ? IOdat : 8'bz;  // Controlled_Buffer controlled_buffer_2
  // Probe on cdm_8_mark5_1_p14
  assign cdm_8_mark5_1_p14 = data ? IOdat : 8'bz;  // Controlled_Buffer controlled_buffer_3
  Pull_Resistor pull_resistor_1 (.node(data));
  ROM rom_1 (.addr(cdm_8_mark5_1_p11), .data(IOdat), .sel(code));
  RAM ram_1 (.addr(cdm_8_mark5_1_p11), .data(IOdat), .sel(data), .clk(clk), .ld(rd_wr));  // open: clr

  // Notes on the sheet:
  //   contents of rom_1 (hex, n*v repeats v):
  //   d0 8 f0 8c d1 9 a4 d4 3
endmodule

module golod (
  input  stop_golod,
  input  clr,
  input  clock,
  input  clr_2,
  input  hz,
  output golod
);

  wire comparator_1_eq, comparator_1_gt, comparator_2_gt, or_1_out, or_2_out;
  wire [9:0] counter_1_q, counter_2_q;

  Counter #(.width(10), .max('h3ff)) counter_1 (
    .Q(counter_1_q), .clk(clock), .clr(or_1_out));  // open: load, D, count, carry
  or or_1 (or_1_out, clr_2, hz);
  Comparator #(.width(10), .mode("unsigned")) comparator_1 (
    .a(counter_1_q), .b(10'hf1), .gt(comparator_1_gt), .eq(comparator_1_eq));  // open: lt
  or or_2 (or_2_out, comparator_1_gt, comparator_1_eq);
  Counter #(.width(10), .max('h3ff)) counter_2 (
    .Q(counter_2_q), .clk(or_2_out), .clr(clr));  // open: load, D, count, carry
  and and_1 (golod, ~stop_golod, comparator_2_gt);  // AND_Gate
  Comparator #(.width(10), .mode("unsigned")) comparator_2 (
    .a(counter_2_q), .b({10{1'b0}}), .gt(comparator_2_gt));  // open: eq, lt

  // Notes on the sheet:
  //   тут 0f1 это константа после такого количества clockов в голод пойдет 1 которая остановит такты
endmodule

module Acceleratiaon (
  input  takt,
  input  clr,
  input  acceleration,
  output clockout
);

  wire and_1_out, and_2_out, comparator_1_eq, comparator_2_gt, comparator_3_eq, comparator_3_lt, or_1_out,
       or_2_out, or_3_out;
  wire [9:0] counter_1_q, counter_2_q, port;
  wire [9:1] hz2;
  wire [9:9] counter_3_q;

  // Probe on port
  Subtractor #(.width(10)) subtractor_1 (.a(10'h14), .b({hz2, 1'b0}), .out(port));  // open: bin, bout
  Counter #(.width(10), .max('h3ff)) counter_1 (
    .Q(counter_1_q), .clk(takt), .clr(or_1_out));  // open: load, D, count, carry
  or or_1 (or_1_out, clr, comparator_1_eq);
  Comparator #(.width(10), .mode("unsigned")) comparator_1 (
    .a(counter_1_q), .b(10'h120), .eq(comparator_1_eq));  // open: gt, lt
  Counter #(.width(10), .max('h3ff)) counter_2 (
    .Q(counter_2_q), .clk(takt), .clr(or_2_out));  // open: load, D, count, carry
  or or_2 (or_2_out, clr, clockout);
  Comparator #(.width(10), .mode("unsigned")) comparator_2 (.a(port), .b(10'h4), .gt(comparator_2_gt));  // open: eq, lt
  Comparator #(.width(10), .mode("unsigned")) comparator_3 (
    .a(port), .b(counter_2_q), .eq(comparator_3_eq), .lt(comparator_3_lt));  // open: gt
  Counter #(.width(10), .max('h3ff)) counter_3 (
    .Q({counter_3_q[9], hz2}), .clk(and_1_out), .clr(or_3_out));  // open: load, D, count, carry
  and and_1 (and_1_out, comparator_1_eq, comparator_2_gt);
  or or_3 (or_3_out, clr, and_2_out);
  and and_2 (and_2_out, clockout, ~acceleration);  // AND_Gate
  or or_4 (clockout, comparator_3_eq, comparator_3_lt);

  // Other names for the same wires on the sheet: clock = clockout

  // Notes on the sheet:
  //   004 это конечная скорость при ускорении тоже менять можно
  //   014 это константа базовая задержка если надо меньше или больше менять ее 
  //   Идет счёт количества тактов пока не дойдет до 120
  //   также если поменять такты на яблоки то будет ускорение от яблок когда наберется количество как в константе
  //   порт это тунель который передает значение после вычитания задержки и говорит когда надо остановить ускорение
  //   если включено ускорение то оно будет обнулять значение в счетчике
  //   hz2 это то сколько мы вычитаем из базовой задержки чтобы уменьшить ее
endmodule
