// Logisim project last_version_3.circ as structural Verilog
// 1
module main (
);

  wire and_1_out, button_2_out, button_3_out, button_4_out, button_out, cdm_8_mark5_1_p1, cdm_8_mark5_1_p2,
       cdm_8_mark5_1_p5, cdm_8_mark5_1_p6, cdm_8_mark5_1_p7, cdm_8_mark5_1_p8, cdm_8_mark5_1_p9,
       cdm_8_mark5_1_p10, cl, clock, clock_1_out, clr, code, comparator_1_eq, comparator_2_eq,
       comparator_3_eq, comparator_3_lt, d_ff_1_qn, data, down, granca_detection_1_out_6, hz, I_osel, in_out,
       left, nand_1_out, not_1_out, not_2_out, or_1_out, or_2_out, or_3_out, or_20_out, or_21_out, RAM_prime,
       right, up;
  wire [3:0] I_Odar;
  wire [7:0] adder_1_out, cdm_8_mark5_1_p13, cdm_8_mark5_1_p14, counter_2_q, I_odat, inc_dec_2_r,
       negator_1_out, random_1_out, register_1_q;
  wire [7:4] cdm_8_mark5_1_p12;
  wire [9:0] counter_1_q, counter_3_q, subtractor_1_out;
  wire [9:1] hz2;
  wire [9:4] undriven;
  wire [9:9] counter_4_q;
  wire [15:0] or_4_out, or_5_out, or_6_out, or_7_out, or_8_out, or_9_out, or_10_out, or_11_out, or_12_out,
       or_13_out, or_14_out, or_15_out, or_16_out, or_17_out, or_18_out, or_19_out, pseudo_reg_1_out_3,
       pseudo_reg_1_out_4, pseudo_reg_1_out_5, pseudo_reg_1_out_6, pseudo_reg_1_out_7, pseudo_reg_1_out_8,
       pseudo_reg_1_out_9, pseudo_reg_1_out_10, pseudo_reg_1_out_11, pseudo_reg_1_out_12,
       pseudo_reg_1_out_13, pseudo_reg_1_out_14, pseudo_reg_1_out_15, pseudo_reg_1_out_16,
       pseudo_reg_1_out_17, pseudo_reg_1_out_18, pseudo_reg_2_out_3, pseudo_reg_2_out_4, pseudo_reg_2_out_5,
       pseudo_reg_2_out_6, pseudo_reg_2_out_7, pseudo_reg_2_out_8, pseudo_reg_2_out_9, pseudo_reg_2_out_10,
       pseudo_reg_2_out_11, pseudo_reg_2_out_12, pseudo_reg_2_out_13, pseudo_reg_2_out_14,
       pseudo_reg_2_out_15, pseudo_reg_2_out_16, pseudo_reg_2_out_17, pseudo_reg_2_out_18;

  granca_detection granca_detection_1 (
    .in_3(register_1_q), .Left(left), .Right(right), .out_6(granca_detection_1_out_6), .Up(up), .Down(down));
  Register register_1 (.D(inc_dec_2_r), .Q(register_1_q), .clk(and_1_out), .clr(clr));  // open: en
  and and_1 (and_1_out, clock, d_ff_1_qn);
  D_Flip_Flop d_ff_1 (.Qn(d_ff_1_qn), .preset(granca_detection_1_out_6), .reset(clr));  // open: clk, D, Q, en
  Random #(.seed(16)) random_1 (.clk(or_1_out), .out(random_1_out));  // open: next, clr
  or or_1 (or_1_out, clr, hz);
  Negator negator_1 (.in(register_1_q), .out(negator_1_out));
  // Probe on cdm_8_mark5_1_p6
  // Probe on cdm_8_mark5_1_p5
  // Probe on cdm_8_mark5_1_p2
  // Probe on cdm_8_mark5_1_p1
  and and_2 (I_osel, not_1_out, cl, data);
  or or_2 (or_2_out, left, right);
  Adder adder_1 (.a(random_1_out), .b(negator_1_out), .out(adder_1_out));  // open: cin, cout
  // Probe on cdm_8_mark5_1_p8
  // Probe on cdm_8_mark5_1_p7
  // CdM_8_mark5 cdm_8_mark5_1: pin names not known; wires that end beside it: cdm_8_mark5_1_p1, cdm_8_mark5_1_p2, cl, cl, cdm_8_mark5_1_p5, cdm_8_mark5_1_p6, cdm_8_mark5_1_p7, cdm_8_mark5_1_p8, cdm_8_mark5_1_p9, cdm_8_mark5_1_p10, in_out, {cdm_8_mark5_1_p12, I_Odar}, cdm_8_mark5_1_p13, cdm_8_mark5_1_p14
  not not_1 (not_1_out, nand_1_out);
  and and_3 (RAM_prime, nand_1_out, data);
  inc_dec inc_dec_1 (.X(register_1_q[7:4]), .on_off(or_2_out), .inc_dec(right), .R(inc_dec_2_r[7:4]));  // open: OFL
  inc_dec inc_dec_2 (.X(register_1_q[3:0]), .on_off(or_3_out), .inc_dec(up), .R(inc_dec_2_r[3:0]));  // open: OFL
  Comparator #(.width(10), .mode("unsigned")) comparator_1 (
    .b({undriven, random_1_out[3:0]}), .eq(comparator_1_eq));  // open: a, gt, lt
  nor nor_1 (hz, adder_1_out[0], adder_1_out[1], adder_1_out[2], adder_1_out[3], adder_1_out[4], adder_1_out[5], adder_1_out[6], adder_1_out[7]);
  nand nand_1 (nand_1_out, cdm_8_mark5_1_p12[4], cdm_8_mark5_1_p12[5], cdm_8_mark5_1_p12[6], cdm_8_mark5_1_p12[7]);
  Register #(.width(4)) register_2 (.D(register_1_q[7:4]), .clk(clock), .clr(clr));  // open: en, Q
  or or_3 (or_3_out, up, down);
  Decoder decoder_1 (.out0(code), .out1(data), .sel(cdm_8_mark5_1_p9), .en(cdm_8_mark5_1_p10));
  assign I_odat = not_2_out ? cdm_8_mark5_1_p13 : 8'bz;  // Controlled_Buffer controlled_buffer_1
  not not_2 (not_2_out, in_out);
  assign cdm_8_mark5_1_p14 = in_out ? I_odat : 8'bz;  // Controlled_Buffer controlled_buffer_2
  Register #(.width(4)) register_3 (.D(register_1_q[3:0]), .clk(clock), .clr(clr));  // open: en, Q
  pseudo_reg pseudo_reg_1 (
    .in_1(register_1_q[3:0]), .in_2(register_1_q[7:4]), .out_11(pseudo_reg_1_out_11),
    .out_3(pseudo_reg_1_out_3), .out_4(pseudo_reg_1_out_4), .out_12(pseudo_reg_1_out_12),
    .out_5(pseudo_reg_1_out_5), .out_13(pseudo_reg_1_out_13), .out_6(pseudo_reg_1_out_6),
    .out_14(pseudo_reg_1_out_14), .out_7(pseudo_reg_1_out_7), .out_15(pseudo_reg_1_out_15),
    .out_8(pseudo_reg_1_out_8), .out_16(pseudo_reg_1_out_16), .out_9(pseudo_reg_1_out_9),
    .out_17(pseudo_reg_1_out_17), .out_10(pseudo_reg_1_out_10), .out_18(pseudo_reg_1_out_18));
  assign or_4_out = pseudo_reg_1_out_11 | pseudo_reg_2_out_11;  // OR_Gate or_4, 16 bits wide
  pseudo_reg pseudo_reg_2 (
    .out_11(pseudo_reg_2_out_11), .out_3(pseudo_reg_2_out_3), .out_4(pseudo_reg_2_out_4),
    .out_12(pseudo_reg_2_out_12), .out_5(pseudo_reg_2_out_5), .out_13(pseudo_reg_2_out_13),
    .out_6(pseudo_reg_2_out_6), .out_14(pseudo_reg_2_out_14), .out_7(pseudo_reg_2_out_7),
    .out_15(pseudo_reg_2_out_15), .out_8(pseudo_reg_2_out_8), .out_16(pseudo_reg_2_out_16),
    .out_9(pseudo_reg_2_out_9), .out_17(pseudo_reg_2_out_17), .out_10(pseudo_reg_2_out_10),
    .out_18(pseudo_reg_2_out_18));  // open: in_1, in_2
  DotMatrix #(.matrixcols(16), .matrixrows(16)) dotmatrix_1 (
    .col0(or_4_out), .col1(or_7_out), .col2(or_6_out), .col3(or_5_out), .col4(or_8_out), .col5(or_9_out),
    .col6(or_10_out), .col7(or_11_out), .col8(or_12_out), .col9(or_13_out), .col10(or_14_out),
    .col11(or_15_out), .col12(or_17_out), .col13(or_18_out), .col14(or_16_out), .col15(or_19_out));
  assign or_5_out = pseudo_reg_1_out_4 | pseudo_reg_2_out_4;  // OR_Gate or_5, 16 bits wide
  assign or_6_out = pseudo_reg_1_out_12 | pseudo_reg_2_out_12;  // OR_Gate or_6, 16 bits wide
  assign or_7_out = pseudo_reg_1_out_3 | pseudo_reg_2_out_3;  // OR_Gate or_7, 16 bits wide
  Pull_Resistor pull_resistor_1 (.node(I_Odar[0]));
  Pull_Resistor pull_resistor_2 (.node(I_Odar[1]));
  Pull_Resistor pull_resistor_3 (.node(I_Odar[2]));
  Pull_Resistor pull_resistor_4 (.node(I_Odar[3]));
  Pull_Resistor pull_resistor_5 (.node(cdm_8_mark5_1_p12[4]));
  Pull_Resistor pull_resistor_6 (.node(cdm_8_mark5_1_p12[5]));
  Pull_Resistor pull_resistor_7 (.node(cdm_8_mark5_1_p12[6]));
  Pull_Resistor pull_resistor_8 (.node(cdm_8_mark5_1_p12[7]));
  \рп  \u_рп_1  ();
  assign or_8_out = pseudo_reg_1_out_13 | pseudo_reg_2_out_13;  // OR_Gate or_8, 16 bits wide
  assign or_9_out = pseudo_reg_1_out_5 | pseudo_reg_2_out_5;  // OR_Gate or_9, 16 bits wide
  assign or_10_out = pseudo_reg_1_out_14 | pseudo_reg_2_out_14;  // OR_Gate or_10, 16 bits wide
  Hex_Digit_Display hex_digit_display_1 (.value(counter_2_q[7:4]));  // open: dp
  assign or_11_out = pseudo_reg_1_out_6 | pseudo_reg_2_out_6;  // OR_Gate or_11, 16 bits wide
  assign or_12_out = pseudo_reg_1_out_15 | pseudo_reg_2_out_15;  // OR_Gate or_12, 16 bits wide
  ROM rom_1 (.addr({cdm_8_mark5_1_p12, I_Odar}), .data(I_odat), .sel(code));
  RAM ram_1 (.addr({cdm_8_mark5_1_p12, I_Odar}), .data(I_odat), .sel(RAM_prime), .clk(cl), .ld(in_out));  // open: clr
  Hex_Digit_Display hex_digit_display_2 (.value(counter_2_q[3:0]));  // open: dp
  Button button (.out(button_out));
  Button button_2 (.out(button_2_out));
  assign or_13_out = pseudo_reg_1_out_7 | pseudo_reg_2_out_7;  // OR_Gate or_13, 16 bits wide
  assign or_14_out = pseudo_reg_1_out_16 | pseudo_reg_2_out_16;  // OR_Gate or_14, 16 bits wide
  assign or_15_out = pseudo_reg_1_out_8 | pseudo_reg_2_out_8;  // OR_Gate or_15, 16 bits wide
  Button button_3 (.out(button_3_out));
  Button button_4 (.out(button_4_out));
  movement movement_1 (
    .Right(button_3_out), .Down(button_4_out), .Left(button_2_out), .Up(button_out), .Clock(clock),
    .Clear(clr), .out_7(up), .out_8(down), .out_9(left), .out_10(right));
  assign or_16_out = pseudo_reg_1_out_18 | pseudo_reg_2_out_18;  // OR_Gate or_16, 16 bits wide
  assign or_17_out = pseudo_reg_1_out_17 | pseudo_reg_2_out_17;  // OR_Gate or_17, 16 bits wide
  assign or_18_out = pseudo_reg_1_out_9 | pseudo_reg_2_out_9;  // OR_Gate or_18, 16 bits wide
  Button button_5 (.out(clr));
  assign or_19_out = pseudo_reg_1_out_10 | pseudo_reg_2_out_10;  // OR_Gate or_19, 16 bits wide
  or or_20 (or_20_out, clr, comparator_2_eq);
  Clock clock_1 (.out(clock_1_out));
  or or_21 (or_21_out, clr, clock);
  Counter #(.width(10), .max('h3ff)) counter_1 (
    .Q(counter_1_q), .clk(clock), .clr(or_20_out));  // open: load, D, count, carry
  Counter counter_2 (.Q(counter_2_q), .clk(hz), .clr(clr));  // open: load, D, count, carry
  Counter #(.width(10), .max('h3ff)) counter_3 (
    .Q(counter_3_q), .clk(clock_1_out), .clr(or_21_out));  // open: load, D, count, carry
  Comparator #(.width(10), .mode("unsigned")) comparator_2 (
    .a(counter_1_q), .b(10'h40), .eq(comparator_2_eq));  // open: gt, lt
  // Probe on subtractor_1_out
  Subtractor #(.width(10)) subtractor_1 (.a(10'h14), .b({hz2, 1'b0}), .out(subtractor_1_out));  // open: bin, bout
  Comparator #(.width(10), .mode("unsigned")) comparator_3 (
    .a(subtractor_1_out), .b(counter_3_q), .eq(comparator_3_eq), .lt(comparator_3_lt));  // open: gt
  or or_22 (clock, comparator_3_eq, comparator_3_lt);
  Counter #(.width(10), .max('h3ff)) counter_4 (
    .Q({counter_4_q[9], hz2}), .clk(comparator_2_eq), .clr(clr));  // open: load, D, count, carry
  // Pins of 4 and 10 bits meet at {undriven, random_1_out[3:0]}

  // Other names for the same wires on the sheet: rd_wr = in_out

  // Notes on the sheet:
  //   coor X
  //   coor Y
endmodule

module _16_bit_AND (
  input  [15:0] \input ,
  input  switch,
  output [15:0] \output 
);

  assign \output  = \input  & {16{switch}};  // AND_Gate and_1, 16 bits wide
endmodule

module column_switch (
  input  [9:0] in_1,
  input  in_2,
  output [9:0] out_3
);

  wire comparator_1_eq;
  wire [9:0] multiplexer_1_out;

  Multiplexer #(.width(10)) multiplexer_1 (
    .in0(in_1), .in1({1'b0, in_1[9:1]}), .out(multiplexer_1_out), .sel(in_2));  // open: en
  Comparator #(.width(10)) comparator_1 (.a(in_1), .b({10{1'b0}}), .eq(comparator_1_eq));  // open: gt, lt
  Multiplexer #(.width(10)) multiplexer_2 (
    .in0(multiplexer_1_out), .in1(10'h10), .out(out_3), .sel(comparator_1_eq));  // open: en
endmodule

module inc_dec (
  input  [3:0] X,
  input  on_off,
  input  inc_dec,
  output [3:0] R,
  output OFL
);

  wire and_2_out, and_3_out;
  wire [3:0] and_1_out, xor_1_out, xor_2_out, xor_3_out;
  wire [3:3] decoder_1_out0, decoder_1_out1;

  Decoder #(.enable("false")) decoder_1 (.out0(decoder_1_out0[3]), .out1(decoder_1_out1[3]), .sel(inc_dec));
  assign xor_1_out = {4{decoder_1_out0[3]}} ^ X;  // XOR_Gate xor_1, 4 bits wide
  assign xor_2_out = {4{decoder_1_out1[3]}} ^ xor_3_out;  // XOR_Gate xor_2, 4 bits wide
  assign and_1_out = xor_1_out & xor_2_out;  // AND_Gate and_1, 4 bits wide
  and and_2 (and_2_out, and_1_out[3], inc_dec);
  and and_3 (and_3_out, and_1_out[3], ~inc_dec);  // AND_Gate
  assign xor_3_out = X ^ {and_1_out[2:0], 1'b1};  // XOR_Gate xor_3, 4 bits wide
  or or_1 (OFL, and_2_out, and_3_out);
  Multiplexer #(.width(4), .enable("false")) multiplexer_1 (.in0(X), .in1(xor_3_out), .out(R), .sel(on_off));
endmodule

module granca_detection (
  input  Up,
  input  Down,
  input  [7:0] in_3,
  input  Left,
  input  Right,
  output out_6
);

  wire and_1_out, and_2_out, nor_1_out, nor_2_out;

  Pull_Resistor pull_resistor_1 (.node(Up));
  Pull_Resistor pull_resistor_2 (.node(Down));
  Pull_Resistor pull_resistor_3 (.node(Left));
  Pull_Resistor pull_resistor_4 (.node(Right));
  and and_1 (and_1_out, Up, in_3[3], in_3[2], in_3[1], in_3[0]);
  and and_2 (and_2_out, in_3[7], in_3[6], in_3[5], in_3[4], Right);
  nor nor_1 (nor_1_out, ~Down, in_3[0], in_3[1], in_3[2], in_3[3]);  // NOR_Gate
  nor nor_2 (nor_2_out, in_3[4], in_3[5], in_3[6], in_3[7], ~Left);  // NOR_Gate
  or or_1 (out_6, and_1_out, nor_1_out, nor_2_out, and_2_out);
endmodule

module movement (
  input  Right,
  input  Down,
  input  Left,
  input  Up,
  input  Clock,
  input  Clear,
  output out_7,
  output out_8,
  output out_9,
  output out_10
);

  wire and_1_out, counter_1_carry, or_3_out, xnor_1_out, xor_1_out;
  wire [1:0] multiplexer_1_out, or_1_out, register_1_q, register_2_q;

  or or_1 (or_1_out[0], Down, Right);
  or or_2 (or_1_out[1], Right, Left);
  or or_3 (or_3_out, Right, Down, Left, Up);
  Register #(.width(2)) register_1 (.D(or_1_out), .Q(register_1_q), .clk(or_3_out), .clr(Clear));  // open: en
  Register #(.width(2)) register_2 (.D(multiplexer_1_out), .Q(register_2_q), .clk(or_3_out), .clr(Clear));  // open: en
  xnor xnor_1 (xnor_1_out, register_2_q[1], register_1_q[1]);
  and and_1 (and_1_out, xnor_1_out, xor_1_out);
  xor xor_1 (xor_1_out, register_2_q[0], register_1_q[0]);
  Multiplexer #(.width(2)) multiplexer_1 (
    .in0(register_1_q), .in1(register_2_q), .out(multiplexer_1_out), .sel(and_1_out));  // open: en
  Counter #(.width(3), .max('h5)) counter_1 (
    .carry(counter_1_carry), .clk(Clock), .clr(Clear));  // open: load, D, count, Q
  Demultiplexer #(.select(2)) demultiplexer_1 (
    .out0(out_7), .out1(out_8), .out2(out_9), .out3(out_10), .in(counter_1_carry), .sel(multiplexer_1_out));  // open: en

  // Other names for the same wires on the sheet: clr = Clear

  // Notes on the sheet:
  //   новое напр.
  //   текушее напр.
endmodule

module pseudo_reg (
  input  [3:0] in_1,
  input  [3:0] in_2,
  output [15:0] out_3,
  output [15:0] out_4,
  output [15:0] out_5,
  output [15:0] out_6,
  output [15:0] out_7,
  output [15:0] out_8,
  output [15:0] out_9,
  output [15:0] out_10,
  output [15:0] out_11,
  output [15:0] out_12,
  output [15:0] out_13,
  output [15:0] out_14,
  output [15:0] out_15,
  output [15:0] out_16,
  output [15:0] out_17,
  output [15:0] out_18
);

  wire decoder_2_out0, decoder_2_out1, decoder_2_out2, decoder_2_out3, decoder_2_out4, decoder_2_out5,
       decoder_2_out6, decoder_2_out7, decoder_2_out8, decoder_2_out9, decoder_2_out10, decoder_2_out11,
       decoder_2_out12, decoder_2_out13, decoder_2_out14, decoder_2_out15;
  wire [15:0] decoder_1_out0;

  Decoder #(.select(4), .disabled(0), .enable("false")) decoder_1 (
    .out0(decoder_1_out0[0]), .out1(decoder_1_out0[1]), .out2(decoder_1_out0[2]), .out3(decoder_1_out0[3]),
    .out4(decoder_1_out0[4]), .out5(decoder_1_out0[5]), .out6(decoder_1_out0[6]), .out7(decoder_1_out0[7]),
    .out8(decoder_1_out0[8]), .out9(decoder_1_out0[9]), .out10(decoder_1_out0[10]),
    .out11(decoder_1_out0[11]), .out12(decoder_1_out0[12]), .out13(decoder_1_out0[13]),
    .out14(decoder_1_out0[14]), .out15(decoder_1_out0[15]), .sel(in_1));
  _16_bit_AND u_16_bit_and_1 (.\input (decoder_1_out0), .switch(decoder_2_out1), .\output (out_3));
  _16_bit_AND u_16_bit_and_2 (.\input (decoder_1_out0), .switch(decoder_2_out0), .\output (out_11));
  _16_bit_AND u_16_bit_and_3 (.\input (decoder_1_out0), .switch(decoder_2_out3), .\output (out_4));
  _16_bit_AND u_16_bit_and_4 (.\input (decoder_1_out0), .switch(decoder_2_out2), .\output (out_12));
  Decoder #(.select(4), .disabled(0), .enable("false")) decoder_2 (
    .out0(decoder_2_out0), .out1(decoder_2_out1), .out2(decoder_2_out2), .out3(decoder_2_out3),
    .out4(decoder_2_out4), .out5(decoder_2_out5), .out6(decoder_2_out6), .out7(decoder_2_out7),
    .out8(decoder_2_out8), .out9(decoder_2_out9), .out10(decoder_2_out10), .out11(decoder_2_out11),
    .out12(decoder_2_out12), .out13(decoder_2_out13), .out14(decoder_2_out14), .out15(decoder_2_out15),
    .sel(in_2));
  _16_bit_AND u_16_bit_and_5 (.\input (decoder_1_out0), .switch(decoder_2_out4), .\output (out_13));
  _16_bit_AND u_16_bit_and_6 (.\input (decoder_1_out0), .switch(decoder_2_out5), .\output (out_5));
  _16_bit_AND u_16_bit_and_7 (.\input (decoder_1_out0), .switch(decoder_2_out7), .\output (out_6));
  _16_bit_AND u_16_bit_and_8 (.\input (decoder_1_out0), .switch(decoder_2_out6), .\output (out_14));
  _16_bit_AND u_16_bit_and_9 (.\input (decoder_1_out0), .switch(decoder_2_out9), .\output (out_7));
  _16_bit_AND u_16_bit_and_10 (.\input (decoder_1_out0), .switch(decoder_2_out8), .\output (out_15));
  _16_bit_AND u_16_bit_and_11 (.\input (decoder_1_out0), .switch(decoder_2_out10), .\output (out_16));
  _16_bit_AND u_16_bit_and_12 (.\input (decoder_1_out0), .switch(decoder_2_out11), .\output (out_8));
  _16_bit_AND u_16_bit_and_13 (.\input (decoder_1_out0), .switch(decoder_2_out13), .\output (out_9));
  _16_bit_AND u_16_bit_and_14 (.\input (decoder_1_out0), .switch(decoder_2_out12), .\output (out_17));
  _16_bit_AND u_16_bit_and_15 (.\input (decoder_1_out0), .switch(decoder_2_out15), .\output (out_10));
  _16_bit_AND u_16_bit_and_16 (.\input (decoder_1_out0), .switch(decoder_2_out14), .\output (out_18));
endmodule
