// Logisim project last_version_41.circ as structural Verilog
// 1
module main (
  input  in_1,
  input  in_2
);

  wire and_3_out, and_4_out, and_5_out, and_6_out, and_7_out, and_8_out, and_9_out, cdm_8_mark5_1_data_inst,
       ChangeHead, clock_1_out, clr, code, comparator_2_eq, comparator_3_eq, controlled_buffer_2_out,
       counter_1_1_out_3, counter_1_1_out_4, counter_1_1_out_5, counter_1_1_out_6, counter_1_1_out_7,
       counter_1_1_out_8, counter_1_1_out_9, counter_1_1_out_10, counter_1_1_out_11, counter_1_1_out_12,
       counter_1_1_out_13, counter_1_1_out_14, counter_1_1_out_15, counter_1_1_out_16, counter_1_1_out_17,
       counter_1_1_out_18, counter_2_1_out_3, counter_2_1_out_4, counter_2_1_out_5, counter_2_1_out_6,
       counter_2_1_out_7, counter_2_1_out_8, counter_2_1_out_9, counter_2_1_out_10, counter_2_1_out_11,
       counter_2_1_out_12, counter_2_1_out_13, counter_2_1_out_14, counter_2_1_out_15, counter_2_1_out_16,
       counter_2_1_out_17, counter_2_1_out_18, counter_2_carry, CYCLE, d_ff_1_q, data, decoder_2_out1,
       decoder_3_out1, decoder_4_out1, decoder_5_out1, down, first_tacktk, golod, hz, I_Osel, In_Out_prime,
       keyboard_1_avail, left, lose, mem, nand_1_out, not_1_out, not_2_out, not_3_out, or_1_out, or_3_out,
       or_4_out, or_5_out, or_6_out, or_7_out, or_8_out, or_10_out, pull_resistor_11_node,
       pull_resistor_17_node, RAM, right, takt, undriven, up, Vivod, win, \Перекус ;
  wire [1:0] Move;
  wire [3:0] cdm_8_mark5_1_ps, inc_dec_4bit_1_r, inc_dec_4bit_2_r;
  wire [6:0] \input ;
  wire [7:0] adder_1_out, adr, Apple_coord, cdm_8_mark5_1_data_out, cdm_8_mark5_1_pc, cdm_8_mark5_1_r0,
       cdm_8_mark5_1_r1, cdm_8_mark5_1_r2, cdm_8_mark5_1_r3, cdm_8_mark5_1_sp, controlled_buffer_1_out,
       controlled_buffer_4_out, Cords, counter_3_q, head, I_Odata, negator_1_out, or_2_out, register_2_q,
       register_3_q, register_4_q, register_5_q;
  wire [15:0] vivod_matrix_1_out_12, vivod_matrix_1_out_16, vivod_matrix_1_out_20, vivod_matrix_1_out_24,
       vivod_matrix_1_out_28, vivod_matrix_1_out_31, vivod_matrix_1_out_33, vivod_matrix_1_out_37,
       vivod_matrix_1_out_41, vivod_matrix_1_out_45, vivod_matrix_1_out_48, vivod_matrix_1_out_50,
       vivod_matrix_1_out_54, vivod_matrix_1_out_58, vivod_matrix_1_out_62, vivod_matrix_1_out_65;
  wire [16:0] vivod_matrix_1_out_15, vivod_matrix_1_out_19, vivod_matrix_1_out_23, vivod_matrix_1_out_27,
       vivod_matrix_1_out_30, vivod_matrix_1_out_35, vivod_matrix_1_out_39, vivod_matrix_1_out_43,
       vivod_matrix_1_out_47, vivod_matrix_1_out_52, vivod_matrix_1_out_56, vivod_matrix_1_out_60,
       vivod_matrix_1_out_64, vivod_matrix_1_out_68, vivod_matrix_1_out_71, vivod_matrix_1_out_74;
  wire [17:0] vivod_matrix_1_out_14, vivod_matrix_1_out_18, vivod_matrix_1_out_22, vivod_matrix_1_out_26,
       vivod_matrix_1_out_29, vivod_matrix_1_out_34, vivod_matrix_1_out_38, vivod_matrix_1_out_42,
       vivod_matrix_1_out_46, vivod_matrix_1_out_51, vivod_matrix_1_out_55, vivod_matrix_1_out_59,
       vivod_matrix_1_out_63, vivod_matrix_1_out_67, vivod_matrix_1_out_70, vivod_matrix_1_out_73;
  wire [18:0] vivod_matrix_1_out_13, vivod_matrix_1_out_17, vivod_matrix_1_out_21, vivod_matrix_1_out_25,
       vivod_matrix_1_out_32, vivod_matrix_1_out_36, vivod_matrix_1_out_40, vivod_matrix_1_out_44,
       vivod_matrix_1_out_49, vivod_matrix_1_out_53, vivod_matrix_1_out_57, vivod_matrix_1_out_61,
       vivod_matrix_1_out_66, vivod_matrix_1_out_69, vivod_matrix_1_out_72, vivod_matrix_1_out_75;
  wire [31:0] counter_1_q;

  assign controlled_buffer_1_out = first_tacktk ? 8'h88 : 8'bz;  // Controlled_Buffer controlled_buffer_1
  Pull_Resistor pull_resistor_1 (.node(controlled_buffer_1_out));
  not not_1 (not_1_out, in_1);
  Clock clock_1 (.out(clock_1_out));
  assign controlled_buffer_2_out = not_1_out ? clock_1_out : 1'bz;  // Controlled_Buffer controlled_buffer_2
  or or_1 (or_1_out, lose, win);
  Register register_1 (.D(or_2_out), .Q(head), .clk(CYCLE), .clr(clr));  // open: en
  assign or_2_out = controlled_buffer_1_out | {inc_dec_4bit_1_r, inc_dec_4bit_2_r};  // OR_Gate or_2, 8 bits wide
  // Probe on head
  golod golod_1 (.golod(golod), .stop_golod(in_2), .clock(Vivod), .clr(clr), .hz(hz));
  and and_1 (I_Osel, not_2_out, takt, data);
  Pull_Resistor pull_resistor_2 (.node(controlled_buffer_2_out));
  Multiplexer #(.enable("false")) multiplexer_1 (.in0(controlled_buffer_2_out), .in1(1'b0), .out(takt), .sel(or_3_out));
  or or_3 (or_3_out, golod, d_ff_1_q);
  D_Flip_Flop d_ff_1 (.Q(d_ff_1_q), .preset(or_1_out), .reset(clr));  // open: clk, D, Qn, en
  or or_4 (or_4_out, left, right);
  or or_5 (or_5_out, clr, hz);
  Negator negator_1 (.in(head), .out(negator_1_out));
  inc_dec_4bit inc_dec_4bit_1 (.X(head[7:4]), .on_off(or_4_out), .inc_dec(right), .R(inc_dec_4bit_1_r));  // open: OFL
  inc_dec_4bit inc_dec_4bit_2 (.X(head[3:0]), .on_off(or_6_out), .inc_dec(up), .R(inc_dec_4bit_2_r));  // open: OFL
  // Probe on Apple_coord
  Random #(.seed(8)) random_1 (.clk(or_5_out), .out(Apple_coord));  // open: next, clr
  Adder adder_1 (.a(Apple_coord), .b(negator_1_out), .out(adder_1_out));  // open: cin, cout
  // Probe on cdm_8_mark5_1_r3
  // Probe on cdm_8_mark5_1_r2
  // Probe on cdm_8_mark5_1_r1
  // Probe on cdm_8_mark5_1_r0
  not not_2 (not_2_out, nand_1_out);
  nand nand_1 (nand_1_out, adr[4], adr[5], adr[6], adr[7]);
  and and_2 (RAM, nand_1_out, data);
  or or_6 (or_6_out, up, down);
  nor nor_1 (hz, adder_1_out[0], adder_1_out[1], adder_1_out[2], adder_1_out[3], adder_1_out[4], adder_1_out[5], adder_1_out[6], adder_1_out[7]);
  movement movement_1 (
    .Clear(clr), .out_4(up), .out_5(down), .out_6(left), .out_7(right), .Move(Move), .\input (\input ));
  // Probe on cdm_8_mark5_1_pc
  // Probe on cdm_8_mark5_1_sp
  // Probe on cdm_8_mark5_1_ps
  CdM_8_mark5 cdm_8_mark5_1 (
    .clock(takt), .addr(adr), .mem_read(In_Out_prime), .mem_cycle(mem), .data_inst(cdm_8_mark5_1_data_inst),
    .data_out(cdm_8_mark5_1_data_out), .data_in(controlled_buffer_4_out), .r0(cdm_8_mark5_1_r0),
    .r1(cdm_8_mark5_1_r1), .r2(cdm_8_mark5_1_r2), .r3(cdm_8_mark5_1_r3), .PC(cdm_8_mark5_1_pc),
    .SP(cdm_8_mark5_1_sp), .PS(cdm_8_mark5_1_ps));
  Counter #(.width(32), .max('hffffffff)) counter_1 (
    .Q(counter_1_q), .clk(CYCLE), .clr(clr));  // open: load, D, count, carry
  or or_7 (or_7_out, hz, or_8_out, clr);
  or or_8 (or_8_out, lose, lose, win);
  Decoder #(.disabled(0)) decoder_1 (.out0(code), .out1(data), .sel(cdm_8_mark5_1_data_inst), .en(mem));
  not not_3 (not_3_out, In_Out_prime);
  assign I_Odata = not_3_out ? cdm_8_mark5_1_data_out : 8'bz;  // Controlled_Buffer controlled_buffer_3
  assign controlled_buffer_4_out = In_Out_prime ? I_Odata : 8'bz;  // Controlled_Buffer controlled_buffer_4
  Comparator #(.width(32), .mode("unsigned")) comparator_1 (
    .a({32{1'b0}}), .b(counter_1_q), .eq(first_tacktk));  // open: gt, lt
  sec_matrix_disp sec_matrix_disp_1 (
    .X(Apple_coord[7:4]), .clock(takt), .Y(Apple_coord[3:0]), .clear(or_7_out));  // open: out_5, out_6, out_7, out_8, out_9, out_10, out_11, out_12, out_13, out_14, out_15, out_16, out_17, out_18, out_19, current, out_21
  Pull_Resistor pull_resistor_3 (.node(adr[0]));
  Pull_Resistor pull_resistor_4 (.node(adr[1]));
  Pull_Resistor pull_resistor_5 (.node(adr[2]));
  Pull_Resistor pull_resistor_6 (.node(adr[3]));
  Pull_Resistor pull_resistor_7 (.node(adr[4]));
  Pull_Resistor pull_resistor_8 (.node(adr[5]));
  Pull_Resistor pull_resistor_9 (.node(adr[6]));
  Pull_Resistor pull_resistor_10 (.node(adr[7]));
  Counter #(.max('ha)) counter_2 (.carry(counter_2_carry), .clk(hz), .clr(clr));  // open: load, D, count, Q
  Register register_2 (.D(Cords), .Q(register_2_q), .clk(undriven));  // open: en, clr
  vivod_matrix vivod_matrix_1 (
    .snake_coord(Cords), .apple_coord(Apple_coord), .paus(in_1), .win(win), .lose(lose), .takt(takt),
    .clr(clr), .vivod(Vivod), .cycle(CYCLE), .apple(hz), .out_13(vivod_matrix_1_out_13),
    .out_14(vivod_matrix_1_out_14), .out_15(vivod_matrix_1_out_15), .out_12(vivod_matrix_1_out_12),
    .out_17(vivod_matrix_1_out_17), .out_18(vivod_matrix_1_out_18), .out_19(vivod_matrix_1_out_19),
    .out_16(vivod_matrix_1_out_16), .out_21(vivod_matrix_1_out_21), .out_22(vivod_matrix_1_out_22),
    .out_23(vivod_matrix_1_out_23), .out_20(vivod_matrix_1_out_20), .out_25(vivod_matrix_1_out_25),
    .out_26(vivod_matrix_1_out_26), .out_27(vivod_matrix_1_out_27), .out_24(vivod_matrix_1_out_24),
    .out_29(vivod_matrix_1_out_29), .out_30(vivod_matrix_1_out_30), .out_28(vivod_matrix_1_out_28),
    .out_32(vivod_matrix_1_out_32), .out_34(vivod_matrix_1_out_34), .out_35(vivod_matrix_1_out_35),
    .out_31(vivod_matrix_1_out_31), .out_36(vivod_matrix_1_out_36), .out_38(vivod_matrix_1_out_38),
    .out_39(vivod_matrix_1_out_39), .out_33(vivod_matrix_1_out_33), .out_40(vivod_matrix_1_out_40),
    .out_42(vivod_matrix_1_out_42), .out_43(vivod_matrix_1_out_43), .out_37(vivod_matrix_1_out_37),
    .out_44(vivod_matrix_1_out_44), .out_46(vivod_matrix_1_out_46), .out_47(vivod_matrix_1_out_47),
    .out_41(vivod_matrix_1_out_41), .out_49(vivod_matrix_1_out_49), .out_51(vivod_matrix_1_out_51),
    .out_52(vivod_matrix_1_out_52), .out_45(vivod_matrix_1_out_45), .out_53(vivod_matrix_1_out_53),
    .out_55(vivod_matrix_1_out_55), .out_56(vivod_matrix_1_out_56), .out_48(vivod_matrix_1_out_48),
    .out_57(vivod_matrix_1_out_57), .out_59(vivod_matrix_1_out_59), .out_60(vivod_matrix_1_out_60),
    .out_50(vivod_matrix_1_out_50), .out_61(vivod_matrix_1_out_61), .out_63(vivod_matrix_1_out_63),
    .out_64(vivod_matrix_1_out_64), .out_54(vivod_matrix_1_out_54), .out_66(vivod_matrix_1_out_66),
    .out_67(vivod_matrix_1_out_67), .out_68(vivod_matrix_1_out_68), .out_58(vivod_matrix_1_out_58),
    .out_69(vivod_matrix_1_out_69), .out_70(vivod_matrix_1_out_70), .out_71(vivod_matrix_1_out_71),
    .out_62(vivod_matrix_1_out_62), .out_72(vivod_matrix_1_out_72), .out_73(vivod_matrix_1_out_73),
    .out_74(vivod_matrix_1_out_74), .out_65(vivod_matrix_1_out_65), .out_75(vivod_matrix_1_out_75),
    .head_coord(head));
  D_Flip_Flop d_ff_2 (.Q(win), .preset(counter_2_carry), .reset(clr));  // open: clk, D, Qn, en
  Comparator comparator_2 (.a(head), .b(register_2_q), .eq(comparator_2_eq));  // open: gt, lt
  ROM rom_1 (.addr(adr), .data(I_Odata), .sel(code));
  RAM ram_1 (.addr(adr), .data(I_Odata), .sel(RAM), .clk(takt), .ld(In_Out_prime));  // open: clr
  Counter counter_3 (.Q(counter_3_q), .clk(comparator_2_eq), .clr(CYCLE));  // open: load, D, count, carry
  and and_3 (and_3_out, I_Osel, adr[0], adr[1], ~adr[2], ~adr[3]);  // AND_Gate
  assign I_Odata = decoder_2_out1 ? register_3_q : 8'bz;  // Controlled_Buffer controlled_buffer_5
  Register register_3 (.D({{6{1'b0}}, Move}), .Q(register_3_q), .clk(takt));  // open: en, clr
  D_Flip_Flop d_ff_3 (.Q(\Перекус ), .preset(comparator_3_eq), .reset(clr));  // open: clk, D, Qn, en
  Comparator comparator_3 (.a(counter_3_q), .b(8'h2), .eq(comparator_3_eq));  // open: gt, lt
  or or_9 (lose, golod, \Перекус );
  Decoder #(.disabled(0)) decoder_2 (.out1(decoder_2_out1), .sel(In_Out_prime), .en(and_3_out));  // open: out0
  _7_Segment_Display u_7_segment_display_1 (
    .g(counter_1_1_out_3), .f(counter_1_1_out_4), .a(counter_1_1_out_5), .b(counter_1_1_out_6),
    .e(counter_1_1_out_11), .d(counter_1_1_out_12), .c(counter_1_1_out_13), .dp(counter_1_1_out_14));
  _7_Segment_Display u_7_segment_display_2 (
    .g(counter_1_1_out_7), .f(counter_1_1_out_8), .a(counter_1_1_out_9), .b(counter_1_1_out_10),
    .e(counter_1_1_out_15), .d(counter_1_1_out_16), .c(counter_1_1_out_17), .dp(counter_1_1_out_18));
  counter_1 counter_1_1 (
    .clock(hz), .clear(clr), .out_11(counter_1_1_out_11), .out_12(counter_1_1_out_12),
    .out_13(counter_1_1_out_13), .out_14(counter_1_1_out_14), .out_15(counter_1_1_out_15),
    .out_16(counter_1_1_out_16), .out_17(counter_1_1_out_17), .out_18(counter_1_1_out_18),
    .out_3(counter_1_1_out_3), .out_4(counter_1_1_out_4), .out_5(counter_1_1_out_5),
    .out_6(counter_1_1_out_6), .out_7(counter_1_1_out_7), .out_8(counter_1_1_out_8),
    .out_9(counter_1_1_out_9), .out_10(counter_1_1_out_10));
  DotMatrix #(.inputtype("row"), .matrixcols(17), .matrixrows(16)) dotmatrix_1 (
    .row0(vivod_matrix_1_out_15), .row1(vivod_matrix_1_out_19), .row2(vivod_matrix_1_out_23),
    .row3(vivod_matrix_1_out_27), .row4(vivod_matrix_1_out_30), .row5(vivod_matrix_1_out_35),
    .row6(vivod_matrix_1_out_39), .row7(vivod_matrix_1_out_43), .row8(vivod_matrix_1_out_47),
    .row9(vivod_matrix_1_out_52), .row10(vivod_matrix_1_out_56), .row11(vivod_matrix_1_out_60),
    .row12(vivod_matrix_1_out_64), .row13(vivod_matrix_1_out_68), .row14(vivod_matrix_1_out_71),
    .row15(vivod_matrix_1_out_74));
  DotMatrix #(.inputtype("row"), .matrixcols(16), .matrixrows(16)) dotmatrix_2 (
    .row0(vivod_matrix_1_out_12), .row1(vivod_matrix_1_out_16), .row2(vivod_matrix_1_out_20),
    .row3(vivod_matrix_1_out_24), .row4(vivod_matrix_1_out_28), .row5(vivod_matrix_1_out_31),
    .row6(vivod_matrix_1_out_33), .row7(vivod_matrix_1_out_37), .row8(vivod_matrix_1_out_41),
    .row9(vivod_matrix_1_out_45), .row10(vivod_matrix_1_out_48), .row11(vivod_matrix_1_out_50),
    .row12(vivod_matrix_1_out_54), .row13(vivod_matrix_1_out_58), .row14(vivod_matrix_1_out_62),
    .row15(vivod_matrix_1_out_65));
  DotMatrix #(.inputtype("row"), .matrixcols(19), .matrixrows(16)) dotmatrix_3 (
    .row0(vivod_matrix_1_out_13), .row1(vivod_matrix_1_out_17), .row2(vivod_matrix_1_out_21),
    .row3(vivod_matrix_1_out_25), .row4(vivod_matrix_1_out_32), .row5(vivod_matrix_1_out_36),
    .row6(vivod_matrix_1_out_40), .row7(vivod_matrix_1_out_44), .row8(vivod_matrix_1_out_49),
    .row9(vivod_matrix_1_out_53), .row10(vivod_matrix_1_out_57), .row11(vivod_matrix_1_out_61),
    .row12(vivod_matrix_1_out_66), .row13(vivod_matrix_1_out_69), .row14(vivod_matrix_1_out_72),
    .row15(vivod_matrix_1_out_75));
  DotMatrix #(.inputtype("row"), .matrixcols(18), .matrixrows(16)) dotmatrix_4 (
    .row0(vivod_matrix_1_out_14), .row1(vivod_matrix_1_out_18), .row2(vivod_matrix_1_out_22),
    .row3(vivod_matrix_1_out_26), .row4(vivod_matrix_1_out_29), .row5(vivod_matrix_1_out_34),
    .row6(vivod_matrix_1_out_38), .row7(vivod_matrix_1_out_42), .row8(vivod_matrix_1_out_46),
    .row9(vivod_matrix_1_out_51), .row10(vivod_matrix_1_out_55), .row11(vivod_matrix_1_out_59),
    .row12(vivod_matrix_1_out_63), .row13(vivod_matrix_1_out_67), .row14(vivod_matrix_1_out_70),
    .row15(vivod_matrix_1_out_73));
  DotMatrix #(.matrixcols(3), .matrixrows(17)) dotmatrix_5 (.col0(17'haaaa), .col1(17'haaaa), .col2(17'haaaa));
  Keyboard keyboard_1 (.clk(pull_resistor_11_node), .clr(clr), .avail(keyboard_1_avail), .data(\input ));  // open: re
  Pull_Resistor pull_resistor_11 (.node(pull_resistor_11_node));
  assign pull_resistor_11_node = keyboard_1_avail ? takt : 1'bz;  // Controlled_Buffer controlled_buffer_6
  Register register_4 (.D(head), .Q(register_4_q), .clk(takt));  // open: en, clr
  assign I_Odata = decoder_3_out1 ? register_4_q : 8'bz;  // Controlled_Buffer controlled_buffer_7
  _7_Segment_Display u_7_segment_display_3 (
    .g(counter_2_1_out_7), .f(counter_2_1_out_8), .a(counter_2_1_out_9), .b(counter_2_1_out_10),
    .e(counter_2_1_out_15), .d(counter_2_1_out_16), .c(counter_2_1_out_17), .dp(counter_2_1_out_18));
  counter_2 counter_2_1 (
    .clock(and_4_out), .clear(or_10_out), .out_11(counter_2_1_out_11), .out_12(counter_2_1_out_12),
    .out_13(counter_2_1_out_13), .out_14(counter_2_1_out_14), .out_15(counter_2_1_out_15),
    .out_16(counter_2_1_out_16), .out_17(counter_2_1_out_17), .out_18(counter_2_1_out_18),
    .out_3(counter_2_1_out_3), .out_4(counter_2_1_out_4), .out_5(counter_2_1_out_5),
    .out_6(counter_2_1_out_6), .out_7(counter_2_1_out_7), .out_8(counter_2_1_out_8),
    .out_9(counter_2_1_out_9), .out_10(counter_2_1_out_10));
  _7_Segment_Display u_7_segment_display_4 (
    .g(counter_2_1_out_3), .f(counter_2_1_out_4), .a(counter_2_1_out_5), .b(counter_2_1_out_6),
    .e(counter_2_1_out_11), .d(counter_2_1_out_12), .c(counter_2_1_out_13), .dp(counter_2_1_out_14));
  and and_4 (and_4_out, Vivod, in_2);
  and and_5 (and_5_out, I_Osel, adr[0], ~adr[1], adr[2], ~adr[3]);  // AND_Gate
  Button button_1 (.out(clr));
  or or_10 (or_10_out, clr, hz);
  Decoder #(.disabled(0)) decoder_3 (.out1(decoder_3_out1), .sel(In_Out_prime), .en(and_5_out));  // open: out0
  assign I_Odata = decoder_4_out1 ? register_5_q : 8'bz;  // Controlled_Buffer controlled_buffer_8
  Register register_5 (.D({{7{1'b0}}, hz}), .Q(register_5_q), .clk(hz), .clr(Vivod));  // open: en
  and and_6 (and_6_out, I_Osel, ~adr[0], adr[1], adr[2], ~adr[3]);  // AND_Gate
  Decoder #(.disabled(0)) decoder_4 (.out1(decoder_4_out1), .sel(In_Out_prime), .en(and_6_out));  // open: out0
  assign ChangeHead = decoder_5_out1 ? 1'b1 : 1'bz;  // Controlled_Buffer controlled_buffer_9
  Pull_Resistor pull_resistor_12 (.node(ChangeHead));
  and and_7 (and_7_out, I_Osel, adr[0], ~adr[1], ~adr[2], adr[3]);  // AND_Gate
  Decoder #(.disabled(0)) decoder_5 (.out1(decoder_5_out1), .sel(In_Out_prime), .en(and_7_out));  // open: out0
  assign Cords = and_8_out ? I_Odata : 8'bz;  // Controlled_Buffer controlled_buffer_10
  and and_8 (and_8_out, adr[0], ~adr[1], ~adr[2], ~adr[3], adr[4], adr[5], ~adr[6], adr[7]);  // AND_Gate
  Pull_Resistor pull_resistor_13 (.node(and_8_out));
  and and_9 (and_9_out, ~adr[0], ~adr[1], ~adr[2], adr[3], adr[4], adr[5], adr[6], adr[7]);  // AND_Gate
  Pull_Resistor pull_resistor_14 (.node(CYCLE));
  assign CYCLE = and_9_out ? 1'b1 : 1'bz;  // Controlled_Buffer controlled_buffer_11
  Pull_Resistor pull_resistor_15 (.node(and_9_out));
  Pull_Resistor pull_resistor_16 (.node(Vivod));
  assign Vivod = pull_resistor_17_node ? 1'b1 : 1'bz;  // Controlled_Buffer controlled_buffer_12
  Pull_Resistor pull_resistor_17 (.node(pull_resistor_17_node));
  and and_10 (pull_resistor_17_node, adr[0], adr[1], adr[2], ~adr[3], adr[4], adr[5], adr[6], adr[7]);  // AND_Gate

  // Other names for the same wires on the sheet: I_Oadr[3:0] = adr[3:0]; porty[3:0] = Apple_coord[7:4]; paus = in_1;
  //   portx[3:0] = Apple_coord[3:0]; rd_wr_prime = In_Out_prime; stop_golod = in_2

  // Notes on the sheet:
  //   contents of rom_1 (hex, n*v repeats v):
  //   cd f0 d1 2 c1 d0 f8 b0 d0 f5 b0 d1 b0 a4 d1 b1 a4 d0 f3 b0 d1 b4 b6 a4 78 e1 22 cb 0 bd 8d ad ee 2a
  //   6*20 8c c0 d0 f6 b0 0 e1 4d d0 ef b1 89 a1 d0 3f 41 e1 4d c8 0 d1 f0 31 85 c6 8c 5 e0 4c b3 a2 8c e
  //   89 ee 43 a2 d0 f7 b0 cb 0 d0 f0 73 e0 9b d0 b3 bd 8f a3 d0 b0 b0 d2 b1 a8 6 d0 c0 41 6*91 d0 3f 48
  //   d2 1 5 e1 77 86 ee 86 76 e1 7c ee 86 8e 76 e1 84 d2 10 ee 86 d2 f0 0 e0 96 d3 b0 bd 19 ad 88 e0 94
  //   d3 b1 ad ee 87 d3 b3 bf ee 52 d0 f8 b0 ee 8
  //   Получение направления
  //   Кол-во яблок
  //   Получение координат головы
  //   Голод змейки
  //   рестарт
  //   1 - пауза 0 играем
  //   1 - есть 0 - нет голода
  //   Бит съеденного яблока
  //   Бит для смены координат головы
  //   Координаты змейки
  //   Бит конца цикла процессора
  //   Бит начала  вывода
endmodule

module _16_bit_AND (
  input  [15:0] \input ,
  input  switch,
  output [16:0] \output 
);

  assign \output [15:0] = \input  & {16{switch}};  // AND_Gate and_1, 16 bits wide

  assign \output [16] = 1'b0;
endmodule

module inc_dec_4bit (
  input  [3:0] X,
  input  on_off,
  input  inc_dec,
  output [3:0] R,
  output OFL
);

  wire and_2_out, and_3_out;
  wire [3:0] and_1_out, xor_1_out, xor_2_out, xor_3_out;
  wire [3:3] decoder_1_out0, decoder_1_out1;

  Decoder #(.enable("false")) decoder_1 (.out0(decoder_1_out0[3]), .out1(decoder_1_out1[3]), .sel(inc_dec));
  assign xor_1_out = {4{decoder_1_out0[3]}} ^ X;  // XOR_Gate xor_1, 4 bits wide
  assign xor_2_out = {4{decoder_1_out1[3]}} ^ xor_3_out;  // XOR_Gate xor_2, 4 bits wide
  assign and_1_out = xor_1_out & xor_2_out;  // AND_Gate and_1, 4 bits wide
  and and_2 (and_2_out, and_1_out[3], inc_dec);
  and and_3 (and_3_out, and_1_out[3], ~inc_dec);  // AND_Gate
  assign xor_3_out = X ^ {and_1_out[2:0], 1'b1};  // XOR_Gate xor_3, 4 bits wide
  or or_1 (OFL, and_2_out, and_3_out);
  Multiplexer #(.width(4), .enable("false")) multiplexer_1 (.in0(X), .in1(xor_3_out), .out(R), .sel(on_off));
endmodule

module granca_detection (
  input  Up,
  input  Down,
  input  [7:0] in_3,
  input  Left,
  input  Right,
  output out_6
);

  wire and_1_out, and_2_out, nor_1_out, nor_2_out;

  Pull_Resistor pull_resistor_1 (.node(Up));
  Pull_Resistor pull_resistor_2 (.node(Down));
  Pull_Resistor pull_resistor_3 (.node(Left));
  Pull_Resistor pull_resistor_4 (.node(Right));
  and and_1 (and_1_out, Up, in_3[3], in_3[2], in_3[1], in_3[0]);
  and and_2 (and_2_out, in_3[7], in_3[6], in_3[5], in_3[4], Right);
  nor nor_1 (nor_1_out, ~Down, in_3[0], in_3[1], in_3[2], in_3[3]);  // NOR_Gate
  nor nor_2 (nor_2_out, in_3[4], in_3[5], in_3[6], in_3[7], ~Left);  // NOR_Gate
  or or_1 (out_6, and_1_out, nor_1_out, nor_2_out, and_2_out);
endmodule

// управление
module movement (
  input  [6:0] \input ,
  input  Clear,
  output [1:0] Move,
  output out_4,
  output out_5,
  output out_6,
  output out_7
);

  wire and_1_out, comparator_1_eq, comparator_2_eq, comparator_3_eq, comparator_4_eq, comparator_5_eq,
       comparator_6_eq, comparator_7_eq, comparator_8_eq, or_1_out, or_2_out, or_3_out, or_4_out, or_7_out,
       xnor_1_out, xor_1_out;
  wire [1:0] or_5_out, register_1_q, register_2_q;

  Comparator #(.width(7)) comparator_1 (.a(\input ), .b(7'b1100100), .eq(comparator_1_eq));  // open: gt, lt
  Comparator #(.width(7)) comparator_2 (.a(\input ), .b(7'b0110010), .eq(comparator_2_eq));  // open: gt, lt
  Comparator #(.width(7)) comparator_3 (.a(\input ), .b(7'b1110011), .eq(comparator_3_eq));  // open: gt, lt
  Comparator #(.width(7)) comparator_4 (.a(\input ), .b(7'b1001011), .eq(comparator_4_eq));  // open: gt, lt
  Comparator #(.width(7)) comparator_5 (.a(\input ), .b(7'b1100001), .eq(comparator_5_eq));  // open: gt, lt
  Comparator #(.width(7)) comparator_6 (.a(\input ), .b(7'b1000100), .eq(comparator_6_eq));  // open: gt, lt
  Comparator #(.width(7)) comparator_7 (.a(\input ), .b(7'b1110111), .eq(comparator_7_eq));  // open: gt, lt
  Comparator #(.width(7)) comparator_8 (.a(\input ), .b(7'b1000110), .eq(comparator_8_eq));  // open: gt, lt
  or or_1 (or_1_out, comparator_1_eq, comparator_2_eq);
  or or_2 (or_2_out, comparator_3_eq, comparator_4_eq);
  or or_3 (or_3_out, comparator_5_eq, comparator_6_eq);
  or or_4 (or_4_out, comparator_7_eq, comparator_8_eq);
  or or_5 (or_5_out[0], or_2_out, or_1_out);
  or or_6 (or_5_out[1], or_1_out, or_3_out);
  or or_7 (or_7_out, or_1_out, or_2_out, or_3_out, or_4_out);
  Register #(.width(2)) register_1 (.D(or_5_out), .Q(register_1_q), .clk(or_7_out), .clr(Clear));  // open: en
  Register #(.width(2)) register_2 (.D(Move), .Q(register_2_q), .clk(or_7_out), .clr(Clear));  // open: en
  xnor xnor_1 (xnor_1_out, register_2_q[1], register_1_q[1]);
  xor xor_1 (xor_1_out, register_2_q[0], register_1_q[0]);
  Multiplexer #(.width(2)) multiplexer_1 (
    .in0(register_1_q), .in1(register_2_q), .out(Move), .sel(and_1_out));  // open: en
  and and_1 (and_1_out, xnor_1_out, xor_1_out);
  Demultiplexer #(.select(2)) demultiplexer_1 (
    .out0(out_4), .out1(out_5), .out2(out_6), .out3(out_7), .in(1'b1), .sel(Move));  // open: en

  // Notes on the sheet:
  //   компараторы для определения команды
  //   создание направления
  //   текушее направление
endmodule

module pseudo_reg (
  input  [3:0] in_1,
  input  [3:0] in_2,
  output [16:0] out_3,
  output [16:0] out_4,
  output [16:0] out_5,
  output [16:0] out_6,
  output [16:0] out_7,
  output [16:0] out_8,
  output [16:0] out_9,
  output [16:0] out_10,
  output [16:0] out_11,
  output [16:0] out_12,
  output [16:0] out_13,
  output [16:0] out_14,
  output [16:0] out_15,
  output [16:0] out_16,
  output [16:0] out_17,
  output [16:0] out_18
);

  wire decoder_2_out0, decoder_2_out1, decoder_2_out2, decoder_2_out3, decoder_2_out4, decoder_2_out5,
       decoder_2_out6, decoder_2_out7, decoder_2_out8, decoder_2_out9, decoder_2_out10, decoder_2_out11,
       decoder_2_out12, decoder_2_out13, decoder_2_out14, decoder_2_out15;
  wire [15:0] decoder_1_out0;

  Decoder #(.select(4), .disabled(0), .enable("false")) decoder_1 (
    .out0(decoder_1_out0[0]), .out1(decoder_1_out0[1]), .out2(decoder_1_out0[2]), .out3(decoder_1_out0[3]),
    .out4(decoder_1_out0[4]), .out5(decoder_1_out0[5]), .out6(decoder_1_out0[6]), .out7(decoder_1_out0[7]),
    .out8(decoder_1_out0[8]), .out9(decoder_1_out0[9]), .out10(decoder_1_out0[10]),
    .out11(decoder_1_out0[11]), .out12(decoder_1_out0[12]), .out13(decoder_1_out0[13]),
    .out14(decoder_1_out0[14]), .out15(decoder_1_out0[15]), .sel(in_1));
  _16_bit_AND u_16_bit_and_1 (.\input (decoder_1_out0), .switch(decoder_2_out1), .\output (out_3));
  _16_bit_AND u_16_bit_and_2 (.\input (decoder_1_out0), .switch(decoder_2_out0), .\output (out_11));
  _16_bit_AND u_16_bit_and_3 (.\input (decoder_1_out0), .switch(decoder_2_out2), .\output (out_12));
  _16_bit_AND u_16_bit_and_4 (.\input (decoder_1_out0), .switch(decoder_2_out3), .\output (out_4));
  Decoder #(.select(4), .disabled(0), .enable("false")) decoder_2 (
    .out0(decoder_2_out0), .out1(decoder_2_out1), .out2(decoder_2_out2), .out3(decoder_2_out3),
    .out4(decoder_2_out4), .out5(decoder_2_out5), .out6(decoder_2_out6), .out7(decoder_2_out7),
    .out8(decoder_2_out8), .out9(decoder_2_out9), .out10(decoder_2_out10), .out11(decoder_2_out11),
    .out12(decoder_2_out12), .out13(decoder_2_out13), .out14(decoder_2_out14), .out15(decoder_2_out15),
    .sel(in_2));
  _16_bit_AND u_16_bit_and_5 (.\input (decoder_1_out0), .switch(decoder_2_out4), .\output (out_13));
  _16_bit_AND u_16_bit_and_6 (.\input (decoder_1_out0), .switch(decoder_2_out5), .\output (out_5));
  _16_bit_AND u_16_bit_and_7 (.\input (decoder_1_out0), .switch(decoder_2_out7), .\output (out_6));
  _16_bit_AND u_16_bit_and_8 (.\input (decoder_1_out0), .switch(decoder_2_out6), .\output (out_14));
  _16_bit_AND u_16_bit_and_9 (.\input (decoder_1_out0), .switch(decoder_2_out8), .\output (out_15));
  _16_bit_AND u_16_bit_and_10 (.\input (decoder_1_out0), .switch(decoder_2_out9), .\output (out_7));
  _16_bit_AND u_16_bit_and_11 (.\input (decoder_1_out0), .switch(decoder_2_out10), .\output (out_16));
  _16_bit_AND u_16_bit_and_12 (.\input (decoder_1_out0), .switch(decoder_2_out11), .\output (out_8));
  _16_bit_AND u_16_bit_and_13 (.\input (decoder_1_out0), .switch(decoder_2_out13), .\output (out_9));
  _16_bit_AND u_16_bit_and_14 (.\input (decoder_1_out0), .switch(decoder_2_out12), .\output (out_17));
  _16_bit_AND u_16_bit_and_15 (.\input (decoder_1_out0), .switch(decoder_2_out15), .\output (out_10));
  _16_bit_AND u_16_bit_and_16 (.\input (decoder_1_out0), .switch(decoder_2_out14), .\output (out_18));
endmodule

module golod (
  input  stop_golod,
  input  clock,
  input  clr,
  input  hz,
  output golod
);

  wire and_1_out, comparator_1_eq, comparator_1_gt, comparator_2_gt, or_1_out, or_2_out;
  wire [9:0] counter_1_q, counter_2_q;

  and and_1 (and_1_out, clock, stop_golod);
  Counter #(.width(10), .max('h3ff)) counter_1 (
    .Q(counter_1_q), .clk(and_1_out), .clr(or_1_out));  // open: load, D, count, carry
  or or_1 (or_1_out, clr, hz);
  Comparator #(.width(10), .mode("unsigned")) comparator_1 (
    .a(counter_1_q), .b(10'h14), .gt(comparator_1_gt), .eq(comparator_1_eq));  // open: lt
  or or_2 (or_2_out, comparator_1_gt, comparator_1_eq);
  Counter #(.width(10), .max('h3ff)) counter_2 (
    .Q(counter_2_q), .clk(or_2_out), .clr(clr));  // open: load, D, count, carry
  Comparator #(.width(10), .mode("unsigned")) comparator_2 (
    .a(counter_2_q), .b({10{1'b0}}), .gt(comparator_2_gt));  // open: eq, lt
  and and_2 (golod, stop_golod, comparator_2_gt);

  // Notes on the sheet:
  //   тут 0f1 это константа после такого количества clockов в голод пойдет 1 которая остановит такты
endmodule

module Apple_Detection (
  input  clr,
  input  [7:0] head,
  input  [1:0] \Static_Направление ,
  input  [7:0] Apple_coord,
  output BIT_FOR_evGENII_KIRILLOV
);

  wire comparator_1_eq, comparator_1_gt, comparator_2_eq, comparator_2_gt;
  wire [3:0] inc_dec_4bit_1_r, inc_dec_4bit_2_r, inc_dec_4bit_3_r, inc_dec_4bit_4_r;
  wire [7:0] adder_1_out, negator_1_out;

  Comparator #(.width(2), .mode("unsigned")) comparator_1 (
    .a(\Static_Направление ), .b(2'b10), .gt(comparator_1_gt), .eq(comparator_1_eq));  // open: lt
  Comparator #(.width(2), .mode("unsigned")) comparator_2 (
    .a(2'b01), .b(\Static_Направление ), .gt(comparator_2_gt), .eq(comparator_2_eq));  // open: lt
  inc_dec_4bit inc_dec_4bit_1 (
    .X(head[3:0]), .on_off(comparator_1_eq), .inc_dec(comparator_1_eq), .R(inc_dec_4bit_1_r));  // open: OFL
  inc_dec_4bit inc_dec_4bit_2 (
    .X(head[7:4]), .on_off(comparator_2_gt), .inc_dec(comparator_2_gt), .R(inc_dec_4bit_2_r));  // open: OFL
  inc_dec_4bit inc_dec_4bit_3 (
    .X(inc_dec_4bit_1_r), .on_off(comparator_1_gt), .inc_dec(comparator_1_eq), .R(inc_dec_4bit_3_r));  // open: OFL
  inc_dec_4bit inc_dec_4bit_4 (
    .X(inc_dec_4bit_2_r), .on_off(comparator_2_eq), .inc_dec(comparator_2_gt), .R(inc_dec_4bit_4_r));  // open: OFL
  Negator negator_1 (.in(Apple_coord), .out(negator_1_out));
  Adder adder_1 (.a({inc_dec_4bit_4_r, inc_dec_4bit_3_r}), .b(negator_1_out), .out(adder_1_out));  // open: cin, cout
  nor nor_1 (BIT_FOR_evGENII_KIRILLOV, adder_1_out[0], adder_1_out[1], adder_1_out[2], adder_1_out[3], adder_1_out[4], adder_1_out[5], adder_1_out[6], adder_1_out[7]);

  // Notes on the sheet:
  //   Эта штука добавляет в счетчик когда следующая клетка после головы это яблоко и мы идем в его сторону
  //   Нужно придумать при какой ситуации будем очищать счетчик 
endmodule

module disp_snake (
  input  [3:0] X,
  input  clock,
  input  [3:0] Y,
  input  clear,
  input  cycle,
  output [15:0] out_6,
  output [15:0] out_7,
  output [15:0] out_8,
  output [15:0] out_9,
  output [15:0] out_10,
  output [15:0] out_11,
  output [15:0] out_12,
  output [15:0] out_13,
  output [15:0] out_14,
  output [15:0] out_15,
  output [15:0] out_16,
  output [15:0] out_17,
  output [15:0] out_18,
  output [15:0] out_19,
  output [15:0] out_20,
  output current,
  output [15:0] out_22
);

  wire demultiplexer_1_out0, demultiplexer_1_out1, demultiplexer_1_out2, demultiplexer_1_out3,
       demultiplexer_1_out4, demultiplexer_1_out5, demultiplexer_1_out6, demultiplexer_1_out7,
       demultiplexer_1_out8, demultiplexer_1_out9, demultiplexer_1_out10, demultiplexer_1_out11,
       demultiplexer_1_out12, demultiplexer_1_out13, demultiplexer_1_out14, demultiplexer_1_out15,
       dispriadok_snake_1_single, dispriadok_snake_2_single, dispriadok_snake_3_single,
       dispriadok_snake_4_single, dispriadok_snake_5_single, dispriadok_snake_6_single,
       dispriadok_snake_7_single, dispriadok_snake_8_single, dispriadok_snake_9_single,
       dispriadok_snake_10_single, dispriadok_snake_11_single, dispriadok_snake_12_single,
       dispriadok_snake_13_single, dispriadok_snake_14_single, dispriadok_snake_15_single,
       dispriadok_snake_16_single;
  wire [15:0] dispriadok_snake_1_riadok, dispriadok_snake_2_riadok, dispriadok_snake_3_riadok,
       dispriadok_snake_4_riadok, dispriadok_snake_5_riadok, dispriadok_snake_6_riadok,
       dispriadok_snake_7_riadok, dispriadok_snake_8_riadok, dispriadok_snake_9_riadok,
       dispriadok_snake_10_riadok, dispriadok_snake_11_riadok, dispriadok_snake_12_riadok,
       dispriadok_snake_13_riadok, dispriadok_snake_14_riadok, dispriadok_snake_15_riadok,
       dispriadok_snake_16_riadok, register_1_q, register_2_q, register_3_q, register_4_q, register_5_q,
       register_6_q, register_7_q, register_8_q, register_9_q, register_10_q, register_11_q, register_12_q,
       register_13_q, register_14_q, register_15_q, register_16_q;

  Demultiplexer #(.select(4)) demultiplexer_1 (
    .out0(demultiplexer_1_out0), .out1(demultiplexer_1_out1), .out2(demultiplexer_1_out2),
    .out3(demultiplexer_1_out3), .out4(demultiplexer_1_out4), .out5(demultiplexer_1_out5),
    .out6(demultiplexer_1_out6), .out7(demultiplexer_1_out7), .out8(demultiplexer_1_out8),
    .out9(demultiplexer_1_out9), .out10(demultiplexer_1_out10), .out11(demultiplexer_1_out11),
    .out12(demultiplexer_1_out12), .out13(demultiplexer_1_out13), .out14(demultiplexer_1_out14),
    .out15(demultiplexer_1_out15), .in(clock), .sel(Y));  // open: en
  dispriadok_snake dispriadok_snake_1 (
    .clock(demultiplexer_1_out15), .hodn(clock), .X(X), .clear(clear), .riadok(dispriadok_snake_1_riadok),
    .single(dispriadok_snake_1_single));
  Register #(.width(16)) register_1 (
    .D(dispriadok_snake_1_riadok), .Q(register_1_q), .clk(clock), .clr(clear));  // open: en
  dispriadok_snake dispriadok_snake_2 (
    .clock(demultiplexer_1_out14), .hodn(clock), .X(X), .clear(clear), .riadok(dispriadok_snake_2_riadok),
    .single(dispriadok_snake_2_single));
  Register #(.width(16)) register_2 (
    .D(dispriadok_snake_2_riadok), .Q(register_2_q), .clk(clock), .clr(clear));  // open: en
  dispriadok_snake dispriadok_snake_3 (
    .clock(demultiplexer_1_out13), .hodn(clock), .X(X), .clear(clear), .riadok(dispriadok_snake_3_riadok),
    .single(dispriadok_snake_3_single));
  Register #(.width(16)) register_3 (
    .D(dispriadok_snake_3_riadok), .Q(register_3_q), .clk(clock), .clr(clear));  // open: en
  dispriadok_snake dispriadok_snake_4 (
    .clock(demultiplexer_1_out12), .hodn(clock), .X(X), .clear(clear), .riadok(dispriadok_snake_4_riadok),
    .single(dispriadok_snake_4_single));
  Register #(.width(16)) register_4 (
    .D(dispriadok_snake_4_riadok), .Q(register_4_q), .clk(clock), .clr(clear));  // open: en
  dispriadok_snake dispriadok_snake_5 (
    .clock(demultiplexer_1_out11), .hodn(clock), .X(X), .clear(clear), .riadok(dispriadok_snake_5_riadok),
    .single(dispriadok_snake_5_single));
  Register #(.width(16)) register_5 (
    .D(dispriadok_snake_5_riadok), .Q(register_5_q), .clk(clock), .clr(clear));  // open: en
  dispriadok_snake dispriadok_snake_6 (
    .clock(demultiplexer_1_out10), .hodn(clock), .X(X), .clear(clear), .riadok(dispriadok_snake_6_riadok),
    .single(dispriadok_snake_6_single));
  Register #(.width(16)) register_6 (
    .D(dispriadok_snake_6_riadok), .Q(register_6_q), .clk(clock), .clr(clear));  // open: en
  dispriadok_snake dispriadok_snake_7 (
    .clock(demultiplexer_1_out9), .hodn(clock), .X(X), .clear(clear), .riadok(dispriadok_snake_7_riadok),
    .single(dispriadok_snake_7_single));
  Register #(.width(16)) register_7 (
    .D(dispriadok_snake_7_riadok), .Q(register_7_q), .clk(clock), .clr(clear));  // open: en
  dispriadok_snake dispriadok_snake_8 (
    .clock(demultiplexer_1_out8), .hodn(clock), .X(X), .clear(clear), .riadok(dispriadok_snake_8_riadok),
    .single(dispriadok_snake_8_single));
  Register #(.width(16)) register_8 (
    .D(dispriadok_snake_8_riadok), .Q(register_8_q), .clk(clock), .clr(clear));  // open: en
  dispriadok_snake dispriadok_snake_9 (
    .clock(demultiplexer_1_out7), .hodn(clock), .X(X), .clear(clear), .riadok(dispriadok_snake_9_riadok),
    .single(dispriadok_snake_9_single));
  Register #(.width(16)) register_9 (
    .D(dispriadok_snake_9_riadok), .Q(register_9_q), .clk(clock), .clr(clear));  // open: en
  dispriadok_snake dispriadok_snake_10 (
    .clock(demultiplexer_1_out6), .hodn(clock), .X(X), .clear(clear), .riadok(dispriadok_snake_10_riadok),
    .single(dispriadok_snake_10_single));
  Register #(.width(16)) register_10 (
    .D(dispriadok_snake_10_riadok), .Q(register_10_q), .clk(clock), .clr(clear));  // open: en
  dispriadok_snake dispriadok_snake_11 (
    .clock(demultiplexer_1_out5), .hodn(clock), .X(X), .clear(clear), .riadok(dispriadok_snake_11_riadok),
    .single(dispriadok_snake_11_single));
  Register #(.width(16)) register_11 (
    .D(dispriadok_snake_11_riadok), .Q(register_11_q), .clk(clock), .clr(clear));  // open: en
  dispriadok_snake dispriadok_snake_12 (
    .clock(demultiplexer_1_out4), .hodn(clock), .X(X), .clear(clear), .riadok(dispriadok_snake_12_riadok),
    .single(dispriadok_snake_12_single));
  Register #(.width(16)) register_12 (
    .D(dispriadok_snake_12_riadok), .Q(register_12_q), .clk(clock), .clr(clear));  // open: en
  dispriadok_snake dispriadok_snake_13 (
    .clock(demultiplexer_1_out3), .hodn(clock), .X(X), .clear(clear), .riadok(dispriadok_snake_13_riadok),
    .single(dispriadok_snake_13_single));
  Register #(.width(16)) register_13 (
    .D(dispriadok_snake_13_riadok), .Q(register_13_q), .clk(clock), .clr(clear));  // open: en
  dispriadok_snake dispriadok_snake_14 (
    .clock(demultiplexer_1_out2), .hodn(clock), .X(X), .clear(clear), .riadok(dispriadok_snake_14_riadok),
    .single(dispriadok_snake_14_single));
  Register #(.width(16)) register_14 (
    .D(dispriadok_snake_14_riadok), .Q(register_14_q), .clk(clock), .clr(clear));  // open: en
  dispriadok_snake dispriadok_snake_15 (
    .clock(demultiplexer_1_out1), .hodn(clock), .X(X), .clear(clear), .riadok(dispriadok_snake_15_riadok),
    .single(dispriadok_snake_15_single));
  Register #(.width(16)) register_15 (
    .D(dispriadok_snake_15_riadok), .Q(register_15_q), .clk(clock), .clr(clear));  // open: en
  dispriadok_snake dispriadok_snake_16 (
    .clock(demultiplexer_1_out0), .hodn(clock), .X(X), .clear(clear), .riadok(dispriadok_snake_16_riadok),
    .single(dispriadok_snake_16_single));
  Register #(.width(16)) register_16 (
    .D(dispriadok_snake_16_riadok), .Q(register_16_q), .clk(clock), .clr(clear));  // open: en
  Register #(.width(16)) register_17 (.D(register_1_q), .Q(out_6), .clk(cycle));  // open: en, clr
  Register #(.width(16)) register_18 (.D(register_2_q), .Q(out_7), .clk(cycle));  // open: en, clr
  Register #(.width(16)) register_19 (.D(register_3_q), .Q(out_8), .clk(cycle));  // open: en, clr
  Register #(.width(16)) register_20 (.D(register_4_q), .Q(out_9), .clk(cycle));  // open: en, clr
  Register #(.width(16)) register_21 (.D(register_5_q), .Q(out_10), .clk(cycle));  // open: en, clr
  Register #(.width(16)) register_22 (.D(register_6_q), .Q(out_11), .clk(cycle));  // open: en, clr
  Register #(.width(16)) register_23 (.D(register_7_q), .Q(out_12), .clk(cycle));  // open: en, clr
  Register #(.width(16)) register_24 (.D(register_8_q), .Q(out_13), .clk(cycle));  // open: en, clr
  Register #(.width(16)) register_25 (.D(register_9_q), .Q(out_14), .clk(cycle));  // open: en, clr
  Register #(.width(16)) register_26 (.D(register_10_q), .Q(out_15), .clk(cycle));  // open: en, clr
  Register #(.width(16)) register_27 (.D(register_11_q), .Q(out_16), .clk(cycle));  // open: en, clr
  Register #(.width(16)) register_28 (.D(register_12_q), .Q(out_17), .clk(cycle));  // open: en, clr
  Register #(.width(16)) register_29 (.D(register_13_q), .Q(out_18), .clk(cycle));  // open: en, clr
  Register #(.width(16)) register_30 (.D(register_14_q), .Q(out_19), .clk(cycle));  // open: en, clr
  Register #(.width(16)) register_31 (.D(register_15_q), .Q(out_20), .clk(cycle));  // open: en, clr
  Register #(.width(16)) register_32 (.D(register_16_q), .Q(out_22), .clk(cycle));  // open: en, clr
  Multiplexer #(.select(4)) multiplexer_1 (
    .in0(dispriadok_snake_1_single), .in1(dispriadok_snake_2_single), .in2(dispriadok_snake_3_single),
    .in3(dispriadok_snake_4_single), .in4(dispriadok_snake_5_single), .in5(dispriadok_snake_6_single),
    .in6(dispriadok_snake_7_single), .in7(dispriadok_snake_8_single), .in8(dispriadok_snake_9_single),
    .in9(dispriadok_snake_10_single), .in10(dispriadok_snake_11_single), .in11(dispriadok_snake_12_single),
    .in12(dispriadok_snake_13_single), .in13(dispriadok_snake_14_single), .in14(dispriadok_snake_15_single),
    .in15(dispriadok_snake_16_single), .out(current), .sel(Y));  // open: en
endmodule

module dispriadok_snake (
  input  clock,
  input  hodn,
  input  [3:0] X,
  input  clear,
  output [15:0] riadok,
  output single
);

  wire demultiplexer_1_out0, demultiplexer_1_out1, demultiplexer_1_out2, demultiplexer_1_out3,
       demultiplexer_1_out4, demultiplexer_1_out5, demultiplexer_1_out6, demultiplexer_1_out7,
       demultiplexer_1_out8, demultiplexer_1_out9, demultiplexer_1_out10, demultiplexer_1_out11,
       demultiplexer_1_out12, demultiplexer_1_out13, demultiplexer_1_out14, demultiplexer_1_out15;

  Demultiplexer #(.select(4)) demultiplexer_1 (
    .out0(demultiplexer_1_out0), .out1(demultiplexer_1_out1), .out2(demultiplexer_1_out2),
    .out3(demultiplexer_1_out3), .out4(demultiplexer_1_out4), .out5(demultiplexer_1_out5),
    .out6(demultiplexer_1_out6), .out7(demultiplexer_1_out7), .out8(demultiplexer_1_out8),
    .out9(demultiplexer_1_out9), .out10(demultiplexer_1_out10), .out11(demultiplexer_1_out11),
    .out12(demultiplexer_1_out12), .out13(demultiplexer_1_out13), .out14(demultiplexer_1_out14),
    .out15(demultiplexer_1_out15), .in(clock), .sel(X));  // open: en
  D_Flip_Flop d_ff_1 (.clk(demultiplexer_1_out0), .D(hodn), .Q(riadok[15]), .reset(clear));  // open: Qn, preset, en
  D_Flip_Flop d_ff_2 (.clk(demultiplexer_1_out1), .D(hodn), .Q(riadok[14]), .reset(clear));  // open: Qn, preset, en
  D_Flip_Flop d_ff_3 (.clk(demultiplexer_1_out2), .D(hodn), .Q(riadok[13]), .reset(clear));  // open: Qn, preset, en
  D_Flip_Flop d_ff_4 (.clk(demultiplexer_1_out3), .D(hodn), .Q(riadok[12]), .reset(clear));  // open: Qn, preset, en
  D_Flip_Flop d_ff_5 (.clk(demultiplexer_1_out4), .D(hodn), .Q(riadok[11]), .reset(clear));  // open: Qn, preset, en
  D_Flip_Flop d_ff_6 (.clk(demultiplexer_1_out5), .D(hodn), .Q(riadok[10]), .reset(clear));  // open: Qn, preset, en
  D_Flip_Flop d_ff_7 (.clk(demultiplexer_1_out6), .D(hodn), .Q(riadok[9]), .reset(clear));  // open: Qn, preset, en
  D_Flip_Flop d_ff_8 (.clk(demultiplexer_1_out7), .D(hodn), .Q(riadok[8]), .reset(clear));  // open: Qn, preset, en
  D_Flip_Flop d_ff_9 (.clk(demultiplexer_1_out8), .D(hodn), .Q(riadok[7]), .reset(clear));  // open: Qn, preset, en
  D_Flip_Flop d_ff_10 (.clk(demultiplexer_1_out9), .D(hodn), .Q(riadok[6]), .reset(clear));  // open: Qn, preset, en
  Multiplexer #(.select(4)) multiplexer_1 (
    .in0(riadok[15]), .in1(riadok[14]), .in2(riadok[13]), .in3(riadok[12]), .in4(riadok[11]),
    .in5(riadok[10]), .in6(riadok[9]), .in7(riadok[8]), .in8(riadok[7]), .in9(riadok[6]), .in10(riadok[5]),
    .in11(riadok[4]), .in12(riadok[3]), .in13(riadok[2]), .in14(riadok[1]), .in15(riadok[0]), .out(single),
    .sel(X));  // open: en
  D_Flip_Flop d_ff_11 (.clk(demultiplexer_1_out10), .D(hodn), .Q(riadok[5]), .reset(clear));  // open: Qn, preset, en
  D_Flip_Flop d_ff_12 (.clk(demultiplexer_1_out11), .D(hodn), .Q(riadok[4]), .reset(clear));  // open: Qn, preset, en
  D_Flip_Flop d_ff_13 (.clk(demultiplexer_1_out12), .D(hodn), .Q(riadok[3]), .reset(clear));  // open: Qn, preset, en
  D_Flip_Flop d_ff_14 (.clk(demultiplexer_1_out14), .D(hodn), .Q(riadok[1]), .reset(clear));  // open: Qn, preset, en
  D_Flip_Flop d_ff_15 (.clk(demultiplexer_1_out13), .D(hodn), .Q(riadok[2]), .reset(clear));  // open: Qn, preset, en
  D_Flip_Flop d_ff_16 (.clk(demultiplexer_1_out15), .D(hodn), .Q(riadok[0]), .reset(clear));  // open: Qn, preset, en
endmodule

module sec_matrixdispriadok (
  input  clock,
  input  hodn,
  input  [3:0] X,
  input  clear,
  output [16:0] riadok,
  output single
);

  wire demultiplexer_1_out0, demultiplexer_1_out1, demultiplexer_1_out2, demultiplexer_1_out3,
       demultiplexer_1_out4, demultiplexer_1_out5, demultiplexer_1_out6, demultiplexer_1_out7,
       demultiplexer_1_out8, demultiplexer_1_out9, demultiplexer_1_out10, demultiplexer_1_out11,
       demultiplexer_1_out12, demultiplexer_1_out13, demultiplexer_1_out14, demultiplexer_1_out15;

  Demultiplexer #(.select(4)) demultiplexer_1 (
    .out0(demultiplexer_1_out0), .out1(demultiplexer_1_out1), .out2(demultiplexer_1_out2),
    .out3(demultiplexer_1_out3), .out4(demultiplexer_1_out4), .out5(demultiplexer_1_out5),
    .out6(demultiplexer_1_out6), .out7(demultiplexer_1_out7), .out8(demultiplexer_1_out8),
    .out9(demultiplexer_1_out9), .out10(demultiplexer_1_out10), .out11(demultiplexer_1_out11),
    .out12(demultiplexer_1_out12), .out13(demultiplexer_1_out13), .out14(demultiplexer_1_out14),
    .out15(demultiplexer_1_out15), .in(clock), .sel(X));  // open: en
  D_Flip_Flop d_ff_1 (.clk(demultiplexer_1_out0), .D(hodn), .Q(riadok[15]), .reset(clear));  // open: Qn, preset, en
  D_Flip_Flop d_ff_2 (.clk(demultiplexer_1_out1), .D(hodn), .Q(riadok[14]), .reset(clear));  // open: Qn, preset, en
  D_Flip_Flop d_ff_3 (.clk(demultiplexer_1_out2), .D(hodn), .Q(riadok[13]), .reset(clear));  // open: Qn, preset, en
  D_Flip_Flop d_ff_4 (.clk(demultiplexer_1_out3), .D(hodn), .Q(riadok[12]), .reset(clear));  // open: Qn, preset, en
  D_Flip_Flop d_ff_5 (.clk(demultiplexer_1_out5), .D(hodn), .Q(riadok[10]), .reset(clear));  // open: Qn, preset, en
  D_Flip_Flop d_ff_6 (.clk(demultiplexer_1_out4), .D(hodn), .Q(riadok[11]), .reset(clear));  // open: Qn, preset, en
  D_Flip_Flop d_ff_7 (.clk(demultiplexer_1_out6), .D(hodn), .Q(riadok[9]), .reset(clear));  // open: Qn, preset, en
  D_Flip_Flop d_ff_8 (.clk(demultiplexer_1_out7), .D(hodn), .Q(riadok[8]), .reset(clear));  // open: Qn, preset, en
  D_Flip_Flop d_ff_9 (.clk(demultiplexer_1_out8), .D(hodn), .Q(riadok[7]), .reset(clear));  // open: Qn, preset, en
  D_Flip_Flop d_ff_10 (.clk(demultiplexer_1_out9), .D(hodn), .Q(riadok[6]), .reset(clear));  // open: Qn, preset, en
  Multiplexer #(.select(4)) multiplexer_1 (
    .in0(riadok[15]), .in1(riadok[14]), .in2(riadok[13]), .in3(riadok[12]), .in4(riadok[11]),
    .in5(riadok[10]), .in6(riadok[9]), .in7(riadok[8]), .in8(riadok[7]), .in9(riadok[6]), .in10(riadok[5]),
    .in11(riadok[4]), .in12(riadok[3]), .in13(riadok[2]), .in14(riadok[1]), .in15(riadok[0]), .out(single),
    .sel(X));  // open: en
  D_Flip_Flop d_ff_11 (.clk(demultiplexer_1_out10), .D(hodn), .Q(riadok[5]), .reset(clear));  // open: Qn, preset, en
  D_Flip_Flop d_ff_12 (.clk(demultiplexer_1_out11), .D(hodn), .Q(riadok[4]), .reset(clear));  // open: Qn, preset, en
  D_Flip_Flop d_ff_13 (.clk(demultiplexer_1_out12), .D(hodn), .Q(riadok[3]), .reset(clear));  // open: Qn, preset, en
  D_Flip_Flop d_ff_14 (.clk(demultiplexer_1_out13), .D(hodn), .Q(riadok[2]), .reset(clear));  // open: Qn, preset, en
  D_Flip_Flop d_ff_15 (.clk(demultiplexer_1_out14), .D(hodn), .Q(riadok[1]), .reset(clear));  // open: Qn, preset, en
  D_Flip_Flop d_ff_16 (.clk(demultiplexer_1_out15), .D(hodn), .Q(riadok[0]), .reset(clear));  // open: Qn, preset, en

  assign riadok[16] = 1'b0;
endmodule

module sec_matrix_disp (
  input  [3:0] X,
  input  clock,
  input  [3:0] Y,
  input  clear,
  output [16:0] out_5,
  output [16:0] out_6,
  output [16:0] out_7,
  output [16:0] out_8,
  output [16:0] out_9,
  output [16:0] out_10,
  output [16:0] out_11,
  output [16:0] out_12,
  output [16:0] out_13,
  output [16:0] out_14,
  output [16:0] out_15,
  output [16:0] out_16,
  output [16:0] out_17,
  output [16:0] out_18,
  output [16:0] out_19,
  output current,
  output [16:0] out_21
);

  wire demultiplexer_1_out0, demultiplexer_1_out1, demultiplexer_1_out2, demultiplexer_1_out3,
       demultiplexer_1_out4, demultiplexer_1_out5, demultiplexer_1_out6, demultiplexer_1_out7,
       demultiplexer_1_out8, demultiplexer_1_out9, demultiplexer_1_out10, demultiplexer_1_out11,
       demultiplexer_1_out12, demultiplexer_1_out13, demultiplexer_1_out14, demultiplexer_1_out15,
       sec_matrixdispriadok_1_single, sec_matrixdispriadok_2_single, sec_matrixdispriadok_3_single,
       sec_matrixdispriadok_4_single, sec_matrixdispriadok_5_single, sec_matrixdispriadok_6_single,
       sec_matrixdispriadok_7_single, sec_matrixdispriadok_8_single, sec_matrixdispriadok_9_single,
       sec_matrixdispriadok_10_single, sec_matrixdispriadok_11_single, sec_matrixdispriadok_12_single,
       sec_matrixdispriadok_13_single, sec_matrixdispriadok_14_single, sec_matrixdispriadok_15_single,
       sec_matrixdispriadok_16_single;
  wire [16:0] sec_matrixdispriadok_1_riadok, sec_matrixdispriadok_2_riadok, sec_matrixdispriadok_3_riadok,
       sec_matrixdispriadok_4_riadok, sec_matrixdispriadok_5_riadok, sec_matrixdispriadok_6_riadok,
       sec_matrixdispriadok_7_riadok, sec_matrixdispriadok_8_riadok, sec_matrixdispriadok_9_riadok,
       sec_matrixdispriadok_10_riadok, sec_matrixdispriadok_11_riadok, sec_matrixdispriadok_12_riadok,
       sec_matrixdispriadok_13_riadok, sec_matrixdispriadok_14_riadok, sec_matrixdispriadok_15_riadok,
       sec_matrixdispriadok_16_riadok;

  Demultiplexer #(.select(4)) demultiplexer_1 (
    .out0(demultiplexer_1_out0), .out1(demultiplexer_1_out1), .out2(demultiplexer_1_out2),
    .out3(demultiplexer_1_out3), .out4(demultiplexer_1_out4), .out5(demultiplexer_1_out5),
    .out6(demultiplexer_1_out6), .out7(demultiplexer_1_out7), .out8(demultiplexer_1_out8),
    .out9(demultiplexer_1_out9), .out10(demultiplexer_1_out10), .out11(demultiplexer_1_out11),
    .out12(demultiplexer_1_out12), .out13(demultiplexer_1_out13), .out14(demultiplexer_1_out14),
    .out15(demultiplexer_1_out15), .in(clock), .sel(Y));  // open: en
  sec_matrixdispriadok sec_matrixdispriadok_1 (
    .clock(demultiplexer_1_out15), .hodn(clock), .X(X), .clear(clear),
    .riadok(sec_matrixdispriadok_1_riadok), .single(sec_matrixdispriadok_1_single));
  Register #(.width(17)) register_1 (
    .D(sec_matrixdispriadok_1_riadok), .Q(out_5), .clk(clock), .clr(clear));  // open: en
  sec_matrixdispriadok sec_matrixdispriadok_2 (
    .clock(demultiplexer_1_out14), .hodn(clock), .X(X), .clear(clear),
    .riadok(sec_matrixdispriadok_2_riadok), .single(sec_matrixdispriadok_2_single));
  Register #(.width(17)) register_2 (
    .D(sec_matrixdispriadok_2_riadok), .Q(out_6), .clk(clock), .clr(clear));  // open: en
  sec_matrixdispriadok sec_matrixdispriadok_3 (
    .clock(demultiplexer_1_out13), .hodn(clock), .X(X), .clear(clear),
    .riadok(sec_matrixdispriadok_3_riadok), .single(sec_matrixdispriadok_3_single));
  Register #(.width(17)) register_3 (
    .D(sec_matrixdispriadok_3_riadok), .Q(out_7), .clk(clock), .clr(clear));  // open: en
  sec_matrixdispriadok sec_matrixdispriadok_4 (
    .clock(demultiplexer_1_out12), .hodn(clock), .X(X), .clear(clear),
    .riadok(sec_matrixdispriadok_4_riadok), .single(sec_matrixdispriadok_4_single));
  Register #(.width(17)) register_4 (
    .D(sec_matrixdispriadok_4_riadok), .Q(out_8), .clk(clock), .clr(clear));  // open: en
  sec_matrixdispriadok sec_matrixdispriadok_5 (
    .clock(demultiplexer_1_out11), .hodn(clock), .X(X), .clear(clear),
    .riadok(sec_matrixdispriadok_5_riadok), .single(sec_matrixdispriadok_5_single));
  Register #(.width(17)) register_5 (
    .D(sec_matrixdispriadok_5_riadok), .Q(out_9), .clk(clock), .clr(clear));  // open: en
  sec_matrixdispriadok sec_matrixdispriadok_6 (
    .clock(demultiplexer_1_out10), .hodn(clock), .X(X), .clear(clear),
    .riadok(sec_matrixdispriadok_6_riadok), .single(sec_matrixdispriadok_6_single));
  Register #(.width(17)) register_6 (
    .D(sec_matrixdispriadok_6_riadok), .Q(out_10), .clk(clock), .clr(clear));  // open: en
  sec_matrixdispriadok sec_matrixdispriadok_7 (
    .clock(demultiplexer_1_out9), .hodn(clock), .X(X), .clear(clear), .riadok(sec_matrixdispriadok_7_riadok),
    .single(sec_matrixdispriadok_7_single));
  Register #(.width(17)) register_7 (
    .D(sec_matrixdispriadok_7_riadok), .Q(out_11), .clk(clock), .clr(clear));  // open: en
  sec_matrixdispriadok sec_matrixdispriadok_8 (
    .clock(demultiplexer_1_out8), .hodn(clock), .X(X), .clear(clear), .riadok(sec_matrixdispriadok_8_riadok),
    .single(sec_matrixdispriadok_8_single));
  Register #(.width(17)) register_8 (
    .D(sec_matrixdispriadok_8_riadok), .Q(out_12), .clk(clock), .clr(clear));  // open: en
  sec_matrixdispriadok sec_matrixdispriadok_9 (
    .clock(demultiplexer_1_out7), .hodn(clock), .X(X), .clear(clear), .riadok(sec_matrixdispriadok_9_riadok),
    .single(sec_matrixdispriadok_9_single));
  Register #(.width(17)) register_9 (
    .D(sec_matrixdispriadok_9_riadok), .Q(out_13), .clk(clock), .clr(clear));  // open: en
  sec_matrixdispriadok sec_matrixdispriadok_10 (
    .clock(demultiplexer_1_out6), .hodn(clock), .X(X), .clear(clear),
    .riadok(sec_matrixdispriadok_10_riadok), .single(sec_matrixdispriadok_10_single));
  Register #(.width(17)) register_10 (
    .D(sec_matrixdispriadok_10_riadok), .Q(out_14), .clk(clock), .clr(clear));  // open: en
  sec_matrixdispriadok sec_matrixdispriadok_11 (
    .clock(demultiplexer_1_out5), .hodn(clock), .X(X), .clear(clear),
    .riadok(sec_matrixdispriadok_11_riadok), .single(sec_matrixdispriadok_11_single));
  Register #(.width(17)) register_11 (
    .D(sec_matrixdispriadok_11_riadok), .Q(out_15), .clk(clock), .clr(clear));  // open: en
  sec_matrixdispriadok sec_matrixdispriadok_12 (
    .clock(demultiplexer_1_out4), .hodn(clock), .X(X), .clear(clear),
    .riadok(sec_matrixdispriadok_12_riadok), .single(sec_matrixdispriadok_12_single));
  Register #(.width(17)) register_12 (
    .D(sec_matrixdispriadok_12_riadok), .Q(out_16), .clk(clock), .clr(clear));  // open: en
  sec_matrixdispriadok sec_matrixdispriadok_13 (
    .clock(demultiplexer_1_out3), .hodn(clock), .X(X), .clear(clear),
    .riadok(sec_matrixdispriadok_13_riadok), .single(sec_matrixdispriadok_13_single));
  Register #(.width(17)) register_13 (
    .D(sec_matrixdispriadok_13_riadok), .Q(out_17), .clk(clock), .clr(clear));  // open: en
  sec_matrixdispriadok sec_matrixdispriadok_14 (
    .clock(demultiplexer_1_out2), .hodn(clock), .X(X), .clear(clear),
    .riadok(sec_matrixdispriadok_14_riadok), .single(sec_matrixdispriadok_14_single));
  Register #(.width(17)) register_14 (
    .D(sec_matrixdispriadok_14_riadok), .Q(out_18), .clk(clock), .clr(clear));  // open: en
  sec_matrixdispriadok sec_matrixdispriadok_15 (
    .clock(demultiplexer_1_out1), .hodn(clock), .X(X), .clear(clear),
    .riadok(sec_matrixdispriadok_15_riadok), .single(sec_matrixdispriadok_15_single));
  Register #(.width(17)) register_15 (
    .D(sec_matrixdispriadok_15_riadok), .Q(out_19), .clk(clock), .clr(clear));  // open: en
  sec_matrixdispriadok sec_matrixdispriadok_16 (
    .clock(demultiplexer_1_out0), .hodn(clock), .X(X), .clear(clear),
    .riadok(sec_matrixdispriadok_16_riadok), .single(sec_matrixdispriadok_16_single));
  Register #(.width(17)) register_16 (
    .D(sec_matrixdispriadok_16_riadok), .Q(out_21), .clk(clock), .clr(clear));  // open: en
  Multiplexer #(.select(4)) multiplexer_1 (
    .in0(sec_matrixdispriadok_1_single), .in1(sec_matrixdispriadok_2_single),
    .in2(sec_matrixdispriadok_3_single), .in3(sec_matrixdispriadok_4_single),
    .in4(sec_matrixdispriadok_5_single), .in5(sec_matrixdispriadok_6_single),
    .in6(sec_matrixdispriadok_7_single), .in7(sec_matrixdispriadok_8_single),
    .in8(sec_matrixdispriadok_9_single), .in9(sec_matrixdispriadok_10_single),
    .in10(sec_matrixdispriadok_11_single), .in11(sec_matrixdispriadok_12_single),
    .in12(sec_matrixdispriadok_13_single), .in13(sec_matrixdispriadok_14_single),
    .in14(sec_matrixdispriadok_15_single), .in15(sec_matrixdispriadok_16_single), .out(current), .sel(Y));  // open: en
endmodule

module MAIN (
);


  // Notes on the sheet:
  //   КАК ИДЕЯ МОЖНО ПРОСТО СЮДА ВЫНЕСТИ ВСЕ ОТДЕЛЬНЫЕ 
  //   ВХОДЫ ВЗАИМОДЕЙСТВУЮЩИЕ С ПОЛЬЗОВАТЕЛЕМ И ВЫНЕСТИ ПОЛЕ
endmodule

module win (
  input  lose,
  input  win,
  input  pause,
  output [17:0] _1,
  output [17:0] _2,
  output [17:0] _3,
  output [17:0] _4,
  output [17:0] _5,
  output [17:0] _6,
  output [17:0] _7,
  output [17:0] _8,
  output [17:0] _9,
  output [17:0] _10,
  output [17:0] _11,
  output [17:0] _12,
  output [17:0] _13,
  output [17:0] _14,
  output [17:0] _15,
  output [17:0] _16
);

  wire [15:0] _5l, _5p, _5w, _6l, _6p, _6w, _7l, _7p, _7w, _8l, _8p, _8w, _9l, _9p, _9w, _10l, _10p, _10w,
       _11l, _11p, _11w, or_1_out, or_2_out, or_3_out, or_4_out, or_5_out, or_6_out, or_7_out;

  assign _5p = pause ? 16'h200 : 16'bz;  // Controlled_Buffer controlled_buffer_1
  assign _6p = pause ? 16'h300 : 16'bz;  // Controlled_Buffer controlled_buffer_2
  assign _7p = pause ? 16'h380 : 16'bz;  // Controlled_Buffer controlled_buffer_3
  assign _8p = pause ? 16'h3c0 : 16'bz;  // Controlled_Buffer controlled_buffer_4
  Pull_Resistor pull_resistor_1 (.node(_9p));
  assign _9p = pause ? 16'h380 : 16'bz;  // Controlled_Buffer controlled_buffer_5
  assign _10p = pause ? 16'h300 : 16'bz;  // Controlled_Buffer controlled_buffer_6
  Pull_Resistor pull_resistor_2 (.node(_10p));
  assign _11p = pause ? 16'h200 : 16'bz;  // Controlled_Buffer controlled_buffer_7
  Pull_Resistor pull_resistor_3 (.node(_11p));
  assign _5w = win ? {16{1'b0}} : 16'bz;  // Controlled_Buffer controlled_buffer_8
  assign _6w = win ? 16'h4542 : 16'bz;  // Controlled_Buffer controlled_buffer_9
  assign _7w = win ? 16'h4462 : 16'bz;  // Controlled_Buffer controlled_buffer_10
  assign _8w = win ? 16'h4552 : 16'bz;  // Controlled_Buffer controlled_buffer_11
  assign _9w = win ? 16'h554a : 16'bz;  // Controlled_Buffer controlled_buffer_12
  Pull_Resistor pull_resistor_4 (.node(_9w));
  assign _10w = win ? 16'h6d46 : 16'bz;  // Controlled_Buffer controlled_buffer_13
  Pull_Resistor pull_resistor_5 (.node(_10w));
  assign _11w = win ? 16'h4542 : 16'bz;  // Controlled_Buffer controlled_buffer_14
  Pull_Resistor pull_resistor_6 (.node(_11w));
  assign _5l = lose ? {16{1'b0}} : 16'bz;  // Controlled_Buffer controlled_buffer_15
  assign _6l = lose ? 16'h4ef6 : 16'bz;  // Controlled_Buffer controlled_buffer_16
  assign _7l = lose ? 16'h4a84 : 16'bz;  // Controlled_Buffer controlled_buffer_17
  assign _8l = lose ? 16'h4ac4 : 16'bz;  // Controlled_Buffer controlled_buffer_18
  Pull_Resistor pull_resistor_7 (.node(_9l));
  assign _9l = lose ? 16'h4a66 : 16'bz;  // Controlled_Buffer controlled_buffer_19
  Pull_Resistor pull_resistor_8 (.node(_10l));
  assign _10l = lose ? 16'h4a34 : 16'bz;  // Controlled_Buffer controlled_buffer_20
  assign _11l = lose ? 16'h6ef6 : 16'bz;  // Controlled_Buffer controlled_buffer_21
  Pull_Resistor pull_resistor_9 (.node(_11l));
  Pull_Resistor pull_resistor_10 (.node(_5p));
  Pull_Resistor pull_resistor_11 (.node(_6p));
  Pull_Resistor pull_resistor_12 (.node(_7p));
  Pull_Resistor pull_resistor_13 (.node(_8p));
  Pull_Resistor pull_resistor_14 (.node(_5w));
  Pull_Resistor pull_resistor_15 (.node(_6w));
  Pull_Resistor pull_resistor_16 (.node(_7w));
  Pull_Resistor pull_resistor_17 (.node(_8w));
  Pull_Resistor pull_resistor_18 (.node(_5l));
  Pull_Resistor pull_resistor_19 (.node(_6l));
  Pull_Resistor pull_resistor_20 (.node(_7l));
  Pull_Resistor pull_resistor_21 (.node(_8l));
  helper_1 helper_1_1 (.in(or_1_out), .out(_5));
  assign or_1_out = _5p | _5w | _5l;  // OR_Gate or_1, 16 bits wide
  helper_1 helper_1_2 (.in(or_2_out), .out(_6));
  assign or_2_out = _6p | _6w | _6l;  // OR_Gate or_2, 16 bits wide
  assign or_3_out = _7p | _7w | _7l;  // OR_Gate or_3, 16 bits wide
  helper_1 helper_1_3 (.in(or_3_out), .out(_7));
  helper_1 helper_1_4 (.in(or_4_out), .out(_8));
  assign or_4_out = _8p | _8w | _8l;  // OR_Gate or_4, 16 bits wide
  assign or_5_out = _9p | _9w | _9l;  // OR_Gate or_5, 16 bits wide
  helper_1 helper_1_5 (.in(or_5_out), .out(_9));
  assign or_6_out = _10p | _10w | _10l;  // OR_Gate or_6, 16 bits wide
  helper_1 helper_1_6 (.in(or_6_out), .out(_10));
  helper_1 helper_1_7 (.in(or_7_out), .out(_11));
  assign or_7_out = _11p | _11w | _11l;  // OR_Gate or_7, 16 bits wide

  assign _1 = {18{1'b0}};
  assign _2 = {18{1'b0}};
  assign _3 = {18{1'b0}};
  assign _4 = {18{1'b0}};
  assign _12 = {18{1'b0}};
  assign _13 = {18{1'b0}};
  assign _14 = {18{1'b0}};
  assign _15 = {18{1'b0}};
  assign _16 = {18{1'b0}};

  // Other names for the same wires on the sheet: paus = pause
endmodule

module vivod_matrix (
  input  [7:0] snake_coord,
  input  [7:0] apple_coord,
  input  [7:0] head_coord,
  input  paus,
  input  win,
  input  lose,
  input  takt,
  input  clr,
  input  vivod,
  input  cycle,
  input  apple,
  output [15:0] out_12,
  output [18:0] out_13,
  output [17:0] out_14,
  output [16:0] out_15,
  output [15:0] out_16,
  output [18:0] out_17,
  output [17:0] out_18,
  output [16:0] out_19,
  output [15:0] out_20,
  output [18:0] out_21,
  output [17:0] out_22,
  output [16:0] out_23,
  output [15:0] out_24,
  output [18:0] out_25,
  output [17:0] out_26,
  output [16:0] out_27,
  output [15:0] out_28,
  output [17:0] out_29,
  output [16:0] out_30,
  output [15:0] out_31,
  output [18:0] out_32,
  output [15:0] out_33,
  output [17:0] out_34,
  output [16:0] out_35,
  output [18:0] out_36,
  output [15:0] out_37,
  output [17:0] out_38,
  output [16:0] out_39,
  output [18:0] out_40,
  output [15:0] out_41,
  output [17:0] out_42,
  output [16:0] out_43,
  output [18:0] out_44,
  output [15:0] out_45,
  output [17:0] out_46,
  output [16:0] out_47,
  output [15:0] out_48,
  output [18:0] out_49,
  output [15:0] out_50,
  output [17:0] out_51,
  output [16:0] out_52,
  output [18:0] out_53,
  output [15:0] out_54,
  output [17:0] out_55,
  output [16:0] out_56,
  output [18:0] out_57,
  output [15:0] out_58,
  output [17:0] out_59,
  output [16:0] out_60,
  output [18:0] out_61,
  output [15:0] out_62,
  output [17:0] out_63,
  output [16:0] out_64,
  output [15:0] out_65,
  output [18:0] out_66,
  output [17:0] out_67,
  output [16:0] out_68,
  output [18:0] out_69,
  output [17:0] out_70,
  output [16:0] out_71,
  output [18:0] out_72,
  output [17:0] out_73,
  output [16:0] out_74,
  output [18:0] out_75
);

  wire or_1_out, or_2_out, or_3_out, or_4_out, or_5_out;

  or or_1 (or_1_out, vivod, clr);
  or or_2 (or_2_out, lose, cycle, win);
  or or_3 (or_3_out, or_1_out, or_2_out);
  trans trans_1 (.in16(out_12), .in17(out_15), .out19(out_13), .in18(out_14));
  trans trans_2 (.in16(out_16), .in17(out_19), .out19(out_17), .in18(out_18));
  trans trans_3 (.in16(out_20), .in17(out_23), .out19(out_21), .in18(out_22));
  trans trans_4 (.in16(out_24), .in17(out_27), .out19(out_25), .in18(out_26));
  trans trans_5 (.in16(out_28), .in17(out_30), .out19(out_32), .in18(out_29));
  trans trans_6 (.in16(out_31), .in17(out_35), .out19(out_36), .in18(out_34));
  trans trans_7 (.in16(out_33), .in17(out_39), .out19(out_40), .in18(out_38));
  trans trans_8 (.in16(out_37), .in17(out_43), .out19(out_44), .in18(out_42));
  trans trans_9 (.in16(out_41), .in17(out_47), .out19(out_49), .in18(out_46));
  trans trans_10 (.in16(out_45), .in17(out_52), .out19(out_53), .in18(out_51));
  trans trans_11 (.in16(out_48), .in17(out_56), .out19(out_57), .in18(out_55));
  trans trans_12 (.in16(out_50), .in17(out_60), .out19(out_61), .in18(out_59));
  trans trans_13 (.in16(out_54), .in17(out_64), .out19(out_66), .in18(out_63));
  trans trans_14 (.in16(out_58), .in17(out_68), .out19(out_69), .in18(out_67));
  trans trans_15 (.in16(out_62), .in17(out_71), .out19(out_72), .in18(out_70));
  trans trans_16 (.in16(out_65), .in17(out_74), .out19(out_75), .in18(out_73));
  disp_snake disp_snake_1 (
    .X(snake_coord[7:4]), .clock(takt), .Y(snake_coord[3:0]), .out_6(out_12), .out_7(out_16), .out_8(out_20),
    .out_9(out_24), .out_10(out_28), .out_11(out_31), .out_12(out_33), .out_13(out_37), .out_14(out_41),
    .out_15(out_45), .out_16(out_48), .out_17(out_50), .out_18(out_54), .out_19(out_58), .out_20(out_62),
    .out_22(out_65), .clear(or_3_out), .cycle(or_2_out));  // open: current
  or or_4 (or_4_out, lose, win);
  sec_matrix_disp sec_matrix_disp_1 (
    .X(apple_coord[7:4]), .clock(takt), .Y(apple_coord[3:0]), .out_5(out_15), .out_6(out_19), .out_7(out_23),
    .out_8(out_27), .out_9(out_30), .out_10(out_35), .out_11(out_39), .out_12(out_43), .out_13(out_47),
    .out_14(out_52), .out_15(out_56), .out_16(out_60), .out_17(out_64), .out_18(out_68), .out_19(out_71),
    .out_21(out_74), .clear(or_5_out));  // open: current
  or or_5 (or_5_out, apple, or_4_out, clr);
  win win_1 (
    .lose(lose), .win(win), .pause(paus), ._1(out_14), ._2(out_18), ._3(out_22), ._4(out_26), ._5(out_29),
    ._6(out_34), ._7(out_38), ._8(out_42), ._9(out_46), ._10(out_51), ._11(out_55), ._12(out_59),
    ._13(out_63), ._14(out_67), ._15(out_70), ._16(out_73));

  // Other names for the same wires on the sheet: _1[17:0] = out_14; _1a[16:0] = out_15; _1s[15:0] = out_12;
  //   _2[17:0] = out_18; _2a[16:0] = out_19; _2s[15:0] = out_16; _3[17:0] = out_22; _3a[16:0] = out_23;
  //   _3s[15:0] = out_20; _4[17:0] = out_26; _4a[16:0] = out_27; _4s[15:0] = out_24; _5[17:0] = out_29;
  //   _5a[16:0] = out_30; _5s[15:0] = out_28; _6[17:0] = out_34; _6a[16:0] = out_35; _6s[15:0] = out_31;
  //   _7[17:0] = out_38; _7a[16:0] = out_39; _7s[15:0] = out_33; _8[17:0] = out_42; _8a[16:0] = out_43;
  //   _8s[15:0] = out_37; _9[17:0] = out_46; _9a[16:0] = out_47; _9s[15:0] = out_41; _10[17:0] = out_51;
  //   _10a[16:0] = out_52; _10s[15:0] = out_45; _11[17:0] = out_55; _11a[16:0] = out_56; _11s[15:0] = out_48;
  //   _12[17:0] = out_59; _12a[16:0] = out_60; _12s[15:0] = out_50; _13[17:0] = out_63; _13a[16:0] = out_64;
  //   _13s[15:0] = out_54; _14[17:0] = out_67; _14a[16:0] = out_68; _14s[15:0] = out_58; _15[17:0] = out_70;
  //   _15a[16:0] = out_71; _15s[15:0] = out_62; _16[17:0] = out_73; _16a[16:0] = out_74; _16s[15:0] = out_65
endmodule

module trans (
  input  [15:0] in16,
  input  [16:0] in17,
  input  [17:0] in18,
  output [18:0] out19
);

  assign out19[15:0] = in16 | in17[15:0] | in18[15:0];  // OR_Gate or_1, 16 bits wide

  assign out19[18:16] = 3'b111;
endmodule

module helper_1 (
  input  [15:0] in,
  output [17:0] out
);


  assign out = {2'b00, in};
endmodule

module counter_1 (
  input  clock,
  input  clear,
  output out_3,
  output out_4,
  output out_5,
  output out_6,
  output out_7,
  output out_8,
  output out_9,
  output out_10,
  output out_11,
  output out_12,
  output out_13,
  output out_14,
  output out_15,
  output out_16,
  output out_17,
  output out_18
);

  wire counter_1_carry;
  wire [7:0] counter_1_q, counter_2_q;

  Counter #(.max('ha)) counter_1 (
    .Q(counter_1_q), .carry(counter_1_carry), .clk(clock), .clr(clear));  // open: load, D, count
  Counter #(.max('ha)) counter_2 (.Q(counter_2_q), .clk(counter_1_carry), .clr(clear));  // open: load, D, count, carry
  ROM rom_1 (.addr(counter_1_q), .data({out_7, out_8, out_9, out_10, out_18, out_17, out_16, out_15}));  // open: sel
  ROM rom_2 (.addr(counter_2_q), .data({out_3, out_4, out_5, out_6, out_14, out_13, out_12, out_11}));  // open: sel

  // Other names for the same wires on the sheet: _1_1 = out_15; _1_2 = out_16; _1_3 = out_17; _1_4 = out_18;
  //   _1_5 = out_10; _1_6 = out_9; _1_7 = out_8; _1_8 = out_7; _2_1 = out_11; _2_2 = out_12; _2_3 = out_13;
  //   _2_4 = out_14; _2_5 = out_6; _2_6 = out_5; _2_7 = out_4; _2_8 = out_3

  // Notes on the sheet:
  //   contents of rom_1 (hex, n*v repeats v):
  //   77 14 b3 b6 d4 e6 e7 34 f7 f6 77
  //   contents of rom_2 (hex, n*v repeats v):
  //   77 14 b3 b6 d4 e6 e7 34 f7 f6 77
endmodule

module counter_2 (
  input  clock,
  input  clear,
  output out_3,
  output out_4,
  output out_5,
  output out_6,
  output out_7,
  output out_8,
  output out_9,
  output out_10,
  output out_11,
  output out_12,
  output out_13,
  output out_14,
  output out_15,
  output out_16,
  output out_17,
  output out_18
);

  wire comparator_1_eq;
  wire [7:0] counter_1_q, counter_2_q;

  Counter #(.max('h14)) counter_1 (.Q(counter_1_q), .clk(clock), .clr(clear));  // open: load, D, count, carry
  Counter #(.max('h5)) counter_2 (.Q(counter_2_q), .clk(comparator_1_eq), .clr(clear));  // open: load, D, count, carry
  ROM rom_1 (.addr(counter_1_q), .data({out_7, out_8, out_9, out_10, out_18, out_17, out_16, out_15}));  // open: sel
  ROM rom_2 (.addr(counter_2_q), .data({out_3, out_4, out_5, out_6, out_14, out_13, out_12, out_11}));  // open: sel
  Comparator comparator_1 (
    .a(8'hf6), .b({out_7, out_8, out_9, out_10, out_18, out_17, out_16, out_15}), .eq(comparator_1_eq));  // open: gt, lt

  // Other names for the same wires on the sheet: _1_1 = out_15; _1_2 = out_16; _1_3 = out_17; _1_4 = out_18;
  //   _1_5 = out_10; _1_6 = out_9; _1_7 = out_8; _1_8 = out_7; _2_1 = out_11; _2_2 = out_12; _2_3 = out_13;
  //   _2_4 = out_14; _2_5 = out_6; _2_6 = out_5; _2_7 = out_4; _2_8 = out_3

  // Notes on the sheet:
  //   contents of rom_1 (hex, n*v repeats v):
  //   77 f6 f7 34 e7 e6 d4 b6 b3 14 77 f6 f7 34 e7 e6 d4 b6 b3 14 77
  //   contents of rom_2 (hex, n*v repeats v):
  //   b3 14 77
endmodule
