// Logisim project mne_snova_huy.circ as structural Verilog: 7 circuits, main circuit main
module main (
  input  in_1
);

  wire and_2_out, cdm_8_mark5_1_mem_cycle, clk, decoder_1_out0, decoder_1_out1, decoder_1_out2,
       decoder_1_out3, IOsel, not_1_out, READwrite;
  wire [3:0] cdm_8_mark5_1_ps, IOaddr;
  wire [6:0] ebat_1_out_2, ebat_1_out_3, ebat_1_out_4, ebat_1_out_5, ebat_1_out_6, ebat_2_out_2,
       ebat_2_out_3, ebat_2_out_4, ebat_2_out_5, ebat_2_out_6, ebat_3_out_2, ebat_3_out_3, ebat_3_out_4,
       ebat_3_out_5, ebat_3_out_6, ebat_4_out_2, ebat_4_out_3, ebat_4_out_4, ebat_4_out_5, ebat_4_out_6;
  wire [7:0] cdm_8_mark5_1_data_out, cdm_8_mark5_1_pc, cdm_8_mark5_1_r0, cdm_8_mark5_1_r1, cdm_8_mark5_1_r2,
       cdm_8_mark5_1_r3, cdm_8_mark5_1_sp, controlled_buffer_1_out, counter_1_q, IOdat, multiplexer_1_out,
       register_1_q, register_2_q, SCORE_RAM_IN;
  wire [7:4] cdm_8_mark5_1_addr;
  wire [10:0] bit_extender_1_out, divider_1_out, divider_1_rem, divider_2_out, divider_2_rem, divider_3_out,
       divider_3_rem, divider_4_rem;

  Clock clock_1 (.out(clk));
  // Probe on cdm_8_mark5_1_r3
  // Probe on cdm_8_mark5_1_r2
  // Probe on cdm_8_mark5_1_r1
  // Probe on cdm_8_mark5_1_r0
  // Probe on cdm_8_mark5_1_pc
  and and_1 (IOsel, cdm_8_mark5_1_addr[4], cdm_8_mark5_1_addr[5], cdm_8_mark5_1_addr[6], cdm_8_mark5_1_addr[7], cdm_8_mark5_1_mem_cycle);
  // Probe on cdm_8_mark5_1_ps
  // Probe on cdm_8_mark5_1_sp
  CdM_8_mark5 cdm_8_mark5_1 (
    .clock(clk), .addr({cdm_8_mark5_1_addr, IOaddr}), .mem_read(READwrite),
    .mem_cycle(cdm_8_mark5_1_mem_cycle), .data_out(cdm_8_mark5_1_data_out),
    .data_in(controlled_buffer_1_out), .r0(cdm_8_mark5_1_r0), .r1(cdm_8_mark5_1_r1), .r2(cdm_8_mark5_1_r2),
    .r3(cdm_8_mark5_1_r3), .PC(cdm_8_mark5_1_pc), .SP(cdm_8_mark5_1_sp), .PS(cdm_8_mark5_1_ps));  // open: data_inst
  not not_1 (not_1_out, READwrite);
  assign controlled_buffer_1_out = READwrite ? IOdat : 8'bz;  // Controlled_Buffer controlled_buffer_1
  assign IOdat = not_1_out ? cdm_8_mark5_1_data_out : 8'bz;  // Controlled_Buffer controlled_buffer_2
  and and_2 (and_2_out, cdm_8_mark5_1_mem_cycle, ~IOsel);  // AND_Gate
  Multiplexer #(.width(8), .enable("false")) multiplexer_1 (
    .in0({cdm_8_mark5_1_addr, IOaddr}), .in1(SCORE_RAM_IN), .out(multiplexer_1_out), .sel(in_1));
  // Probe on IOdat
  RAM ram_1 (.addr(multiplexer_1_out), .data(IOdat), .sel(and_2_out), .clk(clk), .ld(READwrite));  // open: clr
  Counter #(.max('h3), .trigger("falling")) counter_1 (.Q(counter_1_q), .clk(clk));  // open: load, D, count, carry, clr
  Adder adder_1 (.a(counter_1_q), .b(8'h20), .out(SCORE_RAM_IN));  // open: cin, cout
  Decoder #(.select(2), .enable("false")) decoder_1 (
    .out0(decoder_1_out0), .out1(decoder_1_out1), .out2(decoder_1_out2), .out3(decoder_1_out3),
    .sel(counter_1_q[1:0]));
  Register register_1 (.D(IOdat), .en(decoder_1_out0), .Q(register_1_q), .clk(clk));  // open: clr
  Register register_2 (.D(IOdat), .en(decoder_1_out1), .Q(register_2_q), .clk(clk));  // open: clr
  Register register_3 (.D(IOdat), .en(decoder_1_out2), .clk(clk));  // open: Q, clr
  Register register_4 (.D(IOdat), .en(decoder_1_out3), .clk(clk));  // open: Q, clr
  assign bit_extender_1_out = {{3{1'b0}}, register_1_q};  // Bit_Extender bit_extender_1
  Divider #(.width(11)) divider_1 (
    .a(bit_extender_1_out), .b(11'ha), .out(divider_1_out), .rem(divider_1_rem));  // open: upper
  Divider #(.width(11)) divider_2 (
    .a(divider_1_out), .b(11'ha), .out(divider_2_out), .rem(divider_2_rem));  // open: upper
  Divider #(.width(11)) divider_3 (
    .a(divider_2_out), .b(11'ha), .out(divider_3_out), .rem(divider_3_rem));  // open: upper
  DotMatrix #(.matrixcols(23)) dotmatrix_1 (
    .col0(ebat_1_out_6), .col1(ebat_1_out_5), .col2(ebat_1_out_4), .col3(ebat_1_out_3), .col4(ebat_1_out_2),
    .col5({7{1'b0}}), .col6(ebat_2_out_6), .col7(ebat_2_out_5), .col8(ebat_2_out_4), .col9(ebat_2_out_3),
    .col10(ebat_2_out_2), .col11({7{1'b0}}), .col12(ebat_3_out_6), .col13(ebat_3_out_5),
    .col14(ebat_3_out_4), .col15(ebat_3_out_3), .col16(ebat_3_out_2), .col17({7{1'b0}}),
    .col18(ebat_4_out_6), .col19(ebat_4_out_5), .col20(ebat_4_out_4), .col21(ebat_4_out_3),
    .col22(ebat_4_out_2));
  ebat ebat_1 (
    .in_1(divider_4_rem), .out_2(ebat_1_out_2), .out_3(ebat_1_out_3), .out_4(ebat_1_out_4),
    .out_5(ebat_1_out_5), .out_6(ebat_1_out_6));
  Divider #(.width(11)) divider_4 (.a(divider_3_out), .b(11'ha), .rem(divider_4_rem));  // open: out, upper
  ebat ebat_2 (
    .in_1(divider_3_rem), .out_2(ebat_2_out_2), .out_3(ebat_2_out_3), .out_4(ebat_2_out_4),
    .out_5(ebat_2_out_5), .out_6(ebat_2_out_6));
  ebat ebat_3 (
    .in_1(divider_2_rem), .out_2(ebat_3_out_2), .out_3(ebat_3_out_3), .out_4(ebat_3_out_4),
    .out_5(ebat_3_out_5), .out_6(ebat_3_out_6));
  ebat ebat_4 (
    .in_1(divider_1_rem), .out_2(ebat_4_out_2), .out_3(ebat_4_out_3), .out_4(ebat_4_out_4),
    .out_5(ebat_4_out_5), .out_6(ebat_4_out_6));

  // Other names for the same wires on the sheet: SCORE_RAM_OUT[7:0] = IOdat
endmodule

module ebat (
  input  [10:0] in_1,
  output [6:0] out_2,
  output [6:0] out_3,
  output [6:0] out_4,
  output [6:0] out_5,
  output [6:0] out_6
);

  _1 u_1_1 (
    .D(in_1[3]), .C(in_1[2]), .B(in_1[1]), .A(in_1[0]), .g(out_2[6]), .f(out_2[5]), .e(out_2[4]),
    .d_2(out_2[3]), .c_2(out_2[2]), .b_2(out_2[1]), .a_2(out_2[0]));
  _2 u_2_1 (
    .D(in_1[3]), .C(in_1[2]), .B(in_1[1]), .A(in_1[0]), .g(out_3[6]), .f(out_3[5]), .e(out_3[4]),
    .d_2(out_3[3]), .c_2(out_3[2]), .b_2(out_3[1]), .a_2(out_3[0]));
  _3 u_3_1 (
    .D(in_1[3]), .C(in_1[2]), .B(in_1[1]), .A(in_1[0]), .g(out_4[6]), .f(out_4[5]), .e(out_4[4]),
    .d_2(out_4[3]), .c_2(out_4[2]), .b_2(out_4[1]), .a_2(out_4[0]));
  _4 u_4_1 (
    .D(in_1[3]), .C(in_1[2]), .B(in_1[1]), .A(in_1[0]), .g(out_5[6]), .f(out_5[5]), .e(out_5[4]),
    .d_2(out_5[3]), .c_2(out_5[2]), .b_2(out_5[1]), .a_2(out_5[0]));
  _5 u_5_1 (
    .D(in_1[3]), .C(in_1[2]), .B(in_1[1]), .A(in_1[0]), .g(out_6[6]), .f(out_6[5]), .e(out_6[4]),
    .d_2(out_6[3]), .c_2(out_6[2]), .b_2(out_6[1]), .a_2(out_6[0]));
endmodule

module _1 (
  input  D,
  input  C,
  input  B,
  input  A,
  output g,
  output f,
  output e,
  output d_2,
  output c_2,
  output b_2,
  output a_2
);

  wire and_2_out, and_3_out, and_4_out, and_5_out, and_6_out, and_7_out, and_8_out, and_9_out, and_10_out,
       and_11_out, and_12_out, and_13_out, and_14_out, and_16_out, and_17_out, and_18_out, not_1_out,
       not_2_out, not_3_out, not_4_out, not_5_out, not_6_out, not_7_out, not_8_out, not_9_out, not_10_out,
       not_11_out, not_12_out, not_13_out, not_14_out, not_15_out, not_16_out, not_17_out, not_18_out,
       not_19_out, not_20_out, not_21_out, not_22_out, not_23_out, not_24_out;

  and and_1 (g, C, A);
  not not_1 (not_1_out, C);
  and and_2 (and_2_out, not_1_out, not_2_out);
  not not_2 (not_2_out, A);
  and and_3 (and_3_out, B, A);
  not not_3 (not_3_out, C);
  and and_4 (and_4_out, not_3_out, not_4_out);
  not not_4 (not_4_out, A);
  not not_5 (not_5_out, C);
  and and_5 (and_5_out, not_5_out, B);
  not not_6 (not_6_out, D);
  not not_7 (not_7_out, C);
  not not_8 (not_8_out, B);
  not not_9 (not_9_out, A);
  not not_10 (not_10_out, B);
  not not_11 (not_11_out, D);
  and and_6 (and_6_out, not_11_out, not_12_out, not_13_out);
  not not_12 (not_12_out, B);
  not not_13 (not_13_out, A);
  not not_14 (not_14_out, C);
  and and_7 (and_7_out, not_14_out, B, A);
  and and_8 (and_8_out, C, not_15_out);
  not not_15 (not_15_out, B);
  and and_9 (and_9_out, C, not_16_out);
  not not_16 (not_16_out, A);
  and and_10 (and_10_out, D, A);
  not not_17 (not_17_out, C);
  not not_18 (not_18_out, B);
  and and_11 (and_11_out, not_17_out, not_18_out, not_19_out);
  not not_19 (not_19_out, A);
  not not_20 (not_20_out, C);
  and and_12 (and_12_out, not_20_out, B, A);
  not not_21 (not_21_out, B);
  and and_13 (and_13_out, C, not_21_out, A);
  and and_14 (and_14_out, C, B, not_22_out);
  not not_22 (not_22_out, A);
  not not_23 (not_23_out, C);
  and and_15 (a_2, not_23_out, B, not_24_out);
  not not_24 (not_24_out, A);
  or or_1 (f, and_2_out, and_3_out, D);
  or or_2 (e, and_4_out, and_5_out, D);
  and and_16 (and_16_out, not_6_out, not_7_out, not_8_out, not_9_out);
  and and_17 (and_17_out, C, not_10_out, A);
  or or_3 (d_2, and_16_out, and_17_out, and_18_out);
  and and_18 (and_18_out, D, A);
  or or_4 (c_2, and_6_out, and_7_out, and_8_out, and_9_out, and_10_out);
  or or_5 (b_2, and_11_out, and_12_out, and_13_out, and_14_out);
endmodule

module _2 (
  input  D,
  input  C,
  input  B,
  input  A,
  output g,
  output f,
  output e,
  output d_2,
  output c_2,
  output b_2,
  output a_2
);

  wire and_2_out, and_3_out, and_4_out, and_5_out, and_7_out, and_8_out, and_9_out, and_10_out, and_11_out,
       and_12_out, and_13_out, not_1_out, not_2_out, not_3_out, not_4_out, not_5_out, not_6_out, not_7_out,
       not_8_out, not_9_out, not_10_out, not_11_out, not_12_out, not_13_out, not_14_out, not_15_out,
       not_16_out, not_17_out, not_18_out;

  not not_1 (not_1_out, A);
  not not_2 (not_2_out, B);
  and and_1 (f, C, not_2_out, not_3_out);
  not not_3 (not_3_out, A);
  not not_4 (not_4_out, D);
  not not_5 (not_5_out, B);
  and and_2 (and_2_out, not_4_out, not_5_out, not_6_out);
  not not_6 (not_6_out, A);
  and and_3 (and_3_out, C, A);
  not not_7 (not_7_out, C);
  and and_4 (and_4_out, not_7_out, B);
  and and_5 (and_5_out, C, not_8_out);
  not not_8 (not_8_out, A);
  and and_6 (c_2, C, not_9_out, not_10_out);
  not not_9 (not_9_out, B);
  not not_10 (not_10_out, A);
  not not_11 (not_11_out, B);
  and and_7 (and_7_out, C, not_11_out, not_12_out);
  not not_12 (not_12_out, A);
  and and_8 (and_8_out, D, A);
  not not_13 (not_13_out, D);
  not not_14 (not_14_out, C);
  and and_9 (and_9_out, not_13_out, not_14_out, A);
  not not_15 (not_15_out, C);
  and and_10 (and_10_out, not_15_out, B);
  and and_11 (and_11_out, C, not_16_out);
  not not_16 (not_16_out, B);
  and and_12 (and_12_out, C, not_17_out);
  not not_17 (not_17_out, A);
  and and_13 (and_13_out, D, not_18_out);
  not not_18 (not_18_out, A);
  or or_1 (g, not_1_out, B, C, D);
  or or_2 (e, and_2_out, and_3_out);
  or or_3 (d_2, and_4_out, and_5_out, D);
  or or_4 (b_2, and_7_out, and_8_out);
  or or_5 (a_2, and_9_out, and_10_out, and_11_out, and_12_out, and_13_out);
endmodule

module _3 (
  input  D,
  input  C,
  input  B,
  input  A,
  output g,
  output f,
  output e,
  output d_2,
  output c_2,
  output b_2,
  output a_2
);

  wire and_2_out, and_3_out, and_4_out, and_5_out, and_6_out, and_7_out, not_1_out, not_2_out, not_3_out,
       not_4_out, not_5_out, not_6_out, not_7_out, not_8_out, not_9_out, not_10_out, not_11_out, not_12_out,
       not_13_out, not_14_out, not_15_out, not_16_out, not_17_out, not_18_out, not_19_out, not_20_out;

  not not_1 (not_1_out, C);
  or or_1 (g, not_1_out, A, B);
  not not_2 (not_2_out, D);
  not not_3 (not_3_out, C);
  not not_4 (not_4_out, B);
  not not_5 (not_5_out, B);
  not not_6 (not_6_out, A);
  not not_7 (not_7_out, D);
  not not_8 (not_8_out, B);
  and and_1 (e, not_7_out, not_8_out, A);
  not not_9 (not_9_out, C);
  or or_2 (d_2, not_9_out, B);
  not not_10 (not_10_out, D);
  not not_11 (not_11_out, C);
  not not_12 (not_12_out, B);
  not not_13 (not_13_out, B);
  not not_14 (not_14_out, A);
  not not_15 (not_15_out, D);
  not not_16 (not_16_out, C);
  not not_17 (not_17_out, B);
  not not_18 (not_18_out, C);
  not not_19 (not_19_out, B);
  and and_2 (and_2_out, not_19_out, A);
  and and_3 (and_3_out, B, not_20_out);
  not not_20 (not_20_out, A);
  and and_4 (and_4_out, not_2_out, not_3_out, not_4_out, A);
  or or_3 (f, and_4_out, and_5_out);
  and and_5 (and_5_out, C, not_5_out, not_6_out);
  and and_6 (and_6_out, not_10_out, not_11_out, not_12_out, A);
  or or_4 (c_2, and_6_out, and_7_out);
  and and_7 (and_7_out, C, not_13_out, not_14_out);
  and and_8 (b_2, not_15_out, not_16_out, not_17_out, A);
  or or_5 (a_2, not_18_out, and_2_out, and_3_out);
endmodule

module _4 (
  input  D,
  input  C,
  input  B,
  input  A,
  output g,
  output f,
  output e,
  output d_2,
  output c_2,
  output b_2,
  output a_2
);

  wire and_1_out, and_2_out, and_3_out, and_5_out, and_6_out, and_7_out, and_8_out, and_9_out, and_11_out,
       and_12_out, not_1_out, not_2_out, not_3_out, not_4_out, not_5_out, not_6_out, not_7_out, not_8_out,
       not_9_out, not_10_out, not_11_out, not_12_out, not_13_out, not_14_out, not_15_out, not_16_out,
       not_17_out;

  not not_1 (not_1_out, C);
  and and_1 (and_1_out, not_1_out, not_2_out);
  not not_2 (not_2_out, A);
  not not_3 (not_3_out, C);
  and and_2 (and_2_out, not_3_out, B);
  and and_3 (and_3_out, C, A);
  not not_4 (not_4_out, D);
  not not_5 (not_5_out, C);
  not not_6 (not_6_out, B);
  not not_7 (not_7_out, A);
  and and_4 (e, C, not_8_out);
  not not_8 (not_8_out, B);
  not not_9 (not_9_out, C);
  and and_5 (and_5_out, not_9_out, B, A);
  and and_6 (and_6_out, C, B, not_10_out);
  not not_10 (not_10_out, A);
  not not_11 (not_11_out, D);
  and and_7 (and_7_out, not_11_out, not_12_out, not_13_out);
  not not_12 (not_12_out, C);
  not not_13 (not_13_out, A);
  not not_14 (not_14_out, D);
  not not_15 (not_15_out, B);
  and and_8 (and_8_out, not_14_out, not_15_out, not_16_out);
  not not_16 (not_16_out, A);
  and and_9 (and_9_out, C, B, A);
  and and_10 (b_2, C, B, A);
  not not_17 (not_17_out, C);
  or or_1 (a_2, not_17_out, A, B);
  or or_2 (g, and_1_out, and_2_out, and_3_out, D);
  and and_11 (and_11_out, not_4_out, not_5_out, not_6_out, A);
  or or_3 (f, and_11_out, and_12_out);
  and and_12 (and_12_out, C, B, not_7_out);
  or or_4 (d_2, and_5_out, and_6_out, D);
  or or_5 (c_2, and_7_out, and_8_out, and_9_out);
endmodule

module _5 (
  input  D,
  input  C,
  input  B,
  input  A,
  output g,
  output f,
  output e,
  output d_2,
  output c_2,
  output b_2,
  output a_2
);

  wire and_2_out, and_3_out, and_4_out, and_5_out, and_6_out, and_7_out, and_8_out, and_9_out, and_10_out,
       and_11_out, and_12_out, and_13_out, and_14_out, and_15_out, not_1_out, not_2_out, not_3_out,
       not_4_out, not_5_out, not_6_out, not_7_out, not_8_out, not_9_out, not_10_out, not_11_out, not_12_out,
       not_13_out, not_14_out, not_15_out, not_16_out, not_17_out, not_18_out, not_19_out, not_20_out,
       not_21_out, not_22_out, not_23_out;

  and and_1 (g, C, A);
  not not_1 (not_1_out, C);
  and and_2 (and_2_out, not_1_out, not_2_out);
  not not_2 (not_2_out, A);
  not not_3 (not_3_out, C);
  and and_3 (and_3_out, not_3_out, B);
  and and_4 (and_4_out, C, not_4_out, A);
  not not_4 (not_4_out, B);
  not not_5 (not_5_out, C);
  and and_5 (and_5_out, not_5_out, not_6_out, not_7_out);
  not not_6 (not_6_out, B);
  not not_7 (not_7_out, A);
  and and_6 (and_6_out, C, not_8_out, A);
  not not_8 (not_8_out, B);
  and and_7 (and_7_out, C, B, not_9_out);
  not not_9 (not_9_out, A);
  not not_10 (not_10_out, D);
  not not_11 (not_11_out, B);
  and and_8 (and_8_out, not_10_out, not_11_out, not_12_out);
  not not_12 (not_12_out, A);
  and and_9 (and_9_out, C, not_13_out);
  not not_13 (not_13_out, A);
  not not_14 (not_14_out, B);
  and and_10 (and_10_out, not_14_out, not_15_out);
  not not_15 (not_15_out, A);
  and and_11 (and_11_out, C, not_16_out);
  not not_16 (not_16_out, A);
  not not_17 (not_17_out, C);
  and and_12 (and_12_out, not_17_out, not_18_out);
  not not_18 (not_18_out, A);
  not not_19 (not_19_out, C);
  and and_13 (and_13_out, not_19_out, B);
  and and_14 (and_14_out, B, not_20_out);
  not not_20 (not_20_out, A);
  and and_15 (and_15_out, C, not_21_out, A);
  not not_21 (not_21_out, B);
  not not_22 (not_22_out, C);
  and and_16 (a_2, not_22_out, B, not_23_out);
  not not_23 (not_23_out, A);
  or or_1 (f, and_2_out, and_3_out, and_4_out, D);
  or or_2 (e, and_5_out, and_6_out, and_7_out, D);
  or or_3 (d_2, and_8_out, and_9_out);
  or or_4 (c_2, and_10_out, and_11_out);
  or or_5 (b_2, and_12_out, and_13_out, and_14_out, and_15_out);
endmodule
