// Logisim project version_register.circ as structural Verilog
// 1
module main (
  input  in_1,
  input  in_2,
  input  in_3
);

  wire _1_1, _1_2, _1_3, _1_4, _1_5, _1_6, _1_7, _1_8, _2_1, _2_2, _2_3, _2_4, _2_5, _2_6, _2_7, _2_8,
       and_1_out, clock, clr, counter_1_carry, d_ff_1_qn, disp_snake_1_current, down,
       granca_detection_1_out_6, hz, left, or_1_out, or_2_out, right, up;
  wire [1:0] \Static_направление ;
  wire [3:0] inc_dec_1_r, inc_dec_2_r;
  wire [6:0] \input ;
  wire [7:0] counter_1_q, counter_2_q, head;
  wire [15:0] disp_snake_1_out_7, disp_snake_1_out_8, disp_snake_1_out_9, disp_snake_1_out_10,
       disp_snake_1_out_11, disp_snake_1_out_12, disp_snake_1_out_13, disp_snake_1_out_14,
       disp_snake_1_out_15, disp_snake_1_out_16, disp_snake_1_out_17, disp_snake_1_out_18,
       disp_snake_1_out_19, disp_snake_1_out_20, disp_snake_1_out_21, disp_snake_1_out_23;

  Clock clock_1 (.out(clock));
  granca_detection granca_detection_1 (
    .in_3(head), .Left(left), .Right(right), .out_6(granca_detection_1_out_6), .Up(up), .Down(down));
  and and_1 (and_1_out, clock, d_ff_1_qn);
  D_Flip_Flop d_ff_1 (.Qn(d_ff_1_qn), .preset(granca_detection_1_out_6), .reset(clr));  // open: clk, D, Q, en
  Register register_1 (.D({inc_dec_1_r, inc_dec_2_r}), .Q(head), .clk(and_1_out), .clr(clr));  // open: en
  or or_1 (or_1_out, left, right);
  // NOT_Gate not_1 is placed but not wired
  inc_dec inc_dec_1 (.X(head[7:4]), .on_off(or_1_out), .inc_dec(right), .R(inc_dec_1_r));  // open: OFL
  inc_dec inc_dec_2 (.X(head[3:0]), .on_off(or_2_out), .inc_dec(up), .R(inc_dec_2_r));  // open: OFL
  Register #(.width(4)) register_2 (.D(head[7:4]), .clk(clock), .clr(clr));  // open: en, Q
  or or_2 (or_2_out, up, down);
  Register #(.width(4)) register_3 (.D(head[3:0]), .clk(clock), .clr(clr));  // open: en, Q
  _7_Segment_Display u_7_segment_display_1 (
    .g(_2_8), .f(_2_7), .a(_2_6), .b(_2_5), .e(_2_1), .d(_2_2), .c(_2_3), .dp(_2_4));
  disp_snake disp_snake_1 (
    .hodn(clock), .X(head[7:4]), .clock(clock), .Y(head[3:0]), .rndr(clock), .out_7(disp_snake_1_out_7),
    .out_8(disp_snake_1_out_8), .out_9(disp_snake_1_out_9), .out_10(disp_snake_1_out_10),
    .out_11(disp_snake_1_out_11), .out_12(disp_snake_1_out_12), .out_13(disp_snake_1_out_13),
    .out_14(disp_snake_1_out_14), .out_15(disp_snake_1_out_15), .out_16(disp_snake_1_out_16),
    .out_17(disp_snake_1_out_17), .out_18(disp_snake_1_out_18), .out_19(disp_snake_1_out_19),
    .out_20(disp_snake_1_out_20), .out_21(disp_snake_1_out_21), .current(disp_snake_1_current),
    .out_23(disp_snake_1_out_23), .clear(clr));
  DotMatrix #(.inputtype("row"), .matrixcols(16), .matrixrows(16)) dotmatrix_1 (
    .row0(disp_snake_1_out_7), .row1(disp_snake_1_out_8), .row2(disp_snake_1_out_9),
    .row3(disp_snake_1_out_10), .row4(disp_snake_1_out_11), .row5(disp_snake_1_out_12),
    .row6(disp_snake_1_out_13), .row7(disp_snake_1_out_14), .row8(disp_snake_1_out_15),
    .row9(disp_snake_1_out_16), .row10(disp_snake_1_out_17), .row11(disp_snake_1_out_18),
    .row12(disp_snake_1_out_19), .row13(disp_snake_1_out_20), .row14(disp_snake_1_out_21),
    .row15(disp_snake_1_out_23));
  Keyboard keyboard_1 (.clk(clock), .clr(clr), .data(\input ));  // open: re, avail
  _7_Segment_Display u_7_segment_display_2 (
    .g(_1_8), .f(_1_7), .a(_1_6), .b(_1_5), .e(_1_1), .d(_1_2), .c(_1_3), .dp(_1_4));
  Button button_1 (.out(clr));
  Counter #(.max('ha)) counter_1 (
    .Q(counter_1_q), .carry(counter_1_carry), .clk(hz), .clr(clr));  // open: load, D, count
  Counter #(.max('ha)) counter_2 (.Q(counter_2_q), .clk(counter_1_carry), .clr(clr));  // open: load, D, count, carry
  movement movement_1 (
    .Clock(clock), .Clear(clr), .out_5(up), .out_6(down), .out_7(left), .out_8(right), .\input (\input ),
    .StaticOutist(\Static_направление ));
  ROM rom_1 (.addr(counter_1_q), .data({_1_8, _1_7, _1_6, _1_5, _1_4, _1_3, _1_2, _1_1}));  // open: sel
  ROM rom_2 (.addr(counter_2_q), .data({_2_8, _2_7, _2_6, _2_5, _2_4, _2_3, _2_2, _2_1}));  // open: sel

  // Other names for the same wires on the sheet: acceleration = in_3; paus = in_1; stop_golod = in_2

  // Notes on the sheet:
  //   coor X
  //   coor Y
  //   1 - пауза 0 играем
  //   1 - есть 0 - нет голода
  //   1 - есть ускорение 0 - нет
  //   contents of rom_1 (hex, n*v repeats v):
  //   77 14 b3 b6 d4 e6 e7 34 f7 f6 77
  //   contents of rom_2 (hex, n*v repeats v):
  //   77 14 b3 b6 d4 e6 e7 34 f7 f6 77
endmodule

module _16_bit_AND (
  input  [15:0] \input ,
  input  switch,
  output [15:0] \output 
);

  assign \output  = \input  & {16{switch}};  // AND_Gate and_1, 16 bits wide
endmodule

module column_switch (
  input  [9:0] in_1,
  input  in_2,
  output [9:0] out_3
);

  wire comparator_1_eq;
  wire [9:0] multiplexer_1_out;

  Multiplexer #(.width(10)) multiplexer_1 (
    .in0(in_1), .in1({1'b0, in_1[9:1]}), .out(multiplexer_1_out), .sel(in_2));  // open: en
  Comparator #(.width(10)) comparator_1 (.a(in_1), .b({10{1'b0}}), .eq(comparator_1_eq));  // open: gt, lt
  Multiplexer #(.width(10)) multiplexer_2 (
    .in0(multiplexer_1_out), .in1(10'h10), .out(out_3), .sel(comparator_1_eq));  // open: en
endmodule

module inc_dec (
  input  [3:0] X,
  input  on_off,
  input  inc_dec,
  output [3:0] R,
  output OFL
);

  wire and_2_out, and_3_out;
  wire [3:0] and_1_out, xor_1_out, xor_2_out, xor_3_out;
  wire [3:3] decoder_1_out0, decoder_1_out1;

  Decoder #(.enable("false")) decoder_1 (.out0(decoder_1_out0[3]), .out1(decoder_1_out1[3]), .sel(inc_dec));
  assign xor_1_out = {4{decoder_1_out0[3]}} ^ X;  // XOR_Gate xor_1, 4 bits wide
  assign xor_2_out = {4{decoder_1_out1[3]}} ^ xor_3_out;  // XOR_Gate xor_2, 4 bits wide
  assign and_1_out = xor_1_out & xor_2_out;  // AND_Gate and_1, 4 bits wide
  and and_2 (and_2_out, and_1_out[3], inc_dec);
  and and_3 (and_3_out, and_1_out[3], ~inc_dec);  // AND_Gate
  assign xor_3_out = X ^ {and_1_out[2:0], 1'b1};  // XOR_Gate xor_3, 4 bits wide
  or or_1 (OFL, and_2_out, and_3_out);
  Multiplexer #(.width(4), .enable("false")) multiplexer_1 (.in0(X), .in1(xor_3_out), .out(R), .sel(on_off));
endmodule

module granca_detection (
  input  Up,
  input  Down,
  input  [7:0] in_3,
  input  Left,
  input  Right,
  output out_6
);

  wire and_1_out, and_2_out, nor_1_out, nor_2_out;

  Pull_Resistor pull_resistor_1 (.node(Up));
  Pull_Resistor pull_resistor_2 (.node(Down));
  Pull_Resistor pull_resistor_3 (.node(Left));
  Pull_Resistor pull_resistor_4 (.node(Right));
  and and_1 (and_1_out, Up, in_3[3], in_3[2], in_3[1], in_3[0]);
  and and_2 (and_2_out, in_3[7], in_3[6], in_3[5], in_3[4], Right);
  nor nor_1 (nor_1_out, ~Down, in_3[0], in_3[1], in_3[2], in_3[3]);  // NOR_Gate
  nor nor_2 (nor_2_out, in_3[4], in_3[5], in_3[6], in_3[7], ~Left);  // NOR_Gate
  or or_1 (out_6, and_1_out, nor_1_out, nor_2_out, and_2_out);
endmodule

// управление
module movement (
  input  [6:0] \input ,
  input  Clock,
  input  Clear,
  output [1:0] StaticOutist,
  output out_5,
  output out_6,
  output out_7,
  output out_8
);

  wire and_1_out, comparator_1_eq, comparator_2_eq, comparator_3_eq, comparator_4_eq, counter_1_carry,
       or_3_out, xnor_1_out, xor_1_out;
  wire [1:0] multiplexer_1_out, or_1_out, register_1_q;

  Comparator #(.width(7)) comparator_1 (.a(\input ), .b(7'b1100100), .eq(comparator_1_eq));  // open: gt, lt
  Comparator #(.width(7)) comparator_2 (.a(\input ), .b(7'b1110011), .eq(comparator_2_eq));  // open: gt, lt
  Comparator #(.width(7)) comparator_3 (.a(\input ), .b(7'b1100001), .eq(comparator_3_eq));  // open: gt, lt
  Comparator #(.width(7)) comparator_4 (.a(\input ), .b(7'b1110111), .eq(comparator_4_eq));  // open: gt, lt
  or or_1 (or_1_out[0], comparator_2_eq, comparator_1_eq);
  or or_2 (or_1_out[1], comparator_1_eq, comparator_3_eq);
  or or_3 (or_3_out, comparator_1_eq, comparator_2_eq, comparator_3_eq, comparator_4_eq);
  Register #(.width(2)) register_1 (.D(or_1_out), .Q(register_1_q), .clk(or_3_out), .clr(Clear));  // open: en
  Register #(.width(2)) register_2 (.D(multiplexer_1_out), .Q(StaticOutist), .clk(or_3_out), .clr(Clear));  // open: en
  xor xor_1 (xor_1_out, StaticOutist[0], register_1_q[0]);
  xnor xnor_1 (xnor_1_out, StaticOutist[1], register_1_q[1]);
  and and_1 (and_1_out, xnor_1_out, xor_1_out);
  Multiplexer #(.width(2)) multiplexer_1 (
    .in0(register_1_q), .in1(StaticOutist), .out(multiplexer_1_out), .sel(and_1_out));  // open: en
  Counter #(.width(3), .max('h5)) counter_1 (
    .carry(counter_1_carry), .clk(Clock), .clr(Clear));  // open: load, D, count, Q
  Demultiplexer #(.select(2)) demultiplexer_1 (
    .out0(out_5), .out1(out_6), .out2(out_7), .out3(out_8), .in(counter_1_carry), .sel(multiplexer_1_out));  // open: en

  // Other names for the same wires on the sheet: clr = Clear

  // Notes on the sheet:
  //   новое напр.
  //   текушее напр.
endmodule

module pseudo_reg (
  input  [3:0] in_1,
  input  [3:0] in_2,
  output [15:0] out_3,
  output [15:0] out_4,
  output [15:0] out_5,
  output [15:0] out_6,
  output [15:0] out_7,
  output [15:0] out_8,
  output [15:0] out_9,
  output [15:0] out_10,
  output [15:0] out_11,
  output [15:0] out_12,
  output [15:0] out_13,
  output [15:0] out_14,
  output [15:0] out_15,
  output [15:0] out_16,
  output [15:0] out_17,
  output [15:0] out_18
);

  wire decoder_2_out0, decoder_2_out1, decoder_2_out2, decoder_2_out3, decoder_2_out4, decoder_2_out5,
       decoder_2_out6, decoder_2_out7, decoder_2_out8, decoder_2_out9, decoder_2_out10, decoder_2_out11,
       decoder_2_out12, decoder_2_out13, decoder_2_out14, decoder_2_out15;
  wire [15:0] decoder_1_out0;

  Decoder #(.select(4), .disabled(0), .enable("false")) decoder_1 (
    .out0(decoder_1_out0[0]), .out1(decoder_1_out0[1]), .out2(decoder_1_out0[2]), .out3(decoder_1_out0[3]),
    .out4(decoder_1_out0[4]), .out5(decoder_1_out0[5]), .out6(decoder_1_out0[6]), .out7(decoder_1_out0[7]),
    .out8(decoder_1_out0[8]), .out9(decoder_1_out0[9]), .out10(decoder_1_out0[10]),
    .out11(decoder_1_out0[11]), .out12(decoder_1_out0[12]), .out13(decoder_1_out0[13]),
    .out14(decoder_1_out0[14]), .out15(decoder_1_out0[15]), .sel(in_1));
  _16_bit_AND u_16_bit_and_1 (.\input (decoder_1_out0), .switch(decoder_2_out0), .\output (out_11));
  _16_bit_AND u_16_bit_and_2 (.\input (decoder_1_out0), .switch(decoder_2_out1), .\output (out_3));
  _16_bit_AND u_16_bit_and_3 (.\input (decoder_1_out0), .switch(decoder_2_out2), .\output (out_12));
  _16_bit_AND u_16_bit_and_4 (.\input (decoder_1_out0), .switch(decoder_2_out3), .\output (out_4));
  Decoder #(.select(4), .disabled(0), .enable("false")) decoder_2 (
    .out0(decoder_2_out0), .out1(decoder_2_out1), .out2(decoder_2_out2), .out3(decoder_2_out3),
    .out4(decoder_2_out4), .out5(decoder_2_out5), .out6(decoder_2_out6), .out7(decoder_2_out7),
    .out8(decoder_2_out8), .out9(decoder_2_out9), .out10(decoder_2_out10), .out11(decoder_2_out11),
    .out12(decoder_2_out12), .out13(decoder_2_out13), .out14(decoder_2_out14), .out15(decoder_2_out15),
    .sel(in_2));
  _16_bit_AND u_16_bit_and_5 (.\input (decoder_1_out0), .switch(decoder_2_out4), .\output (out_13));
  _16_bit_AND u_16_bit_and_6 (.\input (decoder_1_out0), .switch(decoder_2_out5), .\output (out_5));
  _16_bit_AND u_16_bit_and_7 (.\input (decoder_1_out0), .switch(decoder_2_out6), .\output (out_14));
  _16_bit_AND u_16_bit_and_8 (.\input (decoder_1_out0), .switch(decoder_2_out7), .\output (out_6));
  _16_bit_AND u_16_bit_and_9 (.\input (decoder_1_out0), .switch(decoder_2_out9), .\output (out_7));
  _16_bit_AND u_16_bit_and_10 (.\input (decoder_1_out0), .switch(decoder_2_out8), .\output (out_15));
  _16_bit_AND u_16_bit_and_11 (.\input (decoder_1_out0), .switch(decoder_2_out10), .\output (out_16));
  _16_bit_AND u_16_bit_and_12 (.\input (decoder_1_out0), .switch(decoder_2_out11), .\output (out_8));
  _16_bit_AND u_16_bit_and_13 (.\input (decoder_1_out0), .switch(decoder_2_out12), .\output (out_17));
  _16_bit_AND u_16_bit_and_14 (.\input (decoder_1_out0), .switch(decoder_2_out13), .\output (out_9));
  _16_bit_AND u_16_bit_and_15 (.\input (decoder_1_out0), .switch(decoder_2_out15), .\output (out_10));
  _16_bit_AND u_16_bit_and_16 (.\input (decoder_1_out0), .switch(decoder_2_out14), .\output (out_18));
endmodule

module CP (
);

  wire cdm_8_mark5_1_p2, cdm_8_mark5_1_p3, cdm_8_mark5_1_p5, cdm_8_mark5_1_p6, cdm_8_mark5_1_p7,
       cdm_8_mark5_1_p8, clk, code, data, IRQ, mem, not_1_out, rd_wr, undriven;
  wire [7:0] cdm_8_mark5_1_p11, cdm_8_mark5_1_p12, cdm_8_mark5_1_p13, cdm_8_mark5_1_p14, IOdat;

  // Probe on undriven
  // Probe on undriven
  // Probe on cdm_8_mark5_1_p3
  // Probe on cdm_8_mark5_1_p2
  // Probe on cdm_8_mark5_1_p6
  // Probe on cdm_8_mark5_1_p5
  // Probe on cdm_8_mark5_1_p7
  // CdM_8_mark5 cdm_8_mark5_1: pin names not known; wires that end beside it: IRQ, cdm_8_mark5_1_p2, cdm_8_mark5_1_p3, clk, cdm_8_mark5_1_p5, cdm_8_mark5_1_p6, cdm_8_mark5_1_p7, cdm_8_mark5_1_p8, mem, rd_wr, cdm_8_mark5_1_p11, cdm_8_mark5_1_p12, cdm_8_mark5_1_p13, cdm_8_mark5_1_p14
  Clock clock_1 (.out(clk));
  Decoder decoder_1 (.out0(code), .out1(data), .sel(cdm_8_mark5_1_p8), .en(mem));
  assign IOdat = not_1_out ? cdm_8_mark5_1_p12 : 8'bz;  // Controlled_Buffer controlled_buffer_1
  not not_1 (not_1_out, rd_wr);
  assign cdm_8_mark5_1_p13 = rd_wr ? IOdat : 8'bz;  // Controlled_Buffer controlled_buffer_2
  assign cdm_8_mark5_1_p14 = data ? IOdat : 8'bz;  // Controlled_Buffer controlled_buffer_3
  // Probe on cdm_8_mark5_1_p14
  Pull_Resistor pull_resistor_1 (.node(data));
  ROM rom_1 (.addr(cdm_8_mark5_1_p11), .data(IOdat), .sel(code));
  RAM ram_1 (.addr(cdm_8_mark5_1_p11), .data(IOdat), .sel(data), .clk(clk), .ld(rd_wr));  // open: clr

  // Notes on the sheet:
  //   contents of rom_1 (hex, n*v repeats v):
  //   d0 8 f0 8c d1 9 a4 d4 3
endmodule

module golod (
  input  stop_golod,
  input  clock,
  input  hz,
  input  clr,
  output golod
);

  wire comparator_1_eq, comparator_1_gt, comparator_2_gt, or_1_out, or_2_out;
  wire [9:0] counter_1_q, counter_2_q;

  Counter #(.width(10), .max('h3ff)) counter_1 (
    .Q(counter_1_q), .clk(clock), .clr(or_1_out));  // open: load, D, count, carry
  or or_1 (or_1_out, clr, hz);
  or or_2 (or_2_out, comparator_1_gt, comparator_1_eq);
  Comparator #(.width(10), .mode("unsigned")) comparator_1 (
    .a(counter_1_q), .b(10'hf1), .gt(comparator_1_gt), .eq(comparator_1_eq));  // open: lt
  Counter #(.width(10), .max('h3ff)) counter_2 (
    .Q(counter_2_q), .clk(or_2_out), .clr(clr));  // open: load, D, count, carry
  and and_1 (golod, stop_golod, comparator_2_gt);
  Comparator #(.width(10), .mode("unsigned")) comparator_2 (
    .a(counter_2_q), .b({10{1'b0}}), .gt(comparator_2_gt));  // open: eq, lt

  // Notes on the sheet:
  //   тут 0f1 это константа после такого количества clockов в голод пойдет 1 которая остановит такты
endmodule

module Acceleratiaon (
  input  takt,
  input  clr,
  input  acceleration,
  output clockout
);

  wire and_1_out, and_2_out, comparator_1_eq, comparator_2_gt, comparator_3_eq, comparator_3_lt, or_1_out,
       or_2_out, or_3_out;
  wire [9:0] counter_1_q, counter_2_q, port;
  wire [9:1] hz2;
  wire [9:9] counter_3_q;

  // Probe on port
  Subtractor #(.width(10)) subtractor_1 (.a(10'h14), .b({hz2, 1'b0}), .out(port));  // open: bin, bout
  Counter #(.width(10), .max('h3ff)) counter_1 (
    .Q(counter_1_q), .clk(takt), .clr(or_1_out));  // open: load, D, count, carry
  or or_1 (or_1_out, clr, comparator_1_eq);
  Comparator #(.width(10), .mode("unsigned")) comparator_1 (
    .a(counter_1_q), .b(10'h120), .eq(comparator_1_eq));  // open: gt, lt
  Counter #(.width(10), .max('h3ff)) counter_2 (
    .Q(counter_2_q), .clk(takt), .clr(or_2_out));  // open: load, D, count, carry
  or or_2 (or_2_out, clr, clockout);
  Comparator #(.width(10), .mode("unsigned")) comparator_2 (.a(port), .b(10'h4), .gt(comparator_2_gt));  // open: eq, lt
  Comparator #(.width(10), .mode("unsigned")) comparator_3 (
    .a(port), .b(counter_2_q), .eq(comparator_3_eq), .lt(comparator_3_lt));  // open: gt
  Counter #(.width(10), .max('h3ff)) counter_3 (
    .Q({counter_3_q[9], hz2}), .clk(and_1_out), .clr(or_3_out));  // open: load, D, count, carry
  or or_3 (or_3_out, clr, and_2_out);
  and and_1 (and_1_out, comparator_1_eq, comparator_2_gt);
  and and_2 (and_2_out, clockout, ~acceleration);  // AND_Gate
  or or_4 (clockout, comparator_3_eq, comparator_3_lt);

  // Other names for the same wires on the sheet: clock = clockout

  // Notes on the sheet:
  //   004 это конечная скорость при ускорении тоже менять можно
  //   014 это константа базовая задержка если надо меньше или больше менять ее 
  //   Идет счёт количества тактов пока не дойдет до 120
  //   также если поменять такты на яблоки то будет ускорение от яблок когда наберется количество как в константе
  //   порт это тунель который передает значение после вычитания задержки и говорит когда надо остановить ускорение
  //   если включено ускорение то оно будет обнулять значение в счетчике
  //   hz2 это то сколько мы вычитаем из базовой задержки чтобы уменьшить ее
endmodule

module Apple_Detection (
  input  [7:0] head,
  input  [1:0] \Static_Направление ,
  input  [7:0] Apple_coord,
  input  clr,
  output BIT_FOR_evGENII_KIRILLOV
);

  wire comparator_1_eq, comparator_1_gt, comparator_2_eq, comparator_2_gt;
  wire [3:0] inc_dec_1_r, inc_dec_2_r, inc_dec_3_r, inc_dec_4_r;
  wire [7:0] adder_1_out, negator_1_out;

  Comparator #(.width(2), .mode("unsigned")) comparator_1 (
    .a(\Static_Направление ), .b(2'b10), .gt(comparator_1_gt), .eq(comparator_1_eq));  // open: lt
  Comparator #(.width(2), .mode("unsigned")) comparator_2 (
    .a(2'b01), .b(\Static_Направление ), .gt(comparator_2_gt), .eq(comparator_2_eq));  // open: lt
  // Probe on head[3:0]
  // Probe on head[7:4]
  inc_dec inc_dec_1 (.X(head[3:0]), .on_off(comparator_1_eq), .inc_dec(comparator_1_eq), .R(inc_dec_1_r));  // open: OFL
  inc_dec inc_dec_2 (
    .X(inc_dec_1_r), .on_off(comparator_1_gt), .inc_dec(comparator_1_eq), .R(inc_dec_2_r));  // open: OFL
  inc_dec inc_dec_3 (
    .X(inc_dec_4_r), .on_off(comparator_2_eq), .inc_dec(comparator_2_gt), .R(inc_dec_3_r));  // open: OFL
  inc_dec inc_dec_4 (.X(head[7:4]), .on_off(comparator_2_gt), .inc_dec(comparator_2_gt), .R(inc_dec_4_r));  // open: OFL
  // Probe on inc_dec_2_r
  // Probe on inc_dec_3_r
  // Probe on {inc_dec_3_r, inc_dec_2_r}
  Negator negator_1 (.in(Apple_coord), .out(negator_1_out));
  // Probe on negator_1_out
  Adder adder_1 (.a({inc_dec_3_r, inc_dec_2_r}), .b(negator_1_out), .out(adder_1_out));  // open: cin, cout
  nor nor_1 (BIT_FOR_evGENII_KIRILLOV, adder_1_out[0], adder_1_out[1], adder_1_out[2], adder_1_out[3], adder_1_out[4], adder_1_out[5], adder_1_out[6], adder_1_out[7]);

  // Notes on the sheet:
  //   Эта штука добавляет в счетчик когда следующая клетка после головы это яблоко и мы идем в его сторону
  //   Нужно придумать при какой ситуации будем очищать счетчик 
endmodule

module matrix (
  input  [31:0] bus_0,
  input  [31:0] bus_0_2
);

  DotMatrix #(.matrixcols(32), .matrixrows(32)) dotmatrix_1 (
    .col11(bus_0_2), .col12(bus_0_2), .col13(bus_0_2), .col14(bus_0_2), .col15(bus_0_2), .col16(bus_0_2),
    .col17(bus_0_2), .col18(bus_0_2), .col19(bus_0_2), .col20(bus_0_2), .col21(bus_0_2), .col22(bus_0_2),
    .col23(bus_0_2), .col24(bus_0_2), .col25(bus_0_2), .col26(bus_0_2), .col27(bus_0_2), .col28(bus_0_2),
    .col29(bus_0_2), .col30(bus_0_2), .col31(bus_0_2));  // open: col0, col1, col2, col3, col4, col5, col6, col7, col8, col9, col10
  DotMatrix #(.matrixcols(32), .matrixrows(32)) dotmatrix_2 (
    .col9(bus_0), .col10(bus_0), .col11(bus_0), .col12(bus_0), .col13(bus_0), .col14(bus_0), .col15(bus_0),
    .col16(bus_0), .col17(bus_0), .col18(bus_0), .col19(bus_0), .col20(bus_0), .col21(bus_0), .col22(bus_0),
    .col23(bus_0), .col24(bus_0), .col25(bus_0), .col26(bus_0), .col27(bus_0), .col28(bus_0), .col29(bus_0),
    .col30(bus_0), .col31(bus_0));  // open: col0, col1, col2, col3, col4, col5, col6, col7, col8
endmodule

module disp_snake (
  input  hodn,
  input  [3:0] X,
  input  clock,
  input  [3:0] Y,
  input  rndr,
  input  clear,
  output [15:0] out_7,
  output [15:0] out_8,
  output [15:0] out_9,
  output [15:0] out_10,
  output [15:0] out_11,
  output [15:0] out_12,
  output [15:0] out_13,
  output [15:0] out_14,
  output [15:0] out_15,
  output [15:0] out_16,
  output [15:0] out_17,
  output [15:0] out_18,
  output [15:0] out_19,
  output [15:0] out_20,
  output [15:0] out_21,
  output current,
  output [15:0] out_23
);

  wire demultiplexer_1_out0, demultiplexer_1_out1, demultiplexer_1_out2, demultiplexer_1_out3,
       demultiplexer_1_out4, demultiplexer_1_out5, demultiplexer_1_out6, demultiplexer_1_out7,
       demultiplexer_1_out8, demultiplexer_1_out9, demultiplexer_1_out10, demultiplexer_1_out11,
       demultiplexer_1_out12, demultiplexer_1_out13, demultiplexer_1_out14, demultiplexer_1_out15,
       dispriadok_snake_1_single, dispriadok_snake_2_single, dispriadok_snake_3_single,
       dispriadok_snake_4_single, dispriadok_snake_5_single, dispriadok_snake_6_single,
       dispriadok_snake_7_single, dispriadok_snake_8_single, dispriadok_snake_9_single,
       dispriadok_snake_10_single, dispriadok_snake_11_single, dispriadok_snake_12_single,
       dispriadok_snake_13_single, dispriadok_snake_14_single, dispriadok_snake_15_single,
       dispriadok_snake_16_single;
  wire [15:0] dispriadok_snake_1_riadok, dispriadok_snake_2_riadok, dispriadok_snake_3_riadok,
       dispriadok_snake_4_riadok, dispriadok_snake_5_riadok, dispriadok_snake_6_riadok,
       dispriadok_snake_7_riadok, dispriadok_snake_8_riadok, dispriadok_snake_9_riadok,
       dispriadok_snake_10_riadok, dispriadok_snake_11_riadok, dispriadok_snake_12_riadok,
       dispriadok_snake_13_riadok, dispriadok_snake_14_riadok, dispriadok_snake_15_riadok,
       dispriadok_snake_16_riadok;

  Demultiplexer #(.select(4)) demultiplexer_1 (
    .out0(demultiplexer_1_out0), .out1(demultiplexer_1_out1), .out2(demultiplexer_1_out2),
    .out3(demultiplexer_1_out3), .out4(demultiplexer_1_out4), .out5(demultiplexer_1_out5),
    .out6(demultiplexer_1_out6), .out7(demultiplexer_1_out7), .out8(demultiplexer_1_out8),
    .out9(demultiplexer_1_out9), .out10(demultiplexer_1_out10), .out11(demultiplexer_1_out11),
    .out12(demultiplexer_1_out12), .out13(demultiplexer_1_out13), .out14(demultiplexer_1_out14),
    .out15(demultiplexer_1_out15), .in(clock), .sel(Y));  // open: en
  dispriadok_snake dispriadok_snake_1 (
    .clock(demultiplexer_1_out15), .hodn(hodn), .X(X), .clear(clear), .riadok(dispriadok_snake_1_riadok),
    .single(dispriadok_snake_1_single));
  Register #(.width(16)) register_1 (.D(dispriadok_snake_1_riadok), .Q(out_7), .clk(rndr), .clr(clear));  // open: en
  dispriadok_snake dispriadok_snake_2 (
    .clock(demultiplexer_1_out14), .hodn(hodn), .X(X), .clear(clear), .riadok(dispriadok_snake_2_riadok),
    .single(dispriadok_snake_2_single));
  Register #(.width(16)) register_2 (.D(dispriadok_snake_2_riadok), .Q(out_8), .clk(rndr), .clr(clear));  // open: en
  dispriadok_snake dispriadok_snake_3 (
    .clock(demultiplexer_1_out13), .hodn(hodn), .X(X), .clear(clear), .riadok(dispriadok_snake_3_riadok),
    .single(dispriadok_snake_3_single));
  Register #(.width(16)) register_3 (.D(dispriadok_snake_3_riadok), .Q(out_9), .clk(rndr), .clr(clear));  // open: en
  dispriadok_snake dispriadok_snake_4 (
    .clock(demultiplexer_1_out12), .hodn(hodn), .X(X), .clear(clear), .riadok(dispriadok_snake_4_riadok),
    .single(dispriadok_snake_4_single));
  Register #(.width(16)) register_4 (.D(dispriadok_snake_4_riadok), .Q(out_10), .clk(rndr), .clr(clear));  // open: en
  dispriadok_snake dispriadok_snake_5 (
    .clock(demultiplexer_1_out11), .hodn(hodn), .X(X), .clear(clear), .riadok(dispriadok_snake_5_riadok),
    .single(dispriadok_snake_5_single));
  Register #(.width(16)) register_5 (.D(dispriadok_snake_5_riadok), .Q(out_11), .clk(rndr), .clr(clear));  // open: en
  dispriadok_snake dispriadok_snake_6 (
    .clock(demultiplexer_1_out10), .hodn(hodn), .X(X), .clear(clear), .riadok(dispriadok_snake_6_riadok),
    .single(dispriadok_snake_6_single));
  Register #(.width(16)) register_6 (.D(dispriadok_snake_6_riadok), .Q(out_12), .clk(rndr), .clr(clear));  // open: en
  dispriadok_snake dispriadok_snake_7 (
    .clock(demultiplexer_1_out9), .hodn(hodn), .X(X), .clear(clear), .riadok(dispriadok_snake_7_riadok),
    .single(dispriadok_snake_7_single));
  Register #(.width(16)) register_7 (.D(dispriadok_snake_7_riadok), .Q(out_13), .clk(rndr), .clr(clear));  // open: en
  dispriadok_snake dispriadok_snake_8 (
    .clock(demultiplexer_1_out8), .hodn(hodn), .X(X), .clear(clear), .riadok(dispriadok_snake_8_riadok),
    .single(dispriadok_snake_8_single));
  Register #(.width(16)) register_8 (.D(dispriadok_snake_8_riadok), .Q(out_14), .clk(rndr), .clr(clear));  // open: en
  dispriadok_snake dispriadok_snake_9 (
    .clock(demultiplexer_1_out7), .hodn(hodn), .X(X), .clear(clear), .riadok(dispriadok_snake_9_riadok),
    .single(dispriadok_snake_9_single));
  Register #(.width(16)) register_9 (.D(dispriadok_snake_9_riadok), .Q(out_15), .clk(rndr), .clr(clear));  // open: en
  dispriadok_snake dispriadok_snake_10 (
    .clock(demultiplexer_1_out6), .hodn(hodn), .X(X), .clear(clear), .riadok(dispriadok_snake_10_riadok),
    .single(dispriadok_snake_10_single));
  Register #(.width(16)) register_10 (.D(dispriadok_snake_10_riadok), .Q(out_16), .clk(rndr), .clr(clear));  // open: en
  dispriadok_snake dispriadok_snake_11 (
    .clock(demultiplexer_1_out5), .hodn(hodn), .X(X), .clear(clear), .riadok(dispriadok_snake_11_riadok),
    .single(dispriadok_snake_11_single));
  Register #(.width(16)) register_11 (.D(dispriadok_snake_11_riadok), .Q(out_17), .clk(rndr), .clr(clear));  // open: en
  dispriadok_snake dispriadok_snake_12 (
    .clock(demultiplexer_1_out4), .hodn(hodn), .X(X), .clear(clear), .riadok(dispriadok_snake_12_riadok),
    .single(dispriadok_snake_12_single));
  Register #(.width(16)) register_12 (.D(dispriadok_snake_12_riadok), .Q(out_18), .clk(rndr), .clr(clear));  // open: en
  dispriadok_snake dispriadok_snake_13 (
    .clock(demultiplexer_1_out3), .hodn(hodn), .X(X), .clear(clear), .riadok(dispriadok_snake_13_riadok),
    .single(dispriadok_snake_13_single));
  Register #(.width(16)) register_13 (.D(dispriadok_snake_13_riadok), .Q(out_19), .clk(rndr), .clr(clear));  // open: en
  dispriadok_snake dispriadok_snake_14 (
    .clock(demultiplexer_1_out2), .hodn(hodn), .X(X), .clear(clear), .riadok(dispriadok_snake_14_riadok),
    .single(dispriadok_snake_14_single));
  Register #(.width(16)) register_14 (.D(dispriadok_snake_14_riadok), .Q(out_20), .clk(rndr), .clr(clear));  // open: en
  dispriadok_snake dispriadok_snake_15 (
    .clock(demultiplexer_1_out1), .hodn(hodn), .X(X), .clear(clear), .riadok(dispriadok_snake_15_riadok),
    .single(dispriadok_snake_15_single));
  Register #(.width(16)) register_15 (.D(dispriadok_snake_15_riadok), .Q(out_21), .clk(rndr), .clr(clear));  // open: en
  dispriadok_snake dispriadok_snake_16 (
    .clock(demultiplexer_1_out0), .hodn(hodn), .X(X), .clear(clear), .riadok(dispriadok_snake_16_riadok),
    .single(dispriadok_snake_16_single));
  Register #(.width(16)) register_16 (.D(dispriadok_snake_16_riadok), .Q(out_23), .clk(rndr), .clr(clear));  // open: en
  Multiplexer #(.select(4)) multiplexer_1 (
    .in0(dispriadok_snake_1_single), .in1(dispriadok_snake_2_single), .in2(dispriadok_snake_3_single),
    .in3(dispriadok_snake_4_single), .in4(dispriadok_snake_5_single), .in5(dispriadok_snake_6_single),
    .in6(dispriadok_snake_7_single), .in7(dispriadok_snake_8_single), .in8(dispriadok_snake_9_single),
    .in9(dispriadok_snake_10_single), .in10(dispriadok_snake_11_single), .in11(dispriadok_snake_12_single),
    .in12(dispriadok_snake_13_single), .in13(dispriadok_snake_14_single), .in14(dispriadok_snake_15_single),
    .in15(dispriadok_snake_16_single), .out(current), .sel(Y));  // open: en
endmodule

module dispriadok_snake (
  input  clock,
  input  hodn,
  input  [3:0] X,
  input  clear,
  output [15:0] riadok,
  output single
);

  wire demultiplexer_1_out0, demultiplexer_1_out1, demultiplexer_1_out2, demultiplexer_1_out3,
       demultiplexer_1_out4, demultiplexer_1_out5, demultiplexer_1_out6, demultiplexer_1_out7,
       demultiplexer_1_out8, demultiplexer_1_out9, demultiplexer_1_out10, demultiplexer_1_out11,
       demultiplexer_1_out12, demultiplexer_1_out13, demultiplexer_1_out14, demultiplexer_1_out15;

  Demultiplexer #(.select(4)) demultiplexer_1 (
    .out0(demultiplexer_1_out0), .out1(demultiplexer_1_out1), .out2(demultiplexer_1_out2),
    .out3(demultiplexer_1_out3), .out4(demultiplexer_1_out4), .out5(demultiplexer_1_out5),
    .out6(demultiplexer_1_out6), .out7(demultiplexer_1_out7), .out8(demultiplexer_1_out8),
    .out9(demultiplexer_1_out9), .out10(demultiplexer_1_out10), .out11(demultiplexer_1_out11),
    .out12(demultiplexer_1_out12), .out13(demultiplexer_1_out13), .out14(demultiplexer_1_out14),
    .out15(demultiplexer_1_out15), .in(clock), .sel(X));  // open: en
  D_Flip_Flop d_ff_1 (.clk(demultiplexer_1_out0), .D(hodn), .Q(riadok[15]), .reset(clear));  // open: Qn, preset, en
  D_Flip_Flop d_ff_2 (.clk(demultiplexer_1_out1), .D(hodn), .Q(riadok[14]), .reset(clear));  // open: Qn, preset, en
  D_Flip_Flop d_ff_3 (.clk(demultiplexer_1_out2), .D(hodn), .Q(riadok[13]), .reset(clear));  // open: Qn, preset, en
  D_Flip_Flop d_ff_4 (.clk(demultiplexer_1_out3), .D(hodn), .Q(riadok[12]), .reset(clear));  // open: Qn, preset, en
  D_Flip_Flop d_ff_5 (.clk(demultiplexer_1_out4), .D(hodn), .Q(riadok[11]), .reset(clear));  // open: Qn, preset, en
  D_Flip_Flop d_ff_6 (.clk(demultiplexer_1_out5), .D(hodn), .Q(riadok[10]), .reset(clear));  // open: Qn, preset, en
  D_Flip_Flop d_ff_7 (.clk(demultiplexer_1_out6), .D(hodn), .Q(riadok[9]), .reset(clear));  // open: Qn, preset, en
  D_Flip_Flop d_ff_8 (.clk(demultiplexer_1_out7), .D(hodn), .Q(riadok[8]), .reset(clear));  // open: Qn, preset, en
  D_Flip_Flop d_ff_9 (.clk(demultiplexer_1_out8), .D(hodn), .Q(riadok[7]), .reset(clear));  // open: Qn, preset, en
  D_Flip_Flop d_ff_10 (.clk(demultiplexer_1_out9), .D(hodn), .Q(riadok[6]), .reset(clear));  // open: Qn, preset, en
  Multiplexer #(.select(4)) multiplexer_1 (
    .in0(riadok[15]), .in1(riadok[14]), .in2(riadok[13]), .in3(riadok[12]), .in4(riadok[11]),
    .in5(riadok[10]), .in6(riadok[9]), .in7(riadok[8]), .in8(riadok[7]), .in9(riadok[6]), .in10(riadok[5]),
    .in11(riadok[4]), .in12(riadok[3]), .in13(riadok[2]), .in14(riadok[1]), .in15(riadok[0]), .out(single),
    .sel(X));  // open: en
  D_Flip_Flop d_ff_11 (.clk(demultiplexer_1_out10), .D(hodn), .Q(riadok[5]), .reset(clear));  // open: Qn, preset, en
  D_Flip_Flop d_ff_12 (.clk(demultiplexer_1_out11), .D(hodn), .Q(riadok[4]), .reset(clear));  // open: Qn, preset, en
  D_Flip_Flop d_ff_13 (.clk(demultiplexer_1_out12), .D(hodn), .Q(riadok[3]), .reset(clear));  // open: Qn, preset, en
  D_Flip_Flop d_ff_14 (.clk(demultiplexer_1_out13), .D(hodn), .Q(riadok[2]), .reset(clear));  // open: Qn, preset, en
  D_Flip_Flop d_ff_15 (.clk(demultiplexer_1_out14), .D(hodn), .Q(riadok[1]), .reset(clear));  // open: Qn, preset, en
  D_Flip_Flop d_ff_16 (.clk(demultiplexer_1_out15), .D(hodn), .Q(riadok[0]), .reset(clear));  // open: Qn, preset, en
endmodule
