// Logisim project version_register_3.circ as structural Verilog
// 1
module main (
  input  in_1,
  input  in_2,
  input  in_3,
  input  in_4
);

  wire _1_1, _1_2, _1_3, _1_4, _1_5, _1_6, _1_7, _1_8, _2_1, _2_2, _2_3, _2_4, _2_5, _2_6, _2_7, _2_8,
       and_1_out, clock, clr, counter_1_carry, d_ff_1_qn, down, granca_detection_1_out_6, hz, left, or_1_out,
       or_2_out, right, up;
  wire [1:0] \Static_направление ;
  wire [3:0] inc_dec_1_r, inc_dec_2_r;
  wire [6:0] \input ;
  wire [7:0] counter_1_q, counter_2_q, head;
  wire [15:0] disp_snake_1_out_7, disp_snake_1_out_8, disp_snake_1_out_9, disp_snake_1_out_10,
       disp_snake_1_out_11, disp_snake_1_out_12, disp_snake_1_out_13, disp_snake_1_out_14,
       disp_snake_1_out_15, disp_snake_1_out_16, disp_snake_1_out_17, disp_snake_1_out_18,
       disp_snake_1_out_19, disp_snake_1_out_20, disp_snake_1_out_21, disp_snake_1_out_23;

  Clock clock_1 (.out(clock));
  granca_detection granca_detection_1 (
    .in_3(head), .Left(left), .Right(right), .out_6(granca_detection_1_out_6), .Up(up), .Down(down));
  and and_1 (and_1_out, clock, d_ff_1_qn);
  D_Flip_Flop d_ff_1 (.Qn(d_ff_1_qn), .preset(granca_detection_1_out_6), .reset(clr));  // open: clk, D, Q, en
  Register register_1 (.D({inc_dec_1_r, inc_dec_2_r}), .Q(head), .clk(and_1_out), .clr(clr));  // open: en
  or or_1 (or_1_out, left, right);
  // NOT_Gate not_1 is placed but not wired
  inc_dec inc_dec_1 (.X(head[7:4]), .on_off(or_1_out), .inc_dec(right), .R(inc_dec_1_r));  // open: OFL
  Register #(.width(4)) register_2 (.D(head[7:4]), .clk(clock), .clr(clr));  // open: en, Q
  or or_2 (or_2_out, up, down);
  inc_dec inc_dec_2 (.X(head[3:0]), .on_off(or_2_out), .inc_dec(up), .R(inc_dec_2_r));  // open: OFL
  Register #(.width(4)) register_3 (.D(head[3:0]), .clk(clock), .clr(clr));  // open: en, Q
  _7_Segment_Display u_7_segment_display_1 (
    .g(_2_8), .f(_2_7), .a(_2_6), .b(_2_5), .e(_2_1), .d(_2_2), .c(_2_3), .dp(_2_4));
  DotMatrix #(.inputtype("row"), .matrixcols(16), .matrixrows(16)) dotmatrix_1 (
    .row0(disp_snake_1_out_7), .row1(disp_snake_1_out_8), .row2(disp_snake_1_out_9),
    .row3(disp_snake_1_out_10), .row4(disp_snake_1_out_11), .row5(disp_snake_1_out_12),
    .row6(disp_snake_1_out_13), .row7(disp_snake_1_out_14), .row8(disp_snake_1_out_15),
    .row9(disp_snake_1_out_16), .row10(disp_snake_1_out_17), .row11(disp_snake_1_out_18),
    .row12(disp_snake_1_out_19), .row13(disp_snake_1_out_20), .row14(disp_snake_1_out_21),
    .row15(disp_snake_1_out_23));
  disp_snake disp_snake_1 (
    .hodn(clock), .X(head[7:4]), .clock(clock), .Y(head[3:0]), .rndr(clock), .out_7(disp_snake_1_out_7),
    .out_8(disp_snake_1_out_8), .out_9(disp_snake_1_out_9), .out_10(disp_snake_1_out_10),
    .out_11(disp_snake_1_out_11), .out_12(disp_snake_1_out_12), .out_13(disp_snake_1_out_13),
    .out_14(disp_snake_1_out_14), .out_15(disp_snake_1_out_15), .out_16(disp_snake_1_out_16),
    .out_17(disp_snake_1_out_17), .out_18(disp_snake_1_out_18), .out_19(disp_snake_1_out_19),
    .out_20(disp_snake_1_out_20), .out_21(disp_snake_1_out_21), .out_23(disp_snake_1_out_23), .clear(clr));  // open: current
  _7_Segment_Display u_7_segment_display_2 (
    .g(_1_8), .f(_1_7), .a(_1_6), .b(_1_5), .e(_1_1), .d(_1_2), .c(_1_3), .dp(_1_4));
  Button button_1 (.out(clr));
  Keyboard keyboard_1 (.clk(clock), .clr(clr), .data(\input ));  // open: re, avail
  Counter #(.max('ha)) counter_1 (
    .Q(counter_1_q), .carry(counter_1_carry), .clk(hz), .clr(clr));  // open: load, D, count
  Counter #(.max('ha)) counter_2 (.Q(counter_2_q), .clk(counter_1_carry), .clr(clr));  // open: load, D, count, carry
  movement movement_1 (
    .Clock(clock), .Clear(clr), .out_5(up), .out_6(down), .out_7(left), .out_8(right), .\input (\input ),
    .StaticOutist(\Static_направление ));
  ROM rom_1 (.addr(counter_1_q), .data({_1_8, _1_7, _1_6, _1_5, _1_4, _1_3, _1_2, _1_1}));  // open: sel
  ROM rom_2 (.addr(counter_2_q), .data({_2_8, _2_7, _2_6, _2_5, _2_4, _2_3, _2_2, _2_1}));  // open: sel

  // Other names for the same wires on the sheet: acceleration = in_4; paus = in_2; stop_golod = in_3

  // Notes on the sheet:
  //   coor X
  //   coor Y
  //   Отвечает за появление или исчезание клетки
  //   1 - пауза 0 играем
  //   1 - есть 0 - нет голода
  //   1 - есть ускорение 0 - нет
  //   contents of rom_1 (hex, n*v repeats v):
  //   77 14 b3 b6 d4 e6 e7 34 f7 f6 77
  //   contents of rom_2 (hex, n*v repeats v):
  //   77 14 b3 b6 d4 e6 e7 34 f7 f6 77
endmodule

module _16_bit_AND (
  input  [15:0] \input ,
  input  switch,
  output [15:0] \output 
);

  assign \output  = \input  & {16{switch}};  // AND_Gate and_1, 16 bits wide
endmodule

module column_switch (
  input  [9:0] in_1,
  input  in_2,
  output [9:0] out_3
);

  wire comparator_1_eq;
  wire [9:0] multiplexer_1_out;

  Multiplexer #(.width(10)) multiplexer_1 (
    .in0(in_1), .in1({1'b0, in_1[9:1]}), .out(multiplexer_1_out), .sel(in_2));  // open: en
  Comparator #(.width(10)) comparator_1 (.a(in_1), .b({10{1'b0}}), .eq(comparator_1_eq));  // open: gt, lt
  Multiplexer #(.width(10)) multiplexer_2 (
    .in0(multiplexer_1_out), .in1(10'h10), .out(out_3), .sel(comparator_1_eq));  // open: en
endmodule

module inc_dec (
  input  [3:0] X,
  input  on_off,
  input  inc_dec,
  output [3:0] R,
  output OFL
);

  wire and_2_out, and_3_out;
  wire [3:0] and_1_out, xor_1_out, xor_2_out, xor_3_out;
  wire [3:3] decoder_1_out0, decoder_1_out1;

  Decoder #(.enable("false")) decoder_1 (.out0(decoder_1_out0[3]), .out1(decoder_1_out1[3]), .sel(inc_dec));
  assign xor_1_out = {4{decoder_1_out0[3]}} ^ X;  // XOR_Gate xor_1, 4 bits wide
  assign xor_2_out = {4{decoder_1_out1[3]}} ^ xor_3_out;  // XOR_Gate xor_2, 4 bits wide
  assign and_1_out = xor_1_out & xor_2_out;  // AND_Gate and_1, 4 bits wide
  and and_2 (and_2_out, and_1_out[3], inc_dec);
  and and_3 (and_3_out, and_1_out[3], ~inc_dec);  // AND_Gate
  assign xor_3_out = X ^ {and_1_out[2:0], 1'b1};  // XOR_Gate xor_3, 4 bits wide
  or or_1 (OFL, and_2_out, and_3_out);
  Multiplexer #(.width(4), .enable("false")) multiplexer_1 (.in0(X), .in1(xor_3_out), .out(R), .sel(on_off));
endmodule

module granca_detection (
  input  Up,
  input  Down,
  input  [7:0] in_3,
  input  Left,
  input  Right,
  output out_6
);

  wire and_1_out, and_2_out, nor_1_out, nor_2_out;

  Pull_Resistor pull_resistor_1 (.node(Up));
  Pull_Resistor pull_resistor_2 (.node(Down));
  Pull_Resistor pull_resistor_3 (.node(Left));
  Pull_Resistor pull_resistor_4 (.node(Right));
  and and_1 (and_1_out, Up, in_3[3], in_3[2], in_3[1], in_3[0]);
  and and_2 (and_2_out, in_3[7], in_3[6], in_3[5], in_3[4], Right);
  nor nor_1 (nor_1_out, ~Down, in_3[0], in_3[1], in_3[2], in_3[3]);  // NOR_Gate
  nor nor_2 (nor_2_out, in_3[4], in_3[5], in_3[6], in_3[7], ~Left);  // NOR_Gate
  or or_1 (out_6, and_1_out, nor_1_out, nor_2_out, and_2_out);
endmodule

// управление
module movement (
  input  [6:0] \input ,
  input  Clock,
  input  Clear,
  output [1:0] StaticOutist,
  output out_5,
  output out_6,
  output out_7,
  output out_8
);

  wire and_1_out, comparator_1_eq, comparator_2_eq, comparator_3_eq, comparator_4_eq, counter_1_carry,
       or_3_out, xnor_1_out, xor_1_out;
  wire [1:0] multiplexer_1_out, or_1_out, register_1_q;

  Comparator #(.width(7)) comparator_1 (.a(\input ), .b(7'b1100100), .eq(comparator_1_eq));  // open: gt, lt
  Comparator #(.width(7)) comparator_2 (.a(\input ), .b(7'b1110011), .eq(comparator_2_eq));  // open: gt, lt
  Comparator #(.width(7)) comparator_3 (.a(\input ), .b(7'b1100001), .eq(comparator_3_eq));  // open: gt, lt
  Comparator #(.width(7)) comparator_4 (.a(\input ), .b(7'b1110111), .eq(comparator_4_eq));  // open: gt, lt
  or or_1 (or_1_out[0], comparator_2_eq, comparator_1_eq);
  or or_2 (or_1_out[1], comparator_1_eq, comparator_3_eq);
  or or_3 (or_3_out, comparator_1_eq, comparator_2_eq, comparator_3_eq, comparator_4_eq);
  Register #(.width(2)) register_1 (.D(or_1_out), .Q(register_1_q), .clk(or_3_out), .clr(Clear));  // open: en
  Register #(.width(2)) register_2 (.D(multiplexer_1_out), .Q(StaticOutist), .clk(or_3_out), .clr(Clear));  // open: en
  xor xor_1 (xor_1_out, StaticOutist[0], register_1_q[0]);
  xnor xnor_1 (xnor_1_out, StaticOutist[1], register_1_q[1]);
  and and_1 (and_1_out, xnor_1_out, xor_1_out);
  Multiplexer #(.width(2)) multiplexer_1 (
    .in0(register_1_q), .in1(StaticOutist), .out(multiplexer_1_out), .sel(and_1_out));  // open: en
  Counter #(.width(3), .max('h5)) counter_1 (
    .carry(counter_1_carry), .clk(Clock), .clr(Clear));  // open: load, D, count, Q
  Demultiplexer #(.select(2)) demultiplexer_1 (
    .out0(out_5), .out1(out_6), .out2(out_7), .out3(out_8), .in(counter_1_carry), .sel(multiplexer_1_out));  // open: en

  // Other names for the same wires on the sheet: clr = Clear

  // Notes on the sheet:
  //   новое напр.
  //   текушее напр.
endmodule

module pseudo_reg (
  input  [3:0] in_1,
  input  [3:0] in_2,
  output [15:0] out_3,
  output [15:0] out_4,
  output [15:0] out_5,
  output [15:0] out_6,
  output [15:0] out_7,
  output [15:0] out_8,
  output [15:0] out_9,
  output [15:0] out_10,
  output [15:0] out_11,
  output [15:0] out_12,
  output [15:0] out_13,
  output [15:0] out_14,
  output [15:0] out_15,
  output [15:0] out_16,
  output [15:0] out_17,
  output [15:0] out_18
);

  wire decoder_2_out0, decoder_2_out1, decoder_2_out2, decoder_2_out3, decoder_2_out4, decoder_2_out5,
       decoder_2_out6, decoder_2_out7, decoder_2_out8, decoder_2_out9, decoder_2_out10, decoder_2_out11,
       decoder_2_out12, decoder_2_out13, decoder_2_out14, decoder_2_out15;
  wire [15:0] decoder_1_out0;

  Decoder #(.select(4), .disabled(0), .enable("false")) decoder_1 (
    .out0(decoder_1_out0[0]), .out1(decoder_1_out0[1]), .out2(decoder_1_out0[2]), .out3(decoder_1_out0[3]),
    .out4(decoder_1_out0[4]), .out5(decoder_1_out0[5]), .out6(decoder_1_out0[6]), .out7(decoder_1_out0[7]),
    .out8(decoder_1_out0[8]), .out9(decoder_1_out0[9]), .out10(decoder_1_out0[10]),
    .out11(decoder_1_out0[11]), .out12(decoder_1_out0[12]), .out13(decoder_1_out0[13]),
    .out14(decoder_1_out0[14]), .out15(decoder_1_out0[15]), .sel(in_1));
  _16_bit_AND u_16_bit_and_1 (.\input (decoder_1_out0), .switch(decoder_2_out1), .\output (out_3));
  _16_bit_AND u_16_bit_and_2 (.\input (decoder_1_out0), .switch(decoder_2_out0), .\output (out_11));
  _16_bit_AND u_16_bit_and_3 (.\input (decoder_1_out0), .switch(decoder_2_out3), .\output (out_4));
  _16_bit_AND u_16_bit_and_4 (.\input (decoder_1_out0), .switch(decoder_2_out2), .\output (out_12));
  Decoder #(.select(4), .disabled(0), .enable("false")) decoder_2 (
    .out0(decoder_2_out0), .out1(decoder_2_out1), .out2(decoder_2_out2), .out3(decoder_2_out3),
    .out4(decoder_2_out4), .out5(decoder_2_out5), .out6(decoder_2_out6), .out7(decoder_2_out7),
    .out8(decoder_2_out8), .out9(decoder_2_out9), .out10(decoder_2_out10), .out11(decoder_2_out11),
    .out12(decoder_2_out12), .out13(decoder_2_out13), .out14(decoder_2_out14), .out15(decoder_2_out15),
    .sel(in_2));
  _16_bit_AND u_16_bit_and_5 (.\input (decoder_1_out0), .switch(decoder_2_out5), .\output (out_5));
  _16_bit_AND u_16_bit_and_6 (.\input (decoder_1_out0), .switch(decoder_2_out4), .\output (out_13));
  _16_bit_AND u_16_bit_and_7 (.\input (decoder_1_out0), .switch(decoder_2_out7), .\output (out_6));
  _16_bit_AND u_16_bit_and_8 (.\input (decoder_1_out0), .switch(decoder_2_out6), .\output (out_14));
  _16_bit_AND u_16_bit_and_9 (.\input (decoder_1_out0), .switch(decoder_2_out8), .\output (out_15));
  _16_bit_AND u_16_bit_and_10 (.\input (decoder_1_out0), .switch(decoder_2_out9), .\output (out_7));
  _16_bit_AND u_16_bit_and_11 (.\input (decoder_1_out0), .switch(decoder_2_out10), .\output (out_16));
  _16_bit_AND u_16_bit_and_12 (.\input (decoder_1_out0), .switch(decoder_2_out11), .\output (out_8));
  _16_bit_AND u_16_bit_and_13 (.\input (decoder_1_out0), .switch(decoder_2_out12), .\output (out_17));
  _16_bit_AND u_16_bit_and_14 (.\input (decoder_1_out0), .switch(decoder_2_out13), .\output (out_9));
  _16_bit_AND u_16_bit_and_15 (.\input (decoder_1_out0), .switch(decoder_2_out14), .\output (out_18));
  _16_bit_AND u_16_bit_and_16 (.\input (decoder_1_out0), .switch(decoder_2_out15), .\output (out_10));
endmodule

module CP (
);

  wire cdm_8_mark5_1_p2, cdm_8_mark5_1_p3, cdm_8_mark5_1_p5, cdm_8_mark5_1_p6, cdm_8_mark5_1_p7,
       cdm_8_mark5_1_p8, clk, code, data, IRQ, mem, not_1_out, rd_wr, undriven;
  wire [7:0] cdm_8_mark5_1_p11, cdm_8_mark5_1_p12, cdm_8_mark5_1_p13, cdm_8_mark5_1_p14, IOdat;

  // Probe on undriven
  // Probe on undriven
  // Probe on cdm_8_mark5_1_p3
  // Probe on cdm_8_mark5_1_p2
  // Probe on cdm_8_mark5_1_p6
  // Probe on cdm_8_mark5_1_p5
  // Probe on cdm_8_mark5_1_p7
  // CdM_8_mark5 cdm_8_mark5_1: pin names not known; wires that end beside it: IRQ, cdm_8_mark5_1_p2, cdm_8_mark5_1_p3, clk, cdm_8_mark5_1_p5, cdm_8_mark5_1_p6, cdm_8_mark5_1_p7, cdm_8_mark5_1_p8, mem, rd_wr, cdm_8_mark5_1_p11, cdm_8_mark5_1_p12, cdm_8_mark5_1_p13, cdm_8_mark5_1_p14
  Clock clock_1 (.out(clk));
  Decoder decoder_1 (.out0(code), .out1(data), .sel(cdm_8_mark5_1_p8), .en(mem));
  assign IOdat = not_1_out ? cdm_8_mark5_1_p12 : 8'bz;  // Controlled_Buffer controlled_buffer_1
  not not_1 (not_1_out, rd_wr);
  assign cdm_8_mark5_1_p13 = rd_wr ? IOdat : 8'bz;  // Controlled_Buffer controlled_buffer_2
  assign cdm_8_mark5_1_p14 = data ? IOdat : 8'bz;  // Controlled_Buffer controlled_buffer_3
  // Probe on cdm_8_mark5_1_p14
  Pull_Resistor pull_resistor_1 (.node(data));
  ROM rom_1 (.addr(cdm_8_mark5_1_p11), .data(IOdat), .sel(code));
  RAM ram_1 (.addr(cdm_8_mark5_1_p11), .data(IOdat), .sel(data), .clk(clk), .ld(rd_wr));  // open: clr

  // Notes on the sheet:
  //   contents of rom_1 (hex, n*v repeats v):
  //   d0 8 f0 8c d1 9 a4 d4 3
endmodule

module golod (
  input  stop_golod,
  input  clock,
  input  hz,
  input  clr,
  output golod
);

  wire comparator_1_eq, comparator_1_gt, comparator_2_gt, or_1_out, or_2_out;
  wire [9:0] counter_1_q, counter_2_q;

  Counter #(.width(10), .max('h3ff)) counter_1 (
    .Q(counter_1_q), .clk(clock), .clr(or_1_out));  // open: load, D, count, carry
  or or_1 (or_1_out, clr, hz);
  or or_2 (or_2_out, comparator_1_gt, comparator_1_eq);
  Comparator #(.width(10), .mode("unsigned")) comparator_1 (
    .a(counter_1_q), .b(10'hf1), .gt(comparator_1_gt), .eq(comparator_1_eq));  // open: lt
  Counter #(.width(10), .max('h3ff)) counter_2 (
    .Q(counter_2_q), .clk(or_2_out), .clr(clr));  // open: load, D, count, carry
  and and_1 (golod, stop_golod, comparator_2_gt);
  Comparator #(.width(10), .mode("unsigned")) comparator_2 (
    .a(counter_2_q), .b({10{1'b0}}), .gt(comparator_2_gt));  // open: eq, lt

  // Notes on the sheet:
  //   тут 0f1 это константа после такого количества clockов в голод пойдет 1 которая остановит такты
endmodule

module Acceleratiaon (
  input  takt,
  input  clr,
  input  acceleration,
  output clockout
);

  wire and_1_out, and_2_out, comparator_1_eq, comparator_2_gt, comparator_3_eq, comparator_3_lt, or_1_out,
       or_2_out, or_3_out;
  wire [9:0] counter_1_q, counter_2_q, port;
  wire [9:1] hz2;
  wire [9:9] counter_3_q;

  // Probe on port
  Subtractor #(.width(10)) subtractor_1 (.a(10'h14), .b({hz2, 1'b0}), .out(port));  // open: bin, bout
  Counter #(.width(10), .max('h3ff)) counter_1 (
    .Q(counter_1_q), .clk(takt), .clr(or_1_out));  // open: load, D, count, carry
  or or_1 (or_1_out, clr, comparator_1_eq);
  Comparator #(.width(10), .mode("unsigned")) comparator_1 (
    .a(counter_1_q), .b(10'h120), .eq(comparator_1_eq));  // open: gt, lt
  Counter #(.width(10), .max('h3ff)) counter_2 (
    .Q(counter_2_q), .clk(takt), .clr(or_2_out));  // open: load, D, count, carry
  or or_2 (or_2_out, clr, clockout);
  Comparator #(.width(10), .mode("unsigned")) comparator_2 (.a(port), .b(10'h4), .gt(comparator_2_gt));  // open: eq, lt
  Comparator #(.width(10), .mode("unsigned")) comparator_3 (
    .a(port), .b(counter_2_q), .eq(comparator_3_eq), .lt(comparator_3_lt));  // open: gt
  Counter #(.width(10), .max('h3ff)) counter_3 (
    .Q({counter_3_q[9], hz2}), .clk(and_1_out), .clr(or_3_out));  // open: load, D, count, carry
  or or_3 (or_3_out, clr, and_2_out);
  and and_1 (and_1_out, comparator_1_eq, comparator_2_gt);
  and and_2 (and_2_out, clockout, ~acceleration);  // AND_Gate
  or or_4 (clockout, comparator_3_eq, comparator_3_lt);

  // Other names for the same wires on the sheet: clock = clockout

  // Notes on the sheet:
  //   004 это конечная скорость при ускорении тоже менять можно
  //   014 это константа базовая задержка если надо меньше или больше менять ее 
  //   Идет счёт количества тактов пока не дойдет до 120
  //   также если поменять такты на яблоки то будет ускорение от яблок когда наберется количество как в константе
  //   порт это тунель который передает значение после вычитания задержки и говорит когда надо остановить ускорение
  //   если включено ускорение то оно будет обнулять значение в счетчике
  //   hz2 это то сколько мы вычитаем из базовой задержки чтобы уменьшить ее
endmodule

module Apple_Detection (
  input  [7:0] head,
  input  [1:0] \Static_Направление ,
  input  [7:0] Apple_coord,
  input  clr,
  output BIT_FOR_evGENII_KIRILLOV
);

  wire comparator_1_eq, comparator_1_gt, comparator_2_eq, comparator_2_gt;
  wire [3:0] inc_dec_1_r, inc_dec_2_r, inc_dec_3_r, inc_dec_4_r;
  wire [7:0] adder_1_out, negator_1_out;

  Comparator #(.width(2), .mode("unsigned")) comparator_1 (
    .a(\Static_Направление ), .b(2'b10), .gt(comparator_1_gt), .eq(comparator_1_eq));  // open: lt
  Comparator #(.width(2), .mode("unsigned")) comparator_2 (
    .a(2'b01), .b(\Static_Направление ), .gt(comparator_2_gt), .eq(comparator_2_eq));  // open: lt
  // Probe on head[3:0]
  // Probe on head[7:4]
  inc_dec inc_dec_1 (.X(head[3:0]), .on_off(comparator_1_eq), .inc_dec(comparator_1_eq), .R(inc_dec_1_r));  // open: OFL
  inc_dec inc_dec_2 (
    .X(inc_dec_1_r), .on_off(comparator_1_gt), .inc_dec(comparator_1_eq), .R(inc_dec_2_r));  // open: OFL
  inc_dec inc_dec_3 (
    .X(inc_dec_4_r), .on_off(comparator_2_eq), .inc_dec(comparator_2_gt), .R(inc_dec_3_r));  // open: OFL
  inc_dec inc_dec_4 (.X(head[7:4]), .on_off(comparator_2_gt), .inc_dec(comparator_2_gt), .R(inc_dec_4_r));  // open: OFL
  // Probe on inc_dec_2_r
  // Probe on inc_dec_3_r
  // Probe on {inc_dec_3_r, inc_dec_2_r}
  Negator negator_1 (.in(Apple_coord), .out(negator_1_out));
  // Probe on negator_1_out
  Adder adder_1 (.a({inc_dec_3_r, inc_dec_2_r}), .b(negator_1_out), .out(adder_1_out));  // open: cin, cout
  nor nor_1 (BIT_FOR_evGENII_KIRILLOV, adder_1_out[0], adder_1_out[1], adder_1_out[2], adder_1_out[3], adder_1_out[4], adder_1_out[5], adder_1_out[6], adder_1_out[7]);

  // Notes on the sheet:
  //   Эта штука добавляет в счетчик когда следующая клетка после головы это яблоко и мы идем в его сторону
  //   Нужно придумать при какой ситуации будем очищать счетчик 
endmodule

module matrix (
  input  [31:0] bus_0,
  input  [31:0] bus_0_2
);

  DotMatrix #(.matrixcols(32), .matrixrows(32)) dotmatrix_1 (
    .col11(bus_0_2), .col12(bus_0_2), .col13(bus_0_2), .col14(bus_0_2), .col15(bus_0_2), .col16(bus_0_2),
    .col17(bus_0_2), .col18(bus_0_2), .col19(bus_0_2), .col20(bus_0_2), .col21(bus_0_2), .col22(bus_0_2),
    .col23(bus_0_2), .col24(bus_0_2), .col25(bus_0_2), .col26(bus_0_2), .col27(bus_0_2), .col28(bus_0_2),
    .col29(bus_0_2), .col30(bus_0_2), .col31(bus_0_2));  // open: col0, col1, col2, col3, col4, col5, col6, col7, col8, col9, col10
  DotMatrix #(.matrixcols(32), .matrixrows(32)) dotmatrix_2 (
    .col9(bus_0), .col10(bus_0), .col11(bus_0), .col12(bus_0), .col13(bus_0), .col14(bus_0), .col15(bus_0),
    .col16(bus_0), .col17(bus_0), .col18(bus_0), .col19(bus_0), .col20(bus_0), .col21(bus_0), .col22(bus_0),
    .col23(bus_0), .col24(bus_0), .col25(bus_0), .col26(bus_0), .col27(bus_0), .col28(bus_0), .col29(bus_0),
    .col30(bus_0), .col31(bus_0));  // open: col0, col1, col2, col3, col4, col5, col6, col7, col8
endmodule

module disp_snake (
  input  hodn,
  input  [3:0] X,
  input  clock,
  input  [3:0] Y,
  input  rndr,
  input  clear,
  output [15:0] out_7,
  output [15:0] out_8,
  output [15:0] out_9,
  output [15:0] out_10,
  output [15:0] out_11,
  output [15:0] out_12,
  output [15:0] out_13,
  output [15:0] out_14,
  output [15:0] out_15,
  output [15:0] out_16,
  output [15:0] out_17,
  output [15:0] out_18,
  output [15:0] out_19,
  output [15:0] out_20,
  output [15:0] out_21,
  output current,
  output [15:0] out_23
);

  wire demultiplexer_1_out0, demultiplexer_1_out1, demultiplexer_1_out2, demultiplexer_1_out3,
       demultiplexer_1_out4, demultiplexer_1_out5, demultiplexer_1_out6, demultiplexer_1_out7,
       demultiplexer_1_out8, demultiplexer_1_out9, demultiplexer_1_out10, demultiplexer_1_out11,
       demultiplexer_1_out12, demultiplexer_1_out13, demultiplexer_1_out14, demultiplexer_1_out15,
       disper_snake_1_single, disper_snake_2_single, disper_snake_3_single, disper_snake_4_single,
       disper_snake_5_single, disper_snake_6_single, disper_snake_7_single, disper_snake_8_single,
       disper_snake_9_single, disper_snake_10_single, disper_snake_11_single, disper_snake_12_single,
       disper_snake_13_single, disper_snake_14_single, disper_snake_15_single, disper_snake_16_single,
       undriven, undriven_2, undriven_3, undriven_4, undriven_5, undriven_6, undriven_7, undriven_8,
       undriven_9, undriven_10, undriven_11, undriven_12, undriven_13, undriven_14, undriven_15, undriven_16,
       undriven_17, undriven_18, undriven_19, undriven_20, undriven_21, undriven_22, undriven_23,
       undriven_24, undriven_25, undriven_26, undriven_27, undriven_28, undriven_29, undriven_30,
       undriven_31, undriven_32, undriven_33, undriven_34, undriven_35;

  Demultiplexer #(.select(4)) demultiplexer_1 (
    .out0(demultiplexer_1_out0), .out1(demultiplexer_1_out1), .out2(demultiplexer_1_out2),
    .out3(demultiplexer_1_out3), .out4(demultiplexer_1_out4), .out5(demultiplexer_1_out5),
    .out6(demultiplexer_1_out6), .out7(demultiplexer_1_out7), .out8(demultiplexer_1_out8),
    .out9(demultiplexer_1_out9), .out10(demultiplexer_1_out10), .out11(demultiplexer_1_out11),
    .out12(demultiplexer_1_out12), .out13(demultiplexer_1_out13), .out14(demultiplexer_1_out14),
    .out15(demultiplexer_1_out15), .in(clock), .sel(Y));  // open: en
  disper_snake disper_snake_1 (
    .dmx(demultiplexer_1_out15), .hodn(hodn), .X(X), .coor(out_7), .single(disper_snake_1_single),
    .clear(clear), .rndr(rndr));
  disper_snake disper_snake_2 (
    .dmx(demultiplexer_1_out14), .hodn(hodn), .X(X), .coor(out_8), .single(disper_snake_2_single),
    .clear(clear), .rndr(rndr));
  disper_snake disper_snake_3 (
    .dmx(demultiplexer_1_out13), .hodn(hodn), .X(X), .coor(out_9), .single(disper_snake_3_single),
    .clear(clear), .rndr(rndr));
  disper_snake disper_snake_4 (
    .dmx(demultiplexer_1_out12), .hodn(hodn), .X(X), .coor(out_10), .single(disper_snake_4_single),
    .clear(clear), .rndr(rndr));
  disper_snake disper_snake_5 (
    .dmx(demultiplexer_1_out11), .hodn(hodn), .X(X), .coor(out_11), .single(disper_snake_5_single),
    .clear(clear), .rndr(rndr));
  disper_snake disper_snake_6 (
    .dmx(demultiplexer_1_out10), .hodn(hodn), .X(X), .coor(out_12), .single(disper_snake_6_single),
    .clear(clear), .rndr(rndr));
  disper_snake disper_snake_7 (
    .dmx(demultiplexer_1_out9), .hodn(hodn), .X(X), .coor(out_13), .single(disper_snake_7_single),
    .clear(clear), .rndr(rndr));
  disper_snake disper_snake_8 (
    .dmx(demultiplexer_1_out8), .hodn(hodn), .X(X), .coor(out_14), .single(disper_snake_8_single),
    .clear(clear), .rndr(rndr));
  disper_snake disper_snake_9 (
    .dmx(demultiplexer_1_out7), .hodn(hodn), .X(X), .coor(out_15), .single(disper_snake_9_single),
    .clear(clear), .rndr(rndr));
  disper_snake disper_snake_10 (
    .dmx(demultiplexer_1_out6), .hodn(hodn), .X(X), .coor(out_16), .single(disper_snake_10_single),
    .clear(clear), .rndr(rndr));
  disper_snake disper_snake_11 (
    .dmx(demultiplexer_1_out5), .hodn(hodn), .X(X), .coor(out_17), .single(disper_snake_11_single),
    .clear(clear), .rndr(rndr));
  disper_snake disper_snake_12 (
    .dmx(demultiplexer_1_out4), .hodn(hodn), .X(X), .coor(out_18), .single(disper_snake_12_single),
    .clear(clear), .rndr(rndr));
  disper_snake disper_snake_13 (
    .dmx(demultiplexer_1_out3), .hodn(hodn), .X(X), .coor(out_19), .single(disper_snake_13_single),
    .clear(clear), .rndr(rndr));
  disper_snake disper_snake_14 (
    .dmx(demultiplexer_1_out2), .hodn(hodn), .X(X), .coor(out_20), .single(disper_snake_14_single),
    .clear(clear), .rndr(rndr));
  disper_snake disper_snake_15 (
    .dmx(demultiplexer_1_out1), .hodn(hodn), .X(X), .coor(out_21), .single(disper_snake_15_single),
    .clear(clear), .rndr(rndr));
  disper_snake disper_snake_16 (
    .dmx(demultiplexer_1_out0), .hodn(hodn), .X(X), .coor(out_23), .single(disper_snake_16_single),
    .clear(clear), .rndr(rndr));
  Multiplexer #(.select(4)) multiplexer_1 (
    .in0(undriven), .in1(undriven_2), .in2(undriven_3), .in3(undriven_4), .in4(undriven_5), .in5(undriven_6),
    .in6(undriven_7), .in7(undriven_8), .in8(undriven_9), .in9(undriven_10), .in10(undriven_11),
    .in11(undriven_12), .in12(undriven_13), .in13(undriven_14), .in14(undriven_15), .in15(undriven_16),
    .out(current), .sel(Y));  // open: en
  counter counter_1 (
    .clock(undriven_34), .hodn(undriven_17), .dmx(undriven_18), .clear(undriven_35));  // open: mux, flag
  counter counter_2 (
    .clock(undriven_34), .hodn(undriven_17), .dmx(undriven_19), .clear(undriven_35));  // open: mux, flag
  counter counter_3 (
    .clock(undriven_34), .hodn(undriven_17), .dmx(undriven_20), .clear(undriven_35));  // open: mux, flag
  counter counter_4 (
    .clock(undriven_34), .hodn(undriven_17), .dmx(undriven_21), .clear(undriven_35));  // open: mux, flag
  counter counter_5 (
    .clock(undriven_34), .hodn(undriven_17), .dmx(undriven_22), .clear(undriven_35));  // open: mux, flag
  counter counter_6 (
    .clock(undriven_34), .hodn(undriven_17), .dmx(undriven_23), .clear(undriven_35));  // open: mux, flag
  counter counter_7 (
    .clock(undriven_34), .hodn(undriven_17), .dmx(undriven_24), .clear(undriven_35));  // open: mux, flag
  counter counter_8 (
    .clock(undriven_34), .hodn(undriven_17), .dmx(undriven_25), .clear(undriven_35));  // open: mux, flag
  counter counter_9 (
    .clock(undriven_34), .hodn(undriven_17), .dmx(undriven_26), .clear(undriven_35));  // open: mux, flag
  counter counter_10 (
    .clock(undriven_34), .hodn(undriven_17), .dmx(undriven_27), .clear(undriven_35));  // open: mux, flag
  counter counter_11 (
    .clock(undriven_34), .hodn(undriven_17), .dmx(undriven_28), .clear(undriven_35));  // open: mux, flag
  counter counter_12 (
    .clock(undriven_34), .hodn(undriven_17), .dmx(undriven_29), .clear(undriven_35));  // open: mux, flag
  counter counter_13 (
    .clock(undriven_34), .hodn(undriven_17), .dmx(undriven_30), .clear(undriven_35));  // open: mux, flag
  counter counter_14 (
    .clock(undriven_34), .hodn(undriven_17), .dmx(undriven_31), .clear(undriven_35));  // open: mux, flag
  counter counter_15 (
    .clock(undriven_34), .hodn(undriven_17), .dmx(undriven_32), .clear(undriven_35));  // open: mux, flag
  counter counter_16 (
    .clock(undriven_34), .hodn(undriven_17), .dmx(undriven_33), .clear(undriven_35));  // open: mux, flag
endmodule

module dispriadok_snake (
  input  clock,
  input  hodn,
  input  [3:0] X,
  input  clear,
  output [15:0] riadok,
  output single
);

  wire demultiplexer_1_out0, demultiplexer_1_out1, demultiplexer_1_out2, demultiplexer_1_out3,
       demultiplexer_1_out4, demultiplexer_1_out5, demultiplexer_1_out6, demultiplexer_1_out7,
       demultiplexer_1_out8, demultiplexer_1_out9, demultiplexer_1_out10, demultiplexer_1_out11,
       demultiplexer_1_out12, demultiplexer_1_out13, demultiplexer_1_out14, demultiplexer_1_out15;

  Demultiplexer #(.select(4)) demultiplexer_1 (
    .out0(demultiplexer_1_out0), .out1(demultiplexer_1_out1), .out2(demultiplexer_1_out2),
    .out3(demultiplexer_1_out3), .out4(demultiplexer_1_out4), .out5(demultiplexer_1_out5),
    .out6(demultiplexer_1_out6), .out7(demultiplexer_1_out7), .out8(demultiplexer_1_out8),
    .out9(demultiplexer_1_out9), .out10(demultiplexer_1_out10), .out11(demultiplexer_1_out11),
    .out12(demultiplexer_1_out12), .out13(demultiplexer_1_out13), .out14(demultiplexer_1_out14),
    .out15(demultiplexer_1_out15), .in(clock), .sel(X));  // open: en
  counter counter_1 (
    .clock(clock), .hodn(hodn), .dmx(demultiplexer_1_out0), .mux(riadok[15]), .clear(clear));  // open: flag
  D_Flip_Flop d_ff_1 ();  // open: clk, D, Q, Qn, preset, en, reset
  T_Flip_Flop t_ff_1 ();  // open: clk, T, Q, Qn, preset, reset, en
  J_K_Flip_Flop j_k_ff_1 ();  // open: J, clk, K, Q, Qn, preset, en, reset
  S_R_Flip_Flop s_r_ff_1 ();  // open: S, clk, R, Q, Qn, preset, reset, en
  counter counter_2 (
    .clock(clock), .hodn(hodn), .dmx(demultiplexer_1_out1), .mux(riadok[14]), .clear(clear));  // open: flag
  D_Flip_Flop d_ff_2 ();  // open: clk, D, Q, Qn, preset, en, reset
  T_Flip_Flop t_ff_2 ();  // open: clk, T, Q, Qn, preset, reset, en
  J_K_Flip_Flop j_k_ff_2 ();  // open: J, clk, K, Q, Qn, preset, en, reset
  S_R_Flip_Flop s_r_ff_2 ();  // open: S, clk, R, Q, Qn, preset, reset, en
  counter counter_3 (
    .clock(clock), .hodn(hodn), .dmx(demultiplexer_1_out2), .mux(riadok[13]), .clear(clear));  // open: flag
  D_Flip_Flop d_ff_3 ();  // open: clk, D, Q, Qn, preset, en, reset
  T_Flip_Flop t_ff_3 ();  // open: clk, T, Q, Qn, preset, reset, en
  J_K_Flip_Flop j_k_ff_3 ();  // open: J, clk, K, Q, Qn, preset, en, reset
  S_R_Flip_Flop s_r_ff_3 ();  // open: S, clk, R, Q, Qn, preset, reset, en
  counter counter_4 (
    .clock(clock), .hodn(hodn), .dmx(demultiplexer_1_out3), .mux(riadok[12]), .clear(clear));  // open: flag
  D_Flip_Flop d_ff_4 ();  // open: clk, D, Q, Qn, preset, en, reset
  T_Flip_Flop t_ff_4 ();  // open: clk, T, Q, Qn, preset, reset, en
  J_K_Flip_Flop j_k_ff_4 ();  // open: J, clk, K, Q, Qn, preset, en, reset
  S_R_Flip_Flop s_r_ff_4 ();  // open: S, clk, R, Q, Qn, preset, reset, en
  counter counter_5 (
    .clock(clock), .hodn(hodn), .dmx(demultiplexer_1_out5), .mux(riadok[10]), .clear(clear));  // open: flag
  counter counter_6 (
    .clock(clock), .hodn(hodn), .dmx(demultiplexer_1_out4), .mux(riadok[11]), .clear(clear));  // open: flag
  D_Flip_Flop d_ff_5 ();  // open: clk, D, Q, Qn, preset, en, reset
  T_Flip_Flop t_ff_5 ();  // open: clk, T, Q, Qn, preset, reset, en
  J_K_Flip_Flop j_k_ff_5 ();  // open: J, clk, K, Q, Qn, preset, en, reset
  S_R_Flip_Flop s_r_ff_5 ();  // open: S, clk, R, Q, Qn, preset, reset, en
  counter counter_7 (
    .clock(clock), .hodn(hodn), .dmx(demultiplexer_1_out6), .mux(riadok[9]), .clear(clear));  // open: flag
  D_Flip_Flop d_ff_6 ();  // open: clk, D, Q, Qn, preset, en, reset
  T_Flip_Flop t_ff_6 ();  // open: clk, T, Q, Qn, preset, reset, en
  J_K_Flip_Flop j_k_ff_6 ();  // open: J, clk, K, Q, Qn, preset, en, reset
  S_R_Flip_Flop s_r_ff_6 ();  // open: S, clk, R, Q, Qn, preset, reset, en
  counter counter_8 (
    .clock(clock), .hodn(hodn), .dmx(demultiplexer_1_out7), .mux(riadok[8]), .clear(clear));  // open: flag
  D_Flip_Flop d_ff_7 ();  // open: clk, D, Q, Qn, preset, en, reset
  T_Flip_Flop t_ff_7 ();  // open: clk, T, Q, Qn, preset, reset, en
  J_K_Flip_Flop j_k_ff_7 ();  // open: J, clk, K, Q, Qn, preset, en, reset
  S_R_Flip_Flop s_r_ff_7 ();  // open: S, clk, R, Q, Qn, preset, reset, en
  counter counter_9 (
    .clock(clock), .hodn(hodn), .dmx(demultiplexer_1_out8), .mux(riadok[7]), .clear(clear));  // open: flag
  D_Flip_Flop d_ff_8 ();  // open: clk, D, Q, Qn, preset, en, reset
  D_Flip_Flop d_ff_9 ();  // open: clk, D, Q, Qn, preset, en, reset
  T_Flip_Flop t_ff_8 ();  // open: clk, T, Q, Qn, preset, reset, en
  T_Flip_Flop t_ff_9 ();  // open: clk, T, Q, Qn, preset, reset, en
  J_K_Flip_Flop j_k_ff_8 ();  // open: J, clk, K, Q, Qn, preset, en, reset
  J_K_Flip_Flop j_k_ff_9 ();  // open: J, clk, K, Q, Qn, preset, en, reset
  S_R_Flip_Flop s_r_ff_8 ();  // open: S, clk, R, Q, Qn, preset, reset, en
  S_R_Flip_Flop s_r_ff_9 ();  // open: S, clk, R, Q, Qn, preset, reset, en
  counter counter_10 (
    .clock(clock), .hodn(hodn), .dmx(demultiplexer_1_out9), .mux(riadok[6]), .clear(clear));  // open: flag
  Multiplexer #(.select(4)) multiplexer_1 (
    .in0(riadok[15]), .in1(riadok[14]), .in2(riadok[13]), .in3(riadok[12]), .in4(riadok[11]),
    .in5(riadok[10]), .in6(riadok[9]), .in7(riadok[8]), .in8(riadok[7]), .in9(riadok[6]), .in10(riadok[5]),
    .in11(riadok[4]), .in12(riadok[3]), .in13(riadok[2]), .in14(riadok[1]), .in15(riadok[0]), .out(single),
    .sel(X));  // open: en
  D_Flip_Flop d_ff_10 ();  // open: clk, D, Q, Qn, preset, en, reset
  T_Flip_Flop t_ff_10 ();  // open: clk, T, Q, Qn, preset, reset, en
  J_K_Flip_Flop j_k_ff_10 ();  // open: J, clk, K, Q, Qn, preset, en, reset
  S_R_Flip_Flop s_r_ff_10 ();  // open: S, clk, R, Q, Qn, preset, reset, en
  counter counter_11 (
    .clock(clock), .hodn(hodn), .dmx(demultiplexer_1_out10), .mux(riadok[5]), .clear(clear));  // open: flag
  D_Flip_Flop d_ff_11 ();  // open: clk, D, Q, Qn, preset, en, reset
  T_Flip_Flop t_ff_11 ();  // open: clk, T, Q, Qn, preset, reset, en
  J_K_Flip_Flop j_k_ff_11 ();  // open: J, clk, K, Q, Qn, preset, en, reset
  S_R_Flip_Flop s_r_ff_11 ();  // open: S, clk, R, Q, Qn, preset, reset, en
  counter counter_12 (
    .clock(clock), .hodn(hodn), .dmx(demultiplexer_1_out11), .mux(riadok[4]), .clear(clear));  // open: flag
  D_Flip_Flop d_ff_12 ();  // open: clk, D, Q, Qn, preset, en, reset
  T_Flip_Flop t_ff_12 ();  // open: clk, T, Q, Qn, preset, reset, en
  J_K_Flip_Flop j_k_ff_12 ();  // open: J, clk, K, Q, Qn, preset, en, reset
  S_R_Flip_Flop s_r_ff_12 ();  // open: S, clk, R, Q, Qn, preset, reset, en
  counter counter_13 (
    .clock(clock), .hodn(hodn), .dmx(demultiplexer_1_out13), .mux(riadok[2]), .clear(clear));  // open: flag
  counter counter_14 (
    .clock(clock), .hodn(hodn), .dmx(demultiplexer_1_out12), .mux(riadok[3]), .clear(clear));  // open: flag
  D_Flip_Flop d_ff_13 ();  // open: clk, D, Q, Qn, preset, en, reset
  T_Flip_Flop t_ff_13 ();  // open: clk, T, Q, Qn, preset, reset, en
  J_K_Flip_Flop j_k_ff_13 ();  // open: J, clk, K, Q, Qn, preset, en, reset
  S_R_Flip_Flop s_r_ff_13 ();  // open: S, clk, R, Q, Qn, preset, reset, en
  counter counter_15 (
    .clock(clock), .hodn(hodn), .dmx(demultiplexer_1_out14), .mux(riadok[1]), .clear(clear));  // open: flag
  D_Flip_Flop d_ff_14 ();  // open: clk, D, Q, Qn, preset, en, reset
  T_Flip_Flop t_ff_14 ();  // open: clk, T, Q, Qn, preset, reset, en
  J_K_Flip_Flop j_k_ff_14 ();  // open: J, clk, K, Q, Qn, preset, en, reset
  S_R_Flip_Flop s_r_ff_14 ();  // open: S, clk, R, Q, Qn, preset, reset, en
  counter counter_16 (
    .clock(clock), .hodn(hodn), .dmx(demultiplexer_1_out15), .mux(riadok[0]), .clear(clear));  // open: flag
  D_Flip_Flop d_ff_15 ();  // open: clk, D, Q, Qn, preset, en, reset
  T_Flip_Flop t_ff_15 ();  // open: clk, T, Q, Qn, preset, reset, en
  J_K_Flip_Flop j_k_ff_15 ();  // open: J, clk, K, Q, Qn, preset, en, reset
  S_R_Flip_Flop s_r_ff_15 ();  // open: S, clk, R, Q, Qn, preset, reset, en
  D_Flip_Flop d_ff_16 ();  // open: clk, D, Q, Qn, preset, en, reset
  T_Flip_Flop t_ff_16 ();  // open: clk, T, Q, Qn, preset, reset, en
  J_K_Flip_Flop j_k_ff_16 ();  // open: J, clk, K, Q, Qn, preset, en, reset
  S_R_Flip_Flop s_r_ff_16 ();  // open: S, clk, R, Q, Qn, preset, reset, en
endmodule

module counter (
  input  dmx,
  input  hodn,
  input  clock,
  input  clear,
  output mux,
  output flag
);

  wire controlled_buffer_1_out, d_ff_2_q, or_1_out;
  wire [4:0] counter_1_q;

  D_Flip_Flop d_ff_1 (.clk(dmx), .D(hodn), .Q(mux), .reset(or_1_out));  // open: Qn, preset, en
  or or_1 (or_1_out, clear, flag);
  D_Flip_Flop d_ff_2 (.clk(dmx), .D(1'b1), .Q(d_ff_2_q), .reset(flag));  // open: Qn, preset, en
  assign controlled_buffer_1_out = d_ff_2_q ? clock : 1'bz;  // Controlled_Buffer controlled_buffer_1
  Counter #(.width(5), .max('hb)) counter_1 (
    .Q(counter_1_q), .clk(controlled_buffer_1_out), .clr(flag));  // open: load, D, count, carry
  Comparator #(.width(5)) comparator_1 (.a(counter_1_q), .b(5'b01010), .eq(flag));  // open: gt, lt
endmodule

module disper_snake (
  input  dmx,
  input  hodn,
  input  [3:0] X,
  input  clear,
  input  rndr,
  output [15:0] coor,
  output single
);

  wire or_1_out;
  wire [15:0] dispriadok_snake_1_riadok;

  dispriadok_snake dispriadok_snake_1 (
    .clock(dmx), .hodn(hodn), .X(X), .riadok(dispriadok_snake_1_riadok), .single(single), .clear(clear));
  Register #(.width(16)) register_1 (.D(dispriadok_snake_1_riadok), .Q(coor), .clk(rndr), .clr(or_1_out));  // open: en
  or or_1 (or_1_out, 1'b0, clear);
  counter counter_1 ();  // open: clock, hodn, dmx, mux, clear, flag
endmodule
