// Logisim project ПОСЛЕДНИЙ_ВАРИАНТ.circ as structural Verilog: 6 circuits, main circuit main
module main (
);

  wire and_1_out, and_2_out, button_2_out, button_3_out, button_4_out, button_5_out, clock, clr,
       counter_1_carry, d_ff_1_qn, decoder_2_out0, decoder_2_out1, decoder_2_out2, decoder_2_out3,
       decoder_2_out4, decoder_2_out5, decoder_2_out6, decoder_2_out7, decoder_2_out8, decoder_2_out9,
       decoder_2_out10, decoder_2_out11, decoder_2_out12, decoder_2_out13, decoder_2_out14, decoder_2_out15,
       down, granca_detection_1_out_6, left, or_1_out, or_4_out, or_5_out, right, up, xnor_1_out, xor_1_out;
  wire [1:0] multiplexer_1_out, or_2_out, register_2_q, register_5_q;
  wire [3:0] inc_dec_1_r, inc_dec_2_r;
  wire [7:0] register_1_q;
  wire [15:0] decoder_1_out0, n16_bit_and_1_output, n16_bit_and_2_output, n16_bit_and_3_output,
       n16_bit_and_4_output, n16_bit_and_5_output, n16_bit_and_6_output, n16_bit_and_7_output,
       n16_bit_and_8_output, n16_bit_and_9_output, n16_bit_and_10_output, n16_bit_and_11_output,
       n16_bit_and_12_output, n16_bit_and_13_output, n16_bit_and_14_output, n16_bit_and_15_output,
       n16_bit_and_16_output;

  Clock clock_1 (.out(clock));
  granca_detection granca_detection_1 (
    .in_3(register_1_q), .Left(left), .Right(right), .out_6(granca_detection_1_out_6), .Up(up), .Down(down));
  Button button_1 (.out(clr));
  Register register_1 (.D({inc_dec_1_r, inc_dec_2_r}), .Q(register_1_q), .clk(and_1_out), .clr(clr));  // open: en
  and and_1 (and_1_out, clock, d_ff_1_qn);
  D_Flip_Flop d_ff_1 (.Qn(d_ff_1_qn), .preset(granca_detection_1_out_6), .reset(clr));  // open: clk, D, Q, en
  or or_1 (or_1_out, left, right);
  Button button_2 (.out(button_2_out));
  or or_2 (or_2_out[0], button_5_out, button_4_out);
  or or_3 (or_2_out[1], button_4_out, button_2_out);
  or or_4 (or_4_out, button_4_out, button_5_out, button_2_out, button_3_out);
  inc_dec inc_dec_1 (.X(register_1_q[7:4]), .on_off(or_1_out), .inc_dec(right), .R(inc_dec_1_r));  // open: OFL
  inc_dec inc_dec_2 (.X(register_1_q[3:0]), .on_off(or_5_out), .inc_dec(up), .R(inc_dec_2_r));  // open: OFL
  Button button_3 (.out(button_3_out));
  Button button_4 (.out(button_4_out));
  Button button_5 (.out(button_5_out));
  or or_5 (or_5_out, up, down);
  Register #(.width(2)) register_2 (.D(or_2_out), .Q(register_2_q), .clk(or_4_out), .clr(clr));  // open: en
  Decoder #(.select(4), .disabled(0), .enable("false")) decoder_1 (
    .out0(decoder_1_out0[0]), .out1(decoder_1_out0[1]), .out2(decoder_1_out0[2]), .out3(decoder_1_out0[3]),
    .out4(decoder_1_out0[4]), .out5(decoder_1_out0[5]), .out6(decoder_1_out0[6]), .out7(decoder_1_out0[7]),
    .out8(decoder_1_out0[8]), .out9(decoder_1_out0[9]), .out10(decoder_1_out0[10]),
    .out11(decoder_1_out0[11]), .out12(decoder_1_out0[12]), .out13(decoder_1_out0[13]),
    .out14(decoder_1_out0[14]), .out15(decoder_1_out0[15]), .sel(register_1_q[3:0]));
  Register #(.width(4)) register_3 (.D(register_1_q[3:0]), .clk(clock), .clr(clr));  // open: en, Q
  Register #(.width(4)) register_4 (.D(register_1_q[7:4]), .clk(clock), .clr(clr));  // open: en, Q
  Register #(.width(2)) register_5 (.D(multiplexer_1_out), .Q(register_5_q), .clk(or_4_out), .clr(clr));  // open: en
  DotMatrix #(.inputtype("row"), .matrixcols(17), .matrixrows(17), .persist(5)) dotmatrix_1 (
    .row0({17{1'b1}}), .row1({17{1'b1}}), .row2({17{1'b1}}), .row3({17{1'b1}}), .row4({17{1'b1}}),
    .row5({17{1'b1}}), .row6({17{1'b1}}), .row7({17{1'b1}}), .row8({17{1'b1}}), .row9({17{1'b1}}),
    .row10({17{1'b1}}), .row11({17{1'b1}}), .row12({17{1'b1}}), .row13({17{1'b1}}), .row14({17{1'b1}}),
    .row15({17{1'b1}}), .row16({17{1'b1}}));
  DotMatrix #(.matrixcols(16), .matrixrows(16)) dotmatrix_2 (
    .col0(n16_bit_and_2_output), .col1(n16_bit_and_1_output), .col2(n16_bit_and_4_output),
    .col3(n16_bit_and_3_output), .col4(n16_bit_and_5_output), .col5(n16_bit_and_6_output),
    .col6(n16_bit_and_7_output), .col7(n16_bit_and_8_output), .col8(n16_bit_and_9_output),
    .col9(n16_bit_and_10_output), .col10(n16_bit_and_12_output), .col11(n16_bit_and_11_output),
    .col12(n16_bit_and_14_output), .col13(n16_bit_and_13_output), .col14(n16_bit_and_15_output),
    .col15(n16_bit_and_16_output));
  _16_bit_AND u_16_bit_and_1 (.\input (decoder_1_out0), .switch(decoder_2_out1), .\output (n16_bit_and_1_output));
  _16_bit_AND u_16_bit_and_2 (.\input (decoder_1_out0), .switch(decoder_2_out0), .\output (n16_bit_and_2_output));
  xnor xnor_1 (xnor_1_out, register_5_q[1], register_2_q[1]);
  xor xor_1 (xor_1_out, register_5_q[0], register_2_q[0]);
  _16_bit_AND u_16_bit_and_3 (.\input (decoder_1_out0), .switch(decoder_2_out3), .\output (n16_bit_and_3_output));
  _16_bit_AND u_16_bit_and_4 (.\input (decoder_1_out0), .switch(decoder_2_out2), .\output (n16_bit_and_4_output));
  Decoder #(.select(4), .disabled(0), .enable("false")) decoder_2 (
    .out0(decoder_2_out0), .out1(decoder_2_out1), .out2(decoder_2_out2), .out3(decoder_2_out3),
    .out4(decoder_2_out4), .out5(decoder_2_out5), .out6(decoder_2_out6), .out7(decoder_2_out7),
    .out8(decoder_2_out8), .out9(decoder_2_out9), .out10(decoder_2_out10), .out11(decoder_2_out11),
    .out12(decoder_2_out12), .out13(decoder_2_out13), .out14(decoder_2_out14), .out15(decoder_2_out15),
    .sel(register_1_q[7:4]));
  Multiplexer #(.width(2)) multiplexer_1 (
    .in0(register_2_q), .in1(register_5_q), .out(multiplexer_1_out), .sel(and_2_out));  // open: en
  and and_2 (and_2_out, xnor_1_out, xor_1_out);
  _16_bit_AND u_16_bit_and_5 (.\input (decoder_1_out0), .switch(decoder_2_out4), .\output (n16_bit_and_5_output));
  _16_bit_AND u_16_bit_and_6 (.\input (decoder_1_out0), .switch(decoder_2_out5), .\output (n16_bit_and_6_output));
  _16_bit_AND u_16_bit_and_7 (.\input (decoder_1_out0), .switch(decoder_2_out6), .\output (n16_bit_and_7_output));
  _16_bit_AND u_16_bit_and_8 (.\input (decoder_1_out0), .switch(decoder_2_out7), .\output (n16_bit_and_8_output));
  Counter #(.width(3), .max('h5)) counter_1 (
    .carry(counter_1_carry), .clk(clock), .clr(clr));  // open: load, D, count, Q
  Demultiplexer #(.select(2)) demultiplexer_1 (
    .out0(up), .out1(down), .out2(left), .out3(right), .in(counter_1_carry), .sel(multiplexer_1_out));  // open: en
  _16_bit_AND u_16_bit_and_9 (.\input (decoder_1_out0), .switch(decoder_2_out8), .\output (n16_bit_and_9_output));
  _16_bit_AND u_16_bit_and_10 (.\input (decoder_1_out0), .switch(decoder_2_out9), .\output (n16_bit_and_10_output));
  _16_bit_AND u_16_bit_and_11 (.\input (decoder_1_out0), .switch(decoder_2_out11), .\output (n16_bit_and_11_output));
  _16_bit_AND u_16_bit_and_12 (.\input (decoder_1_out0), .switch(decoder_2_out10), .\output (n16_bit_and_12_output));
  _16_bit_AND u_16_bit_and_13 (.\input (decoder_1_out0), .switch(decoder_2_out13), .\output (n16_bit_and_13_output));
  _16_bit_AND u_16_bit_and_14 (.\input (decoder_1_out0), .switch(decoder_2_out12), .\output (n16_bit_and_14_output));
  _16_bit_AND u_16_bit_and_15 (.\input (decoder_1_out0), .switch(decoder_2_out14), .\output (n16_bit_and_15_output));
  _16_bit_AND u_16_bit_and_16 (.\input (decoder_1_out0), .switch(decoder_2_out15), .\output (n16_bit_and_16_output));

  // Notes on the sheet:
  //   новое напр.
  //   coor Y
  //   coor X
  //   текушее напр.
endmodule

module _16_bit_AND (
  input  [15:0] \input ,
  input  switch,
  output [15:0] \output 
);

  assign \output  = \input  & {16{switch}};  // AND_Gate and_1, 16 bits wide
endmodule

module column_switch (
  input  [3:0] in_1,
  input  [3:0] in_2
);
endmodule

module inc_dec (
  input  [3:0] X,
  input  on_off,
  input  inc_dec,
  output [3:0] R,
  output OFL
);

  wire and_2_out, and_3_out;
  wire [3:0] and_1_out, xor_1_out, xor_2_out, xor_3_out;
  wire [3:3] decoder_1_out0, decoder_1_out1;

  Decoder #(.enable("false")) decoder_1 (.out0(decoder_1_out0[3]), .out1(decoder_1_out1[3]), .sel(inc_dec));
  assign xor_1_out = {4{decoder_1_out0[3]}} ^ X;  // XOR_Gate xor_1, 4 bits wide
  assign xor_2_out = {4{decoder_1_out1[3]}} ^ xor_3_out;  // XOR_Gate xor_2, 4 bits wide
  assign and_1_out = xor_1_out & xor_2_out;  // AND_Gate and_1, 4 bits wide
  and and_2 (and_2_out, and_1_out[3], inc_dec);
  and and_3 (and_3_out, and_1_out[3], ~inc_dec);  // AND_Gate
  assign xor_3_out = X ^ {and_1_out[2:0], 1'b1};  // XOR_Gate xor_3, 4 bits wide
  or or_1 (OFL, and_2_out, and_3_out);
  Multiplexer #(.width(4), .enable("false")) multiplexer_1 (.in0(X), .in1(xor_3_out), .out(R), .sel(on_off));
endmodule

module granca_detection (
  input  Up,
  input  Down,
  input  [7:0] in_3,
  input  Left,
  input  Right,
  output out_6
);

  wire and_1_out, and_2_out, nor_1_out, nor_2_out;

  Pull_Resistor pull_resistor_1 (.node(Up));
  Pull_Resistor pull_resistor_2 (.node(Down));
  Pull_Resistor pull_resistor_3 (.node(Left));
  Pull_Resistor pull_resistor_4 (.node(Right));
  and and_1 (and_1_out, Up, in_3[3], in_3[2], in_3[1], in_3[0]);
  and and_2 (and_2_out, in_3[7], in_3[6], in_3[5], in_3[4], Right);
  nor nor_1 (nor_1_out, ~Down, in_3[0], in_3[1], in_3[2], in_3[3]);  // NOR_Gate
  nor nor_2 (nor_2_out, in_3[4], in_3[5], in_3[6], in_3[7], ~Left);  // NOR_Gate
  or or_1 (out_6, and_1_out, nor_1_out, nor_2_out, and_2_out);
endmodule

module movement (
  input  Right,
  input  Down,
  input  Left,
  input  Up,
  input  Clock,
  input  Clock_2,
  output out_7,
  output out_8,
  output out_9,
  output out_10
);

  wire and_1_out, counter_1_carry, demultiplexer_1_out0, demultiplexer_1_out1, demultiplexer_1_out2,
       demultiplexer_1_out3, or_3_out, xnor_1_out, xor_1_out;
  wire [1:0] multiplexer_1_out, or_1_out, register_1_q, register_2_q;

  or or_1 (or_1_out[0], Down, Right);
  or or_2 (or_1_out[1], Right, Left);
  or or_3 (or_3_out, Right, Down, Left, Up);
  Register #(.width(2)) register_1 (.D(or_1_out), .Q(register_1_q), .clk(or_3_out), .clr(Clock_2));  // open: en
  Register #(.width(2)) register_2 (
    .D(multiplexer_1_out), .Q(register_2_q), .clk(or_3_out), .clr(Clock_2));  // open: en
  xnor xnor_1 (xnor_1_out, register_2_q[1], register_1_q[1]);
  and and_1 (and_1_out, xnor_1_out, xor_1_out);
  xor xor_1 (xor_1_out, register_2_q[0], register_1_q[0]);
  Multiplexer #(.width(2)) multiplexer_1 (
    .in0(register_1_q), .in1(register_2_q), .out(multiplexer_1_out), .sel(and_1_out));  // open: en
  Counter #(.width(3), .max('h5)) counter_1 (
    .carry(counter_1_carry), .clk(Clock), .clr(Clock_2));  // open: load, D, count, Q
  Demultiplexer #(.select(2)) demultiplexer_1 (
    .out0(demultiplexer_1_out0), .out1(demultiplexer_1_out1), .out2(demultiplexer_1_out2),
    .out3(demultiplexer_1_out3), .in(counter_1_carry), .sel(multiplexer_1_out));  // open: en

  // Other names for the same wires on the sheet: clr = Clock_2

  // Notes on the sheet:
  //   новое напр.
  //   текушее напр.
endmodule
